// Logisim project 00_0_default.circ as structural Verilog: 1 circuit, main circuit main
module main (
  input  in_1,
  input  A,
  input  B,
  input  [3:0] in_4,
  input  A_2,
  input  B_2,
  input  [3:0] in_7,
  input  [3:0] in_8,
  input  [3:0] in_9,
  input  A_3,
  input  B_3,
  input  [3:0] in_12,
  input  [3:0] in_13,
  input  [1:0] in_14,
  input  [3:0] in_15,
  input  in_16,
  input  in_17,
  input  [3:0] in_18,
  input  [3:0] in_19,
  input  [1:0] in_20,
  input  [3:0] in_21,
  input  in_22,
  input  [3:0] in_23,
  input  [3:0] in_24,
  input  [3:0] in_25,
  input  in_26,
  input  [3:0] in_27,
  input  [1:0] in_28,
  input  in_29,
  input  in_30,
  input  in_31,
  output out_32,
  output out_33,
  output out_34,
  output SA,
  output [7:0] out_36,
  output SB,
  output [7:0] out_38,
  output [7:0] out_39,
  output SA_2,
  output SB_2,
  output [3:0] out_42,
  output SA_3,
  output SB_3,
  output [7:0] out_45,
  output [3:0] out_46,
  output [1:0] out_47,
  output [7:0] out_48,
  output [7:0] out_49,
  output out_50,
  output [7:0] out_51,
  output out_52,
  output [1:0] out_53,
  output [7:0] out_54,
  output out_55,
  output out_56,
  output [7:0] out_57,
  output [7:0] out_58,
  output [7:0] out_59,
  output out_60,
  output out_61,
  output [1:0] out_62,
  output [7:0] out_63,
  output [1:0] out_64,
  output [7:0] out_65,
  output [3:0] out_66,
  output [3:0] out_67,
  output [7:0] out_68,
  output [7:0] out_69
);

  wire button_1_out;

  // Probe on 4'b0010
  // Probe on 4'b0010
  // Probe on 4'b0010
  // Probe on 4'b0010
  // Probe on 4'b0010
  Button button_1 (.out(button_1_out));
  LED led_1 (.in(button_1_out));
  // Probe on 4'b0010
  // Probe on 4'b0010
  // Probe on 4'b0010
  // Probe on 4'b0010
  // Probe on 4'b0010
  assign out_38 = {{4{1'b0}}, in_4};  // Bit_Extender bit_extender_1
  assign out_45 = {{4{1'b0}}, in_12};  // Bit_Extender bit_extender_2
  assign out_48 = {{4{1'b1}}, in_15};  // Bit_Extender bit_extender_3
  assign out_54 = {{4{1'b1}}, in_21};  // Bit_Extender bit_extender_4
  assign out_58 = {{4{in_23[3]}}, in_23};  // Bit_Extender bit_extender_5
  assign out_63 = {{4{in_27[3]}}, in_27};  // Bit_Extender bit_extender_6
  assign out_65 = {{7{in_29}}, in_29};  // Bit_Extender bit_extender_7
  assign out_69 = {{7{in_31}}, in_31};  // Bit_Extender bit_extender_8

  assign out_32 = 1'b0;
  assign out_33 = 1'b1;
  assign out_34 = in_1;
  assign out_36 = {4'b0000, in_9};
  assign out_39 = {4'b0000, in_7};
  assign out_42 = {in_8[0], in_8[1], in_8[2], in_8[3]};
  assign out_46 = {in_13[0], in_13[1], in_13[2], in_13[3]};
  assign out_47 = in_14;
  assign out_49 = {4'b1111, in_19};
  assign out_50 = in_16;
  assign out_51 = {4'b1111, in_18};
  assign out_52 = in_17;
  assign out_53 = in_20;
  assign out_55 = in_22;
  assign out_56 = in_22;
  assign out_57 = {{5{in_25[3]}}, in_25[2:0]};
  assign out_59 = {{5{in_24[3]}}, in_24[2:0]};
  assign out_60 = in_26;
  assign out_61 = in_26;
  assign out_62 = in_28;
  assign out_64 = in_28;
  assign out_66 = 4'b0010;
  assign out_67 = 4'b0010;
  assign out_68 = {8{in_30}};
  assign SA = A;
  assign SA_2 = A_2;
  assign SA_3 = A_3;
  assign SB = B;
  assign SB_2 = B_2;
  assign SB_3 = B_3;

  // Other names for the same wires on the sheet: T0 = in_17; T1 = in_26; T2[1:0] = in_20; T3[1:0] = in_28
endmodule
