// Logisim project 00_ADD_S.circ as structural Verilog: 3 circuits, main circuit main_F
module main_F (
  input  [3:0] A,
  input  [3:0] B,
  input  enable,
  input  count,
  input  H,
  input  clear,
  input  clearAff,
  output [3:0] out_8,
  output [3:0] S,
  output out_10
);

  wire adder_1_cout, and_1_out, and_2_out, counter_1_carry, d_ff_1_q, multiplexer_1_out, multiplexer_2_out;
  wire [2:0] counter_1_q;
  wire [3:0] demultiplexer_1_out0, or_1_out;

  // Probe on A
  // Probe on A
  // Probe on A
  // Probe on B
  // Probe on B
  // Probe on B
  and and_1 (and_1_out, enable, count);
  and and_2 (and_2_out, enable, H);
  Multiplexer #(.select(2), .disabled(0)) multiplexer_1 (
    .in0(A[0]), .in1(A[1]), .in2(A[2]), .in3(A[3]), .out(multiplexer_1_out), .sel(counter_1_q[1:0]),
    .en(enable));
  Multiplexer #(.select(2), .disabled(0)) multiplexer_2 (
    .in0(B[0]), .in1(B[1]), .in2(B[2]), .in3(B[3]), .out(multiplexer_2_out), .sel(counter_1_q[1:0]),
    .en(enable));
  Counter #(.width(3), .max('h7), .trigger("falling")) counter_1 (
    .load(1'b0), .D(3'b000), .count(and_1_out), .Q(counter_1_q), .carry(counter_1_carry), .clk(and_2_out),
    .clr(clear));
  D_Flip_Flop d_ff_1 (
    .clk(and_2_out), .D(adder_1_cout), .Q(d_ff_1_q), .preset(1'b0), .en(enable), .reset(clear));  // open: Qn
  Adder #(.width(1)) adder_1 (
    .a(multiplexer_1_out), .b(multiplexer_2_out), .out(out_10), .cin(d_ff_1_q), .cout(adder_1_cout));
  Demultiplexer #(.select(2), .disabled(0)) demultiplexer_1 (
    .out0(demultiplexer_1_out0[0]), .out1(demultiplexer_1_out0[1]), .out2(demultiplexer_1_out0[2]),
    .out3(demultiplexer_1_out0[3]), .in(out_10), .sel(counter_1_q[1:0]), .en(enable));
  assign or_1_out = out_8 | demultiplexer_1_out0;  // OR_Gate or_1, 4 bits wide
  Register #(.width(4)) register_1 (.D(or_1_out), .en(enable), .Q(out_8), .clk(and_2_out), .clr(clear));
  // Probe on out_8
  // Probe on out_8
  // Probe on out_8
  Register #(.width(4)) register_2 (.D(out_8), .en(counter_1_carry), .Q(S), .clk(and_2_out), .clr(clearAff));
endmodule

module main (
  input  [3:0] in_1,
  input  [3:0] in_2,
  input  Enable,
  input  C,
  input  H,
  input  CLR,
  output [3:0] out_7,
  output out_8,
  output out_9,
  output out_10,
  output [3:0] out_11,
  output END
);

  wire adder_1_cout, and_1_out, and_2_out, and_3_out, and_4_out, comparator_1_gt, comparator_1_lt, d_ff_1_q,
       or_1_out, or_2_out;
  wire [2:0] counter_1_q;
  wire [3:0] ps_1_qd, ps_2_qd;

  // Probe on in_1
  // Probe on in_1
  // Probe on in_1
  // Probe on in_2
  // Probe on in_2
  // Probe on in_2
  and and_1 (and_1_out, or_2_out, Enable);
  Counter #(.width(3), .max('h7), .trigger("falling")) counter_1 (
    .load(1'b0), .D(3'b000), .count(and_2_out), .Q(counter_1_q), .clk(and_3_out), .clr(CLR));  // open: carry
  and and_2 (and_2_out, and_1_out, C);
  and and_3 (and_3_out, and_1_out, H);
  // Probe on ps_1_qd
  // Probe on ps_1_qd
  // Probe on ps_1_qd
  // Probe on ps_1_qd
  PS ps_1 (.D(in_1), .V(or_1_out), .H(and_3_out), .P(1'b0), .E(and_1_out), .C(CLR), .Q(out_8), .QD(ps_1_qd));
  PS ps_2 (.D(in_2), .V(or_1_out), .H(and_3_out), .P(1'b0), .E(and_1_out), .C(CLR), .Q(out_10), .QD(ps_2_qd));
  // Probe on ps_2_qd
  // Probe on ps_2_qd
  // Probe on ps_2_qd
  // Probe on ps_2_qd
  or or_1 (or_1_out, counter_1_q[0], counter_1_q[1], counter_1_q[2]);
  Comparator #(.width(3)) comparator_1 (
    .a(counter_1_q), .b(3'b101), .gt(comparator_1_gt), .eq(END), .lt(comparator_1_lt));
  and and_4 (and_4_out, or_1_out, and_3_out);
  or or_2 (or_2_out, comparator_1_gt, comparator_1_lt);
  D_Flip_Flop d_ff_1 (
    .clk(and_4_out), .D(adder_1_cout), .Q(d_ff_1_q), .preset(1'b0), .en(and_1_out), .reset(CLR));  // open: Qn
  Adder #(.width(1)) adder_1 (.a(out_8), .b(out_10), .out(out_9), .cin(d_ff_1_q), .cout(adder_1_cout));
  D_Flip_Flop d_ff_2 (
    .clk(and_4_out), .D(out_9), .Q(out_7[3]), .preset(1'b0), .en(and_1_out), .reset(CLR));  // open: Qn
  D_Flip_Flop d_ff_3 (
    .clk(and_4_out), .D(out_7[3]), .Q(out_7[2]), .preset(1'b0), .en(and_1_out), .reset(CLR));  // open: Qn
  D_Flip_Flop d_ff_4 (
    .clk(and_4_out), .D(out_7[2]), .Q(out_7[1]), .preset(1'b0), .en(and_1_out), .reset(CLR));  // open: Qn
  D_Flip_Flop d_ff_5 (
    .clk(and_4_out), .D(out_7[1]), .Q(out_7[0]), .preset(1'b0), .en(and_1_out), .reset(CLR));  // open: Qn
  // Probe on out_7
  // Probe on out_7
  // Probe on out_7
  Register #(.width(4)) register_1 (.D(out_7), .en(END), .Q(out_11), .clk(H), .clr(CLR));
endmodule

module PS (
  input  [3:0] D,
  input  V,
  input  H,
  input  P,
  input  E,
  input  C,
  output [3:0] QD,
  output Q
);

  wire and_1_out, and_2_out, and_3_out, and_4_out, and_5_out, and_6_out, and_7_out, and_8_out, not_1_out,
       or_1_out, or_2_out, or_3_out, or_4_out;

  and and_1 (and_1_out, D[3], not_1_out);
  and and_2 (and_2_out, V, 1'b0);
  not not_1 (not_1_out, V);
  and and_3 (and_3_out, D[2], not_1_out);
  or or_1 (or_1_out, and_1_out, and_2_out);
  and and_4 (and_4_out, V, QD[3]);
  D_Flip_Flop d_ff_1 (.clk(H), .D(or_1_out), .Q(QD[3]), .preset(P), .en(E), .reset(C));  // open: Qn
  or or_2 (or_2_out, and_3_out, and_4_out);
  and and_5 (and_5_out, D[1], not_1_out);
  and and_6 (and_6_out, V, QD[2]);
  D_Flip_Flop d_ff_2 (.clk(H), .D(or_2_out), .Q(QD[2]), .preset(P), .en(E), .reset(C));  // open: Qn
  and and_7 (and_7_out, D[0], not_1_out);
  or or_3 (or_3_out, and_5_out, and_6_out);
  and and_8 (and_8_out, V, QD[1]);
  D_Flip_Flop d_ff_3 (.clk(H), .D(or_3_out), .Q(QD[1]), .preset(P), .en(E), .reset(C));  // open: Qn
  or or_4 (or_4_out, and_7_out, and_8_out);
  D_Flip_Flop d_ff_4 (.clk(H), .D(or_4_out), .Q(Q), .preset(P), .en(E), .reset(C));  // open: Qn

  assign QD[0] = Q;
endmodule
