// Logisim project 00_SHIFTER_S.circ as structural Verilog: 8 circuits, main circuit main
module main (
  input  [3:0] in_1,
  input  [1:0] in_2,
  output [3:0] out_3,
  output [3:0] out_4,
  output [3:0] out_5,
  output [3:0] out_6,
  output [3:0] out_7,
  output [3:0] out_8,
  output [3:0] out_9,
  output [3:0] out_10
);

  wire clock_1_out;

  Clock clock_1 (.out(clock_1_out));
  Shifter #(.width(4)) shifter_1 (.in(in_1), .\dist (in_2), .out(out_3));
  SFLB sflb_1 (.data(in_1), .\dist (in_2), .S(out_5), .H(clock_1_out));
  Shifter #(.width(4), .shift("rl")) shifter_2 (.in(in_1), .\dist (in_2), .out(out_7));
  SRLB srlb_1 (.data(in_1), .\dist (in_2), .S(out_9), .H(clock_1_out));
  Shifter #(.width(4), .shift("lr")) shifter_3 (.in(in_1), .\dist (in_2), .out(out_4));
  SFRB sfrb_1 (.data(in_1), .\dist (in_2), .S(out_6), .H(clock_1_out));
  Shifter #(.width(4), .shift("rr")) shifter_4 (.in(in_1), .\dist (in_2), .out(out_8));
  SRRB srrb_1 (.data(in_1), .\dist (in_2), .S(out_10), .H(clock_1_out));
endmodule

module MDB (
  input  H,
  input  \end ,
  input  clear,
  input  enable,
  output clearO
);

  wire d_ff_1_q;

  or or_1 (clearO, d_ff_1_q, clear);
  D_Flip_Flop d_ff_1 (.clk(H), .D(\end ), .Q(d_ff_1_q), .preset(1'b0), .en(enable), .reset(clearO));  // open: Qn
endmodule

module SFR (
  input  [3:0] data,
  input  CIN,
  input  [1:0] \dist ,
  input  enable,
  input  H,
  input  clear,
  input  clearO,
  output COUT,
  output [3:0] S,
  output \end 
);

  wire and_1_out, and_2_out, and_3_out, and_4_out, and_5_out, and_6_out, and_7_out, and_8_out, and_9_out,
       and_10_out, and_11_out, comparator_1_eq, comparator_1_lt, not_2_out, not_3_out, not_4_out, not_5_out,
       or_1_out, or_2_out, or_3_out, or_4_out, or_5_out, or_6_out;
  wire [3:0] counter_1_q, not_1_out;
  wire [3:1] d_ff_2_q;

  assign not_1_out = ~counter_1_q;  // NOT_Gate not_1, 4 bits wide
  and and_1 (and_1_out, not_1_out[0], not_1_out[1], not_1_out[2], not_1_out[3]);
  and and_2 (and_2_out, enable, or_6_out);
  not not_2 (not_2_out, and_1_out);
  not not_3 (not_3_out, and_1_out);
  not not_4 (not_4_out, and_1_out);
  not not_5 (not_5_out, and_1_out);
  Counter #(.width(4), .max('hf), .trigger("falling")) counter_1 (
    .load(1'b0), .D(4'b0000), .count(and_2_out), .Q(counter_1_q), .clk(H), .clr(clear));  // open: carry
  and and_3 (and_3_out, data[0], and_1_out);
  or or_1 (or_1_out, and_3_out, and_4_out);
  and and_4 (and_4_out, not_2_out, d_ff_2_q[1]);
  and and_5 (and_5_out, data[1], and_1_out);
  or or_2 (or_2_out, and_5_out, and_6_out);
  and and_6 (and_6_out, not_3_out, d_ff_2_q[2]);
  and and_7 (and_7_out, data[2], and_1_out);
  or or_3 (or_3_out, and_7_out, and_8_out);
  and and_8 (and_8_out, not_4_out, d_ff_2_q[3]);
  and and_9 (and_9_out, data[3], and_1_out);
  or or_4 (or_4_out, and_9_out, and_10_out);
  and and_10 (and_10_out, not_5_out, CIN);
  or or_5 (or_5_out, and_1_out, and_2_out);
  or or_6 (or_6_out, comparator_1_lt, comparator_1_eq);
  D_Flip_Flop #(.trigger("falling")) d_ff_1 (
    .clk(H), .D(or_1_out), .Q(COUT), .preset(1'b0), .en(or_5_out), .reset(clear));  // open: Qn
  D_Flip_Flop #(.trigger("falling")) d_ff_2 (
    .clk(H), .D(or_2_out), .Q(d_ff_2_q[1]), .preset(1'b0), .en(or_5_out), .reset(clear));  // open: Qn
  D_Flip_Flop #(.trigger("falling")) d_ff_3 (
    .clk(H), .D(or_3_out), .Q(d_ff_2_q[2]), .preset(1'b0), .en(or_5_out), .reset(clear));  // open: Qn
  D_Flip_Flop #(.trigger("falling")) d_ff_4 (
    .clk(H), .D(or_4_out), .Q(d_ff_2_q[3]), .preset(1'b0), .en(or_5_out), .reset(clear));  // open: Qn
  Comparator #(.width(4)) comparator_1 (
    .a(counter_1_q), .b({2'b00, \dist }), .gt(\end ), .eq(comparator_1_eq), .lt(comparator_1_lt));
  and and_11 (and_11_out, \end , enable);
  Register #(.width(4)) register_1 (.D({d_ff_2_q, COUT}), .en(and_11_out), .Q(S), .clk(H), .clr(clearO));
endmodule

module SFRB (
  input  H,
  input  [3:0] data,
  input  [1:0] \dist ,
  output [3:0] S
);

  wire mdb_1_clearo, sfr_1_end;

  MDB mdb_1 (.H(H), .\end (sfr_1_end), .clear(1'b0), .enable(1'b1), .clearO(mdb_1_clearo));
  SFR sfr_1 (
    .data(data), .CIN(1'b0), .\dist (\dist ), .enable(1'b1), .H(H), .clear(mdb_1_clearo), .clearO(1'b0),
    .S(S), .\end (sfr_1_end));  // open: COUT
endmodule

module SRRB (
  input  H,
  input  [3:0] data,
  input  [1:0] \dist ,
  output [3:0] S
);

  wire mdb_1_clearo, sfr_1_cout, sfr_1_end;

  MDB mdb_1 (.H(H), .\end (sfr_1_end), .clear(1'b0), .enable(1'b1), .clearO(mdb_1_clearo));
  SFR sfr_1 (
    .data(data), .CIN(sfr_1_cout), .\dist (\dist ), .enable(1'b1), .H(H), .clear(mdb_1_clearo),
    .clearO(1'b0), .COUT(sfr_1_cout), .S(S), .\end (sfr_1_end));
endmodule

module SFL (
  input  CIN,
  input  [3:0] data,
  input  [1:0] \dist ,
  input  enable,
  input  H,
  input  clear,
  input  clearO,
  output [3:0] S,
  output COUT,
  output \end 
);

  wire and_1_out, and_2_out, and_3_out, and_4_out, and_5_out, and_6_out, and_7_out, and_8_out, and_9_out,
       and_10_out, and_11_out, comparator_1_eq, comparator_1_lt, not_2_out, not_3_out, not_4_out, not_5_out,
       or_1_out, or_2_out, or_3_out, or_4_out, or_5_out, or_6_out;
  wire [2:0] d_ff_1_q;
  wire [3:0] counter_1_q, not_1_out;

  assign not_1_out = ~counter_1_q;  // NOT_Gate not_1, 4 bits wide
  and and_1 (and_1_out, not_1_out[0], not_1_out[1], not_1_out[2], not_1_out[3]);
  and and_2 (and_2_out, enable, or_6_out);
  not not_2 (not_2_out, and_1_out);
  not not_3 (not_3_out, and_1_out);
  not not_4 (not_4_out, and_1_out);
  not not_5 (not_5_out, and_1_out);
  Counter #(.width(4), .max('hf), .trigger("falling")) counter_1 (
    .load(1'b0), .D(4'b0000), .count(and_2_out), .Q(counter_1_q), .clk(H), .clr(clear));  // open: carry
  and and_3 (and_3_out, CIN, not_2_out);
  or or_1 (or_1_out, and_3_out, and_4_out);
  and and_4 (and_4_out, and_1_out, data[0]);
  and and_5 (and_5_out, d_ff_1_q[0], not_3_out);
  or or_2 (or_2_out, and_5_out, and_6_out);
  and and_6 (and_6_out, and_1_out, data[1]);
  and and_7 (and_7_out, d_ff_1_q[1], not_4_out);
  or or_3 (or_3_out, and_7_out, and_8_out);
  and and_8 (and_8_out, and_1_out, data[2]);
  and and_9 (and_9_out, d_ff_1_q[2], not_5_out);
  or or_4 (or_4_out, and_9_out, and_10_out);
  and and_10 (and_10_out, and_1_out, data[3]);
  or or_5 (or_5_out, and_1_out, and_2_out);
  or or_6 (or_6_out, comparator_1_lt, comparator_1_eq);
  D_Flip_Flop #(.trigger("falling")) d_ff_1 (
    .clk(H), .D(or_1_out), .Q(d_ff_1_q[0]), .preset(1'b0), .en(or_5_out), .reset(clear));  // open: Qn
  D_Flip_Flop #(.trigger("falling")) d_ff_2 (
    .clk(H), .D(or_2_out), .Q(d_ff_1_q[1]), .preset(1'b0), .en(or_5_out), .reset(clear));  // open: Qn
  D_Flip_Flop #(.trigger("falling")) d_ff_3 (
    .clk(H), .D(or_3_out), .Q(d_ff_1_q[2]), .preset(1'b0), .en(or_5_out), .reset(clear));  // open: Qn
  D_Flip_Flop #(.trigger("falling")) d_ff_4 (
    .clk(H), .D(or_4_out), .Q(COUT), .preset(1'b0), .en(or_5_out), .reset(clear));  // open: Qn
  Comparator #(.width(4)) comparator_1 (
    .a(counter_1_q), .b({2'b00, \dist }), .gt(\end ), .eq(comparator_1_eq), .lt(comparator_1_lt));
  and and_11 (and_11_out, \end , enable);
  Register #(.width(4)) register_1 (.D({COUT, d_ff_1_q}), .en(and_11_out), .Q(S), .clk(H), .clr(clearO));
endmodule

module SFLB (
  input  H,
  input  [3:0] data,
  input  [1:0] \dist ,
  output [3:0] S
);

  wire mdb_1_clearo, sfl_1_end;

  MDB mdb_1 (.H(H), .\end (sfl_1_end), .clear(1'b0), .enable(1'b1), .clearO(mdb_1_clearo));
  SFL sfl_1 (
    .data(data), .CIN(1'b0), .\dist (\dist ), .enable(1'b1), .H(H), .clear(mdb_1_clearo), .clearO(1'b0),
    .S(S), .\end (sfl_1_end));  // open: COUT
endmodule

module SRLB (
  input  H,
  input  [3:0] data,
  input  [1:0] \dist ,
  output [3:0] S
);

  wire mdb_1_clearo, sfl_1_cout, sfl_1_end;

  MDB mdb_1 (.H(H), .\end (sfl_1_end), .clear(1'b0), .enable(1'b1), .clearO(mdb_1_clearo));
  SFL sfl_1 (
    .data(data), .CIN(sfl_1_cout), .\dist (\dist ), .enable(1'b1), .H(H), .clear(mdb_1_clearo),
    .clearO(1'b0), .COUT(sfl_1_cout), .S(S), .\end (sfl_1_end));
endmodule
