// Logisim project 03_SHIFTER_V.circ as structural Verilog: 7 circuits, main circuit main
module main (
  input  [3:0] in_1,
  input  [1:0] in_2,
  output [3:0] out_3,
  output [3:0] out_4,
  output [3:0] out_5,
  output [3:0] out_6,
  output [3:0] out_7,
  output [3:0] out_8,
  output [3:0] out_9,
  output [3:0] out_10
);

  Shifter #(.width(4)) shifter_1 (.in(in_1), .\dist (in_2), .out(out_3));
  SHL shl_1 (.Input(in_1), .Distance(in_2), .Output(out_5));
  Shifter #(.width(4), .shift("rl")) shifter_2 (.in(in_1), .\dist (in_2), .out(out_7));
  ROL rol_1 (.Input(in_1), .Distance(in_2), .Output(out_9));
  Shifter #(.width(4), .shift("lr")) shifter_3 (.in(in_1), .\dist (in_2), .out(out_4));
  SHR shr_1 (.Input(in_1), .Distance(in_2), .Output(out_6));
  Shifter #(.width(4), .shift("rr")) shifter_4 (.in(in_1), .\dist (in_2), .out(out_8));
  ROR ror_1 (.Input(in_1), .Distance(in_2), .Output(out_10));
endmodule

module SHLD (
  input  [3:0] Input,
  input  [3:0] Default,
  input  [1:0] Distance,
  output [3:0] Output
);

  Multiplexer #(.select(2), .enable("false")) multiplexer_1 (
    .in0(Input[0]), .in1(Default[3]), .in2(Default[2]), .in3(Default[1]), .out(Output[0]), .sel(Distance));
  Multiplexer #(.select(2), .enable("false")) multiplexer_2 (
    .in0(Input[1]), .in1(Input[0]), .in2(Default[3]), .in3(Default[2]), .out(Output[1]), .sel(Distance));
  Multiplexer #(.select(2), .enable("false")) multiplexer_3 (
    .in0(Input[2]), .in1(Input[1]), .in2(Input[0]), .in3(Default[3]), .out(Output[2]), .sel(Distance));
  Multiplexer #(.select(2), .enable("false")) multiplexer_4 (
    .in0(Input[3]), .in1(Input[2]), .in2(Input[1]), .in3(Input[0]), .out(Output[3]), .sel(Distance));
endmodule

module SHL (
  input  [3:0] Input,
  input  [1:0] Distance,
  output [3:0] Output
);

  SHLD shld_1 (.Input(Input), .Default(4'b0000), .Distance(Distance), .Output(Output));
endmodule

module ROL (
  input  [3:0] Input,
  input  [1:0] Distance,
  output [3:0] Output
);

  SHLD shld_1 (.Input(Input), .Default(Input), .Distance(Distance), .Output(Output));
endmodule

module SHRD (
  input  [3:0] Input,
  input  [3:0] Default,
  input  [1:0] Distance,
  output [3:0] Output
);

  Multiplexer #(.select(2), .enable("false")) multiplexer_1 (
    .in0(Input[0]), .in1(Input[1]), .in2(Input[2]), .in3(Input[3]), .out(Output[0]), .sel(Distance));
  Multiplexer #(.select(2), .enable("false")) multiplexer_2 (
    .in0(Input[1]), .in1(Input[2]), .in2(Input[3]), .in3(Default[0]), .out(Output[1]), .sel(Distance));
  Multiplexer #(.select(2), .enable("false")) multiplexer_3 (
    .in0(Input[2]), .in1(Input[3]), .in2(Default[0]), .in3(Default[1]), .out(Output[2]), .sel(Distance));
  Multiplexer #(.select(2), .enable("false")) multiplexer_4 (
    .in0(Input[3]), .in1(Default[0]), .in2(Default[1]), .in3(Default[2]), .out(Output[3]), .sel(Distance));
endmodule

module SHR (
  input  [3:0] Input,
  input  [1:0] Distance,
  output [3:0] Output
);

  SHRD shrd_1 (.Input(Input), .Default(4'b0000), .Distance(Distance), .Output(Output));
endmodule

module ROR (
  input  [3:0] Input,
  input  [1:0] Distance,
  output [3:0] Output
);

  SHRD shrd_1 (.Input(Input), .Default(Input), .Distance(Distance), .Output(Output));
endmodule
