// Logisim project 04_ARITHMETIC_00_V.circ as structural Verilog: 38 circuits, main circuit main
module main (
  input  [3:0] in_1,
  input  [3:0] in_2,
  input  [3:0] in_3,
  input  [3:0] in_4,
  input  [3:0] in_5,
  input  [3:0] in_6,
  input  in_7,
  input  [7:0] in_8,
  input  [7:0] in_9,
  input  in_10,
  input  [3:0] in_11,
  input  in_12,
  input  [3:0] in_13,
  input  [3:0] in_14,
  output out_15,
  output out_16,
  output out_17,
  output out_18,
  output [7:0] out_19,
  output [1:0] out_20,
  output [1:0] out_21
);

  wire addsp2_4_1_carry_out, afn4_1_sign, afn4_2_sign, afn4_3_sign, afn4_4_sign, comp_1_equal,
       comp_1_greater, comp_1_less, comparator_1_eq, comparator_1_gt, comparator_1_lt, comparator_2_eq,
       comparator_2_gt, comparator_2_lt, comparator_3_eq, comparator_3_gt, comparator_3_lt;
  wire [3:0] add1_4_1_output, add204_1_output, addb_1_output, adder_1_out, addsp2_4_3_output,
       addsp2_b_1_output, addsptr4_1_output, addsptrdef4_1_output, addt4_1_output, addui4_1_out_4,
       addui04_1_output, afin_1_ouptu_unit, afin_1_output_ten, afin_2_ouptu_unit, afin_2_output_ten,
       afin_3_ouptu_unit, afin_3_output_ten, afin_4_ouptu_unit, afin_4_output_ten, afn4_1_output,
       afn4_2_output, afn4_3_output, afn4_4_output, neg4_1_output, negator_1_out, sub4_1_output,
       sub4d_1_output, subtractor_1_out;
  wire [4:0] afsi2_3_output, afsi2_3_output_2, afsi2_3_output_3, afsi2_4_output, afsi2_4_output_2,
       afsi2_4_output_3;
  wire [29:0] afsi2_1_output, afsi2_2_output;
  wire [29:15] afsi2_3_output_4, afsi2_4_output_4;

  // Probe on in_1
  // Probe on in_1
  // Probe on in_1
  // Probe on in_2
  // Probe on in_2
  // Probe on in_2
  // Probe on in_5
  // Probe on in_5
  // Probe on in_5
  // Probe on in_6
  // Probe on in_6
  // Probe on in_6
  Adder #(.width(4)) adder_1 (.a(in_1), .b(in_2), .out(adder_1_out), .cin(1'b0), .cout(out_15));
  ADDB addb_1 (.Output(addb_1_output), .Input_A(in_1), .Input_B(in_2));
  Subtractor #(.width(4)) subtractor_1 (.a(in_5), .b(in_6), .out(subtractor_1_out), .bin(1'b0), .bout(out_17));
  // Probe on subtractor_1_out
  // Probe on subtractor_1_out
  // Probe on subtractor_1_out
  // Probe on subtractor_1_out
  // Probe on in_8
  // Probe on in_9
  // Probe on in_14
  // Probe on in_14
  // Probe on in_14
  // Probe on adder_1_out
  // Probe on adder_1_out
  // Probe on adder_1_out
  // Probe on adder_1_out
  // Probe on addb_1_output
  // Probe on addb_1_output
  // Probe on addb_1_output
  // Probe on addb_1_output
  SUB4D sub4d_1 (.Borrow_In(1'b0), .Minuend(in_5), .Subtrahend(in_6), .Output(sub4d_1_output), .Borrow_Out(out_18));
  ADDSP2_4 addsp2_4_1 (
    .Carry_In(in_7), .Input_A(in_8[3:0]), .Output(out_19[3:0]), .Input_B(in_9[3:0]),
    .Carry_Out(addsp2_4_1_carry_out));
  ADDSP2_4 addsp2_4_2 (
    .Carry_In(addsp2_4_1_carry_out), .Input_A(in_8[7:4]), .Output(out_19[7:4]), .Input_B(in_9[7:4]));  // open: Carry_Out
  Negator #(.width(4)) negator_1 (.in(in_14), .out(negator_1_out));
  // Probe on negator_1_out
  // Probe on negator_1_out
  // Probe on negator_1_out
  // Probe on negator_1_out
  ADDSP2_4 addsp2_4_3 (.Carry_In(1'b0), .Input_A(in_1), .Output(addsp2_4_3_output), .Input_B(in_2), .Carry_Out(out_16));
  ADDSP2_B addsp2_b_1 (.Input_A(in_1), .Output(addsp2_b_1_output), .Input_B(in_2));
  // Probe on sub4d_1_output
  // Probe on sub4d_1_output
  // Probe on sub4d_1_output
  // Probe on sub4d_1_output
  // Probe on addsp2_4_3_output
  // Probe on addsp2_4_3_output
  // Probe on addsp2_4_3_output
  // Probe on addsp2_4_3_output
  // Probe on addsp2_b_1_output
  // Probe on addsp2_b_1_output
  // Probe on addsp2_b_1_output
  // Probe on addsp2_b_1_output
  SUB4 sub4_1 (.Minuend(in_5), .Subtrahend(in_6), .Output(sub4_1_output));
  // Probe on out_19
  NEG4 neg4_1 (.Input(in_14), .Output(neg4_1_output));
  // Probe on neg4_1_output
  // Probe on neg4_1_output
  // Probe on neg4_1_output
  // Probe on neg4_1_output
  ADD1_4 add1_4_1 (.Carry_In(1'b0), .Input_A(in_1), .Input_B(in_2), .Output(add1_4_1_output));  // open: Carry_Out
  // Probe on add1_4_1_output
  // Probe on add1_4_1_output
  // Probe on add1_4_1_output
  // Probe on add1_4_1_output
  ADDT4 addt4_1 (.Carry_In(1'b0), .Input_A(in_1), .Input_B(in_2), .Output(addt4_1_output));  // open: Carry_Out
  // Probe on addt4_1_output
  // Probe on addt4_1_output
  // Probe on addt4_1_output
  // Probe on addt4_1_output
  // Probe on sub4_1_output
  // Probe on sub4_1_output
  // Probe on sub4_1_output
  // Probe on sub4_1_output
  ADDSPTRDEF4 addsptrdef4_1 (
    .Carry_In(1'b0), .Input_A(in_1), .Input_B(in_2), .Output(addsptrdef4_1_output));  // open: Carry_Out
  // Probe on addsptrdef4_1_output
  // Probe on addsptrdef4_1_output
  // Probe on addsptrdef4_1_output
  // Probe on addsptrdef4_1_output
  ADDSPTR4 addsptr4_1 (.Carry_In(1'b0), .Input_A(in_2), .Input_B(in_1), .Output(addsptr4_1_output));  // open: Carry_Out
  // Probe on addsptr4_1_output
  // Probe on addsptr4_1_output
  // Probe on addsptr4_1_output
  // Probe on addsptr4_1_output
  ADDUI4 addui4_1 (.in_2(in_2), .in_3(in_1), .out_4(addui4_1_out_4), .in_1(1'b0));  // open: out_5
  // Probe on addui4_1_out_4
  // Probe on addui4_1_out_4
  // Probe on addui4_1_out_4
  // Probe on addui4_1_out_4
  ADDUI04 addui04_1 (.Carry_In(1'b0), .Input_A(in_2), .Input_B(in_1), .Output(addui04_1_output));  // open: Carry_Out
  // Probe on addui04_1_output
  // Probe on addui04_1_output
  // Probe on addui04_1_output
  // Probe on addui04_1_output
  ADD204 add204_1 (.Carry_In(1'b0), .Input_A(in_2), .Input_B(in_1), .Output(add204_1_output));  // open: Carry_Out
  // Probe on add204_1_output
  // Probe on add204_1_output
  // Probe on add204_1_output
  // Probe on add204_1_output
  ADDSP_V1 addsp_v1_1 (.Input_A(in_10), .Input_B(in_12), .Output(out_20[0]), .Carry_Out(out_20[1]));
  ADDSP addsp_1 (.Input_A(in_10), .Input_B(in_12), .Output(out_21[0]), .Carry_Out(out_21[1]));
  // Probe on in_3
  // Probe on in_3
  // Probe on in_3
  _7_Segment_Display u_7_segment_display_1 (.g(afn4_1_sign));  // open: f, a, b, e, d, c, dp
  AFN4 afn4_1 (.Sign(afn4_1_sign), .Input(in_3), .Output(afn4_1_output));
  COMP comp_1 (.A(in_3), .B(in_4), .Less(comp_1_less), .Equal(comp_1_equal), .Greater(comp_1_greater));
  _7_Segment_Display u_7_segment_display_2 (.g(afn4_2_sign));  // open: f, a, b, e, d, c, dp
  AFN4 afn4_2 (.Sign(afn4_2_sign), .Input(in_3), .Output(afn4_2_output));
  Comparator #(.width(4)) comparator_1 (
    .a(in_3), .b(in_4), .gt(comparator_1_gt), .eq(comparator_1_eq), .lt(comparator_1_lt));
  AFIN afin_1 (.INPUT(in_11), .Ouptu_unit(afin_1_ouptu_unit), .Output_ten(afin_1_output_ten));
  AFIN afin_2 (.INPUT(in_11), .Ouptu_unit(afin_2_ouptu_unit), .Output_ten(afin_2_output_ten));
  // Probe on in_11
  // Probe on in_11
  // Probe on in_11
  Hex_Digit_Display hex_digit_display_1 (.value(afn4_1_output));  // open: dp
  DotMatrix #(.matrixcols(6), .matrixrows(5)) dotmatrix_1 (
    .col0(afsi2_1_output[29:25]), .col1(afsi2_1_output[24:20]), .col2(afsi2_1_output[19:15]),
    .col3(afsi2_1_output[14:10]), .col4(afsi2_1_output[9:5]), .col5(afsi2_1_output[4:0]));
  AFSI2 afsi2_1 (
    .Greater(comp_1_greater), .Equal(comp_1_equal), .Less(comp_1_less), .ENABLE(1'b1), .Output(afsi2_1_output));
  Hex_Digit_Display hex_digit_display_2 (.value(afn4_2_output));  // open: dp
  DotMatrix #(.matrixcols(6), .matrixrows(5)) dotmatrix_2 (
    .col0(afsi2_2_output[29:25]), .col1(afsi2_2_output[24:20]), .col2(afsi2_2_output[19:15]),
    .col3(afsi2_2_output[14:10]), .col4(afsi2_2_output[9:5]), .col5(afsi2_2_output[4:0]));
  AFSI2 afsi2_2 (
    .Greater(comparator_1_gt), .Equal(comparator_1_eq), .Less(comparator_1_lt), .ENABLE(1'b1),
    .Output(afsi2_2_output));
  Hex_Digit_Display hex_digit_display_3 (.value(afin_1_ouptu_unit));  // open: dp
  Hex_Digit_Display hex_digit_display_4 (.value(afin_1_output_ten));  // open: dp
  Comparator #(.width(4), .mode("unsigned")) comparator_2 (
    .a(in_11), .b(in_13), .gt(comparator_2_gt), .eq(comparator_2_eq), .lt(comparator_2_lt));
  Hex_Digit_Display hex_digit_display_5 (.value(afin_2_output_ten));  // open: dp
  Hex_Digit_Display hex_digit_display_6 (.value(afin_2_ouptu_unit));  // open: dp
  _7_Segment_Display u_7_segment_display_3 (.g(afn4_3_sign));  // open: f, a, b, e, d, c, dp
  _7_Segment_Display u_7_segment_display_4 (.g(afn4_4_sign));  // open: f, a, b, e, d, c, dp
  DotMatrix #(.matrixcols(6), .matrixrows(5)) dotmatrix_3 (
    .col0(afsi2_3_output_4[29:25]), .col1(afsi2_3_output_4[24:20]), .col2(afsi2_3_output_4[19:15]),
    .col3(afsi2_3_output_3), .col4(afsi2_3_output_2), .col5(afsi2_3_output));
  AFSI2 afsi2_3 (
    .Greater(comparator_2_gt), .Equal(comparator_2_eq), .Less(comparator_2_lt), .ENABLE(1'b1),
    .Output({afsi2_3_output_4, afsi2_3_output_3, afsi2_3_output_2, afsi2_3_output}));
  DotMatrix #(.matrixcols(6), .matrixrows(5)) dotmatrix_4 (
    .col0(afsi2_4_output_4[29:25]), .col1(afsi2_4_output_4[24:20]), .col2(afsi2_4_output_4[19:15]),
    .col3(afsi2_4_output_3), .col4(afsi2_4_output_2), .col5(afsi2_4_output));
  Comparator #(.width(5)) comparator_3 (
    .a({1'b0, in_11}), .b({1'b0, in_13}), .gt(comparator_3_gt), .eq(comparator_3_eq), .lt(comparator_3_lt));
  Hex_Digit_Display hex_digit_display_7 (.value(afn4_3_output));  // open: dp
  Hex_Digit_Display hex_digit_display_8 (.value(afn4_4_output));  // open: dp
  Hex_Digit_Display hex_digit_display_9 (.value(afin_3_ouptu_unit));  // open: dp
  Hex_Digit_Display hex_digit_display_10 (.value(afin_3_output_ten));  // open: dp
  AFIN afin_3 (.INPUT(in_13), .Ouptu_unit(afin_3_ouptu_unit), .Output_ten(afin_3_output_ten));
  Hex_Digit_Display hex_digit_display_11 (.value(afin_4_output_ten));  // open: dp
  Hex_Digit_Display hex_digit_display_12 (.value(afin_4_ouptu_unit));  // open: dp
  AFIN afin_4 (.INPUT(in_13), .Ouptu_unit(afin_4_ouptu_unit), .Output_ten(afin_4_output_ten));
  AFSI2 afsi2_4 (
    .Greater(comparator_3_gt), .Equal(comparator_3_eq), .Less(comparator_3_lt), .ENABLE(1'b1),
    .Output({afsi2_4_output_4, afsi2_4_output_3, afsi2_4_output_2, afsi2_4_output}));
  AFN4 afn4_3 (.Sign(afn4_3_sign), .Input(in_4), .Output(afn4_3_output));
  AFN4 afn4_4 (.Sign(afn4_4_sign), .Input(in_4), .Output(afn4_4_output));
  // Probe on in_4
  // Probe on in_4
  // Probe on in_4
  // Probe on in_13
  // Probe on in_13
  // Probe on in_13
endmodule

module main2 (
);

  wire C0, C1, C2, C3, C4, C5, C6, C7, C8;
  wire [7:0] L1_0, L1_1, L1_2, L1_3, L1_4, L1_5, L1_6, L1_7, L1_8, L2_0, L2_1, L2_2, L2_3, L2_4, L2_5, L2_6,
       L2_7, L2_8, negator_1_out, R0, R1, R2, R3, R4, R5, R6, R7, R8;

  // Probe on L1_0
  // Probe on L1_0
  // Probe on L2_0
  // Probe on L2_0
  // Probe on L1_1
  // Probe on L1_1
  // Probe on L2_1
  // Probe on L2_1
  // Probe on L1_2
  // Probe on L1_2
  // Probe on L2_2
  // Probe on L2_2
  // Probe on C0
  Adder adder_1 (.a(L1_0), .b(L2_0), .out(R0), .cin(1'b0), .cout(C0));
  // Probe on C1
  Adder adder_2 (.a(L1_1), .b(L2_1), .out(R1), .cin(1'b0), .cout(C1));
  // Probe on C2
  Adder adder_3 (.a(L1_2), .b(L2_2), .out(R2), .cin(1'b0), .cout(C2));
  // Probe on R0
  // Probe on R0
  // Probe on R0
  // Probe on R1
  // Probe on R1
  // Probe on R1
  // Probe on R2
  // Probe on R2
  // Probe on R2
  // Probe on L1_6
  // Probe on L1_6
  // Probe on L2_6
  // Probe on L2_6
  // Probe on L1_7
  // Probe on L1_7
  // Probe on L2_7
  // Probe on L2_7
  // Probe on L1_8
  // Probe on L1_8
  // Probe on L2_8
  // Probe on L2_8
  // Probe on C6
  Adder adder_4 (.a(L1_6), .b(L2_6), .out(R6), .cin(1'b0), .cout(C6));
  // Probe on C7
  Adder adder_5 (.a(L1_7), .b(L2_7), .out(R7), .cin(1'b0), .cout(C7));
  // Probe on C8
  Adder adder_6 (.a(L1_8), .b(L2_8), .out(R8), .cin(1'b0), .cout(C8));
  // Probe on L1_3
  // Probe on L1_3
  // Probe on L2_3
  // Probe on L2_3
  // Probe on L1_4
  // Probe on L1_4
  // Probe on L2_4
  // Probe on L2_4
  // Probe on L1_5
  // Probe on L1_5
  // Probe on L2_5
  // Probe on L2_5
  Adder adder_7 (.a(L1_3), .b(L2_3), .out(R3), .cin(1'b0), .cout(C3));
  Adder adder_8 (.a(L1_4), .b(L2_4), .out(R4), .cin(1'b0), .cout(C4));
  Adder adder_9 (.a(L1_5), .b(L2_5), .out(R5), .cin(1'b0), .cout(C5));
  // Probe on R6
  // Probe on R6
  // Probe on R6
  // Probe on R7
  // Probe on R7
  // Probe on R7
  // Probe on R8
  // Probe on R8
  // Probe on R8
  // Probe on C3
  // Probe on C4
  // Probe on C5
  Negator negator_1 (.in(R7), .out(negator_1_out));
  // Probe on R3
  // Probe on R3
  // Probe on R3
  // Probe on R4
  // Probe on R4
  // Probe on R4
  // Probe on R5
  // Probe on R5
  // Probe on R5
  // Probe on negator_1_out
  // Probe on negator_1_out
  // Probe on negator_1_out
  // Probe on L1_0
  // Probe on L2_0
  // Probe on R0
  // Probe on C0
  // Probe on L1_1
  // Probe on L2_1
  // Probe on R1
  // Probe on C1
  // Probe on L1_2
  // Probe on L2_2
  // Probe on R2
  // Probe on C2
  // Probe on L1_3
  // Probe on L2_3
  // Probe on R3
  // Probe on C3
  // Probe on L1_4
  // Probe on L2_4
  // Probe on R4
  // Probe on C4
  // Probe on L1_0
  // Probe on L2_0
  // Probe on R0
  // Probe on L1_1
  // Probe on L2_1
  // Probe on R1
  // Probe on L1_2
  // Probe on L2_2
  // Probe on R2
  // Probe on L1_3
  // Probe on L2_3
  // Probe on R3
  // Probe on L1_4
  // Probe on L2_4
  // Probe on R4
  // Probe on L1_5
  // Probe on L2_5
  // Probe on R5
  // Probe on C5
  // Probe on L1_6
  // Probe on L2_6
  // Probe on R6
  // Probe on C6
  // Probe on L1_7
  // Probe on L2_7
  // Probe on R7
  // Probe on C7
  // Probe on L1_8
  // Probe on L2_8
  // Probe on R8
  // Probe on C8
  // Probe on L1_5
  // Probe on L2_5
  // Probe on R5
  // Probe on L1_6
  // Probe on L2_6
  // Probe on R6
  // Probe on L1_7
  // Probe on L2_7
  // Probe on R7
  // Probe on L1_8
  // Probe on L2_8
  // Probe on R8
  list1 list1_1 (
    .out_1(L1_0), .out_2(L1_1), .out_3(L1_2), .out_4(L1_3), .out_5(L1_4), .out_6(L1_5), .out_7(L1_6),
    .out_8(L1_7), .out_9(L1_8));
  list2 list2_1 (
    .out_1(L2_0), .out_2(L2_1), .out_3(L2_2), .out_4(L2_3), .out_5(L2_4), .out_6(L2_5), .out_7(L2_6),
    .out_8(L2_7), .out_9(L2_8));
endmodule

module ADD0 (
  input  Carry_In,
  input  Input_A,
  input  Input_B,
  output Output,
  output Carry_Out
);

  wire and_1_out, and_2_out, nor_1_out, nor_2_out, nor_3_out;

  nor nor_1 (nor_1_out, Input_A, Input_B);
  nor nor_2 (nor_2_out, nor_1_out, and_1_out);
  and and_1 (and_1_out, Input_A, Input_B);
  nor nor_3 (nor_3_out, Carry_In, nor_2_out);
  and and_2 (and_2_out, Carry_In, nor_2_out);
  nor nor_4 (Output, nor_3_out, and_2_out);
  or or_1 (Carry_Out, and_2_out, and_1_out);

  // Notes on the sheet:
  //   0+0=0 (R=0)
  //   0+1=1 (R=0)
  //   1+0=1 (R=0)
  //   1+1=0 (R=1)
endmodule

module ADD1 (
  input  Carry_In,
  input  Input_A,
  input  Input_B,
  output Output,
  output Carry_Out
);

  wire and_1_out, and_2_out, xor_1_out;

  xor xor_1 (xor_1_out, Input_A, Input_B);
  and and_1 (and_1_out, Input_A, Input_B);
  xor xor_2 (Output, Carry_In, xor_1_out);
  and and_2 (and_2_out, Carry_In, xor_1_out);
  or or_1 (Carry_Out, and_2_out, and_1_out);
endmodule

module ADD1_4 (
  input  Carry_In,
  input  [3:0] Input_A,
  input  [3:0] Input_B,
  output [3:0] Output,
  output Carry_Out
);

  wire add1_1_carry_out, add1_2_carry_out, add1_3_carry_out;

  ADD1 add1_1 (
    .Carry_In(Carry_In), .Input_A(Input_A[0]), .Input_B(Input_B[0]), .Output(Output[0]),
    .Carry_Out(add1_1_carry_out));
  ADD1 add1_2 (
    .Carry_In(add1_1_carry_out), .Input_A(Input_A[1]), .Input_B(Input_B[1]), .Output(Output[1]),
    .Carry_Out(add1_2_carry_out));
  ADD1 add1_3 (
    .Carry_In(add1_2_carry_out), .Input_A(Input_A[2]), .Input_B(Input_B[2]), .Output(Output[2]),
    .Carry_Out(add1_3_carry_out));
  ADD1 add1_4 (
    .Carry_In(add1_3_carry_out), .Input_A(Input_A[3]), .Input_B(Input_B[3]), .Output(Output[3]),
    .Carry_Out(Carry_Out));
endmodule

module ADDB (
  input  [3:0] Input_A,
  input  [3:0] Input_B,
  output [3:0] Output
);

  wire and_1_out, and_2_out, and_3_out, and_4_out, and_6_out, and_7_out, and_8_out, and_9_out, and_10_out,
       and_11_out, not_1_out, not_2_out, not_3_out, not_4_out, not_5_out, not_6_out, not_7_out, or_1_out,
       or_2_out, or_3_out, or_4_out, or_5_out, or_6_out, or_7_out, or_8_out, or_9_out;

  or or_1 (or_1_out, Input_A[0], Input_B[0]);
  and and_1 (and_1_out, Input_A[0], Input_B[0]);
  or or_2 (or_2_out, Input_A[1], Input_B[1]);
  and and_2 (and_2_out, Input_A[1], Input_B[1]);
  or or_3 (or_3_out, Input_A[2], Input_B[2]);
  and and_3 (and_3_out, Input_A[2], Input_B[2]);
  or or_4 (or_4_out, Input_A[3], Input_B[3]);
  and and_4 (and_4_out, Input_A[3], Input_B[3]);
  not not_1 (not_1_out, and_1_out);
  not not_2 (not_2_out, and_2_out);
  not not_3 (not_3_out, and_3_out);
  not not_4 (not_4_out, and_4_out);
  and and_5 (Output[0], or_1_out, not_1_out);
  and and_6 (and_6_out, or_2_out, not_2_out);
  and and_7 (and_7_out, or_3_out, not_3_out);
  and and_8 (and_8_out, or_4_out, not_4_out);
  or or_5 (or_5_out, and_9_out, and_2_out);
  or or_6 (or_6_out, and_10_out, and_3_out);
  or or_7 (or_7_out, and_1_out, and_6_out);
  and and_9 (and_9_out, and_1_out, and_6_out);
  not not_5 (not_5_out, and_9_out);
  or or_8 (or_8_out, or_5_out, and_7_out);
  not not_6 (not_6_out, and_10_out);
  and and_10 (and_10_out, or_5_out, and_7_out);
  or or_9 (or_9_out, or_6_out, and_8_out);
  not not_7 (not_7_out, and_11_out);
  and and_11 (and_11_out, or_6_out, and_8_out);
  and and_12 (Output[1], or_7_out, not_5_out);
  and and_13 (Output[2], or_8_out, not_6_out);
  and and_14 (Output[3], or_9_out, not_7_out);
endmodule

module ADD2 (
  input  Carry_In,
  input  Input_A,
  input  Input_B,
  output Output,
  output Carry_Out
);

  wire and_1_out, and_2_out, and_3_out, not_1_out, not_2_out, or_1_out, or_2_out;

  or or_1 (or_1_out, Input_A, Input_B);
  and and_1 (and_1_out, Input_A, Input_B);
  not not_1 (not_1_out, and_1_out);
  and and_2 (and_2_out, or_1_out, not_1_out);
  or or_2 (or_2_out, Carry_In, and_2_out);
  not not_2 (not_2_out, and_3_out);
  and and_3 (and_3_out, Carry_In, and_2_out);
  and and_4 (Output, or_2_out, not_2_out);
  or or_3 (Carry_Out, and_3_out, and_1_out);

  // Notes on the sheet:
  //   0+0=0 (R=0)
  //   0+1=1 (R=0)
  //   1+0=1 (R=0)
  //   1+1=0 (R=1)
endmodule

module ADDSP_V1 (
  input  Input_A,
  input  Input_B,
  output Output,
  output Carry_Out
);

  wire not_1_out, or_1_out;

  or or_1 (or_1_out, Input_A, Input_B);
  and and_1 (Carry_Out, Input_A, Input_B);
  and and_2 (Output, or_1_out, not_1_out);
  not not_1 (not_1_out, Carry_Out);

  // Notes on the sheet:
  //   0+0=0 (R=0)
  //   0+1=1 (R=0)
  //   1+0=1 (R=0)
  //   1+1=0 (R=1)
endmodule

module ADDSP (
  input  Input_A,
  input  Input_B,
  output Output,
  output Carry_Out
);

  wire nor_1_out;

  nor nor_1 (nor_1_out, Input_A, Input_B);
  and and_1 (Carry_Out, Input_A, Input_B);
  nor nor_2 (Output, nor_1_out, Carry_Out);

  // Notes on the sheet:
  //   0+0=0 (R=0)
  //   0+1=1 (R=0)
  //   1+0=1 (R=0)
  //   1+1=0 (R=1)
endmodule

module ADDSP2 (
  input  Carry_In,
  input  Input_A,
  input  Input_B,
  output Output,
  output Carry_Out
);

  wire addsp_1_carry_out, addsp_2_carry_out, addsp_2_output;

  ADDSP addsp_1 (.Input_A(Carry_In), .Input_B(addsp_2_output), .Output(Output), .Carry_Out(addsp_1_carry_out));
  ADDSP addsp_2 (.Input_A(Input_A), .Input_B(Input_B), .Output(addsp_2_output), .Carry_Out(addsp_2_carry_out));
  or or_1 (Carry_Out, addsp_1_carry_out, addsp_2_carry_out);

  // Notes on the sheet:
  //   C_IN
  //   C_ABIN
  //   V_AB
  //   A
  //   B
  //   C_AB
  //   0+0=0 (R=0)
  //   0+1=1 (R=0)
  //   1+0=1 (R=0)
  //   1+1=0 (R=1)
  //   V_OUT
  //   C_OUT
endmodule

module ADDSP_B (
  input  [3:0] Input_A,
  input  [3:0] Input_B,
  output [3:0] Output
);

  wire addsp_1_carry_out, addsp_2_carry_out, addsp_3_carry_out, addsp_3_output, addsp_4_carry_out,
       addsp_5_carry_out, addsp_5_output, addsp_7_output, or_1_out, or_2_out;

  ADDSP addsp_1 (.Input_A(Input_A[0]), .Input_B(Input_B[0]), .Output(Output[0]), .Carry_Out(addsp_1_carry_out));
  ADDSP addsp_2 (
    .Input_A(addsp_1_carry_out), .Input_B(addsp_3_output), .Output(Output[1]), .Carry_Out(addsp_2_carry_out));
  ADDSP addsp_3 (.Input_A(Input_A[1]), .Input_B(Input_B[1]), .Output(addsp_3_output), .Carry_Out(addsp_3_carry_out));
  or or_1 (or_1_out, addsp_2_carry_out, addsp_3_carry_out);
  ADDSP addsp_4 (.Input_A(or_1_out), .Input_B(addsp_5_output), .Output(Output[2]), .Carry_Out(addsp_4_carry_out));
  ADDSP addsp_5 (.Input_A(Input_A[2]), .Input_B(Input_B[2]), .Output(addsp_5_output), .Carry_Out(addsp_5_carry_out));
  or or_2 (or_2_out, addsp_4_carry_out, addsp_5_carry_out);
  ADDSP addsp_6 (.Input_A(or_2_out), .Input_B(addsp_7_output), .Output(Output[3]));  // open: Carry_Out
  ADDSP addsp_7 (.Input_A(Input_A[3]), .Input_B(Input_B[3]), .Output(addsp_7_output));  // open: Carry_Out
endmodule

module ADDSP2_B (
  input  [3:0] Input_A,
  input  [3:0] Input_B,
  output [3:0] Output
);

  wire addsp2_1_carry_out, addsp2_2_carry_out, addsp2_3_carry_out;

  ADDSP2 addsp2_1 (
    .Carry_In(1'b0), .Input_A(Input_A[0]), .Input_B(Input_B[0]), .Output(Output[0]),
    .Carry_Out(addsp2_1_carry_out));
  ADDSP2 addsp2_2 (
    .Carry_In(addsp2_1_carry_out), .Input_A(Input_A[1]), .Input_B(Input_B[1]), .Output(Output[1]),
    .Carry_Out(addsp2_2_carry_out));
  ADDSP2 addsp2_3 (
    .Carry_In(addsp2_2_carry_out), .Input_A(Input_A[2]), .Input_B(Input_B[2]), .Output(Output[2]),
    .Carry_Out(addsp2_3_carry_out));
  ADDSP2 addsp2_4 (
    .Carry_In(addsp2_3_carry_out), .Input_A(Input_A[3]), .Input_B(Input_B[3]), .Output(Output[3]));  // open: Carry_Out
endmodule

module ADDSP2_4 (
  input  Carry_In,
  input  [3:0] Input_A,
  input  [3:0] Input_B,
  output [3:0] Output,
  output Carry_Out
);

  wire addsp2_1_carry_out, addsp2_2_carry_out, addsp2_3_carry_out;

  ADDSP2 addsp2_1 (
    .Carry_In(Carry_In), .Input_A(Input_A[0]), .Input_B(Input_B[0]), .Output(Output[0]),
    .Carry_Out(addsp2_1_carry_out));
  ADDSP2 addsp2_2 (
    .Carry_In(addsp2_1_carry_out), .Input_A(Input_A[1]), .Input_B(Input_B[1]), .Output(Output[1]),
    .Carry_Out(addsp2_2_carry_out));
  ADDSP2 addsp2_3 (
    .Carry_In(addsp2_2_carry_out), .Input_A(Input_A[2]), .Input_B(Input_B[2]), .Output(Output[2]),
    .Carry_Out(addsp2_3_carry_out));
  ADDSP2 addsp2_4 (
    .Carry_In(addsp2_3_carry_out), .Input_A(Input_A[3]), .Input_B(Input_B[3]), .Output(Output[3]),
    .Carry_Out(Carry_Out));

  // Notes on the sheet:
  //   0+0=0 (R=0)
  //   0+1=1 (R=0)
  //   1+0=1 (R=0)
  //   1+1=0 (R=1)
endmodule

module ADDSPTR (
  input  Input_A,
  input  Input_B,
  output Output,
  output Carry_Out
);

  wire pull_resistor_8_node, transistor_1_out, transistor_2_out, transistor_3_out, transistor_4_out,
       transistor_5_out, transistor_6_out, transistor_11_out, transistor_13_out, transistor_14_out,
       transistor_15_out, transistor_18_out;

  Transistor transistor_1 (.in(1'b1), .out(transistor_1_out), .gate(Input_A));
  Transistor #(.\type ("n")) transistor_2 (.in(transistor_1_out), .out(transistor_2_out), .gate(Input_A));
  Transistor #(.\type ("n"), .gate("br")) transistor_3 (.in(transistor_2_out), .out(transistor_3_out), .gate(Input_B));
  Transistor #(.gate("br")) transistor_4 (.in(1'b1), .out(transistor_4_out), .gate(Input_A));
  Transistor transistor_5 (.in(transistor_4_out), .out(transistor_5_out), .gate(Input_B));
  Transistor #(.\type ("n")) transistor_6 (.in(transistor_5_out), .out(transistor_6_out), .gate(Input_B));
  Transistor #(.\type ("n"), .gate("br")) transistor_7 (.in(transistor_5_out), .out(transistor_6_out), .gate(Input_A));
  Transistor #(.gate("br")) transistor_8 (.in(1'b1), .out(transistor_1_out), .gate(Input_B));
  Pull_Resistor pull_resistor_1 (.node(transistor_1_out));
  Pull_Resistor pull_resistor_2 (.node(transistor_2_out));
  Pull_Resistor pull_resistor_3 (.node(transistor_4_out));
  Pull_Resistor pull_resistor_4 (.node(transistor_5_out));
  Transistor transistor_9 (.in(1'b1), .out(Carry_Out), .gate(transistor_1_out));
  Pull_Resistor pull_resistor_5 (.node(Carry_Out));
  Transistor #(.\type ("n")) transistor_10 (.in(Carry_Out), .out(transistor_3_out), .gate(transistor_1_out));
  Transistor transistor_11 (.in(1'b1), .out(transistor_11_out), .gate(transistor_5_out));
  Pull_Resistor pull_resistor_6 (.node(transistor_11_out));
  Transistor #(.\type ("n")) transistor_12 (.in(transistor_11_out), .out(transistor_6_out), .gate(transistor_5_out));
  Transistor transistor_13 (.in(1'b1), .out(transistor_13_out), .gate(Carry_Out));
  Pull_Resistor pull_resistor_7 (.node(transistor_13_out));
  Transistor #(.\type ("n")) transistor_14 (.in(transistor_13_out), .out(transistor_14_out), .gate(Carry_Out));
  Transistor transistor_15 (.in(1'b1), .out(transistor_15_out), .gate(transistor_11_out));
  Transistor #(.gate("br")) transistor_16 (.in(1'b1), .out(transistor_15_out), .gate(transistor_13_out));
  Pull_Resistor pull_resistor_8 (.node(pull_resistor_8_node));
  Transistor #(.\type ("n")) transistor_17 (
    .in(transistor_15_out), .out(pull_resistor_8_node), .gate(transistor_11_out));
  Transistor #(.\type ("n"), .gate("br")) transistor_18 (
    .in(pull_resistor_8_node), .out(transistor_18_out), .gate(transistor_13_out));
  Pull_Resistor pull_resistor_9 (.node(transistor_15_out));
  Transistor transistor_19 (.in(1'b1), .out(Output), .gate(transistor_15_out));
  Pull_Resistor pull_resistor_10 (.node(Output));
  Transistor #(.\type ("n")) transistor_20 (.in(Output), .out(transistor_18_out), .gate(transistor_15_out));
  // also tied to GND on the sheet: {transistor_3_out, transistor_6_out, transistor_14_out, transistor_18_out}

  // Notes on the sheet:
  //   NON-ET
  //   NON-OU
  //   NON
  //   NON
  //   ET
  //   NON
  //   OU
  //   NON-ET
  //   NON
  //   ET
endmodule

module ADDSPTR2 (
  input  Carry_In,
  input  Input_A,
  input  Input_B,
  output Output,
  output Carry_Out
);

  wire addsptr_1_carry_out, addsptr_1_output, addsptr_2_carry_out;

  ADDSPTR addsptr_1 (.Input_A(Input_A), .Input_B(Input_B), .Output(addsptr_1_output), .Carry_Out(addsptr_1_carry_out));
  ADDSPTR addsptr_2 (.Input_A(Carry_In), .Input_B(addsptr_1_output), .Output(Output), .Carry_Out(addsptr_2_carry_out));
  OU ou_1 (.in_1(addsptr_2_carry_out), .in_2(addsptr_1_carry_out), .out_3(Carry_Out));
endmodule

module ADDSPTR4 (
  input  Carry_In,
  input  [3:0] Input_A,
  input  [3:0] Input_B,
  output [3:0] Output,
  output Carry_Out
);

  wire addsptr2_1_carry_out, addsptr2_2_carry_out, addsptr2_3_carry_out;

  ADDSPTR2 addsptr2_1 (
    .Carry_In(Carry_In), .Input_A(Input_A[0]), .Input_B(Input_B[0]), .Output(Output[0]),
    .Carry_Out(addsptr2_1_carry_out));
  ADDSPTR2 addsptr2_2 (
    .Carry_In(addsptr2_1_carry_out), .Input_A(Input_A[1]), .Input_B(Input_B[1]), .Output(Output[1]),
    .Carry_Out(addsptr2_2_carry_out));
  ADDSPTR2 addsptr2_3 (
    .Carry_In(addsptr2_2_carry_out), .Input_A(Input_A[2]), .Input_B(Input_B[2]), .Output(Output[2]),
    .Carry_Out(addsptr2_3_carry_out));
  ADDSPTR2 addsptr2_4 (
    .Carry_In(addsptr2_3_carry_out), .Input_A(Input_A[3]), .Input_B(Input_B[3]), .Output(Output[3]),
    .Carry_Out(Carry_Out));
endmodule

module ADDSPTRDEF (
  input  Input_A,
  input  Input_B,
  output Output,
  output Carry_Out
);

  wire pull_resistor_1_node, transistor_1_out, transistor_2_out, transistor_3_out, transistor_4_out,
       transistor_7_out, transistor_11_out, transistor_13_out;

  Transistor #(.gate("br")) transistor_1 (.in(1'b1), .out(transistor_1_out), .gate(Input_A));
  Transistor transistor_2 (.in(transistor_1_out), .out(transistor_2_out), .gate(Input_B));
  Transistor #(.\type ("n")) transistor_3 (.in(transistor_2_out), .out(transistor_3_out), .gate(Input_B));
  Transistor #(.gate("br")) transistor_4 (.in(1'b1), .out(transistor_4_out), .gate(Input_B));
  Transistor transistor_5 (.in(1'b1), .out(transistor_4_out), .gate(Input_A));
  Pull_Resistor pull_resistor_1 (.node(pull_resistor_1_node));
  Transistor #(.\type ("n")) transistor_6 (.in(transistor_4_out), .out(pull_resistor_1_node), .gate(Input_A));
  Transistor #(.\type ("n"), .gate("br")) transistor_7 (
    .in(pull_resistor_1_node), .out(transistor_7_out), .gate(Input_B));
  Pull_Resistor pull_resistor_2 (.node(transistor_1_out));
  Pull_Resistor pull_resistor_3 (.node(transistor_2_out));
  Transistor #(.\type ("n"), .gate("br")) transistor_8 (.in(transistor_2_out), .out(transistor_3_out), .gate(Input_A));
  Pull_Resistor pull_resistor_4 (.node(transistor_4_out));
  Transistor transistor_9 (.in(1'b1), .out(Carry_Out), .gate(transistor_4_out));
  Pull_Resistor pull_resistor_5 (.node(Carry_Out));
  Transistor #(.\type ("n")) transistor_10 (.in(Carry_Out), .out(transistor_7_out), .gate(transistor_4_out));
  Transistor #(.gate("br")) transistor_11 (.in(1'b1), .out(transistor_11_out), .gate(transistor_2_out));
  Transistor transistor_12 (.in(transistor_11_out), .out(Output), .gate(Carry_Out));
  Transistor #(.\type ("n")) transistor_13 (.in(Output), .out(transistor_13_out), .gate(Carry_Out));
  Transistor #(.\type ("n"), .gate("br")) transistor_14 (.in(Output), .out(transistor_13_out), .gate(transistor_2_out));
  Pull_Resistor pull_resistor_6 (.node(transistor_11_out));
  Pull_Resistor pull_resistor_7 (.node(Output));
  // also tied to GND on the sheet: {transistor_3_out, transistor_7_out, transistor_13_out}

  // Notes on the sheet:
  //   NON-ET
  //   NON-OU
  //   NON
  //   ET
  //   NON-OU
endmodule

module ADDSPTRDEF2 (
  input  Carry_In,
  input  Input_A,
  input  Input_B,
  output Output,
  output Carry_Out
);

  wire addsptrdef_1_carry_out, addsptrdef_1_output, addsptrdef_2_carry_out;

  ADDSPTRDEF addsptrdef_1 (
    .Input_A(Input_A), .Input_B(Input_B), .Output(addsptrdef_1_output), .Carry_Out(addsptrdef_1_carry_out));
  ADDSPTRDEF addsptrdef_2 (
    .Input_A(Carry_In), .Input_B(addsptrdef_1_output), .Output(Output), .Carry_Out(addsptrdef_2_carry_out));
  OU ou_1 (.in_1(addsptrdef_2_carry_out), .in_2(addsptrdef_1_carry_out), .out_3(Carry_Out));
endmodule

module ADDSPTRDEF4 (
  input  Carry_In,
  input  [3:0] Input_A,
  input  [3:0] Input_B,
  output [3:0] Output,
  output Carry_Out
);

  wire addsptrdef2_1_carry_out, addsptrdef2_2_carry_out, addsptrdef2_3_carry_out;

  ADDSPTRDEF2 addsptrdef2_1 (
    .Carry_In(Carry_In), .Input_A(Input_A[0]), .Input_B(Input_B[0]), .Output(Output[0]),
    .Carry_Out(addsptrdef2_1_carry_out));
  ADDSPTRDEF2 addsptrdef2_2 (
    .Carry_In(addsptrdef2_1_carry_out), .Input_A(Input_A[1]), .Input_B(Input_B[1]), .Output(Output[1]),
    .Carry_Out(addsptrdef2_2_carry_out));
  ADDSPTRDEF2 addsptrdef2_3 (
    .Carry_In(addsptrdef2_2_carry_out), .Input_A(Input_A[2]), .Input_B(Input_B[2]), .Output(Output[2]),
    .Carry_Out(addsptrdef2_3_carry_out));
  ADDSPTRDEF2 addsptrdef2_4 (
    .Carry_In(addsptrdef2_3_carry_out), .Input_A(Input_A[3]), .Input_B(Input_B[3]), .Output(Output[3]),
    .Carry_Out(Carry_Out));
endmodule

module ADDTR (
  input  Carry_In,
  input  Input_A,
  input  Input_B,
  output Output,
  output Carry_Out
);

  wire pull_resistor_8_node, transistor_1_out, transistor_2_out, transistor_3_out, transistor_4_out,
       transistor_5_out, transistor_6_out, transistor_9_out, transistor_11_out, transistor_12_out,
       transistor_13_out, transistor_15_out, transistor_18_out, transistor_19_out, transistor_20_out,
       transistor_21_out, transistor_23_out, transistor_25_out, transistor_26_out, transistor_27_out,
       transistor_29_out, transistor_31_out;

  Transistor transistor_1 (.in(1'b1), .out(transistor_1_out), .gate(Input_A));
  Transistor #(.\type ("n")) transistor_2 (.in(transistor_1_out), .out(transistor_2_out), .gate(Input_A));
  Transistor #(.\type ("n"), .gate("br")) transistor_3 (.in(transistor_2_out), .out(transistor_3_out), .gate(Input_B));
  Transistor #(.gate("br")) transistor_4 (.in(1'b1), .out(transistor_4_out), .gate(Input_A));
  Transistor transistor_5 (.in(transistor_4_out), .out(transistor_5_out), .gate(Input_B));
  Transistor #(.\type ("n"), .gate("br")) transistor_6 (.in(transistor_5_out), .out(transistor_6_out), .gate(Input_A));
  Transistor #(.\type ("n")) transistor_7 (.in(transistor_5_out), .out(transistor_6_out), .gate(Input_B));
  Transistor #(.gate("br")) transistor_8 (.in(1'b1), .out(transistor_1_out), .gate(Input_B));
  Pull_Resistor pull_resistor_1 (.node(transistor_1_out));
  Pull_Resistor pull_resistor_2 (.node(transistor_2_out));
  Pull_Resistor pull_resistor_3 (.node(transistor_5_out));
  Pull_Resistor pull_resistor_4 (.node(transistor_4_out));
  Transistor transistor_9 (.in(1'b1), .out(transistor_9_out), .gate(transistor_1_out));
  Pull_Resistor pull_resistor_5 (.node(transistor_9_out));
  Transistor #(.\type ("n")) transistor_10 (.in(transistor_9_out), .out(transistor_3_out), .gate(transistor_1_out));
  Transistor #(.gate("br")) transistor_11 (.in(1'b1), .out(transistor_11_out), .gate(transistor_5_out));
  Transistor transistor_12 (.in(transistor_11_out), .out(transistor_12_out), .gate(transistor_9_out));
  Transistor #(.\type ("n"), .gate("br")) transistor_13 (
    .in(transistor_12_out), .out(transistor_13_out), .gate(transistor_5_out));
  Transistor #(.\type ("n")) transistor_14 (.in(transistor_12_out), .out(transistor_13_out), .gate(transistor_9_out));
  Pull_Resistor pull_resistor_6 (.node(transistor_12_out));
  Pull_Resistor pull_resistor_7 (.node(transistor_11_out));
  Transistor #(.gate("br")) transistor_15 (.in(1'b1), .out(transistor_15_out), .gate(transistor_12_out));
  Transistor transistor_16 (.in(1'b1), .out(transistor_15_out), .gate(Carry_In));
  Pull_Resistor pull_resistor_8 (.node(pull_resistor_8_node));
  Transistor #(.\type ("n")) transistor_17 (.in(transistor_15_out), .out(pull_resistor_8_node), .gate(Carry_In));
  Transistor #(.\type ("n"), .gate("br")) transistor_18 (
    .in(pull_resistor_8_node), .out(transistor_18_out), .gate(transistor_12_out));
  Transistor #(.gate("br")) transistor_19 (.in(1'b1), .out(transistor_19_out), .gate(Carry_In));
  Transistor transistor_20 (.in(transistor_19_out), .out(transistor_20_out), .gate(transistor_12_out));
  Transistor #(.\type ("n")) transistor_21 (.in(transistor_20_out), .out(transistor_21_out), .gate(transistor_12_out));
  Transistor #(.\type ("n"), .gate("br")) transistor_22 (
    .in(transistor_20_out), .out(transistor_21_out), .gate(Carry_In));
  Pull_Resistor pull_resistor_9 (.node(transistor_15_out));
  Pull_Resistor pull_resistor_10 (.node(transistor_20_out));
  Pull_Resistor pull_resistor_11 (.node(transistor_19_out));
  Transistor transistor_23 (.in(1'b1), .out(transistor_23_out), .gate(transistor_15_out));
  Pull_Resistor pull_resistor_12 (.node(transistor_23_out));
  Transistor #(.\type ("n")) transistor_24 (.in(transistor_23_out), .out(transistor_18_out), .gate(transistor_15_out));
  Transistor #(.gate("br")) transistor_25 (.in(1'b1), .out(transistor_25_out), .gate(transistor_23_out));
  Transistor transistor_26 (.in(transistor_25_out), .out(transistor_26_out), .gate(transistor_9_out));
  Transistor #(.\type ("n"), .gate("br")) transistor_27 (
    .in(transistor_26_out), .out(transistor_27_out), .gate(transistor_23_out));
  Transistor #(.\type ("n")) transistor_28 (.in(transistor_26_out), .out(transistor_27_out), .gate(transistor_9_out));
  Transistor #(.gate("br")) transistor_29 (.in(1'b1), .out(transistor_29_out), .gate(transistor_20_out));
  Transistor transistor_30 (.in(transistor_29_out), .out(Output), .gate(transistor_23_out));
  Transistor #(.\type ("n")) transistor_31 (.in(Output), .out(transistor_31_out), .gate(transistor_23_out));
  Pull_Resistor pull_resistor_13 (.node(transistor_25_out));
  Pull_Resistor pull_resistor_14 (.node(transistor_26_out));
  Pull_Resistor pull_resistor_15 (.node(transistor_29_out));
  Pull_Resistor pull_resistor_16 (.node(Output));
  Transistor #(.\type ("n"), .gate("br")) transistor_32 (
    .in(Output), .out(transistor_31_out), .gate(transistor_20_out));
  Transistor transistor_33 (.in(1'b1), .out(Carry_Out), .gate(transistor_26_out));
  Pull_Resistor pull_resistor_17 (.node(Carry_Out));
  Transistor #(.\type ("n")) transistor_34 (.in(Carry_Out), .out(transistor_27_out), .gate(transistor_26_out));
  // also tied to GND on the sheet: {transistor_6_out, transistor_3_out, transistor_13_out, transistor_18_out, transistor_21_out, transistor_27_out, transistor_31_out}

  // Notes on the sheet:
  //   NON-ET
  //   NON-OU
  //   NON
  //   ET
  //   NON-OU
  //   OU_EX
  //   NON-ET
  //   NON-OU
  //   NON
  //   ET
  //   NON-OU
  //   NON
  //   OU_EX
  //   NON-OU
  //   OU
endmodule

module ADDT4 (
  input  Carry_In,
  input  [3:0] Input_A,
  input  [3:0] Input_B,
  output [3:0] Output,
  output Carry_Out
);

  wire addtr_1_carry_out, addtr_2_carry_out, addtr_3_carry_out;

  ADDTR addtr_1 (
    .Carry_In(Carry_In), .Input_A(Input_A[0]), .Input_B(Input_B[0]), .Output(Output[0]),
    .Carry_Out(addtr_1_carry_out));
  ADDTR addtr_2 (
    .Carry_In(addtr_1_carry_out), .Input_A(Input_A[1]), .Input_B(Input_B[1]), .Output(Output[1]),
    .Carry_Out(addtr_2_carry_out));
  ADDTR addtr_3 (
    .Carry_In(addtr_2_carry_out), .Input_A(Input_A[2]), .Input_B(Input_B[2]), .Output(Output[2]),
    .Carry_Out(addtr_3_carry_out));
  ADDTR addtr_4 (
    .Carry_In(addtr_3_carry_out), .Input_A(Input_A[3]), .Input_B(Input_B[3]), .Output(Output[3]),
    .Carry_Out(Carry_Out));
endmodule

module NEG4 (
  input  [3:0] Input,
  output [3:0] Output
);

  wire [3:0] not_1_out;

  assign not_1_out = ~Input;  // NOT_Gate not_1, 4 bits wide
  Adder #(.width(4)) adder_1 (.a(not_1_out), .b(4'b0001), .out(Output), .cin(1'b0));  // open: cout
endmodule

module SUB4 (
  input  [3:0] Minuend,
  input  [3:0] Subtrahend,
  output [3:0] Output
);

  wire [3:0] negator_1_out;

  Negator #(.width(4)) negator_1 (.in(Subtrahend), .out(negator_1_out));
  Adder #(.width(4)) adder_1 (.a(Minuend), .b(negator_1_out), .out(Output), .cin(1'b0));  // open: cout
endmodule

module SUB4D (
  input  Borrow_In,
  input  [3:0] Minuend,
  input  [3:0] Subtrahend,
  output [3:0] Output,
  output Borrow_Out
);

  wire [3:0] adder_1_out;
  wire [4:0] negator_1_out;

  Adder #(.width(4)) adder_1 (.a({3'b000, Borrow_In}), .b(Subtrahend), .out(adder_1_out), .cin(1'b0));  // open: cout
  Negator #(.width(5)) negator_1 (.in({1'b0, adder_1_out}), .out(negator_1_out));
  Adder #(.width(5)) adder_2 (
    .a({1'b0, Minuend}), .b(negator_1_out), .out({Borrow_Out, Output}), .cin(1'b0));  // open: cout
endmodule

module COMP (
  input  [3:0] A,
  input  [3:0] B,
  output Less,
  output Equal,
  output Greater
);

  wire and_1_out, and_2_out, and_3_out, and_4_out, and_6_out, and_7_out, and_8_out, nor_1_out, nor_2_out,
       not_1_out, not_2_out, not_3_out, or_1_out;
  wire [3:0] subtractor_1_out, subtractor_2_out;

  Subtractor #(.width(4)) subtractor_1 (.a(A), .b(B), .out(subtractor_1_out), .bin(1'b0));  // open: bout
  Subtractor #(.width(4)) subtractor_2 (.a(B), .b(A), .out(subtractor_2_out), .bin(1'b0));  // open: bout
  and and_1 (and_1_out, B[3], A[3]);
  nor nor_1 (nor_1_out, A[3], B[3]);
  or or_1 (or_1_out, and_1_out, nor_1_out);
  not not_1 (not_1_out, subtractor_1_out[3]);
  not not_2 (not_2_out, subtractor_2_out[3]);
  and and_2 (and_2_out, not_1_out, subtractor_2_out[3]);
  nor nor_2 (nor_2_out, and_2_out, and_3_out);
  and and_3 (and_3_out, subtractor_1_out[3], not_2_out);
  and and_4 (and_4_out, and_2_out, or_1_out);
  and and_5 (Equal, nor_2_out, or_1_out);
  and and_6 (and_6_out, and_3_out, or_1_out);
  and and_7 (and_7_out, A[3], not_3_out);
  not not_3 (not_3_out, or_1_out);
  and and_8 (and_8_out, not_3_out, B[3]);
  or or_2 (Less, and_6_out, and_7_out);
  or or_3 (Greater, and_4_out, and_8_out);
endmodule

module AFSI (
  input  Less,
  input  equal,
  input  Greater,
  input  Enable,
  output [5:0] Output_0,
  output [5:0] Output_1,
  output [5:0] Output_2,
  output [5:0] Output_3,
  output [5:0] Output_4
);

  wire and_1_out, and_2_out, and_3_out;
  wire [5:0] and_4_out, and_5_out, and_6_out, and_7_out, and_8_out, and_9_out, and_10_out, and_11_out,
       and_12_out, and_13_out, and_14_out, and_15_out, and_16_out, and_17_out, and_18_out,
       bit_extender_1_out, bit_extender_2_out, bit_extender_3_out, bit_extender_4_out, bit_extender_5_out,
       bit_extender_6_out, bit_extender_7_out, bit_extender_8_out, bit_extender_9_out, bit_extender_10_out,
       bit_extender_11_out, bit_extender_12_out, bit_extender_13_out, bit_extender_14_out,
       bit_extender_15_out;

  and and_1 (and_1_out, Less, Enable);
  and and_2 (and_2_out, equal, Enable);
  and and_3 (and_3_out, Greater, Enable);
  assign and_4_out = {6{1'b0}} & bit_extender_1_out;  // AND_Gate and_4, 6 bits wide
  assign bit_extender_1_out = {{5{and_2_out}}, and_2_out};  // Bit_Extender bit_extender_1
  assign and_5_out = {6{1'b1}} & bit_extender_2_out;  // AND_Gate and_5, 6 bits wide
  assign bit_extender_2_out = {{5{and_2_out}}, and_2_out};  // Bit_Extender bit_extender_2
  assign and_6_out = {6{1'b0}} & bit_extender_3_out;  // AND_Gate and_6, 6 bits wide
  assign bit_extender_3_out = {{5{and_2_out}}, and_2_out};  // Bit_Extender bit_extender_3
  assign and_7_out = {6{1'b1}} & bit_extender_4_out;  // AND_Gate and_7, 6 bits wide
  assign bit_extender_4_out = {{5{and_2_out}}, and_2_out};  // Bit_Extender bit_extender_4
  assign and_8_out = {6{1'b0}} & bit_extender_5_out;  // AND_Gate and_8, 6 bits wide
  assign bit_extender_5_out = {{5{and_2_out}}, and_2_out};  // Bit_Extender bit_extender_5
  assign bit_extender_6_out = {{5{and_1_out}}, and_1_out};  // Bit_Extender bit_extender_6
  assign bit_extender_7_out = {{5{and_1_out}}, and_1_out};  // Bit_Extender bit_extender_7
  assign bit_extender_8_out = {{5{and_1_out}}, and_1_out};  // Bit_Extender bit_extender_8
  assign bit_extender_9_out = {{5{and_1_out}}, and_1_out};  // Bit_Extender bit_extender_9
  assign bit_extender_10_out = {{5{and_1_out}}, and_1_out};  // Bit_Extender bit_extender_10
  assign bit_extender_11_out = {{5{and_3_out}}, and_3_out};  // Bit_Extender bit_extender_11
  assign bit_extender_12_out = {{5{and_3_out}}, and_3_out};  // Bit_Extender bit_extender_12
  assign bit_extender_13_out = {{5{and_3_out}}, and_3_out};  // Bit_Extender bit_extender_13
  assign bit_extender_14_out = {{5{and_3_out}}, and_3_out};  // Bit_Extender bit_extender_14
  assign bit_extender_15_out = {{5{and_3_out}}, and_3_out};  // Bit_Extender bit_extender_15
  assign and_9_out = 6'b000011 & bit_extender_6_out;  // AND_Gate and_9, 6 bits wide
  assign and_10_out = 6'b001100 & bit_extender_7_out;  // AND_Gate and_10, 6 bits wide
  assign and_11_out = 6'b110000 & bit_extender_8_out;  // AND_Gate and_11, 6 bits wide
  assign and_12_out = 6'b001100 & bit_extender_9_out;  // AND_Gate and_12, 6 bits wide
  assign and_13_out = 6'b000011 & bit_extender_10_out;  // AND_Gate and_13, 6 bits wide
  assign and_14_out = 6'b110000 & bit_extender_11_out;  // AND_Gate and_14, 6 bits wide
  assign and_15_out = 6'b001100 & bit_extender_12_out;  // AND_Gate and_15, 6 bits wide
  assign and_16_out = 6'b000011 & bit_extender_13_out;  // AND_Gate and_16, 6 bits wide
  assign and_17_out = 6'b001100 & bit_extender_14_out;  // AND_Gate and_17, 6 bits wide
  assign and_18_out = 6'b110000 & bit_extender_15_out;  // AND_Gate and_18, 6 bits wide
  assign {Output_4, Output_3, Output_2, Output_1, Output_0} = {and_13_out, and_12_out, and_11_out, and_10_out, and_9_out} | {and_8_out, and_7_out, and_6_out, and_5_out, and_4_out} | {and_18_out, and_17_out, and_16_out, and_15_out, and_14_out};  // OR_Gate or_1, 30 bits wide

  // Notes on the sheet:
  //   ________
  //   ******
  //   ________
  //   ******
  //   ________
  //   ____**
  //   __**__
  //   **____
  //   __**__
  //   ____**
  //   **____
  //   __**__
  //   ____**
  //   __**__
  //   **____
endmodule

module AFSI2 (
  input  Greater,
  input  Equal,
  input  Less,
  input  ENABLE,
  output [29:0] Output
);

  wire and_1_out, and_2_out, and_3_out;
  wire [4:0] and_4_out, and_5_out, and_6_out, and_7_out, and_8_out, and_9_out, and_10_out, and_11_out,
       and_12_out, and_13_out, and_14_out, and_15_out, and_16_out, and_17_out, and_18_out, and_19_out,
       and_20_out, and_21_out, bit_extender_1_out, bit_extender_2_out, bit_extender_3_out,
       bit_extender_4_out, bit_extender_5_out, bit_extender_6_out, bit_extender_7_out, bit_extender_8_out,
       bit_extender_9_out, bit_extender_10_out, bit_extender_11_out, bit_extender_12_out,
       bit_extender_13_out, bit_extender_14_out, bit_extender_15_out, bit_extender_16_out,
       bit_extender_17_out, bit_extender_18_out;

  and and_1 (and_1_out, Greater, ENABLE);
  and and_2 (and_2_out, Equal, ENABLE);
  and and_3 (and_3_out, Less, ENABLE);
  assign bit_extender_1_out = {{4{and_2_out}}, and_2_out};  // Bit_Extender bit_extender_1
  assign bit_extender_2_out = {{4{and_2_out}}, and_2_out};  // Bit_Extender bit_extender_2
  assign bit_extender_3_out = {{4{and_2_out}}, and_2_out};  // Bit_Extender bit_extender_3
  assign bit_extender_4_out = {{4{and_2_out}}, and_2_out};  // Bit_Extender bit_extender_4
  assign bit_extender_5_out = {{4{and_2_out}}, and_2_out};  // Bit_Extender bit_extender_5
  assign bit_extender_6_out = {{4{and_2_out}}, and_2_out};  // Bit_Extender bit_extender_6
  assign and_4_out = 5'b01010 & bit_extender_1_out;  // AND_Gate and_4, 5 bits wide
  assign and_5_out = 5'b01010 & bit_extender_2_out;  // AND_Gate and_5, 5 bits wide
  assign and_6_out = 5'b01010 & bit_extender_3_out;  // AND_Gate and_6, 5 bits wide
  assign and_7_out = 5'b01010 & bit_extender_4_out;  // AND_Gate and_7, 5 bits wide
  assign and_8_out = 5'b01010 & bit_extender_5_out;  // AND_Gate and_8, 5 bits wide
  assign and_9_out = 5'b01010 & bit_extender_6_out;  // AND_Gate and_9, 5 bits wide
  assign bit_extender_7_out = {{4{and_3_out}}, and_3_out};  // Bit_Extender bit_extender_7
  assign bit_extender_8_out = {{4{and_3_out}}, and_3_out};  // Bit_Extender bit_extender_8
  assign bit_extender_9_out = {{4{and_3_out}}, and_3_out};  // Bit_Extender bit_extender_9
  assign bit_extender_10_out = {{4{and_3_out}}, and_3_out};  // Bit_Extender bit_extender_10
  assign bit_extender_11_out = {{4{and_3_out}}, and_3_out};  // Bit_Extender bit_extender_11
  assign bit_extender_12_out = {{4{and_3_out}}, and_3_out};  // Bit_Extender bit_extender_12
  assign bit_extender_13_out = {{4{and_1_out}}, and_1_out};  // Bit_Extender bit_extender_13
  assign bit_extender_14_out = {{4{and_1_out}}, and_1_out};  // Bit_Extender bit_extender_14
  assign bit_extender_15_out = {{4{and_1_out}}, and_1_out};  // Bit_Extender bit_extender_15
  assign bit_extender_16_out = {{4{and_1_out}}, and_1_out};  // Bit_Extender bit_extender_16
  assign bit_extender_17_out = {{4{and_1_out}}, and_1_out};  // Bit_Extender bit_extender_17
  assign bit_extender_18_out = {{4{and_1_out}}, and_1_out};  // Bit_Extender bit_extender_18
  assign and_10_out = 5'b10001 & bit_extender_7_out;  // AND_Gate and_10, 5 bits wide
  assign and_11_out = 5'b10001 & bit_extender_8_out;  // AND_Gate and_11, 5 bits wide
  assign and_12_out = 5'b01010 & bit_extender_9_out;  // AND_Gate and_12, 5 bits wide
  assign and_13_out = 5'b01010 & bit_extender_10_out;  // AND_Gate and_13, 5 bits wide
  assign and_14_out = 5'b00100 & bit_extender_11_out;  // AND_Gate and_14, 5 bits wide
  assign and_15_out = 5'b00100 & bit_extender_12_out;  // AND_Gate and_15, 5 bits wide
  assign and_16_out = 5'b00100 & bit_extender_13_out;  // AND_Gate and_16, 5 bits wide
  assign and_17_out = 5'b00100 & bit_extender_14_out;  // AND_Gate and_17, 5 bits wide
  assign and_18_out = 5'b01010 & bit_extender_15_out;  // AND_Gate and_18, 5 bits wide
  assign and_19_out = 5'b01010 & bit_extender_16_out;  // AND_Gate and_19, 5 bits wide
  assign and_20_out = 5'b10001 & bit_extender_17_out;  // AND_Gate and_20, 5 bits wide
  assign and_21_out = 5'b10001 & bit_extender_18_out;  // AND_Gate and_21, 5 bits wide
  assign Output = {and_15_out, and_14_out, and_13_out, and_12_out, and_11_out, and_10_out} | {and_9_out, and_8_out, and_7_out, and_6_out, and_5_out, and_4_out} | {and_21_out, and_20_out, and_19_out, and_18_out, and_17_out, and_16_out};  // OR_Gate or_1, 30 bits wide

  // Notes on the sheet:
  //   _*_*_
  //   _*_*_
  //   _*_*_
  //   _*_*_
  //   _*_*_
  //   _*_*_
  //   __*__
  //   __*__
  //   _*_*_
  //   _*_*_
  //   *___*
  //   *___*
  //   *___*
  //   *___*
  //   _*_*_
  //   _*_*_
  //   __*__
  //   __*__
endmodule

module AFN4 (
  input  [3:0] Input,
  output Sign,
  output [3:0] Output
);

  wire [3:0] and_1_out, and_2_out, negator_1_out, not_1_out;

  assign and_1_out = {4{Input[3]}} & Input;  // AND_Gate and_1, 4 bits wide
  assign not_1_out = ~{4{Input[3]}};  // NOT_Gate not_1, 4 bits wide
  Negator #(.width(4)) negator_1 (.in(and_1_out), .out(negator_1_out));
  assign and_2_out = not_1_out & Input;  // AND_Gate and_2, 4 bits wide
  assign Output = negator_1_out | and_2_out;  // OR_Gate or_1, 4 bits wide

  assign Sign = Input[3];
endmodule

module AFIN (
  input  [3:0] INPUT,
  output [3:0] Ouptu_unit,
  output [3:0] Output_ten
);

  wire comparator_1_gt, not_1_out;
  wire [3:0] and_1_out, and_2_out, bit_extender_1_out, bit_extender_2_out, subtractor_1_out;

  Subtractor #(.width(4)) subtractor_1 (.a(INPUT), .b(4'b1010), .out(subtractor_1_out), .bin(1'b0));  // open: bout
  Comparator #(.width(4), .mode("unsigned")) comparator_1 (
    .a(INPUT), .b(4'b1001), .gt(comparator_1_gt));  // open: eq, lt
  assign bit_extender_1_out = {{3{comparator_1_gt}}, comparator_1_gt};  // Bit_Extender bit_extender_1
  assign bit_extender_2_out = {{3{not_1_out}}, not_1_out};  // Bit_Extender bit_extender_2
  not not_1 (not_1_out, comparator_1_gt);
  assign and_1_out = subtractor_1_out & bit_extender_1_out;  // AND_Gate and_1, 4 bits wide
  assign Ouptu_unit = and_1_out | and_2_out;  // OR_Gate or_1, 4 bits wide
  assign and_2_out = INPUT & bit_extender_2_out;  // AND_Gate and_2, 4 bits wide
  assign Output_ten = {{3{1'b0}}, comparator_1_gt};  // Bit_Extender bit_extender_3
endmodule

module list1 (
  output [7:0] out_1,
  output [7:0] out_2,
  output [7:0] out_3,
  output [7:0] out_4,
  output [7:0] out_5,
  output [7:0] out_6,
  output [7:0] out_7,
  output [7:0] out_8,
  output [7:0] out_9
);

  // Probe on 8'h5
  // Probe on 8'h7
  // Probe on 8'h14
  // Probe on 8'hf1
  // Probe on 8'h5
  // Probe on 8'h14
  // Probe on 8'h32
  // Probe on 8'h73
  // Probe on 8'h92

  assign out_1 = 8'h5;
  assign out_2 = 8'h7;
  assign out_3 = 8'h14;
  assign out_4 = 8'hf1;
  assign out_5 = 8'h5;
  assign out_6 = 8'h14;
  assign out_7 = 8'h32;
  assign out_8 = 8'h73;
  assign out_9 = 8'h92;
endmodule

module list2 (
  output [7:0] out_1,
  output [7:0] out_2,
  output [7:0] out_3,
  output [7:0] out_4,
  output [7:0] out_5,
  output [7:0] out_6,
  output [7:0] out_7,
  output [7:0] out_8,
  output [7:0] out_9
);

  // Probe on 8'h5
  // Probe on 8'h7
  // Probe on 8'h14
  // Probe on 8'ha
  // Probe on 8'hec
  // Probe on 8'hf1
  // Probe on 8'h32
  // Probe on 8'h73
  // Probe on 8'h92

  assign out_1 = 8'h5;
  assign out_2 = 8'h7;
  assign out_3 = 8'h14;
  assign out_4 = 8'ha;
  assign out_5 = 8'hec;
  assign out_6 = 8'hf1;
  assign out_7 = 8'h32;
  assign out_8 = 8'h73;
  assign out_9 = 8'h92;
endmodule

module ADD3 (
  input  R,
  input  R_2,
  input  A,
  input  A_2,
  input  in_5,
  input  B,
  input  B_2,
  input  in_8,
  input  in_9,
  input  R_3,
  input  R_4,
  input  A_3,
  input  A_4,
  input  B_3,
  input  B_4,
  input  R_5,
  input  R_6,
  input  A_5,
  input  A_6,
  input  B_5,
  input  B_6,
  input  R_7,
  input  R_8,
  input  A_7,
  input  A_8,
  input  B_7,
  input  B_8,
  output S,
  output S_2,
  output RS,
  output RS_2,
  output out_32,
  output out_33,
  output S_3,
  output S_4,
  output RS_3,
  output RS_4,
  output S_5,
  output S_6,
  output RS_5,
  output RS_6,
  output S_7,
  output S_8,
  output RS_7,
  output RS_8
);

  wire adder_1_cout, adder_1_out, adder_2_cout;

  Adder #(.width(1)) adder_1 (.a(in_8), .b(in_9), .out(adder_1_out), .cin(1'b0), .cout(adder_1_cout));
  Adder #(.width(1)) adder_2 (.a(in_5), .b(adder_1_out), .out(out_32), .cin(1'b0), .cout(adder_2_cout));
  or or_1 (out_33, adder_2_cout, adder_1_cout);
  Adder #(.width(1)) adder_3 (.a(A), .b(B), .out(S), .cin(R), .cout(RS));
  Adder #(.width(1)) adder_4 (.a(A_3), .b(B_3), .out(S_3), .cin(R_3), .cout(RS_3));
  Adder #(.width(1)) adder_5 (.a(A_5), .b(B_5), .out(S_5), .cin(R_5), .cout(RS_5));
  Adder #(.width(1)) adder_6 (.a(A_7), .b(B_7), .out(S_7), .cin(R_7), .cout(RS_7));
  Adder #(.width(1)) adder_7 (.a(A_2), .b(B_2), .out(S_2), .cin(R_2), .cout(RS_2));
  Adder #(.width(1)) adder_8 (.a(A_4), .b(B_4), .out(S_4), .cin(R_4), .cout(RS_4));
  Adder #(.width(1)) adder_9 (.a(A_6), .b(B_6), .out(S_6), .cin(R_6), .cout(RS_6));
  Adder #(.width(1)) adder_10 (.a(A_8), .b(B_8), .out(S_8), .cin(R_8), .cout(RS_8));
endmodule

module main_ADD_OU_EX (
  input  Input_A,
  input  Input_A_2,
  input  A,
  input  Input_B,
  input  Input_B_2,
  input  B,
  input  Input_A_3,
  input  Input_A_4,
  input  Input_B_3,
  input  Input_B_4,
  input  Input_A_5,
  input  Input_B_5,
  input  Input_A_6,
  input  Input_B_6,
  output Output,
  output Output_2,
  output Carry_Out,
  output Carry_Out_2,
  output out_19,
  output Output_3,
  output Output_4,
  output out_22,
  output Carry_Out_3,
  output Carry_Out_4,
  output out_25,
  output Output_5,
  output Carry_Out_5,
  output out_28,
  output Output_6,
  output Carry_Out_6
);

  wire and_2_out, and_10_out, and_12_out, and_13_out, nand_1_out, nand_2_out, nor_1_out, nor_2_out,
       nor_5_out, not_1_out, not_2_out, not_3_out, or_1_out, or_2_out, or_3_out, or_4_out, or_5_out;

  or or_1 (or_1_out, Input_A, Input_B);
  and and_1 (Carry_Out, Input_A, Input_B);
  or or_2 (or_2_out, Input_A_3, Input_B_3);
  and and_2 (and_2_out, Input_A_3, Input_B_3);
  and and_3 (Carry_Out_3, Input_A_3, Input_B_3);
  or or_3 (or_3_out, Input_A_5, Input_B_5);
  nand nand_1 (nand_1_out, Input_A_5, Input_B_5);
  and and_4 (Carry_Out_5, Input_A_5, Input_B_5);
  and and_5 (Output, or_1_out, not_1_out);
  not not_1 (not_1_out, Carry_Out);
  and and_6 (Output_3, or_2_out, not_2_out);
  not not_2 (not_2_out, and_2_out);
  and and_7 (Output_5, or_3_out, nand_1_out);
  xor xor_1 (Output_6, Input_A_6, Input_B_6);
  and and_8 (Carry_Out_6, Input_A_6, Input_B_6);
  nor nor_1 (nor_1_out, Input_A_2, Input_B_2);
  and and_9 (Carry_Out_2, Input_A_2, Input_B_2);
  nor nor_2 (nor_2_out, Input_A_4, Input_B_4);
  and and_10 (and_10_out, Input_A_4, Input_B_4);
  and and_11 (Carry_Out_4, Input_A_4, Input_B_4);
  nor nor_3 (Output_2, nor_1_out, Carry_Out_2);
  nor nor_4 (Output_4, nor_2_out, and_10_out);
  nor nor_5 (nor_5_out, A, B);
  and and_12 (and_12_out, A, B);
  xor xor_2 (out_22, A, B);
  or or_4 (or_4_out, A, B);
  nand nand_2 (nand_2_out, A, B);
  or or_5 (or_5_out, A, B);
  not not_3 (not_3_out, and_13_out);
  and and_13 (and_13_out, A, B);
  nor nor_6 (out_19, nor_5_out, and_12_out);
  and and_14 (out_25, or_4_out, nand_2_out);
  and and_15 (out_28, or_5_out, not_3_out);
endmodule

module ADDB_OU_EX (
  input  Carry_In,
  input  [3:0] Input_A,
  input  Input_A_2,
  input  Input_B,
  input  [3:0] Input_B_2,
  output Output,
  output [3:0] Output_2,
  output Carry_Out
);

  wire and_1_out, and_2_out, and_3_out, and_4_out, and_5_out, and_6_out, and_7_out, or_1_out, or_2_out,
       xor_1_out, xor_3_out, xor_4_out, xor_8_out;

  xor xor_1 (xor_1_out, Input_A[3], Input_B_2[3]);
  xor xor_2 (Output_2[0], Input_A[0], Input_B_2[0]);
  and and_1 (and_1_out, Input_A[0], Input_B_2[0]);
  xor xor_3 (xor_3_out, Input_A[1], Input_B_2[1]);
  and and_2 (and_2_out, Input_A[1], Input_B_2[1]);
  xor xor_4 (xor_4_out, Input_A[2], Input_B_2[2]);
  and and_3 (and_3_out, Input_A[2], Input_B_2[2]);
  or or_1 (or_1_out, and_4_out, and_2_out);
  or or_2 (or_2_out, and_5_out, and_3_out);
  xor xor_5 (Output_2[1], and_1_out, xor_3_out);
  and and_4 (and_4_out, and_1_out, xor_3_out);
  xor xor_6 (Output_2[2], or_1_out, xor_4_out);
  and and_5 (and_5_out, or_1_out, xor_4_out);
  xor xor_7 (Output_2[3], or_2_out, xor_1_out);
  // Probe on and_1_out
  // Probe on or_1_out
  // Probe on or_2_out
  xor xor_8 (xor_8_out, Input_A_2, Input_B);
  and and_6 (and_6_out, Input_A_2, Input_B);
  xor xor_9 (Output, Carry_In, xor_8_out);
  and and_7 (and_7_out, Carry_In, xor_8_out);
  or or_3 (Carry_Out, and_7_out, and_6_out);
endmodule

module ADDUI (
  input  Carry_In,
  input  Input_A,
  input  Input_B,
  output Output,
  output Carry_Out
);

  wire pull_resistor_2_node, pull_resistor_7_node, pull_resistor_17_node, transistor_1_out, transistor_2_out,
       transistor_3_out, transistor_5_out, transistor_8_out, transistor_9_out, transistor_11_out,
       transistor_13_out, transistor_16_out, transistor_17_out, transistor_18_out, transistor_19_out,
       transistor_21_out, transistor_22_out, transistor_23_out, transistor_24_out, transistor_25_out,
       transistor_26_out, transistor_29_out, transistor_31_out, transistor_33_out, transistor_36_out,
       transistor_37_out, transistor_38_out, transistor_41_out, transistor_42_out, transistor_43_out;

  Transistor #(.gate("br")) transistor_1 (.in(1'b1), .out(transistor_1_out), .gate(Input_A));
  Transistor transistor_2 (.in(transistor_1_out), .out(transistor_2_out), .gate(Input_B));
  Pull_Resistor pull_resistor_1 (.node(transistor_1_out));
  Transistor #(.\type ("n")) transistor_3 (.in(transistor_2_out), .out(transistor_3_out), .gate(Input_B));
  Transistor #(.\type ("n"), .gate("br")) transistor_4 (.in(transistor_2_out), .out(transistor_3_out), .gate(Input_A));
  Transistor transistor_5 (.in(1'b1), .out(transistor_5_out), .gate(Input_A));
  Transistor #(.gate("br")) transistor_6 (.in(1'b1), .out(transistor_5_out), .gate(Input_B));
  Pull_Resistor pull_resistor_2 (.node(pull_resistor_2_node));
  Transistor #(.\type ("n")) transistor_7 (.in(transistor_5_out), .out(pull_resistor_2_node), .gate(Input_A));
  Transistor #(.\type ("n"), .gate("br")) transistor_8 (
    .in(pull_resistor_2_node), .out(transistor_8_out), .gate(Input_B));
  Transistor transistor_9 (.in(1'b1), .out(transistor_9_out), .gate(transistor_2_out));
  Pull_Resistor pull_resistor_3 (.node(transistor_9_out));
  Pull_Resistor pull_resistor_4 (.node(transistor_2_out));
  Transistor #(.\type ("n")) transistor_10 (.in(transistor_9_out), .out(transistor_3_out), .gate(transistor_2_out));
  Transistor transistor_11 (.in(1'b1), .out(transistor_11_out), .gate(transistor_5_out));
  Pull_Resistor pull_resistor_5 (.node(transistor_11_out));
  Pull_Resistor pull_resistor_6 (.node(transistor_5_out));
  Transistor #(.\type ("n")) transistor_12 (.in(transistor_11_out), .out(transistor_8_out), .gate(transistor_5_out));
  Transistor #(.gate("br")) transistor_13 (.in(1'b1), .out(transistor_13_out), .gate(transistor_17_out));
  Transistor transistor_14 (.in(1'b1), .out(transistor_13_out), .gate(transistor_9_out));
  Pull_Resistor pull_resistor_7 (.node(pull_resistor_7_node));
  Transistor #(.\type ("n")) transistor_15 (
    .in(transistor_13_out), .out(pull_resistor_7_node), .gate(transistor_9_out));
  Transistor #(.\type ("n"), .gate("br")) transistor_16 (
    .in(pull_resistor_7_node), .out(transistor_16_out), .gate(transistor_17_out));
  Transistor transistor_17 (.in(1'b1), .out(transistor_17_out), .gate(transistor_11_out));
  Pull_Resistor pull_resistor_8 (.node(transistor_17_out));
  Transistor #(.\type ("n")) transistor_18 (.in(transistor_17_out), .out(transistor_18_out), .gate(transistor_11_out));
  Transistor transistor_19 (.in(1'b1), .out(transistor_19_out), .gate(transistor_13_out));
  Pull_Resistor pull_resistor_9 (.node(transistor_13_out));
  Transistor #(.\type ("n")) transistor_20 (.in(transistor_19_out), .out(transistor_16_out), .gate(transistor_13_out));
  Transistor #(.gate("br")) transistor_21 (.in(1'b1), .out(transistor_21_out), .gate(Carry_In));
  Pull_Resistor pull_resistor_10 (.node(transistor_19_out));
  Transistor transistor_22 (.in(transistor_21_out), .out(transistor_22_out), .gate(transistor_19_out));
  Transistor #(.\type ("n")) transistor_23 (.in(transistor_22_out), .out(transistor_23_out), .gate(transistor_19_out));
  Transistor transistor_24 (.in(1'b1), .out(transistor_24_out), .gate(Carry_In));
  Transistor #(.\type ("n")) transistor_25 (.in(transistor_24_out), .out(transistor_25_out), .gate(Carry_In));
  Transistor #(.\type ("n"), .gate("br")) transistor_26 (
    .in(transistor_25_out), .out(transistor_26_out), .gate(transistor_19_out));
  Pull_Resistor pull_resistor_11 (.node(transistor_21_out));
  Pull_Resistor pull_resistor_12 (.node(transistor_22_out));
  Transistor #(.\type ("n"), .gate("br")) transistor_27 (
    .in(transistor_22_out), .out(transistor_23_out), .gate(Carry_In));
  Transistor #(.gate("br")) transistor_28 (.in(1'b1), .out(transistor_24_out), .gate(transistor_19_out));
  Pull_Resistor pull_resistor_13 (.node(transistor_24_out));
  Pull_Resistor pull_resistor_14 (.node(transistor_25_out));
  Transistor transistor_29 (.in(1'b1), .out(transistor_29_out), .gate(transistor_22_out));
  Pull_Resistor pull_resistor_15 (.node(transistor_29_out));
  Transistor #(.\type ("n")) transistor_30 (.in(transistor_29_out), .out(transistor_23_out), .gate(transistor_22_out));
  Transistor transistor_31 (.in(1'b1), .out(transistor_31_out), .gate(transistor_24_out));
  Pull_Resistor pull_resistor_16 (.node(transistor_31_out));
  Transistor #(.\type ("n")) transistor_32 (.in(transistor_31_out), .out(transistor_26_out), .gate(transistor_24_out));
  Transistor transistor_33 (.in(1'b1), .out(transistor_33_out), .gate(transistor_29_out));
  Transistor #(.gate("br")) transistor_34 (.in(1'b1), .out(transistor_33_out), .gate(transistor_37_out));
  Pull_Resistor pull_resistor_17 (.node(pull_resistor_17_node));
  Transistor #(.\type ("n")) transistor_35 (
    .in(transistor_33_out), .out(pull_resistor_17_node), .gate(transistor_29_out));
  Transistor #(.\type ("n"), .gate("br")) transistor_36 (
    .in(pull_resistor_17_node), .out(transistor_36_out), .gate(transistor_37_out));
  Transistor transistor_37 (.in(1'b1), .out(transistor_37_out), .gate(transistor_31_out));
  Pull_Resistor pull_resistor_18 (.node(transistor_37_out));
  Transistor #(.\type ("n")) transistor_38 (.in(transistor_37_out), .out(transistor_38_out), .gate(transistor_31_out));
  Transistor transistor_39 (.in(1'b1), .out(Output), .gate(transistor_33_out));
  Pull_Resistor pull_resistor_19 (.node(Output));
  Pull_Resistor pull_resistor_20 (.node(transistor_33_out));
  Transistor #(.\type ("n")) transistor_40 (.in(Output), .out(transistor_36_out), .gate(transistor_33_out));
  Transistor #(.gate("br")) transistor_41 (.in(1'b1), .out(transistor_41_out), .gate(transistor_11_out));
  Transistor transistor_42 (.in(transistor_41_out), .out(transistor_42_out), .gate(transistor_31_out));
  Transistor #(.\type ("n")) transistor_43 (.in(transistor_42_out), .out(transistor_43_out), .gate(transistor_31_out));
  Transistor #(.\type ("n"), .gate("br")) transistor_44 (
    .in(transistor_42_out), .out(transistor_43_out), .gate(transistor_11_out));
  Transistor transistor_45 (.in(1'b1), .out(Carry_Out), .gate(transistor_42_out));
  Pull_Resistor pull_resistor_21 (.node(transistor_42_out));
  Pull_Resistor pull_resistor_22 (.node(transistor_41_out));
  Transistor #(.\type ("n")) transistor_46 (.in(Carry_Out), .out(transistor_43_out), .gate(transistor_42_out));
  Pull_Resistor pull_resistor_23 (.node(Carry_Out));
  // also tied to GND on the sheet: {transistor_3_out, transistor_8_out, transistor_18_out, transistor_16_out, transistor_23_out, transistor_26_out, transistor_36_out, transistor_38_out, transistor_43_out}
endmodule

module ADDUI4 (
  input  in_1,
  input  [3:0] in_2,
  input  [3:0] in_3,
  output [3:0] out_4,
  output out_5
);

  wire addui_1_carry_out, addui_2_carry_out, addui_3_carry_out;

  // Probe on in_2
  // Probe on in_2
  // Probe on in_2
  // Probe on in_3
  // Probe on in_3
  // Probe on in_3
  ADDUI addui_1 (
    .Input_A(in_2[0]), .Input_B(in_3[0]), .Carry_In(in_1), .Output(out_4[0]), .Carry_Out(addui_1_carry_out));
  ADDUI addui_2 (
    .Input_A(in_2[1]), .Input_B(in_3[1]), .Carry_In(addui_1_carry_out), .Output(out_4[1]),
    .Carry_Out(addui_2_carry_out));
  ADDUI addui_3 (
    .Input_A(in_2[2]), .Input_B(in_3[2]), .Carry_In(addui_2_carry_out), .Output(out_4[2]),
    .Carry_Out(addui_3_carry_out));
  ADDUI addui_4 (
    .Input_A(in_2[3]), .Input_B(in_3[3]), .Carry_In(addui_3_carry_out), .Output(out_4[3]), .Carry_Out(out_5));
  // Probe on out_4
  // Probe on out_4
  // Probe on out_4
endmodule

module ADDUI04 (
  input  Carry_In,
  input  [3:0] Input_A,
  input  [3:0] Input_B,
  output [3:0] Output,
  output Carry_Out
);

  wire pull_resistor_2_node, pull_resistor_4_node, pull_resistor_13_node, pull_resistor_15_node,
       pull_resistor_33_node, pull_resistor_36_node, pull_resistor_59_node, pull_resistor_61_node,
       pull_resistor_67_node, transistor_1_out, transistor_2_out, transistor_3_out, transistor_5_out,
       transistor_8_out, transistor_9_out, transistor_10_out, transistor_11_out, transistor_13_out,
       transistor_16_out, transistor_17_out, transistor_19_out, transistor_21_out, transistor_23_out,
       transistor_25_out, transistor_28_out, transistor_29_out, transistor_30_out, transistor_31_out,
       transistor_34_out, transistor_35_out, transistor_36_out, transistor_37_out, transistor_39_out,
       transistor_41_out, transistor_42_out, transistor_43_out, transistor_44_out, transistor_45_out,
       transistor_46_out, transistor_47_out, transistor_48_out, transistor_49_out, transistor_50_out,
       transistor_51_out, transistor_52_out, transistor_57_out, transistor_59_out, transistor_61_out,
       transistor_63_out, transistor_65_out, transistor_68_out, transistor_69_out, transistor_70_out,
       transistor_71_out, transistor_74_out, transistor_75_out, transistor_76_out, transistor_79_out,
       transistor_80_out, transistor_81_out, transistor_85_out, transistor_86_out, transistor_87_out,
       transistor_89_out, transistor_91_out, transistor_93_out, transistor_94_out, transistor_95_out,
       transistor_96_out, transistor_97_out, transistor_98_out, transistor_99_out, transistor_100_out,
       transistor_101_out, transistor_102_out, transistor_103_out, transistor_104_out, transistor_109_out,
       transistor_111_out, transistor_113_out, transistor_115_out, transistor_117_out, transistor_120_out,
       transistor_121_out, transistor_122_out, transistor_123_out, transistor_126_out, transistor_127_out,
       transistor_128_out, transistor_129_out, transistor_131_out, transistor_133_out, transistor_134_out,
       transistor_135_out, transistor_137_out, transistor_139_out, transistor_140_out, transistor_141_out,
       transistor_142_out, transistor_143_out, transistor_145_out, transistor_148_out, transistor_149_out,
       transistor_150_out, transistor_151_out, transistor_152_out, transistor_154_out, transistor_156_out,
       transistor_157_out, transistor_158_out, transistor_159_out, transistor_161_out, transistor_164_out,
       transistor_165_out, transistor_167_out, transistor_168_out, transistor_171_out, transistor_172_out,
       transistor_173_out, transistor_177_out, transistor_178_out, transistor_179_out, transistor_181_out;

  Transistor #(.gate("br")) transistor_1 (.in(1'b1), .out(transistor_1_out), .gate(Input_A[0]));
  Transistor transistor_2 (.in(transistor_1_out), .out(transistor_2_out), .gate(Input_B[0]));
  Pull_Resistor pull_resistor_1 (.node(transistor_1_out));
  Transistor #(.\type ("n")) transistor_3 (.in(transistor_2_out), .out(transistor_3_out), .gate(Input_B[0]));
  Transistor #(.\type ("n"), .gate("br")) transistor_4 (
    .in(transistor_2_out), .out(transistor_3_out), .gate(Input_A[0]));
  Transistor transistor_5 (.in(1'b1), .out(transistor_5_out), .gate(Input_A[0]));
  Transistor #(.gate("br")) transistor_6 (.in(1'b1), .out(transistor_5_out), .gate(Input_B[0]));
  Pull_Resistor pull_resistor_2 (.node(pull_resistor_2_node));
  Transistor #(.\type ("n")) transistor_7 (.in(transistor_5_out), .out(pull_resistor_2_node), .gate(Input_A[0]));
  Transistor #(.\type ("n"), .gate("br")) transistor_8 (
    .in(pull_resistor_2_node), .out(transistor_8_out), .gate(Input_B[0]));
  Transistor #(.gate("br")) transistor_9 (.in(1'b1), .out(transistor_9_out), .gate(Input_A[1]));
  Transistor transistor_10 (.in(transistor_9_out), .out(transistor_10_out), .gate(Input_B[1]));
  Pull_Resistor pull_resistor_3 (.node(transistor_9_out));
  Transistor #(.\type ("n"), .gate("br")) transistor_11 (
    .in(transistor_10_out), .out(transistor_11_out), .gate(Input_A[1]));
  Transistor #(.\type ("n")) transistor_12 (.in(transistor_10_out), .out(transistor_11_out), .gate(Input_B[1]));
  Transistor #(.gate("br")) transistor_13 (.in(1'b1), .out(transistor_13_out), .gate(Input_B[1]));
  Transistor transistor_14 (.in(1'b1), .out(transistor_13_out), .gate(Input_A[1]));
  Pull_Resistor pull_resistor_4 (.node(pull_resistor_4_node));
  Pull_Resistor pull_resistor_5 (.node(transistor_13_out));
  Transistor #(.\type ("n")) transistor_15 (.in(transistor_13_out), .out(pull_resistor_4_node), .gate(Input_A[1]));
  Transistor #(.\type ("n"), .gate("br")) transistor_16 (
    .in(pull_resistor_4_node), .out(transistor_16_out), .gate(Input_B[1]));
  Transistor transistor_17 (.in(1'b1), .out(transistor_17_out), .gate(transistor_2_out));
  Pull_Resistor pull_resistor_6 (.node(transistor_2_out));
  Pull_Resistor pull_resistor_7 (.node(transistor_17_out));
  Transistor #(.\type ("n")) transistor_18 (.in(transistor_17_out), .out(transistor_3_out), .gate(transistor_2_out));
  Transistor transistor_19 (.in(1'b1), .out(transistor_19_out), .gate(transistor_5_out));
  Pull_Resistor pull_resistor_8 (.node(transistor_19_out));
  Pull_Resistor pull_resistor_9 (.node(transistor_5_out));
  Transistor #(.\type ("n")) transistor_20 (.in(transistor_19_out), .out(transistor_8_out), .gate(transistor_5_out));
  Transistor transistor_21 (.in(1'b1), .out(transistor_21_out), .gate(transistor_10_out));
  Pull_Resistor pull_resistor_10 (.node(transistor_10_out));
  Pull_Resistor pull_resistor_11 (.node(transistor_21_out));
  Transistor #(.\type ("n")) transistor_22 (.in(transistor_21_out), .out(transistor_11_out), .gate(transistor_10_out));
  Transistor transistor_23 (.in(1'b1), .out(transistor_23_out), .gate(transistor_13_out));
  Pull_Resistor pull_resistor_12 (.node(transistor_23_out));
  Transistor #(.\type ("n")) transistor_24 (.in(transistor_23_out), .out(transistor_16_out), .gate(transistor_13_out));
  Transistor #(.gate("br")) transistor_25 (.in(1'b1), .out(transistor_25_out), .gate(transistor_29_out));
  Transistor transistor_26 (.in(1'b1), .out(transistor_25_out), .gate(transistor_17_out));
  Pull_Resistor pull_resistor_13 (.node(pull_resistor_13_node));
  Transistor #(.\type ("n")) transistor_27 (
    .in(transistor_25_out), .out(pull_resistor_13_node), .gate(transistor_17_out));
  Transistor #(.\type ("n"), .gate("br")) transistor_28 (
    .in(pull_resistor_13_node), .out(transistor_28_out), .gate(transistor_29_out));
  Transistor transistor_29 (.in(1'b1), .out(transistor_29_out), .gate(transistor_19_out));
  Pull_Resistor pull_resistor_14 (.node(transistor_29_out));
  Transistor #(.\type ("n")) transistor_30 (.in(transistor_29_out), .out(transistor_30_out), .gate(transistor_19_out));
  Transistor #(.gate("br")) transistor_31 (.in(1'b1), .out(transistor_31_out), .gate(transistor_35_out));
  Transistor transistor_32 (.in(1'b1), .out(transistor_31_out), .gate(transistor_21_out));
  Pull_Resistor pull_resistor_15 (.node(pull_resistor_15_node));
  Transistor #(.\type ("n")) transistor_33 (
    .in(transistor_31_out), .out(pull_resistor_15_node), .gate(transistor_21_out));
  Transistor #(.\type ("n"), .gate("br")) transistor_34 (
    .in(pull_resistor_15_node), .out(transistor_34_out), .gate(transistor_35_out));
  Transistor transistor_35 (.in(1'b1), .out(transistor_35_out), .gate(transistor_23_out));
  Pull_Resistor pull_resistor_16 (.node(transistor_35_out));
  Transistor #(.\type ("n")) transistor_36 (.in(transistor_35_out), .out(transistor_36_out), .gate(transistor_23_out));
  Transistor transistor_37 (.in(1'b1), .out(transistor_37_out), .gate(transistor_25_out));
  Pull_Resistor pull_resistor_17 (.node(transistor_25_out));
  Transistor #(.\type ("n")) transistor_38 (.in(transistor_37_out), .out(transistor_28_out), .gate(transistor_25_out));
  Transistor transistor_39 (.in(1'b1), .out(transistor_39_out), .gate(transistor_31_out));
  Pull_Resistor pull_resistor_18 (.node(transistor_31_out));
  Transistor #(.\type ("n")) transistor_40 (.in(transistor_39_out), .out(transistor_34_out), .gate(transistor_31_out));
  Transistor #(.gate("br")) transistor_41 (.in(1'b1), .out(transistor_41_out), .gate(Carry_In));
  Pull_Resistor pull_resistor_19 (.node(transistor_37_out));
  Transistor transistor_42 (.in(transistor_41_out), .out(transistor_42_out), .gate(transistor_37_out));
  Transistor #(.\type ("n")) transistor_43 (.in(transistor_42_out), .out(transistor_43_out), .gate(transistor_37_out));
  Transistor transistor_44 (.in(1'b1), .out(transistor_44_out), .gate(Carry_In));
  Transistor #(.\type ("n")) transistor_45 (.in(transistor_44_out), .out(transistor_45_out), .gate(Carry_In));
  Transistor #(.\type ("n"), .gate("br")) transistor_46 (
    .in(transistor_45_out), .out(transistor_46_out), .gate(transistor_37_out));
  Transistor #(.gate("br")) transistor_47 (.in(1'b1), .out(transistor_47_out), .gate(transistor_89_out));
  Pull_Resistor pull_resistor_20 (.node(transistor_39_out));
  Transistor transistor_48 (.in(transistor_47_out), .out(transistor_48_out), .gate(transistor_39_out));
  Transistor #(.\type ("n")) transistor_49 (.in(transistor_48_out), .out(transistor_49_out), .gate(transistor_39_out));
  Transistor transistor_50 (.in(1'b1), .out(transistor_50_out), .gate(transistor_89_out));
  Transistor #(.\type ("n")) transistor_51 (.in(transistor_50_out), .out(transistor_51_out), .gate(transistor_89_out));
  Transistor #(.\type ("n"), .gate("br")) transistor_52 (
    .in(transistor_51_out), .out(transistor_52_out), .gate(transistor_39_out));
  Pull_Resistor pull_resistor_21 (.node(transistor_41_out));
  Pull_Resistor pull_resistor_22 (.node(transistor_42_out));
  Transistor #(.\type ("n"), .gate("br")) transistor_53 (
    .in(transistor_42_out), .out(transistor_43_out), .gate(Carry_In));
  Transistor #(.gate("br")) transistor_54 (.in(1'b1), .out(transistor_44_out), .gate(transistor_37_out));
  Pull_Resistor pull_resistor_23 (.node(transistor_44_out));
  Pull_Resistor pull_resistor_24 (.node(transistor_45_out));
  Pull_Resistor pull_resistor_25 (.node(transistor_47_out));
  Pull_Resistor pull_resistor_26 (.node(transistor_48_out));
  Transistor #(.\type ("n"), .gate("br")) transistor_55 (
    .in(transistor_48_out), .out(transistor_49_out), .gate(transistor_89_out));
  Transistor #(.gate("br")) transistor_56 (.in(1'b1), .out(transistor_50_out), .gate(transistor_39_out));
  Pull_Resistor pull_resistor_27 (.node(transistor_51_out));
  Pull_Resistor pull_resistor_28 (.node(transistor_50_out));
  Transistor transistor_57 (.in(1'b1), .out(transistor_57_out), .gate(transistor_42_out));
  Pull_Resistor pull_resistor_29 (.node(transistor_57_out));
  Transistor #(.\type ("n")) transistor_58 (.in(transistor_57_out), .out(transistor_43_out), .gate(transistor_42_out));
  Transistor transistor_59 (.in(1'b1), .out(transistor_59_out), .gate(transistor_44_out));
  Pull_Resistor pull_resistor_30 (.node(transistor_59_out));
  Transistor #(.\type ("n")) transistor_60 (.in(transistor_59_out), .out(transistor_46_out), .gate(transistor_44_out));
  Transistor transistor_61 (.in(1'b1), .out(transistor_61_out), .gate(transistor_48_out));
  Pull_Resistor pull_resistor_31 (.node(transistor_61_out));
  Transistor #(.\type ("n")) transistor_62 (.in(transistor_61_out), .out(transistor_49_out), .gate(transistor_48_out));
  Transistor transistor_63 (.in(1'b1), .out(transistor_63_out), .gate(transistor_50_out));
  Pull_Resistor pull_resistor_32 (.node(transistor_63_out));
  Transistor #(.\type ("n")) transistor_64 (.in(transistor_63_out), .out(transistor_52_out), .gate(transistor_50_out));
  Transistor transistor_65 (.in(1'b1), .out(transistor_65_out), .gate(transistor_57_out));
  Transistor #(.gate("br")) transistor_66 (.in(1'b1), .out(transistor_65_out), .gate(transistor_69_out));
  Pull_Resistor pull_resistor_33 (.node(pull_resistor_33_node));
  Transistor #(.\type ("n")) transistor_67 (
    .in(transistor_65_out), .out(pull_resistor_33_node), .gate(transistor_57_out));
  Transistor #(.\type ("n"), .gate("br")) transistor_68 (
    .in(pull_resistor_33_node), .out(transistor_68_out), .gate(transistor_69_out));
  Transistor transistor_69 (.in(1'b1), .out(transistor_69_out), .gate(transistor_59_out));
  Pull_Resistor pull_resistor_34 (.node(transistor_69_out));
  Transistor #(.\type ("n")) transistor_70 (.in(transistor_69_out), .out(transistor_70_out), .gate(transistor_59_out));
  Transistor #(.gate("br")) transistor_71 (.in(1'b1), .out(transistor_71_out), .gate(transistor_75_out));
  Transistor transistor_72 (.in(1'b1), .out(transistor_71_out), .gate(transistor_61_out));
  Pull_Resistor pull_resistor_35 (.node(transistor_71_out));
  Pull_Resistor pull_resistor_36 (.node(pull_resistor_36_node));
  Transistor #(.\type ("n")) transistor_73 (
    .in(transistor_71_out), .out(pull_resistor_36_node), .gate(transistor_61_out));
  Transistor #(.\type ("n"), .gate("br")) transistor_74 (
    .in(pull_resistor_36_node), .out(transistor_74_out), .gate(transistor_75_out));
  Transistor transistor_75 (.in(1'b1), .out(transistor_75_out), .gate(transistor_63_out));
  Pull_Resistor pull_resistor_37 (.node(transistor_75_out));
  Transistor #(.\type ("n")) transistor_76 (.in(transistor_75_out), .out(transistor_76_out), .gate(transistor_63_out));
  Transistor transistor_77 (.in(1'b1), .out(Output[0]), .gate(transistor_65_out));
  Pull_Resistor pull_resistor_38 (.node(Output[0]));
  Pull_Resistor pull_resistor_39 (.node(transistor_65_out));
  Transistor #(.\type ("n")) transistor_78 (.in(Output[0]), .out(transistor_68_out), .gate(transistor_65_out));
  Transistor #(.gate("br")) transistor_79 (.in(1'b1), .out(transistor_79_out), .gate(transistor_19_out));
  Transistor transistor_80 (.in(transistor_79_out), .out(transistor_80_out), .gate(transistor_59_out));
  Transistor #(.\type ("n"), .gate("br")) transistor_81 (
    .in(transistor_80_out), .out(transistor_81_out), .gate(transistor_19_out));
  Transistor #(.\type ("n")) transistor_82 (.in(transistor_80_out), .out(transistor_81_out), .gate(transistor_59_out));
  Transistor transistor_83 (.in(1'b1), .out(Output[1]), .gate(transistor_71_out));
  Pull_Resistor pull_resistor_40 (.node(Output[1]));
  Transistor #(.\type ("n")) transistor_84 (.in(Output[1]), .out(transistor_74_out), .gate(transistor_71_out));
  Transistor #(.gate("br")) transistor_85 (.in(1'b1), .out(transistor_85_out), .gate(transistor_23_out));
  Transistor transistor_86 (.in(transistor_85_out), .out(transistor_86_out), .gate(transistor_63_out));
  Transistor #(.\type ("n"), .gate("br")) transistor_87 (
    .in(transistor_86_out), .out(transistor_87_out), .gate(transistor_23_out));
  Transistor #(.\type ("n")) transistor_88 (.in(transistor_86_out), .out(transistor_87_out), .gate(transistor_63_out));
  Transistor transistor_89 (.in(1'b1), .out(transistor_89_out), .gate(transistor_80_out));
  Pull_Resistor pull_resistor_41 (.node(transistor_79_out));
  Pull_Resistor pull_resistor_42 (.node(transistor_80_out));
  Transistor #(.\type ("n")) transistor_90 (.in(transistor_89_out), .out(transistor_81_out), .gate(transistor_80_out));
  Transistor transistor_91 (.in(1'b1), .out(transistor_91_out), .gate(transistor_86_out));
  Pull_Resistor pull_resistor_43 (.node(transistor_85_out));
  Pull_Resistor pull_resistor_44 (.node(transistor_86_out));
  Transistor #(.\type ("n")) transistor_92 (.in(transistor_91_out), .out(transistor_87_out), .gate(transistor_86_out));
  Pull_Resistor pull_resistor_45 (.node(transistor_89_out));
  Pull_Resistor pull_resistor_46 (.node(transistor_91_out));
  Transistor #(.gate("br")) transistor_93 (.in(1'b1), .out(transistor_93_out), .gate(Input_A[2]));
  Transistor transistor_94 (.in(transistor_93_out), .out(transistor_94_out), .gate(Input_B[2]));
  Transistor #(.\type ("n")) transistor_95 (.in(transistor_94_out), .out(transistor_95_out), .gate(Input_B[2]));
  Transistor transistor_96 (.in(1'b1), .out(transistor_96_out), .gate(Input_A[2]));
  Transistor #(.\type ("n")) transistor_97 (.in(transistor_96_out), .out(transistor_97_out), .gate(Input_A[2]));
  Transistor #(.\type ("n"), .gate("br")) transistor_98 (
    .in(transistor_97_out), .out(transistor_98_out), .gate(Input_B[2]));
  Transistor #(.gate("br")) transistor_99 (.in(1'b1), .out(transistor_99_out), .gate(Input_A[3]));
  Transistor transistor_100 (.in(transistor_99_out), .out(transistor_100_out), .gate(Input_B[3]));
  Transistor #(.\type ("n")) transistor_101 (.in(transistor_100_out), .out(transistor_101_out), .gate(Input_B[3]));
  Transistor transistor_102 (.in(1'b1), .out(transistor_102_out), .gate(Input_A[3]));
  Transistor #(.\type ("n")) transistor_103 (.in(transistor_102_out), .out(transistor_103_out), .gate(Input_A[3]));
  Transistor #(.\type ("n"), .gate("br")) transistor_104 (
    .in(transistor_103_out), .out(transistor_104_out), .gate(Input_B[3]));
  Pull_Resistor pull_resistor_47 (.node(transistor_94_out));
  Pull_Resistor pull_resistor_48 (.node(transistor_93_out));
  Transistor #(.\type ("n"), .gate("br")) transistor_105 (
    .in(transistor_94_out), .out(transistor_95_out), .gate(Input_A[2]));
  Transistor #(.gate("br")) transistor_106 (.in(1'b1), .out(transistor_96_out), .gate(Input_B[2]));
  Pull_Resistor pull_resistor_49 (.node(transistor_96_out));
  Pull_Resistor pull_resistor_50 (.node(transistor_97_out));
  Pull_Resistor pull_resistor_51 (.node(transistor_100_out));
  Pull_Resistor pull_resistor_52 (.node(transistor_99_out));
  Transistor #(.\type ("n"), .gate("br")) transistor_107 (
    .in(transistor_100_out), .out(transistor_101_out), .gate(Input_A[3]));
  Transistor #(.gate("br")) transistor_108 (.in(1'b1), .out(transistor_102_out), .gate(Input_B[3]));
  Pull_Resistor pull_resistor_53 (.node(transistor_103_out));
  Pull_Resistor pull_resistor_54 (.node(transistor_102_out));
  Transistor transistor_109 (.in(1'b1), .out(transistor_109_out), .gate(transistor_94_out));
  Pull_Resistor pull_resistor_55 (.node(transistor_109_out));
  Transistor #(.\type ("n")) transistor_110 (
    .in(transistor_109_out), .out(transistor_95_out), .gate(transistor_94_out));
  Transistor transistor_111 (.in(1'b1), .out(transistor_111_out), .gate(transistor_96_out));
  Pull_Resistor pull_resistor_56 (.node(transistor_111_out));
  Transistor #(.\type ("n")) transistor_112 (
    .in(transistor_111_out), .out(transistor_98_out), .gate(transistor_96_out));
  Transistor transistor_113 (.in(1'b1), .out(transistor_113_out), .gate(transistor_100_out));
  Pull_Resistor pull_resistor_57 (.node(transistor_113_out));
  Transistor #(.\type ("n")) transistor_114 (
    .in(transistor_113_out), .out(transistor_101_out), .gate(transistor_100_out));
  Transistor transistor_115 (.in(1'b1), .out(transistor_115_out), .gate(transistor_102_out));
  Pull_Resistor pull_resistor_58 (.node(transistor_115_out));
  Transistor #(.\type ("n")) transistor_116 (
    .in(transistor_115_out), .out(transistor_104_out), .gate(transistor_102_out));
  Transistor #(.gate("br")) transistor_117 (.in(1'b1), .out(transistor_117_out), .gate(transistor_121_out));
  Transistor transistor_118 (.in(1'b1), .out(transistor_117_out), .gate(transistor_109_out));
  Pull_Resistor pull_resistor_59 (.node(pull_resistor_59_node));
  Transistor #(.\type ("n")) transistor_119 (
    .in(transistor_117_out), .out(pull_resistor_59_node), .gate(transistor_109_out));
  Transistor #(.\type ("n"), .gate("br")) transistor_120 (
    .in(pull_resistor_59_node), .out(transistor_120_out), .gate(transistor_121_out));
  Transistor transistor_121 (.in(1'b1), .out(transistor_121_out), .gate(transistor_111_out));
  Pull_Resistor pull_resistor_60 (.node(transistor_121_out));
  Transistor #(.\type ("n")) transistor_122 (
    .in(transistor_121_out), .out(transistor_122_out), .gate(transistor_111_out));
  Transistor #(.gate("br")) transistor_123 (.in(1'b1), .out(transistor_123_out), .gate(transistor_127_out));
  Transistor transistor_124 (.in(1'b1), .out(transistor_123_out), .gate(transistor_113_out));
  Pull_Resistor pull_resistor_61 (.node(pull_resistor_61_node));
  Pull_Resistor pull_resistor_62 (.node(transistor_123_out));
  Transistor #(.\type ("n")) transistor_125 (
    .in(transistor_123_out), .out(pull_resistor_61_node), .gate(transistor_113_out));
  Transistor #(.\type ("n"), .gate("br")) transistor_126 (
    .in(pull_resistor_61_node), .out(transistor_126_out), .gate(transistor_127_out));
  Transistor transistor_127 (.in(1'b1), .out(transistor_127_out), .gate(transistor_115_out));
  Pull_Resistor pull_resistor_63 (.node(transistor_127_out));
  Transistor #(.\type ("n")) transistor_128 (
    .in(transistor_127_out), .out(transistor_128_out), .gate(transistor_115_out));
  Transistor transistor_129 (.in(1'b1), .out(transistor_129_out), .gate(transistor_117_out));
  Pull_Resistor pull_resistor_64 (.node(transistor_117_out));
  Pull_Resistor pull_resistor_65 (.node(transistor_129_out));
  Transistor #(.\type ("n")) transistor_130 (
    .in(transistor_129_out), .out(transistor_120_out), .gate(transistor_117_out));
  Transistor transistor_131 (.in(1'b1), .out(transistor_131_out), .gate(transistor_123_out));
  Pull_Resistor pull_resistor_66 (.node(transistor_131_out));
  Transistor #(.\type ("n")) transistor_132 (
    .in(transistor_131_out), .out(transistor_126_out), .gate(transistor_123_out));
  Transistor #(.gate("br")) transistor_133 (.in(1'b1), .out(transistor_133_out), .gate(transistor_91_out));
  Transistor transistor_134 (.in(transistor_133_out), .out(transistor_134_out), .gate(transistor_129_out));
  Transistor #(.\type ("n"), .gate("br")) transistor_135 (
    .in(transistor_134_out), .out(transistor_135_out), .gate(transistor_91_out));
  Transistor #(.\type ("n")) transistor_136 (
    .in(transistor_134_out), .out(transistor_135_out), .gate(transistor_129_out));
  Transistor #(.gate("br")) transistor_137 (.in(1'b1), .out(transistor_137_out), .gate(transistor_129_out));
  Transistor transistor_138 (.in(1'b1), .out(transistor_137_out), .gate(transistor_91_out));
  Transistor #(.\type ("n")) transistor_139 (
    .in(transistor_137_out), .out(transistor_139_out), .gate(transistor_91_out));
  Transistor #(.\type ("n"), .gate("br")) transistor_140 (
    .in(transistor_139_out), .out(transistor_140_out), .gate(transistor_129_out));
  Transistor #(.gate("br")) transistor_141 (.in(1'b1), .out(transistor_141_out), .gate(transistor_181_out));
  Transistor transistor_142 (.in(transistor_141_out), .out(transistor_142_out), .gate(transistor_131_out));
  Transistor #(.\type ("n")) transistor_143 (
    .in(transistor_142_out), .out(transistor_143_out), .gate(transistor_131_out));
  Transistor #(.\type ("n"), .gate("br")) transistor_144 (
    .in(transistor_142_out), .out(transistor_143_out), .gate(transistor_181_out));
  Transistor #(.gate("br")) transistor_145 (.in(1'b1), .out(transistor_145_out), .gate(transistor_131_out));
  Transistor transistor_146 (.in(1'b1), .out(transistor_145_out), .gate(transistor_181_out));
  Pull_Resistor pull_resistor_67 (.node(pull_resistor_67_node));
  Transistor #(.\type ("n")) transistor_147 (
    .in(transistor_145_out), .out(pull_resistor_67_node), .gate(transistor_181_out));
  Transistor #(.\type ("n"), .gate("br")) transistor_148 (
    .in(pull_resistor_67_node), .out(transistor_148_out), .gate(transistor_131_out));
  Pull_Resistor pull_resistor_68 (.node(transistor_134_out));
  Pull_Resistor pull_resistor_69 (.node(transistor_133_out));
  Pull_Resistor pull_resistor_70 (.node(transistor_137_out));
  Pull_Resistor pull_resistor_71 (.node(transistor_139_out));
  Pull_Resistor pull_resistor_72 (.node(transistor_142_out));
  Pull_Resistor pull_resistor_73 (.node(transistor_141_out));
  Pull_Resistor pull_resistor_74 (.node(transistor_145_out));
  Transistor transistor_149 (.in(1'b1), .out(transistor_149_out), .gate(transistor_151_out));
  Transistor #(.\type ("n")) transistor_150 (
    .in(transistor_149_out), .out(transistor_150_out), .gate(transistor_151_out));
  Transistor transistor_151 (.in(1'b1), .out(transistor_151_out), .gate(transistor_134_out));
  Pull_Resistor pull_resistor_75 (.node(transistor_151_out));
  Transistor #(.\type ("n"), .gate("br")) transistor_152 (
    .in(transistor_150_out), .out(transistor_152_out), .gate(transistor_164_out));
  Transistor #(.\type ("n")) transistor_153 (
    .in(transistor_151_out), .out(transistor_135_out), .gate(transistor_134_out));
  Transistor transistor_154 (.in(1'b1), .out(transistor_154_out), .gate(transistor_137_out));
  Pull_Resistor pull_resistor_76 (.node(transistor_154_out));
  Transistor #(.\type ("n")) transistor_155 (
    .in(transistor_154_out), .out(transistor_140_out), .gate(transistor_137_out));
  Transistor transistor_156 (.in(1'b1), .out(transistor_156_out), .gate(transistor_158_out));
  Transistor #(.\type ("n")) transistor_157 (
    .in(transistor_156_out), .out(transistor_157_out), .gate(transistor_158_out));
  Transistor transistor_158 (.in(1'b1), .out(transistor_158_out), .gate(transistor_142_out));
  Pull_Resistor pull_resistor_77 (.node(transistor_158_out));
  Transistor #(.\type ("n"), .gate("br")) transistor_159 (
    .in(transistor_157_out), .out(transistor_159_out), .gate(transistor_167_out));
  Transistor #(.\type ("n")) transistor_160 (
    .in(transistor_158_out), .out(transistor_143_out), .gate(transistor_142_out));
  Transistor transistor_161 (.in(1'b1), .out(transistor_161_out), .gate(transistor_145_out));
  Pull_Resistor pull_resistor_78 (.node(transistor_161_out));
  Transistor #(.\type ("n")) transistor_162 (
    .in(transistor_161_out), .out(transistor_148_out), .gate(transistor_145_out));
  Transistor #(.gate("br")) transistor_163 (.in(1'b1), .out(transistor_149_out), .gate(transistor_164_out));
  Pull_Resistor pull_resistor_79 (.node(transistor_149_out));
  Pull_Resistor pull_resistor_80 (.node(transistor_150_out));
  Transistor transistor_164 (.in(1'b1), .out(transistor_164_out), .gate(transistor_154_out));
  Pull_Resistor pull_resistor_81 (.node(transistor_164_out));
  Transistor #(.\type ("n")) transistor_165 (
    .in(transistor_164_out), .out(transistor_165_out), .gate(transistor_154_out));
  Transistor #(.gate("br")) transistor_166 (.in(1'b1), .out(transistor_156_out), .gate(transistor_167_out));
  Pull_Resistor pull_resistor_82 (.node(transistor_157_out));
  Pull_Resistor pull_resistor_83 (.node(transistor_156_out));
  Transistor transistor_167 (.in(1'b1), .out(transistor_167_out), .gate(transistor_161_out));
  Pull_Resistor pull_resistor_84 (.node(transistor_167_out));
  Transistor #(.\type ("n")) transistor_168 (
    .in(transistor_167_out), .out(transistor_168_out), .gate(transistor_161_out));
  Transistor transistor_169 (.in(1'b1), .out(Output[2]), .gate(transistor_149_out));
  Pull_Resistor pull_resistor_85 (.node(Output[2]));
  Transistor #(.\type ("n")) transistor_170 (.in(Output[2]), .out(transistor_152_out), .gate(transistor_149_out));
  Transistor #(.gate("br")) transistor_171 (.in(1'b1), .out(transistor_171_out), .gate(transistor_111_out));
  Transistor transistor_172 (.in(transistor_171_out), .out(transistor_172_out), .gate(transistor_154_out));
  Pull_Resistor pull_resistor_86 (.node(transistor_171_out));
  Transistor #(.\type ("n"), .gate("br")) transistor_173 (
    .in(transistor_172_out), .out(transistor_173_out), .gate(transistor_111_out));
  Transistor #(.\type ("n")) transistor_174 (
    .in(transistor_172_out), .out(transistor_173_out), .gate(transistor_154_out));
  Transistor transistor_175 (.in(1'b1), .out(Output[3]), .gate(transistor_156_out));
  Pull_Resistor pull_resistor_87 (.node(Output[3]));
  Transistor #(.\type ("n")) transistor_176 (.in(Output[3]), .out(transistor_159_out), .gate(transistor_156_out));
  Transistor #(.gate("br")) transistor_177 (.in(1'b1), .out(transistor_177_out), .gate(transistor_115_out));
  Transistor transistor_178 (.in(transistor_177_out), .out(transistor_178_out), .gate(transistor_161_out));
  Pull_Resistor pull_resistor_88 (.node(transistor_177_out));
  Transistor #(.\type ("n")) transistor_179 (
    .in(transistor_178_out), .out(transistor_179_out), .gate(transistor_161_out));
  Transistor #(.\type ("n"), .gate("br")) transistor_180 (
    .in(transistor_178_out), .out(transistor_179_out), .gate(transistor_115_out));
  Transistor transistor_181 (.in(1'b1), .out(transistor_181_out), .gate(transistor_172_out));
  Pull_Resistor pull_resistor_89 (.node(transistor_181_out));
  Pull_Resistor pull_resistor_90 (.node(transistor_172_out));
  Transistor #(.\type ("n")) transistor_182 (
    .in(transistor_181_out), .out(transistor_173_out), .gate(transistor_172_out));
  Transistor transistor_183 (.in(1'b1), .out(Carry_Out), .gate(transistor_178_out));
  Pull_Resistor pull_resistor_91 (.node(Carry_Out));
  Pull_Resistor pull_resistor_92 (.node(transistor_178_out));
  Transistor #(.\type ("n")) transistor_184 (.in(Carry_Out), .out(transistor_179_out), .gate(transistor_178_out));
  // also tied to GND on the sheet: {transistor_11_out, transistor_3_out, transistor_8_out, transistor_16_out, transistor_34_out, transistor_28_out, transistor_36_out, transistor_30_out, transistor_49_out, transistor_43_out, transistor_46_out, transistor_52_out, transistor_74_out, transistor_68_out, transistor_76_out, transistor_70_out, transistor_87_out, transistor_81_out, transistor_101_out, transistor_95_out, transistor_104_out, transistor_98_out, transistor_120_out, transistor_128_out, transistor_122_out, transistor_126_out, transistor_143_out, transistor_148_out, transistor_135_out, transistor_140_out, transistor_152_out, transistor_168_out, transistor_165_out, transistor_179_out, transistor_173_out, transistor_159_out}
endmodule

module ADD204 (
  input  Carry_In,
  input  [3:0] Input_A,
  input  [3:0] Input_B,
  output [3:0] Output,
  output Carry_Out
);

  wire and_1_out, and_2_out, and_3_out, and_4_out, and_5_out, and_6_out, and_9_out, and_10_out, and_11_out,
       and_12_out, and_13_out, and_14_out, not_1_out, not_2_out, not_3_out, not_4_out, not_5_out, not_6_out,
       not_7_out, not_8_out, or_1_out, or_2_out, or_3_out, or_4_out, or_5_out, or_6_out, or_7_out, or_8_out,
       or_9_out, or_10_out, or_11_out;

  or or_1 (or_1_out, Input_A[0], Input_B[0]);
  not not_1 (not_1_out, and_1_out);
  and and_1 (and_1_out, Input_A[0], Input_B[0]);
  or or_2 (or_2_out, Input_A[1], Input_B[1]);
  and and_2 (and_2_out, Input_A[1], Input_B[1]);
  not not_2 (not_2_out, and_2_out);
  and and_3 (and_3_out, or_1_out, not_1_out);
  and and_4 (and_4_out, or_2_out, not_2_out);
  or or_3 (or_3_out, Carry_In, and_3_out);
  and and_5 (and_5_out, Carry_In, and_3_out);
  not not_3 (not_3_out, and_5_out);
  or or_4 (or_4_out, and_5_out, and_1_out);
  or or_5 (or_5_out, or_4_out, and_4_out);
  not not_4 (not_4_out, and_6_out);
  and and_6 (and_6_out, or_4_out, and_4_out);
  or or_6 (or_6_out, and_6_out, and_2_out);
  and and_7 (Output[0], or_3_out, not_3_out);
  and and_8 (Output[1], or_5_out, not_4_out);
  or or_7 (or_7_out, Input_A[2], Input_B[2]);
  and and_9 (and_9_out, Input_A[2], Input_B[2]);
  or or_8 (or_8_out, Input_A[3], Input_B[3]);
  and and_10 (and_10_out, Input_A[3], Input_B[3]);
  and and_11 (and_11_out, or_7_out, not_5_out);
  not not_5 (not_5_out, and_9_out);
  and and_12 (and_12_out, or_8_out, not_6_out);
  not not_6 (not_6_out, and_10_out);
  or or_9 (or_9_out, or_6_out, and_11_out);
  and and_13 (and_13_out, or_6_out, and_11_out);
  or or_10 (or_10_out, or_11_out, and_12_out);
  and and_14 (and_14_out, or_11_out, and_12_out);
  and and_15 (Output[2], or_9_out, not_7_out);
  not not_7 (not_7_out, and_13_out);
  or or_11 (or_11_out, and_13_out, and_9_out);
  and and_16 (Output[3], or_10_out, not_8_out);
  not not_8 (not_8_out, and_14_out);
  or or_12 (Carry_Out, and_14_out, and_10_out);
endmodule
