// Logisim project 05_ARITHMETIC_01_V.circ as structural Verilog: 13 circuits, main circuit main
module main (
  input  [3:0] in_1,
  input  [3:0] in_2,
  input  [3:0] in_3,
  input  [1:0] Upper,
  input  [1:0] Dividend,
  input  [1:0] Divisor,
  output out_7,
  output out_8,
  output out_9,
  output [1:0] remainder,
  output [1:0] remainder_2,
  output [1:0] Output,
  output [1:0] Output_2
);

  wire [3:0] div4_1_1_output, div4_1_1_remainder, div4_2_1_output, div4_2_1_remainder, divider_1_out,
       divider_1_rem, divider_3_out, divider_3_rem, mult4_1_carry_out, mult4_1_output, multiplier_1_cout,
       multiplier_1_out, multisp_1_out_4, multisp_1_out_5;

  // Probe on in_2
  // Probe on in_2
  // Probe on in_2
  // Probe on in_3
  // Probe on in_3
  // Probe on in_3
  Multiplier #(.width(4)) multiplier_1 (
    .a(in_2), .b(in_3), .out(multiplier_1_out), .cin(in_1), .cout(multiplier_1_cout));
  // Probe on multiplier_1_out
  // Probe on multiplier_1_out
  // Probe on multiplier_1_out
  // Probe on multiplier_1_cout
  // Probe on multiplier_1_cout
  // Probe on multiplier_1_out
  // Probe on multiplier_1_cout
  // Probe on multiplier_1_cout
  Divider #(.width(4)) divider_1 (.a(in_2), .b(in_3), .out(divider_1_out), .upper(in_1), .rem(divider_1_rem));
  // Probe on divider_1_out
  // Probe on divider_1_rem
  // Probe on divider_1_out
  // Probe on divider_1_rem
  // Probe on divider_1_out
  // Probe on divider_1_rem
  // Probe on divider_1_out
  // Probe on divider_1_rem
  Divider #(.width(2)) divider_2 (.a(Dividend), .b(Divisor), .out(remainder), .upper(Upper), .rem(Output));
  MULTISP multisp_1 (.in_1(in_2), .in_2(in_3), .out_4(multisp_1_out_4), .out_5(multisp_1_out_5), .in_3(in_1));
  // Probe on multisp_1_out_5
  // Probe on multisp_1_out_5
  // Probe on multisp_1_out_5
  // Probe on multisp_1_out_5
  DIV4_1 div4_1_1 (
    .Dividend(in_2), .remainder(div4_1_1_remainder), .Divisor(in_3), .Output(div4_1_1_output), .Error(out_7));
  // Probe on div4_1_1_output
  // Probe on div4_1_1_remainder
  // Probe on div4_1_1_output
  // Probe on div4_1_1_remainder
  // Probe on div4_1_1_remainder
  // Probe on div4_1_1_output
  // Probe on div4_1_1_remainder
  // Probe on div4_1_1_output
  DIV2L div2l_1 (.Upper(Upper), .Dividend(Dividend), .Divisor(Divisor), .remainder(remainder_2), .Output(Output_2));
  // Probe on multisp_1_out_4
  // Probe on multisp_1_out_4
  // Probe on multisp_1_out_4
  // Probe on multisp_1_out_4
  MULT4 mult4_1 (
    .Input_A(in_2), .Input_B(in_3), .Carry_In(in_1), .Output(mult4_1_output), .Carry_Out(mult4_1_carry_out));
  // Probe on mult4_1_carry_out
  // Probe on mult4_1_carry_out
  // Probe on mult4_1_carry_out
  // Probe on mult4_1_carry_out
  DIV4_2 div4_2_1 (
    .Dividend(in_2), .Divisor(in_3), .remainder(div4_2_1_remainder), .Output(div4_2_1_output), .Error(out_8));
  // Probe on div4_2_1_remainder
  // Probe on div4_2_1_output
  // Probe on div4_2_1_output
  // Probe on div4_2_1_remainder
  // Probe on div4_2_1_output
  // Probe on div4_2_1_remainder
  // Probe on div4_2_1_remainder
  // Probe on div4_2_1_output
  // Probe on mult4_1_output
  // Probe on mult4_1_output
  // Probe on mult4_1_output
  // Probe on mult4_1_output
  Divider #(.width(4)) divider_3 (.a(in_2), .b(in_3), .out(divider_3_out), .upper(in_1), .rem(divider_3_rem));
  // Probe on divider_3_rem
  // Probe on divider_3_out
  // Probe on divider_3_out
  // Probe on divider_3_rem
  // Probe on divider_3_out
  // Probe on divider_3_rem
  // Probe on divider_3_rem
  // Probe on divider_3_out
  nor nor_1 (out_9, in_3[0], in_3[1], in_3[3], in_3[2]);
endmodule

module MULTISP (
  input  [3:0] in_1,
  input  [3:0] in_2,
  input  [3:0] in_3,
  output [3:0] out_4,
  output [3:0] out_5
);

  wire adder_1_cout, adder_2_cout, adder_3_cout, adder_4_cout, adder_5_cout, adder_6_cout, adder_7_cout,
       adder_8_cout, adder_9_cout, adder_10_cout, adder_11_cout, adder_12_cout, adder_13_cout;
  wire [7:0] adder_1_out, adder_2_out, adder_3_out, adder_4_out, adder_5_out, adder_6_out, adder_7_out,
       adder_8_out, adder_9_out, adder_10_out, adder_11_out, adder_12_out, adder_13_out, adder_14_out,
       bit_extender_1_out, bit_extender_2_out, multiplexer_1_out;

  assign bit_extender_1_out = {{4{1'b0}}, in_1};  // Bit_Extender bit_extender_1
  Adder adder_1 (.a(bit_extender_1_out), .b(bit_extender_1_out), .out(adder_1_out), .cin(1'b0), .cout(adder_1_cout));
  Adder adder_2 (.a(adder_1_out), .b(bit_extender_1_out), .out(adder_2_out), .cin(adder_1_cout), .cout(adder_2_cout));
  Adder adder_3 (.a(adder_2_out), .b(bit_extender_1_out), .out(adder_3_out), .cin(adder_2_cout), .cout(adder_3_cout));
  assign bit_extender_2_out = {{4{1'b0}}, in_3};  // Bit_Extender bit_extender_2
  Adder adder_4 (.a(adder_3_out), .b(bit_extender_1_out), .out(adder_4_out), .cin(adder_3_cout), .cout(adder_4_cout));
  Adder adder_5 (.a(adder_4_out), .b(bit_extender_1_out), .out(adder_5_out), .cin(adder_4_cout), .cout(adder_5_cout));
  Adder adder_6 (.a(adder_5_out), .b(bit_extender_1_out), .out(adder_6_out), .cin(adder_5_cout), .cout(adder_6_cout));
  Adder adder_7 (.a(adder_6_out), .b(bit_extender_1_out), .out(adder_7_out), .cin(adder_6_cout), .cout(adder_7_cout));
  Adder adder_8 (.a(adder_7_out), .b(bit_extender_1_out), .out(adder_8_out), .cin(adder_7_cout), .cout(adder_8_cout));
  Adder adder_9 (.a(adder_8_out), .b(bit_extender_1_out), .out(adder_9_out), .cin(adder_8_cout), .cout(adder_9_cout));
  Adder adder_10 (
    .a(adder_9_out), .b(bit_extender_1_out), .out(adder_10_out), .cin(adder_9_cout), .cout(adder_10_cout));
  Adder adder_11 (
    .a(adder_10_out), .b(bit_extender_1_out), .out(adder_11_out), .cin(adder_10_cout), .cout(adder_11_cout));
  Adder adder_12 (
    .a(adder_11_out), .b(bit_extender_1_out), .out(adder_12_out), .cin(adder_11_cout), .cout(adder_12_cout));
  Adder adder_13 (
    .a(adder_12_out), .b(bit_extender_1_out), .out(adder_13_out), .cin(adder_12_cout), .cout(adder_13_cout));
  Adder adder_14 (.a(adder_13_out), .b(bit_extender_1_out), .out(adder_14_out), .cin(adder_13_cout));  // open: cout
  Multiplexer #(.select(4), .width(8), .enable("false")) multiplexer_1 (
    .in0({8{1'b0}}), .in1(bit_extender_1_out), .in2(adder_1_out), .in3(adder_2_out), .in4(adder_3_out),
    .in5(adder_4_out), .in6(adder_5_out), .in7(adder_6_out), .in8(adder_7_out), .in9(adder_8_out),
    .in10(adder_9_out), .in11(adder_10_out), .in12(adder_11_out), .in13(adder_12_out), .in14(adder_13_out),
    .in15(adder_14_out), .out(multiplexer_1_out), .sel(in_2));
  Adder adder_15 (.a(multiplexer_1_out), .b(bit_extender_2_out), .out({out_5, out_4}), .cin(1'b0));  // open: cout
endmodule

module DIV1 (
  input  Upper,
  input  Dividend,
  input  Divisor,
  output Output,
  output Error,
  output remainder
);

  not not_1 (Error, Divisor);

  assign Output = Dividend;
  assign remainder = 1'b0;
endmodule

module DIV2 (
  input  [1:0] Dividend,
  input  [1:0] Divisor,
  output [1:0] remainder,
  output [1:0] Output,
  output Error
);

  wire [1:0] and_2_out, and_3_out, bitfinder_1_index, multiplexer_1_out, subtractor_1_out, subtractor_2_out,
       subtractor_3_out, subtractor_4_out;
  wire [1:1] or_1_out;
  wire [2:0] subtractor_5_out;
  wire [3:0] subtractor_1_bout;

  Subtractor #(.width(2)) subtractor_1 (
    .a(Dividend), .b(Divisor), .out(subtractor_1_out), .bin(1'b0), .bout(subtractor_1_bout[0]));
  or or_1 (or_1_out[1], Divisor[0], Divisor[1]);
  Subtractor #(.width(2)) subtractor_2 (
    .a(subtractor_1_out), .b(Divisor), .out(subtractor_2_out), .bin(1'b0), .bout(subtractor_1_bout[1]));
  Subtractor #(.width(2)) subtractor_3 (
    .a(subtractor_2_out), .b(Divisor), .out(subtractor_3_out), .bin(1'b0), .bout(subtractor_1_bout[2]));
  BitFinder #(.width(4)) bitfinder_1 (.in(subtractor_1_bout), .index(bitfinder_1_index));  // open: found
  not not_1 (Error, or_1_out[1]);
  Subtractor #(.width(2)) subtractor_4 (
    .a(subtractor_3_out), .b(Divisor), .out(subtractor_4_out), .bin(1'b0), .bout(subtractor_1_bout[3]));
  Subtractor #(.width(3)) subtractor_5 (
    .a({1'b0, bitfinder_1_index}), .b(3'b001), .out(subtractor_5_out), .bin(1'b0));  // open: bout
  Multiplexer #(.select(2), .width(2), .enable("false")) multiplexer_1 (
    .in0(subtractor_1_out), .in1(subtractor_2_out), .in2(subtractor_3_out), .in3(subtractor_4_out),
    .out(multiplexer_1_out), .sel(subtractor_5_out[1:0]));
  assign remainder = multiplexer_1_out & {2{or_1_out[1]}};  // AND_Gate and_1, 2 bits wide
  assign and_2_out = {2{or_1_out[1]}} & bitfinder_1_index;  // AND_Gate and_2, 2 bits wide
  assign and_3_out = Dividend & {2{Error}};  // AND_Gate and_3, 2 bits wide
  assign Output = and_2_out | and_3_out;  // OR_Gate or_2, 2 bits wide
endmodule

module DIV4_1 (
  input  [3:0] Dividend,
  input  [3:0] Divisor,
  output [3:0] remainder,
  output [3:0] Output,
  output Error
);

  wire [2:0] bitfinder_1_index;
  wire [3:0] and_2_out, and_3_out, multiplexer_1_out, subtractor_1_out, subtractor_2_out, subtractor_3_out,
       subtractor_4_out, subtractor_5_out, subtractor_6_out, subtractor_7_out, subtractor_8_out,
       subtractor_9_out;
  wire [3:3] or_1_out;
  wire [7:0] subtractor_1_bout;

  Subtractor #(.width(4)) subtractor_1 (
    .a(Dividend), .b(Divisor), .out(subtractor_1_out), .bin(1'b0), .bout(subtractor_1_bout[0]));
  Subtractor #(.width(4)) subtractor_2 (
    .a(subtractor_1_out), .b(Divisor), .out(subtractor_2_out), .bin(1'b0), .bout(subtractor_1_bout[1]));
  Subtractor #(.width(4)) subtractor_3 (
    .a(subtractor_2_out), .b(Divisor), .out(subtractor_3_out), .bin(1'b0), .bout(subtractor_1_bout[2]));
  or or_1 (or_1_out[3], Divisor[0], Divisor[1], Divisor[3], Divisor[2]);
  Subtractor #(.width(4)) subtractor_4 (
    .a(subtractor_3_out), .b(Divisor), .out(subtractor_4_out), .bin(1'b0), .bout(subtractor_1_bout[3]));
  BitFinder bitfinder_1 (.in(subtractor_1_bout), .index(bitfinder_1_index));  // open: found
  not not_1 (Error, or_1_out[3]);
  Subtractor #(.width(4)) subtractor_5 (
    .a(subtractor_4_out), .b(Divisor), .out(subtractor_5_out), .bin(1'b0), .bout(subtractor_1_bout[4]));
  Subtractor #(.width(4)) subtractor_6 (
    .a(subtractor_5_out), .b(Divisor), .out(subtractor_6_out), .bin(1'b0), .bout(subtractor_1_bout[5]));
  Subtractor #(.width(4)) subtractor_7 (
    .a(subtractor_6_out), .b(Divisor), .out(subtractor_7_out), .bin(1'b0), .bout(subtractor_1_bout[6]));
  Subtractor #(.width(4)) subtractor_8 (
    .a({1'b0, bitfinder_1_index}), .b(4'b0001), .out(subtractor_8_out), .bin(1'b0));  // open: bout
  Subtractor #(.width(4)) subtractor_9 (
    .a(subtractor_7_out), .b(Divisor), .out(subtractor_9_out), .bin(1'b0), .bout(subtractor_1_bout[7]));
  Multiplexer #(.select(3), .width(4), .enable("false")) multiplexer_1 (
    .in0(subtractor_1_out), .in1(subtractor_2_out), .in2(subtractor_3_out), .in3(subtractor_4_out),
    .in4(subtractor_5_out), .in5(subtractor_6_out), .in6(subtractor_7_out), .in7(subtractor_9_out),
    .out(multiplexer_1_out), .sel(subtractor_8_out[2:0]));
  assign remainder = multiplexer_1_out & {4{or_1_out[3]}};  // AND_Gate and_1, 4 bits wide
  assign and_2_out = {4{or_1_out[3]}} & {1'b0, bitfinder_1_index};  // AND_Gate and_2, 4 bits wide
  assign Output = and_2_out | and_3_out;  // OR_Gate or_2, 4 bits wide
  assign and_3_out = Dividend & {4{Error}};  // AND_Gate and_3, 4 bits wide
endmodule

module DIV4_2 (
  input  [3:0] Dividend,
  input  [3:0] Divisor,
  output [3:0] remainder,
  output [3:0] Output,
  output Error
);

  wire [2:0] bitfinder_1_index;
  wire [3:0] and_2_out, and_3_out, multiplexer_1_out, sub4d_1_output, sub4d_2_output, sub4d_3_output,
       sub4d_4_output, sub4d_5_output, sub4d_6_output, sub4d_7_output, sub4d_8_output, subtractor_1_out;
  wire [3:3] or_1_out;
  wire [7:0] sub4d_1_borrow_out;

  SUB4D sub4d_1 (
    .Borrow_In(1'b0), .Minuend(Dividend), .Subtrahend(Divisor), .Output(sub4d_1_output),
    .Borrow_Out(sub4d_1_borrow_out[0]));
  SUB4D sub4d_2 (
    .Borrow_In(1'b0), .Minuend(sub4d_1_output), .Subtrahend(Divisor), .Output(sub4d_2_output),
    .Borrow_Out(sub4d_1_borrow_out[1]));
  SUB4D sub4d_3 (
    .Borrow_In(1'b0), .Minuend(sub4d_2_output), .Subtrahend(Divisor), .Output(sub4d_3_output),
    .Borrow_Out(sub4d_1_borrow_out[2]));
  or or_1 (or_1_out[3], Divisor[0], Divisor[1], Divisor[3], Divisor[2]);
  SUB4D sub4d_4 (
    .Borrow_In(1'b0), .Minuend(sub4d_3_output), .Subtrahend(Divisor), .Output(sub4d_4_output),
    .Borrow_Out(sub4d_1_borrow_out[3]));
  BitFinder bitfinder_1 (.in(sub4d_1_borrow_out), .index(bitfinder_1_index));  // open: found
  not not_1 (Error, or_1_out[3]);
  SUB4D sub4d_5 (
    .Borrow_In(1'b0), .Minuend(sub4d_4_output), .Subtrahend(Divisor), .Output(sub4d_5_output),
    .Borrow_Out(sub4d_1_borrow_out[4]));
  SUB4D sub4d_6 (
    .Borrow_In(1'b0), .Minuend(sub4d_5_output), .Subtrahend(Divisor), .Output(sub4d_6_output),
    .Borrow_Out(sub4d_1_borrow_out[5]));
  SUB4D sub4d_7 (
    .Borrow_In(1'b0), .Minuend(sub4d_6_output), .Subtrahend(Divisor), .Output(sub4d_7_output),
    .Borrow_Out(sub4d_1_borrow_out[6]));
  Subtractor #(.width(4)) subtractor_1 (
    .a({1'b0, bitfinder_1_index}), .b(4'b0001), .out(subtractor_1_out), .bin(1'b0));  // open: bout
  SUB4D sub4d_8 (
    .Borrow_In(1'b0), .Minuend(sub4d_7_output), .Subtrahend(Divisor), .Output(sub4d_8_output),
    .Borrow_Out(sub4d_1_borrow_out[7]));
  Multiplexer #(.select(3), .width(4), .enable("false")) multiplexer_1 (
    .in0(sub4d_1_output), .in1(sub4d_2_output), .in2(sub4d_3_output), .in3(sub4d_4_output),
    .in4(sub4d_5_output), .in5(sub4d_6_output), .in6(sub4d_7_output), .in7(sub4d_8_output),
    .out(multiplexer_1_out), .sel(subtractor_1_out[2:0]));
  assign remainder = multiplexer_1_out & {4{or_1_out[3]}};  // AND_Gate and_1, 4 bits wide
  assign and_2_out = {4{or_1_out[3]}} & {1'b0, bitfinder_1_index};  // AND_Gate and_2, 4 bits wide
  assign Output = and_2_out | and_3_out;  // OR_Gate or_2, 4 bits wide
  assign and_3_out = Dividend & {4{Error}};  // AND_Gate and_3, 4 bits wide
endmodule

module DIV2L (
  input  [1:0] Upper,
  input  [1:0] Dividend,
  input  [1:0] Divisor,
  output [1:0] remainder,
  output [1:0] Output
);

  wire [3:2] div4_1_1_output, div4_1_1_remainder;

  DIV4_1 div4_1_1 (
    .Dividend({Upper, Dividend}), .remainder({div4_1_1_remainder, Output}), .Divisor({2'b00, Divisor}),
    .Output({div4_1_1_output, remainder}));  // open: Error
  // Probe on div4_1_1_output
  // Probe on div4_1_1_remainder
endmodule

module SUB4D (
  input  Borrow_In,
  input  [3:0] Minuend,
  input  [3:0] Subtrahend,
  output [3:0] Output,
  output Borrow_Out
);

  wire [3:0] adder_1_out;
  wire [4:0] negator_1_out;

  Adder #(.width(4)) adder_1 (.a({3'b000, Borrow_In}), .b(Subtrahend), .out(adder_1_out), .cin(1'b0));  // open: cout
  Negator #(.width(5)) negator_1 (.in({1'b0, adder_1_out}), .out(negator_1_out));
  Adder #(.width(5)) adder_2 (
    .a({1'b0, Minuend}), .b(negator_1_out), .out({Borrow_Out, Output}), .cin(1'b0));  // open: cout
endmodule

module MULT1 (
  input  Input_A,
  input  Input_B,
  input  Carry_In,
  output Output,
  output Carry_Out
);

  wire and_1_out;

  and and_1 (and_1_out, Input_A, Input_B);
  xor xor_1 (Output, Carry_In, and_1_out);
  and and_2 (Carry_Out, and_1_out, Carry_In);
endmodule

module MULTA1 (
  input  Input_A,
  input  Input_B,
  input  Carry_In,
  output Output,
  output Carry_Out
);

  wire and_1_out, nor_1_out;

  and and_1 (and_1_out, Input_A, Input_B);
  nor nor_1 (nor_1_out, and_1_out, Carry_In);
  and and_2 (Carry_Out, and_1_out, Carry_In);
  nor nor_2 (Output, nor_1_out, Carry_Out);
endmodule

module MULT2 (
  input  [1:0] Carry_In,
  input  [1:0] Input_A,
  input  [1:0] Input_B,
  output [1:0] Output,
  output [1:0] Carry_Out
);

  wire multa1_1_carry_out, multa1_3_carry_out;
  wire [1:0] multa1_1_output, multa1_3_output;

  MULTA1 multa1_1 (
    .Input_A(Input_A[0]), .Input_B(Input_B[0]), .Carry_In(Carry_In[0]), .Output(multa1_1_output[0]),
    .Carry_Out(multa1_1_carry_out));
  MULTA1 multa1_2 (
    .Input_A(Input_A[0]), .Input_B(Input_B[1]), .Carry_In(multa1_1_carry_out), .Output(multa1_1_output[1]));  // open: Carry_Out
  MULTA1 multa1_3 (
    .Input_A(Input_A[1]), .Input_B(Input_B[0]), .Carry_In(Carry_In[1]), .Output(multa1_3_output[0]),
    .Carry_Out(multa1_3_carry_out));
  MULTA1 multa1_4 (
    .Input_A(Input_A[1]), .Input_B(Input_B[1]), .Carry_In(multa1_3_carry_out), .Output(multa1_3_output[1]));  // open: Carry_Out
  // Probe on {Carry_Out, Output}
  Adder #(.width(4)) adder_1 (
    .a({2'b00, multa1_1_output}), .b({1'b0, multa1_3_output, 1'b0}), .out({Carry_Out, Output}), .cin(1'b0));  // open: cout
endmodule

module MULT4 (
  input  [3:0] Carry_In,
  input  [3:0] Input_A,
  input  [3:0] Input_B,
  output [3:0] Output,
  output [3:0] Carry_Out
);

  wire [1:0] mult2_1_carry_out, mult2_1_output, mult2_2_output, mult2_3_carry_out, mult2_3_output,
       mult2_4_output;

  MULT2 mult2_1 (
    .Input_A(Input_A[1:0]), .Input_B(Input_B[1:0]), .Carry_In(Carry_In[1:0]), .Output(mult2_1_output),
    .Carry_Out(mult2_1_carry_out));
  MULT2 mult2_2 (
    .Input_A(Input_A[1:0]), .Input_B(Input_B[3:2]), .Carry_In(mult2_1_carry_out), .Output(mult2_2_output));  // open: Carry_Out
  MULT2 mult2_3 (
    .Input_A(Input_A[3:2]), .Input_B(Input_B[1:0]), .Carry_In(Carry_In[3:2]), .Output(mult2_3_output),
    .Carry_Out(mult2_3_carry_out));
  MULT2 mult2_4 (
    .Input_A(Input_A[3:2]), .Input_B(Input_B[3:2]), .Carry_In(mult2_3_carry_out), .Output(mult2_4_output));  // open: Carry_Out
  Adder adder_1 (
    .a({4'b0000, mult2_2_output, mult2_1_output}), .b({2'b00, mult2_4_output, mult2_3_output, 2'b00}),
    .out({Carry_Out, Output}), .cin(1'b0));  // open: cout
endmodule

module MULT2A (
  input  [1:0] in_1,
  input  [1:0] in_2,
  input  [1:0] in_3,
  output [1:0] out_4,
  output [1:0] out_5
);

  wire [3:0] adder_1_out, adder_2_out, adder_3_out;

  Adder #(.width(4)) adder_1 (.a({2'b00, in_1}), .b({2'b00, in_2}), .out(adder_1_out), .cin(1'b0));  // open: cout
  Adder #(.width(4)) adder_2 (.a(adder_1_out), .b({2'b00, in_2}), .out(adder_2_out), .cin(1'b0));  // open: cout
  Multiplexer #(.select(2), .width(4), .enable("false")) multiplexer_1 (
    .in0(4'b0000), .in1(adder_1_out), .in2(adder_2_out), .in3(adder_3_out), .out({out_5, out_4}), .sel(in_3));
  Adder #(.width(4)) adder_3 (.a(adder_2_out), .b({2'b00, in_2}), .out(adder_3_out), .cin(1'b0));  // open: cout
endmodule
