// Logisim project 06_COMPARATOR_V.circ as structural Verilog: 13 circuits, main circuit main
module main (
  input  [3:0] in_1,
  input  [3:0] in_2,
  input  [3:0] in_3,
  input  [3:0] in_4
);

  wire afn4_1_sign, afn4_2_sign, afn4_3_sign, afn4_4_sign, comp4b_1_equal, comp4b_1_greater, comp4b_1_less,
       comp4bn_1_equal, comp4bn_1_greater, comp4bn_1_less, comparator_1_eq, comparator_1_gt, comparator_1_lt,
       comparator_2_eq, comparator_2_gt, comparator_2_lt;
  wire [3:0] afin_1_ouptu_unit, afin_1_output_ten, afin_2_ouptu_unit, afin_2_output_ten, afin_3_ouptu_unit,
       afin_3_output_ten, afin_4_ouptu_unit, afin_4_output_ten, afn4_1_output, afn4_2_output, afn4_3_output,
       afn4_4_output;
  wire [4:0] afsi2_1_output, afsi2_1_output_2, afsi2_1_output_3, afsi2_1_output_4, afsi2_1_output_5,
       afsi2_1_output_6, afsi2_2_output, afsi2_2_output_2, afsi2_2_output_3, afsi2_2_output_4,
       afsi2_2_output_5, afsi2_2_output_6;
  wire [29:0] afsi2_3_output, afsi2_4_output;

  // Probe on in_1
  // Probe on in_1
  // Probe on in_1
  AFIN afin_1 (.INPUT(in_1), .Ouptu_unit(afin_1_ouptu_unit), .Output_ten(afin_1_output_ten));
  Hex_Digit_Display hex_digit_display_1 (.value(afin_1_output_ten));  // open: dp
  COMP4B comp4b_1 (.Greater(comp4b_1_greater), .A(in_1), .Equal(comp4b_1_equal), .B(in_4), .Less(comp4b_1_less));
  AFIN afin_2 (.INPUT(in_1), .Ouptu_unit(afin_2_ouptu_unit), .Output_ten(afin_2_output_ten));
  Hex_Digit_Display hex_digit_display_2 (.value(afin_2_output_ten));  // open: dp
  Hex_Digit_Display hex_digit_display_3 (.value(afin_1_ouptu_unit));  // open: dp
  DotMatrix #(.matrixcols(6), .matrixrows(5)) dotmatrix_1 (
    .col0(afsi2_1_output_6), .col1(afsi2_1_output_5), .col2(afsi2_1_output_4), .col3(afsi2_1_output_3),
    .col4(afsi2_1_output_2), .col5(afsi2_1_output));
  AFSI2 afsi2_1 (
    .Greater(comp4b_1_greater), .Equal(comp4b_1_equal), .Less(comp4b_1_less), .ENABLE(1'b1),
    .Output({afsi2_1_output_6, afsi2_1_output_5, afsi2_1_output_4, afsi2_1_output_3, afsi2_1_output_2, afsi2_1_output}));
  DotMatrix #(.matrixcols(6), .matrixrows(5)) dotmatrix_2 (
    .col0(afsi2_2_output_6), .col1(afsi2_2_output_5), .col2(afsi2_2_output_4), .col3(afsi2_2_output_3),
    .col4(afsi2_2_output_2), .col5(afsi2_2_output));
  Hex_Digit_Display hex_digit_display_4 (.value(afin_2_ouptu_unit));  // open: dp
  Comparator #(.width(4), .mode("unsigned")) comparator_1 (
    .a(in_1), .b(in_4), .gt(comparator_1_gt), .eq(comparator_1_eq), .lt(comparator_1_lt));
  Hex_Digit_Display hex_digit_display_5 (.value(afin_3_output_ten));  // open: dp
  Hex_Digit_Display hex_digit_display_6 (.value(afin_4_output_ten));  // open: dp
  AFSI2 afsi2_2 (
    .Greater(comparator_1_gt), .Equal(comparator_1_eq), .Less(comparator_1_lt), .ENABLE(1'b1),
    .Output({afsi2_2_output_6, afsi2_2_output_5, afsi2_2_output_4, afsi2_2_output_3, afsi2_2_output_2, afsi2_2_output}));
  Hex_Digit_Display hex_digit_display_7 (.value(afin_3_ouptu_unit));  // open: dp
  AFIN afin_3 (.INPUT(in_4), .Ouptu_unit(afin_3_ouptu_unit), .Output_ten(afin_3_output_ten));
  Hex_Digit_Display hex_digit_display_8 (.value(afin_4_ouptu_unit));  // open: dp
  AFIN afin_4 (.INPUT(in_4), .Ouptu_unit(afin_4_ouptu_unit), .Output_ten(afin_4_output_ten));
  // Probe on in_4
  // Probe on in_4
  // Probe on in_4
  // Probe on in_2
  // Probe on in_2
  // Probe on in_2
  _7_Segment_Display u_7_segment_display_1 (.g(afn4_1_sign));  // open: f, a, b, e, d, c, dp
  AFN4 afn4_1 (.Sign(afn4_1_sign), .Input(in_2), .Output(afn4_1_output));
  COMP4BN comp4bn_1 (.A(in_2), .B(in_3), .Greater(comp4bn_1_greater), .Equal(comp4bn_1_equal), .Less(comp4bn_1_less));
  _7_Segment_Display u_7_segment_display_2 (.g(afn4_2_sign));  // open: f, a, b, e, d, c, dp
  AFN4 afn4_2 (.Sign(afn4_2_sign), .Input(in_2), .Output(afn4_2_output));
  Comparator #(.width(4)) comparator_2 (
    .a(in_2), .b(in_3), .gt(comparator_2_gt), .eq(comparator_2_eq), .lt(comparator_2_lt));
  DotMatrix #(.matrixcols(6), .matrixrows(5)) dotmatrix_3 (
    .col0(afsi2_3_output[29:25]), .col1(afsi2_3_output[24:20]), .col2(afsi2_3_output[19:15]),
    .col3(afsi2_3_output[14:10]), .col4(afsi2_3_output[9:5]), .col5(afsi2_3_output[4:0]));
  Hex_Digit_Display hex_digit_display_9 (.value(afn4_1_output));  // open: dp
  AFSI2 afsi2_3 (
    .Greater(comp4bn_1_greater), .Equal(comp4bn_1_equal), .Less(comp4bn_1_less), .ENABLE(1'b1),
    .Output(afsi2_3_output));
  Hex_Digit_Display hex_digit_display_10 (.value(afn4_2_output));  // open: dp
  DotMatrix #(.matrixcols(6), .matrixrows(5)) dotmatrix_4 (
    .col0(afsi2_4_output[29:25]), .col1(afsi2_4_output[24:20]), .col2(afsi2_4_output[19:15]),
    .col3(afsi2_4_output[14:10]), .col4(afsi2_4_output[9:5]), .col5(afsi2_4_output[4:0]));
  AFSI2 afsi2_4 (
    .Greater(comparator_2_gt), .Equal(comparator_2_eq), .Less(comparator_2_lt), .ENABLE(1'b1),
    .Output(afsi2_4_output));
  _7_Segment_Display u_7_segment_display_3 (.g(afn4_3_sign));  // open: f, a, b, e, d, c, dp
  _7_Segment_Display u_7_segment_display_4 (.g(afn4_4_sign));  // open: f, a, b, e, d, c, dp
  Hex_Digit_Display hex_digit_display_11 (.value(afn4_3_output));  // open: dp
  Hex_Digit_Display hex_digit_display_12 (.value(afn4_4_output));  // open: dp
  AFN4 afn4_3 (.Sign(afn4_3_sign), .Input(in_3), .Output(afn4_3_output));
  AFN4 afn4_4 (.Sign(afn4_4_sign), .Input(in_3), .Output(afn4_4_output));
  // Probe on in_3
  // Probe on in_3
  // Probe on in_3
endmodule

module COMPN (
  input  GreaterE,
  input  EqualE,
  input  LessE,
  input  msb0,
  input  msb1,
  output Greater,
  output Equal,
  output Less
);

  wire and_1_out, and_2_out, and_3_out, and_4_out, not_1_out, xor_1_out;

  not not_1 (not_1_out, xor_1_out);
  xor xor_1 (xor_1_out, msb0, msb1);
  and and_1 (and_1_out, GreaterE, not_1_out);
  or or_1 (Greater, and_1_out, and_2_out);
  and and_2 (and_2_out, LessE, xor_1_out);
  and and_3 (and_3_out, LessE, not_1_out);
  or or_2 (Less, and_3_out, and_4_out);
  and and_4 (and_4_out, GreaterE, xor_1_out);

  assign Equal = EqualE;
endmodule

module COMP2E (
  input  Greater1,
  input  Greater0,
  input  Less1,
  input  Less0,
  input  Equal1,
  input  Equal0,
  output Greater,
  output Less,
  output Equal
);

  wire and_1_out, and_2_out;

  or or_1 (Greater, Greater1, and_1_out);
  and and_1 (and_1_out, Greater0, Equal1);
  or or_2 (Less, Less1, and_2_out);
  and and_2 (and_2_out, Less0, Equal1);
  and and_3 (Equal, Equal1, Equal0);
endmodule

module COMP1B (
  input  A,
  input  B,
  output Less,
  output Equal,
  output Greater
);

  wire not_1_out, not_2_out;

  not not_1 (not_1_out, A);
  and and_1 (Less, not_1_out, B);
  and and_2 (Greater, A, not_2_out);
  not not_2 (not_2_out, B);
  nor nor_1 (Equal, Less, Greater);
endmodule

module COMP2B (
  input  [1:0] A,
  input  [1:0] B,
  output Greater,
  output Equal,
  output Less
);

  wire comp1b_1_equal, comp1b_1_greater, comp1b_1_less, comp1b_2_equal, comp1b_2_greater, comp1b_2_less;

  COMP1B comp1b_1 (.A(A[0]), .B(B[0]), .Greater(comp1b_1_greater), .Equal(comp1b_1_equal), .Less(comp1b_1_less));
  COMP1B comp1b_2 (.A(A[1]), .B(B[1]), .Greater(comp1b_2_greater), .Equal(comp1b_2_equal), .Less(comp1b_2_less));
  COMP2E comp2e_1 (
    .Greater0(comp1b_1_greater), .Equal0(comp1b_1_equal), .Less0(comp1b_1_less), .Greater1(comp1b_2_greater),
    .Equal1(comp1b_2_equal), .Less1(comp1b_2_less), .Greater(Greater), .Equal(Equal), .Less(Less));
endmodule

module COMP3B (
  input  [2:0] A,
  input  [2:0] B,
  output Greater,
  output Equal,
  output Less
);

  wire comp1b_1_equal, comp1b_1_greater, comp1b_1_less, comp2b_1_equal, comp2b_1_greater, comp2b_1_less;

  COMP2B comp2b_1 (.A(A[1:0]), .Greater(comp2b_1_greater), .Equal(comp2b_1_equal), .Less(comp2b_1_less), .B(B[1:0]));
  COMP1B comp1b_1 (.A(A[2]), .B(B[2]), .Greater(comp1b_1_greater), .Equal(comp1b_1_equal), .Less(comp1b_1_less));
  COMP2E comp2e_1 (
    .Greater0(comp2b_1_greater), .Equal0(comp2b_1_equal), .Less0(comp2b_1_less), .Greater1(comp1b_1_greater),
    .Equal1(comp1b_1_equal), .Less1(comp1b_1_less), .Greater(Greater), .Equal(Equal), .Less(Less));
endmodule

module COMP4B (
  input  [3:0] A,
  input  [3:0] B,
  output Greater,
  output Equal,
  output Less
);

  wire comp1b_1_equal, comp1b_1_greater, comp1b_1_less, comp3b_1_equal, comp3b_1_greater, comp3b_1_less;

  COMP3B comp3b_1 (.A(A[2:0]), .B(B[2:0]), .Equal(comp3b_1_equal), .Greater(comp3b_1_greater), .Less(comp3b_1_less));
  COMP1B comp1b_1 (.A(A[3]), .B(B[3]), .Greater(comp1b_1_greater), .Equal(comp1b_1_equal), .Less(comp1b_1_less));
  COMP2E comp2e_1 (
    .Greater0(comp3b_1_greater), .Equal0(comp3b_1_equal), .Less0(comp3b_1_less), .Greater1(comp1b_1_greater),
    .Equal1(comp1b_1_equal), .Less1(comp1b_1_less), .Greater(Greater), .Equal(Equal), .Less(Less));
endmodule

module COMP4BN (
  input  [3:0] A,
  input  [3:0] B,
  output Greater,
  output Equal,
  output Less
);

  wire comp4b_1_equal, comp4b_1_greater, comp4b_1_less;

  COMP4B comp4b_1 (.Greater(comp4b_1_greater), .A(A), .Equal(comp4b_1_equal), .B(B), .Less(comp4b_1_less));
  COMPN compn_1 (
    .GreaterE(comp4b_1_greater), .EqualE(comp4b_1_equal), .LessE(comp4b_1_less), .msb0(A[3]), .msb1(B[3]),
    .Greater(Greater), .Equal(Equal), .Less(Less));
endmodule

module COMP4B2 (
  input  [3:0] A,
  input  [3:0] B,
  output Greater,
  output Equal,
  output Less
);

  wire comp1b_1_equal, comp1b_1_greater, comp1b_1_less, comp1b_2_equal, comp1b_2_greater, comp1b_2_less,
       comp1b_3_equal, comp1b_3_greater, comp1b_3_less, comp1b_4_equal, comp1b_4_greater, comp1b_4_less,
       comp2e_1_equal, comp2e_1_greater, comp2e_1_less, comp2e_2_equal, comp2e_2_greater, comp2e_2_less;

  COMP1B comp1b_1 (.A(A[0]), .B(B[0]), .Greater(comp1b_1_greater), .Equal(comp1b_1_equal), .Less(comp1b_1_less));
  COMP1B comp1b_2 (.A(A[1]), .B(B[1]), .Greater(comp1b_2_greater), .Equal(comp1b_2_equal), .Less(comp1b_2_less));
  COMP1B comp1b_3 (.A(A[2]), .B(B[2]), .Greater(comp1b_3_greater), .Equal(comp1b_3_equal), .Less(comp1b_3_less));
  COMP1B comp1b_4 (.A(A[3]), .B(B[3]), .Greater(comp1b_4_greater), .Equal(comp1b_4_equal), .Less(comp1b_4_less));
  COMP2E comp2e_1 (
    .Greater0(comp1b_1_greater), .Equal0(comp1b_1_equal), .Less0(comp1b_1_less), .Greater1(comp1b_2_greater),
    .Equal1(comp1b_2_equal), .Less1(comp1b_2_less), .Greater(comp2e_1_greater), .Equal(comp2e_1_equal),
    .Less(comp2e_1_less));
  COMP2E comp2e_2 (
    .Greater0(comp2e_1_greater), .Equal0(comp2e_1_equal), .Less0(comp2e_1_less), .Greater1(comp1b_3_greater),
    .Equal1(comp1b_3_equal), .Less1(comp1b_3_less), .Greater(comp2e_2_greater), .Equal(comp2e_2_equal),
    .Less(comp2e_2_less));
  COMP2E comp2e_3 (
    .Greater0(comp2e_2_greater), .Equal0(comp2e_2_equal), .Less0(comp2e_2_less), .Greater1(comp1b_4_greater),
    .Equal1(comp1b_4_equal), .Less1(comp1b_4_less), .Greater(Greater), .Equal(Equal), .Less(Less));
endmodule

module AFSI2 (
  input  Greater,
  input  Equal,
  input  Less,
  input  ENABLE,
  output [29:0] Output
);

  wire and_1_out, and_2_out, and_3_out;
  wire [4:0] and_4_out, and_5_out, and_6_out, and_7_out, and_8_out, and_9_out, and_10_out, and_11_out,
       and_12_out, and_13_out, and_14_out, and_15_out, and_16_out, and_17_out, and_18_out, and_19_out,
       and_20_out, and_21_out, bit_extender_1_out, bit_extender_2_out, bit_extender_3_out,
       bit_extender_4_out, bit_extender_5_out, bit_extender_6_out, bit_extender_7_out, bit_extender_8_out,
       bit_extender_9_out, bit_extender_10_out, bit_extender_11_out, bit_extender_12_out,
       bit_extender_13_out, bit_extender_14_out, bit_extender_15_out, bit_extender_16_out,
       bit_extender_17_out, bit_extender_18_out;

  and and_1 (and_1_out, Greater, ENABLE);
  and and_2 (and_2_out, Equal, ENABLE);
  and and_3 (and_3_out, Less, ENABLE);
  assign bit_extender_1_out = {{4{and_2_out}}, and_2_out};  // Bit_Extender bit_extender_1
  assign bit_extender_2_out = {{4{and_2_out}}, and_2_out};  // Bit_Extender bit_extender_2
  assign bit_extender_3_out = {{4{and_2_out}}, and_2_out};  // Bit_Extender bit_extender_3
  assign bit_extender_4_out = {{4{and_2_out}}, and_2_out};  // Bit_Extender bit_extender_4
  assign bit_extender_5_out = {{4{and_2_out}}, and_2_out};  // Bit_Extender bit_extender_5
  assign bit_extender_6_out = {{4{and_2_out}}, and_2_out};  // Bit_Extender bit_extender_6
  assign and_4_out = 5'b01010 & bit_extender_1_out;  // AND_Gate and_4, 5 bits wide
  assign and_5_out = 5'b01010 & bit_extender_2_out;  // AND_Gate and_5, 5 bits wide
  assign and_6_out = 5'b01010 & bit_extender_3_out;  // AND_Gate and_6, 5 bits wide
  assign and_7_out = 5'b01010 & bit_extender_4_out;  // AND_Gate and_7, 5 bits wide
  assign and_8_out = 5'b01010 & bit_extender_5_out;  // AND_Gate and_8, 5 bits wide
  assign and_9_out = 5'b01010 & bit_extender_6_out;  // AND_Gate and_9, 5 bits wide
  assign bit_extender_7_out = {{4{and_3_out}}, and_3_out};  // Bit_Extender bit_extender_7
  assign bit_extender_8_out = {{4{and_3_out}}, and_3_out};  // Bit_Extender bit_extender_8
  assign bit_extender_9_out = {{4{and_3_out}}, and_3_out};  // Bit_Extender bit_extender_9
  assign bit_extender_10_out = {{4{and_3_out}}, and_3_out};  // Bit_Extender bit_extender_10
  assign bit_extender_11_out = {{4{and_3_out}}, and_3_out};  // Bit_Extender bit_extender_11
  assign bit_extender_12_out = {{4{and_3_out}}, and_3_out};  // Bit_Extender bit_extender_12
  assign bit_extender_13_out = {{4{and_1_out}}, and_1_out};  // Bit_Extender bit_extender_13
  assign bit_extender_14_out = {{4{and_1_out}}, and_1_out};  // Bit_Extender bit_extender_14
  assign bit_extender_15_out = {{4{and_1_out}}, and_1_out};  // Bit_Extender bit_extender_15
  assign bit_extender_16_out = {{4{and_1_out}}, and_1_out};  // Bit_Extender bit_extender_16
  assign bit_extender_17_out = {{4{and_1_out}}, and_1_out};  // Bit_Extender bit_extender_17
  assign bit_extender_18_out = {{4{and_1_out}}, and_1_out};  // Bit_Extender bit_extender_18
  assign and_10_out = 5'b10001 & bit_extender_7_out;  // AND_Gate and_10, 5 bits wide
  assign and_11_out = 5'b10001 & bit_extender_8_out;  // AND_Gate and_11, 5 bits wide
  assign and_12_out = 5'b01010 & bit_extender_9_out;  // AND_Gate and_12, 5 bits wide
  assign and_13_out = 5'b01010 & bit_extender_10_out;  // AND_Gate and_13, 5 bits wide
  assign and_14_out = 5'b00100 & bit_extender_11_out;  // AND_Gate and_14, 5 bits wide
  assign and_15_out = 5'b00100 & bit_extender_12_out;  // AND_Gate and_15, 5 bits wide
  assign and_16_out = 5'b00100 & bit_extender_13_out;  // AND_Gate and_16, 5 bits wide
  assign and_17_out = 5'b00100 & bit_extender_14_out;  // AND_Gate and_17, 5 bits wide
  assign and_18_out = 5'b01010 & bit_extender_15_out;  // AND_Gate and_18, 5 bits wide
  assign and_19_out = 5'b01010 & bit_extender_16_out;  // AND_Gate and_19, 5 bits wide
  assign and_20_out = 5'b10001 & bit_extender_17_out;  // AND_Gate and_20, 5 bits wide
  assign and_21_out = 5'b10001 & bit_extender_18_out;  // AND_Gate and_21, 5 bits wide
  assign Output = {and_15_out, and_14_out, and_13_out, and_12_out, and_11_out, and_10_out} | {and_9_out, and_8_out, and_7_out, and_6_out, and_5_out, and_4_out} | {and_21_out, and_20_out, and_19_out, and_18_out, and_17_out, and_16_out};  // OR_Gate or_1, 30 bits wide

  // Notes on the sheet:
  //   _*_*_
  //   _*_*_
  //   _*_*_
  //   _*_*_
  //   _*_*_
  //   _*_*_
  //   __*__
  //   __*__
  //   _*_*_
  //   _*_*_
  //   *___*
  //   *___*
  //   *___*
  //   *___*
  //   _*_*_
  //   _*_*_
  //   __*__
  //   __*__
endmodule

module AFN4 (
  input  [3:0] Input,
  output Sign,
  output [3:0] Output
);

  wire [3:0] and_1_out, and_2_out, negator_1_out, not_1_out;

  assign and_1_out = {4{Input[3]}} & Input;  // AND_Gate and_1, 4 bits wide
  assign not_1_out = ~{4{Input[3]}};  // NOT_Gate not_1, 4 bits wide
  Negator #(.width(4)) negator_1 (.in(and_1_out), .out(negator_1_out));
  assign and_2_out = not_1_out & Input;  // AND_Gate and_2, 4 bits wide
  assign Output = negator_1_out | and_2_out;  // OR_Gate or_1, 4 bits wide

  assign Sign = Input[3];
endmodule

module AFIN (
  input  [3:0] INPUT,
  output [3:0] Ouptu_unit,
  output [3:0] Output_ten
);

  wire comparator_1_gt, not_1_out;
  wire [3:0] and_1_out, and_2_out, bit_extender_1_out, bit_extender_2_out, subtractor_1_out;

  Subtractor #(.width(4)) subtractor_1 (.a(INPUT), .b(4'b1010), .out(subtractor_1_out), .bin(1'b0));  // open: bout
  Comparator #(.width(4), .mode("unsigned")) comparator_1 (
    .a(INPUT), .b(4'b1001), .gt(comparator_1_gt));  // open: eq, lt
  assign bit_extender_1_out = {{3{comparator_1_gt}}, comparator_1_gt};  // Bit_Extender bit_extender_1
  assign bit_extender_2_out = {{3{not_1_out}}, not_1_out};  // Bit_Extender bit_extender_2
  not not_1 (not_1_out, comparator_1_gt);
  assign and_1_out = subtractor_1_out & bit_extender_1_out;  // AND_Gate and_1, 4 bits wide
  assign Ouptu_unit = and_1_out | and_2_out;  // OR_Gate or_1, 4 bits wide
  assign and_2_out = INPUT & bit_extender_2_out;  // AND_Gate and_2, 4 bits wide
  assign Output_ten = {{3{1'b0}}, comparator_1_gt};  // Bit_Extender bit_extender_3
endmodule

module test (
  input  in_1,
  input  in_2,
  input  in_3,
  input  in_4,
  input  in_5,
  input  in_6,
  input  in_7,
  input  in_8,
  input  in_9,
  input  in_10,
  input  in_11,
  input  in_12
);

  wire afn4_1_sign, afn4_2_sign, afn4_3_sign, afn4_4_sign, comp2b_1_equal, comp2b_1_greater, comp2b_1_less,
       comp2b_2_equal, comp2b_2_greater, comp2b_2_less, comp4b2_1_equal, comp4b2_1_greater, comp4b2_1_less,
       comp4b2_2_equal, comp4b2_2_greater, comp4b2_2_less, comp4b_1_equal, comp4b_1_greater, comp4b_1_less,
       comp4bn_1_equal, comp4bn_1_greater, comp4bn_1_less;
  wire [1:0] counter_5_q, counter_6_q, counter_9_q;
  wire [3:0] afn4_1_output, afn4_2_output, afn4_3_output, afn4_4_output, counter_1_q, counter_2_q,
       counter_3_q, counter_4_q, counter_7_q, counter_8_q, counter_10_q, counter_11_q, counter_12_q;
  wire [4:0] afsi2_1_output, afsi2_1_output_2, afsi2_1_output_3, afsi2_1_output_4, afsi2_1_output_5,
       afsi2_1_output_6, afsi2_2_output, afsi2_2_output_2, afsi2_2_output_3, afsi2_2_output_4,
       afsi2_2_output_5, afsi2_2_output_6, afsi2_3_output, afsi2_3_output_2, afsi2_3_output_3,
       afsi2_3_output_4, afsi2_3_output_5, afsi2_3_output_6, afsi2_4_output, afsi2_4_output_2,
       afsi2_4_output_3, afsi2_4_output_4, afsi2_4_output_5, afsi2_4_output_6, afsi2_5_output,
       afsi2_5_output_2, afsi2_5_output_3, afsi2_5_output_4, afsi2_5_output_5, afsi2_5_output_6,
       afsi2_6_output, afsi2_6_output_2, afsi2_6_output_3, afsi2_6_output_4, afsi2_6_output_5,
       afsi2_6_output_6;

  Hex_Digit_Display hex_digit_display_1 (.value(counter_1_q));  // open: dp
  Counter #(.width(4), .max('hf)) counter_1 (
    .load(1'b0), .D(4'b0000), .count(1'b1), .Q(counter_1_q), .clk(in_1), .clr(1'b0));  // open: carry
  Counter #(.width(4), .max('hf)) counter_2 (
    .load(1'b0), .D(4'b0000), .count(1'b1), .Q(counter_2_q), .clk(in_4), .clr(1'b0));  // open: carry
  Counter #(.width(4), .max('hf)) counter_3 (
    .load(1'b0), .D(4'b0000), .count(1'b1), .Q(counter_3_q), .clk(in_9), .clr(1'b0));  // open: carry
  Counter #(.width(4), .max('hf)) counter_4 (
    .load(1'b0), .D(4'b0000), .count(1'b1), .Q(counter_4_q), .clk(in_12), .clr(1'b0));  // open: carry
  DotMatrix #(.matrixcols(6), .matrixrows(5)) dotmatrix_1 (
    .col0(afsi2_1_output_6), .col1(afsi2_1_output_5), .col2(afsi2_1_output_4), .col3(afsi2_1_output_3),
    .col4(afsi2_1_output_2), .col5(afsi2_1_output));
  AFSI2 afsi2_1 (
    .Greater(comp4b_1_greater), .Equal(comp4b_1_equal), .Less(comp4b_1_less), .ENABLE(1'b1),
    .Output({afsi2_1_output_6, afsi2_1_output_5, afsi2_1_output_4, afsi2_1_output_3, afsi2_1_output_2, afsi2_1_output}));
  COMP4B comp4b_1 (
    .Greater(comp4b_1_greater), .A(counter_1_q), .Equal(comp4b_1_equal), .B(counter_2_q), .Less(comp4b_1_less));
  _7_Segment_Display u_7_segment_display_1 (.g(afn4_1_sign));  // open: f, a, b, e, d, c, dp
  AFN4 afn4_1 (.Sign(afn4_1_sign), .Input(counter_3_q), .Output(afn4_1_output));
  Hex_Digit_Display hex_digit_display_2 (.value(counter_2_q));  // open: dp
  DotMatrix #(.matrixcols(6), .matrixrows(5)) dotmatrix_2 (
    .col0(afsi2_2_output_6), .col1(afsi2_2_output_5), .col2(afsi2_2_output_4), .col3(afsi2_2_output_3),
    .col4(afsi2_2_output_2), .col5(afsi2_2_output));
  Hex_Digit_Display hex_digit_display_3 (.value(afn4_1_output));  // open: dp
  COMP4BN comp4bn_1 (
    .A(counter_3_q), .B(counter_4_q), .Greater(comp4bn_1_greater), .Equal(comp4bn_1_equal),
    .Less(comp4bn_1_less));
  _7_Segment_Display u_7_segment_display_2 (.g(afn4_2_sign));  // open: f, a, b, e, d, c, dp
  AFSI2 afsi2_2 (
    .Greater(comp4bn_1_greater), .Equal(comp4bn_1_equal), .Less(comp4bn_1_less), .ENABLE(1'b1),
    .Output({afsi2_2_output_6, afsi2_2_output_5, afsi2_2_output_4, afsi2_2_output_3, afsi2_2_output_2, afsi2_2_output}));
  Counter #(.width(2), .max('h3)) counter_5 (
    .load(1'b0), .D(2'b00), .count(1'b1), .Q(counter_5_q), .clk(in_2), .clr(1'b0));  // open: carry
  Counter #(.width(2), .max('h3)) counter_6 (
    .load(1'b0), .D(2'b00), .count(1'b1), .Q(counter_6_q), .clk(in_5), .clr(1'b0));  // open: carry
  Hex_Digit_Display hex_digit_display_4 (.value(afn4_2_output));  // open: dp
  AFN4 afn4_2 (.Sign(afn4_2_sign), .Input(counter_4_q), .Output(afn4_2_output));
  Hex_Digit_Display hex_digit_display_5 (.value({2'b00, counter_5_q}));  // open: dp
  DotMatrix #(.matrixcols(6), .matrixrows(5)) dotmatrix_3 (
    .col0(afsi2_3_output_6), .col1(afsi2_3_output_5), .col2(afsi2_3_output_4), .col3(afsi2_3_output_3),
    .col4(afsi2_3_output_2), .col5(afsi2_3_output));
  AFSI2 afsi2_3 (
    .Greater(comp2b_1_greater), .Equal(comp2b_1_equal), .Less(comp2b_1_less), .ENABLE(1'b1),
    .Output({afsi2_3_output_6, afsi2_3_output_5, afsi2_3_output_4, afsi2_3_output_3, afsi2_3_output_2, afsi2_3_output}));
  COMP2B comp2b_1 (
    .A(counter_5_q), .Greater(comp2b_1_greater), .Equal(comp2b_1_equal), .Less(comp2b_1_less), .B(counter_6_q));
  Counter #(.width(4), .max('hf)) counter_7 (
    .load(1'b0), .D(4'b0000), .count(1'b1), .Q(counter_7_q), .clk(in_7), .clr(1'b0));  // open: carry
  Counter #(.width(4), .max('hf)) counter_8 (
    .load(1'b0), .D(4'b0000), .count(1'b1), .Q(counter_8_q), .clk(in_10), .clr(1'b0));  // open: carry
  Hex_Digit_Display hex_digit_display_6 (.value({2'b00, counter_6_q}));  // open: dp
  DotMatrix #(.matrixcols(6), .matrixrows(5)) dotmatrix_4 (
    .col0(afsi2_4_output_6), .col1(afsi2_4_output_5), .col2(afsi2_4_output_4), .col3(afsi2_4_output_3),
    .col4(afsi2_4_output_2), .col5(afsi2_4_output));
  Hex_Digit_Display hex_digit_display_7 (.value(counter_7_q));  // open: dp
  COMP4B2 comp4b2_1 (
    .A(counter_7_q), .B(counter_8_q), .Greater(comp4b2_1_greater), .Equal(comp4b2_1_equal),
    .Less(comp4b2_1_less));
  Hex_Digit_Display hex_digit_display_8 (.value(counter_8_q));  // open: dp
  AFSI2 afsi2_4 (
    .Greater(comp4b2_1_greater), .Equal(comp4b2_1_equal), .Less(comp4b2_1_less), .ENABLE(1'b1),
    .Output({afsi2_4_output_6, afsi2_4_output_5, afsi2_4_output_4, afsi2_4_output_3, afsi2_4_output_2, afsi2_4_output}));
  Counter #(.width(2), .max('h3)) counter_9 (
    .load(1'b0), .D(2'b00), .count(1'b1), .Q(counter_9_q), .clk(in_3), .clr(1'b0));  // open: carry
  Counter #(.width(2), .max('h3)) counter_10 (
    .load(1'b0), .D(2'b00), .count(1'b1), .Q({counter_10_q[3], counter_10_q[0]}), .clk(in_6), .clr(1'b0));  // open: carry
  _7_Segment_Display u_7_segment_display_3 (.g(afn4_3_sign));  // open: f, a, b, e, d, c, dp
  AFN4 afn4_3 (.Sign(afn4_3_sign), .Input({{3{counter_9_q[1]}}, counter_9_q[0]}), .Output(afn4_3_output));
  Counter #(.width(4), .max('hf)) counter_11 (
    .load(1'b0), .D(4'b0000), .count(1'b1), .Q(counter_11_q), .clk(in_8), .clr(1'b0));  // open: carry
  Counter #(.width(4), .max('hf)) counter_12 (
    .load(1'b0), .D(4'b0000), .count(1'b1), .Q(counter_12_q), .clk(in_11), .clr(1'b0));  // open: carry
  DotMatrix #(.matrixcols(6), .matrixrows(5)) dotmatrix_5 (
    .col0(afsi2_5_output_6), .col1(afsi2_5_output_5), .col2(afsi2_5_output_4), .col3(afsi2_5_output_3),
    .col4(afsi2_5_output_2), .col5(afsi2_5_output));
  Hex_Digit_Display hex_digit_display_9 (.value(afn4_3_output));  // open: dp
  COMP2B comp2b_2 (
    .A(counter_9_q), .Greater(comp2b_2_greater), .Equal(comp2b_2_equal), .Less(comp2b_2_less),
    .B({counter_10_q[3], counter_10_q[0]}));
  DotMatrix #(.matrixcols(6), .matrixrows(5)) dotmatrix_6 (
    .col0(afsi2_6_output_6), .col1(afsi2_6_output_5), .col2(afsi2_6_output_4), .col3(afsi2_6_output_3),
    .col4(afsi2_6_output_2), .col5(afsi2_6_output));
  Hex_Digit_Display hex_digit_display_10 (.value(counter_11_q));  // open: dp
  COMP4B2 comp4b2_2 (
    .A(counter_11_q), .B(counter_12_q), .Greater(comp4b2_2_greater), .Equal(comp4b2_2_equal),
    .Less(comp4b2_2_less));
  _7_Segment_Display u_7_segment_display_4 (.g(afn4_4_sign));  // open: f, a, b, e, d, c, dp
  AFSI2 afsi2_5 (
    .Greater(comp2b_2_greater), .Equal(comp2b_2_equal), .Less(comp2b_2_less), .ENABLE(1'b1),
    .Output({afsi2_5_output_6, afsi2_5_output_5, afsi2_5_output_4, afsi2_5_output_3, afsi2_5_output_2, afsi2_5_output}));
  Hex_Digit_Display hex_digit_display_11 (.value(counter_12_q));  // open: dp
  AFSI2 afsi2_6 (
    .Greater(comp4b2_2_greater), .Equal(comp4b2_2_equal), .Less(comp4b2_2_less), .ENABLE(1'b1),
    .Output({afsi2_6_output_6, afsi2_6_output_5, afsi2_6_output_4, afsi2_6_output_3, afsi2_6_output_2, afsi2_6_output}));
  Hex_Digit_Display hex_digit_display_12 (.value(afn4_4_output));  // open: dp
  AFN4 afn4_4 (.Sign(afn4_4_sign), .Input({{3{counter_10_q[3]}}, counter_10_q[0]}), .Output(afn4_4_output));
endmodule
