// Logisim project 07_FLIP_FLOP_V.circ as structural Verilog: 18 circuits, main circuit main
module main (
  input  S,
  input  Clock,
  input  R,
  input  D,
  input  S_2,
  input  Clock_2,
  input  R_2,
  input  present,
  input  present_2,
  input  enable,
  input  enable_2,
  input  clear,
  input  clear_2,
  input  S_3,
  input  J,
  input  J_2,
  input  H,
  input  K,
  input  K_2,
  input  R_3,
  input  Clock_3,
  input  Clock_4,
  input  present_3,
  input  present_4,
  input  enable_3,
  input  enable_4,
  input  S_4,
  input  clear_3,
  input  clear_4,
  input  R_4,
  input  Clock_5,
  input  Clock_6,
  input  D_2,
  input  D_3,
  input  present_5,
  input  present_6,
  input  enable_5,
  input  enable_6,
  input  clear_5,
  input  clear_6,
  input  Clock_7,
  input  Clock_8,
  input  present_7,
  input  present_8,
  input  enable_7,
  input  enable_8,
  input  clear_7,
  input  clear_8,
  input  Clock_9,
  input  Clock_10,
  input  T,
  input  T_2,
  input  present_9,
  input  present_10,
  input  enable_9,
  input  enable_10,
  input  clear_9,
  input  clear_10,
  output out_59,
  output out_60,
  output out_61,
  output out_62,
  output out_63,
  output out_64,
  output out_65,
  output out_66,
  output out_67,
  output out_68,
  output out_69,
  output out_70,
  output out_71,
  output out_72,
  output out_73,
  output out_74,
  output out_75,
  output out_76,
  output out_77,
  output out_78,
  output out_79,
  output out_80,
  output out_81
);

  S_R_Flip_Flop #(.trigger("high")) s_r_ff_1 (
    .S(S), .clk(Clock_2), .R(R), .Q(out_59), .preset(present), .reset(clear), .en(enable));  // open: Qn
  J_K_Flip_Flop #(.trigger("falling")) j_k_ff_1 (
    .J(J), .clk(Clock_3), .K(K), .Q(out_65), .preset(present_3), .en(enable_3), .reset(clear_3));  // open: Qn
  D_Flip_Flop #(.trigger("falling")) d_ff_1 (
    .clk(Clock_5), .D(D_2), .Q(out_70), .preset(present_5), .en(enable_5), .reset(clear_5));  // open: Qn
  T_Flip_Flop #(.trigger("falling")) t_ff_1 (
    .clk(Clock_7), .T(1'b1), .Q(out_74), .preset(present_7), .reset(clear_7), .en(enable_7));  // open: Qn
  T_Flip_Flop #(.trigger("falling")) t_ff_2 (
    .clk(Clock_9), .T(T), .Q(out_78), .preset(present_9), .reset(clear_9), .en(enable_9));  // open: Qn
  RSHE rshe_1 (.Preset(present), .S(S), .H(Clock_2), .R(R), .Clear(clear), .Q(out_60), .Enable(enable));  // open: QN
  JKD jkd_1 (
    .J(J), .CLK(Clock_3), .K(K), .Q(out_66), .Preset(present_3), .Enable(enable_3), .Clear(clear_3));  // open: QN
  DD dd_1 (.D(D_2), .H(Clock_5), .Q(out_71), .Preset(present_5), .Enable(enable_5), .Clear(clear_5));  // open: QN
  TD td_1 (.Clock(Clock_7), .present(present_7), .enable(enable_7), .clear(clear_7), .Q(out_75));  // open: QN
  TLD tld_1 (.T(T), .present(present_9), .enable(enable_9), .clear(clear_9), .Q(out_79), .Clock(Clock_9));  // open: QN
  D_Flip_Flop #(.trigger("high")) d_ff_2 (
    .clk(Clock), .D(D), .Q(out_61), .preset(present_2), .en(enable_2), .reset(clear_2));  // open: Qn
  J_K_Flip_Flop j_k_ff_2 (
    .J(J_2), .clk(Clock_4), .K(K_2), .Q(out_67), .preset(present_4), .en(enable_4), .reset(clear_4));  // open: Qn
  D_Flip_Flop d_ff_3 (
    .clk(Clock_6), .D(D_3), .Q(out_72), .preset(present_6), .en(enable_6), .reset(clear_6));  // open: Qn
  T_Flip_Flop t_ff_3 (
    .clk(Clock_8), .T(1'b1), .Q(out_76), .preset(present_8), .reset(clear_8), .en(enable_8));  // open: Qn
  T_Flip_Flop t_ff_4 (
    .clk(Clock_10), .T(T_2), .Q(out_80), .preset(present_10), .reset(clear_10), .en(enable_10));  // open: Qn
  DE de_1 (.D(D), .H(Clock), .Q(out_62), .Preset(present_2), .Enable(enable_2), .Clear(clear_2));  // open: Q_Not
  JKM jkm_1 (
    .J(J_2), .CLK(Clock_4), .K(K_2), .Q(out_68), .Preset(present_4), .Enable(enable_4), .Clear(clear_4));  // open: QN
  DM dm_1 (.D(D_3), .Q(out_73), .H(Clock_6), .Preset(present_6), .Enable(enable_6), .Clear(clear_6));  // open: QN
  TM tm_1 (.Clock(Clock_8), .present(present_8), .enable(enable_8), .clear(clear_8), .Q(out_77));  // open: QN
  TLM tlm_1 (
    .T(T_2), .present(present_10), .enable(enable_10), .clear(clear_10), .Q(out_81), .clock(Clock_10));  // open: QN
  RS rs_1 (.R(R_2), .Q(out_63), .S(S_2));  // open: Q_Not
  RSH rsh_1 (.S(S_3), .H(H), .R(R_3), .Q(out_64));  // open: Q_Not
  D d_1 (.D(R_4), .H(S_4), .Q(out_69));  // open: Q_Not
endmodule

module main_tr (
  input  in_1,
  input  in_2,
  output out_3,
  output out_4
);

  RSTR rstr_1 (.S(in_1), .R(in_2), .Q(out_3), .Q_Not(out_4));
endmodule

module RS (
  input  R,
  input  S,
  output Q,
  output Q_Not
);

  nor nor_1 (Q, R, Q_Not);
  nor nor_2 (Q_Not, Q, S);
endmodule

module RSH (
  input  S,
  input  H,
  input  R,
  output Q,
  output Q_Not
);

  wire and_1_out, and_2_out;

  and and_1 (and_1_out, S, H);
  and and_2 (and_2_out, H, R);
  RS rs_1 (.R(and_2_out), .Q(Q), .Q_Not(Q_Not), .S(and_1_out));

  // Notes on the sheet:
  //   S0
  //   R0
endmodule

module D (
  input  D,
  input  H,
  output Q,
  output Q_Not
);

  wire not_1_out;

  RSH rsh_1 (.S(D), .H(H), .R(not_1_out), .Q(Q), .Q_Not(Q_Not));
  not not_1 (not_1_out, D);

  // Notes on the sheet:
  //   S0
  //   R0
endmodule

module RSHEM (
  input  S,
  input  H,
  input  R,
  input  Preset,
  input  Enable,
  input  Clear,
  output Q,
  output QN
);

  wire and_1_out, and_2_out, and_3_out, and_4_out, or_1_out, or_2_out;

  and and_1 (and_1_out, S, Enable);
  and and_2 (and_2_out, Enable, R);
  or or_1 (or_1_out, Preset, and_3_out);
  and and_3 (and_3_out, and_1_out, H);
  and and_4 (and_4_out, H, and_2_out);
  or or_2 (or_2_out, and_4_out, Clear);
  RS rs_1 (.R(or_2_out), .Q(Q), .Q_Not(QN), .S(or_1_out));

  // Notes on the sheet:
  //   S0
  //   R0
endmodule

module RSHE (
  input  S,
  input  H,
  input  R,
  input  Preset,
  input  Enable,
  input  Clear,
  output Q,
  output QN
);

  wire and_1_out, not_1_out;

  not not_1 (not_1_out, Clear);
  RSHEM rshem_1 (.S(S), .H(H), .R(R), .Preset(and_1_out), .Enable(Enable), .Clear(Clear), .Q(Q), .QN(QN));
  and and_1 (and_1_out, not_1_out, Preset);

  // Notes on the sheet:
  //   P0
endmodule

module DE (
  input  D,
  input  H,
  input  Preset,
  input  Enable,
  input  Clear,
  output Q,
  output Q_Not
);

  wire not_1_out;

  RSHE rshe_1 (.Preset(Preset), .S(D), .H(H), .R(not_1_out), .Clear(Clear), .Q(Q), .QN(Q_Not), .Enable(Enable));
  not not_1 (not_1_out, D);
endmodule

module JKD (
  input  J,
  input  CLK,
  input  K,
  input  Preset,
  input  Enable,
  input  Clear,
  output Q,
  output QN
);

  wire not_1_out, rshe_1_q, rshe_1_qn;

  not not_1 (not_1_out, CLK);
  RSHE rshe_1 (.Preset(Preset), .S(J), .H(CLK), .R(K), .Clear(Clear), .Q(rshe_1_q), .QN(rshe_1_qn), .Enable(Enable));
  RSHE rshe_2 (
    .Preset(Preset), .S(rshe_1_q), .H(not_1_out), .R(rshe_1_qn), .Clear(Clear), .Q(Q), .QN(QN),
    .Enable(Enable));
endmodule

module JKM (
  input  J,
  input  CLK,
  input  K,
  input  Preset,
  input  Enable,
  input  Clear,
  output Q,
  output QN
);

  wire not_1_out, rshe_1_q, rshe_1_qn;

  RSHE rshe_1 (
    .Preset(Preset), .S(J), .H(not_1_out), .R(K), .Clear(Clear), .Q(rshe_1_q), .QN(rshe_1_qn), .Enable(Enable));
  not not_1 (not_1_out, CLK);
  RSHE rshe_2 (.Preset(Preset), .S(rshe_1_q), .H(CLK), .R(rshe_1_qn), .Clear(Clear), .Q(Q), .QN(QN), .Enable(Enable));
endmodule

module DD (
  input  D,
  input  H,
  input  Preset,
  input  Enable,
  input  Clear,
  output Q,
  output QN
);

  wire not_1_out;

  not not_1 (not_1_out, D);
  JKD jkd_1 (.J(D), .CLK(H), .K(not_1_out), .Q(Q), .QN(QN), .Preset(Preset), .Enable(Enable), .Clear(Clear));
endmodule

module DM (
  input  D,
  input  H,
  input  Preset,
  input  Enable,
  input  Clear,
  output Q,
  output QN
);

  wire not_1_out;

  not not_1 (not_1_out, D);
  JKM jkm_1 (.J(D), .CLK(H), .K(not_1_out), .Q(Q), .QN(QN), .Preset(Preset), .Enable(Enable), .Clear(Clear));
endmodule

module TD (
  input  Clock,
  input  present,
  input  enable,
  input  clear,
  output Q,
  output QN
);

  DD dd_1 (.D(QN), .H(Clock), .Q(Q), .QN(QN), .Preset(present), .Enable(enable), .Clear(clear));
endmodule

module TM (
  input  Clock,
  input  present,
  input  enable,
  input  clear,
  output Q,
  output QN
);

  DM dm_1 (.D(QN), .Q(Q), .H(Clock), .QN(QN), .Preset(present), .Enable(enable), .Clear(clear));
endmodule

module TLD (
  input  Clock,
  input  T,
  input  present,
  input  enable,
  input  clear,
  output Q,
  output QN
);

  wire and_1_out, and_2_out;

  and and_1 (and_1_out, Clock, T);
  and and_2 (and_2_out, T, enable);
  DD dd_1 (.D(QN), .H(and_1_out), .Q(Q), .QN(QN), .Preset(present), .Enable(and_2_out), .Clear(clear));
endmodule

module TLM (
  input  clock,
  input  T,
  input  present,
  input  enable,
  input  clear,
  output Q,
  output QN
);

  wire and_1_out, and_2_out;

  and and_1 (and_1_out, clock, T);
  and and_2 (and_2_out, T, enable);
  DM dm_1 (.D(QN), .Q(Q), .H(and_1_out), .QN(QN), .Preset(present), .Enable(and_2_out), .Clear(clear));
endmodule

module RSTR (
  input  S,
  input  R,
  output Q,
  output Q_Not
);

  wire transistor_1_out, transistor_3_out, transistor_5_out, transistor_7_out;

  Transistor #(.gate("br")) transistor_1 (.in(1'b1), .out(transistor_1_out), .gate(Q));
  Pull_Resistor pull_resistor_1 (.node(transistor_1_out));
  Transistor transistor_2 (.in(transistor_1_out), .out(Q_Not), .gate(S));
  Transistor #(.\type ("n"), .gate("br")) transistor_3 (.in(Q_Not), .out(transistor_3_out), .gate(Q));
  Transistor #(.\type ("n")) transistor_4 (.in(Q_Not), .out(transistor_3_out), .gate(S));
  Pull_Resistor pull_resistor_2 (.node(Q_Not));
  Pull_Resistor pull_resistor_3 (.node(Q));
  Transistor transistor_5 (.in(1'b1), .out(transistor_5_out), .gate(Q_Not));
  Pull_Resistor pull_resistor_4 (.node(transistor_5_out));
  Transistor #(.gate("br")) transistor_6 (.in(transistor_5_out), .out(Q), .gate(R));
  Transistor #(.\type ("n"), .gate("br")) transistor_7 (.in(Q), .out(transistor_7_out), .gate(R));
  Transistor #(.\type ("n")) transistor_8 (.in(Q), .out(transistor_7_out), .gate(Q_Not));
  // also tied to GND on the sheet: {transistor_3_out, transistor_7_out}

  // Notes on the sheet:
  //   NON-OU
  //   NON-OU
endmodule

module DTR (
  input  D,
  input  Clock,
  output Q,
  output Q_Not
);

  wire transistor_1_out, transistor_2_out, transistor_3_out, transistor_5_out, transistor_6_out,
       transistor_9_out, transistor_11_out, transistor_13_out;

  Transistor transistor_1 (.in(1'b1), .out(transistor_1_out), .gate(D));
  Pull_Resistor pull_resistor_1 (.node(transistor_1_out));
  Transistor #(.\type ("n")) transistor_2 (.in(transistor_1_out), .out(transistor_2_out), .gate(D));
  Transistor transistor_3 (.in(1'b1), .out(transistor_3_out), .gate(D));
  Pull_Resistor pull_resistor_2 (.node(transistor_3_out));
  Transistor #(.gate("br")) transistor_4 (.in(transistor_3_out), .out(Q_Not), .gate(Q));
  Transistor #(.\type ("n")) transistor_5 (.in(Q_Not), .out(transistor_5_out), .gate(D));
  Transistor #(.\type ("n"), .gate("br")) transistor_6 (.in(Q_Not), .out(transistor_6_out), .gate(Q));
  Pull_Resistor pull_resistor_3 (.node(transistor_5_out));
  Transistor #(.\type ("n")) transistor_7 (.in(transistor_5_out), .out(transistor_6_out), .gate(Clock));
  Transistor #(.gate("br")) transistor_8 (.in(1'b1), .out(transistor_3_out), .gate(Clock));
  Transistor transistor_9 (.in(1'b1), .out(transistor_9_out), .gate(Clock));
  Transistor transistor_10 (.in(transistor_9_out), .out(Q), .gate(Q_Not));
  Transistor #(.\type ("n")) transistor_11 (.in(Q), .out(transistor_11_out), .gate(Q_Not));
  Transistor #(.gate("br")) transistor_12 (.in(1'b1), .out(transistor_9_out), .gate(transistor_1_out));
  Pull_Resistor pull_resistor_4 (.node(transistor_9_out));
  Pull_Resistor pull_resistor_5 (.node(Q));
  Transistor #(.\type ("n"), .gate("br")) transistor_13 (.in(Q), .out(transistor_13_out), .gate(transistor_1_out));
  Pull_Resistor pull_resistor_6 (.node(transistor_13_out));
  Transistor #(.\type ("n"), .gate("br")) transistor_14 (.in(transistor_13_out), .out(transistor_11_out), .gate(Clock));
  Pull_Resistor pull_resistor_7 (.node(Q_Not));
  // also tied to GND on the sheet: {transistor_2_out, transistor_6_out, transistor_11_out}
endmodule
