// Logisim project 08_COUNTER_V.circ as structural Verilog: 11 circuits, main circuit main
module main (
  input  count,
  input  enable,
  input  clear,
  input  choice,
  input  choise
);

  wire cmp4_1_carry, counter_1_carry, counter_3_carry, dcmp4_1_carry;
  wire [3:0] cmp4_1_output, cmp4_2_output, counter_1_q, counter_2_q;
  wire [7:0] counter_3_q, dcmp4_1_output;

  CMP4 cmp4_1 (.Clock(count), .Count(enable), .Clear(clear), .Output(cmp4_1_output), .Carry(cmp4_1_carry));
  Counter #(.width(4), .max('hf), .trigger("falling")) counter_1 (
    .load(choice), .D(4'b0000), .count(enable), .Q(counter_1_q), .carry(counter_1_carry), .clk(count),
    .clr(clear));
  Hex_Digit_Display hex_digit_display_1 (.value(cmp4_2_output));  // open: dp
  Hex_Digit_Display hex_digit_display_2 (.value(cmp4_1_output));  // open: dp
  Hex_Digit_Display hex_digit_display_3 (.value(counter_1_q));  // open: dp
  Hex_Digit_Display hex_digit_display_4 (.value(counter_2_q));  // open: dp
  CMP4 cmp4_2 (.Clock(cmp4_1_carry), .Count(count), .Clear(clear), .Output(cmp4_2_output));  // open: Carry
  Counter #(.width(4), .max('hf), .trigger("falling")) counter_2 (
    .load(choice), .D(4'b0000), .count(enable), .Q(counter_2_q), .clk(counter_1_carry), .clr(clear));  // open: carry
  // Probe on {cmp4_2_output, cmp4_1_output}
  // Probe on {cmp4_2_output, cmp4_1_output}
  // Probe on {cmp4_2_output, cmp4_1_output}
  // Probe on {cmp4_2_output, cmp4_1_output}
  // Probe on {counter_2_q, counter_1_q}
  // Probe on {counter_2_q, counter_1_q}
  // Probe on {counter_2_q, counter_1_q}
  // Probe on {counter_2_q, counter_1_q}
  Counter #(.width(4), .max('hf)) counter_3 (
    .load(choise), .D(4'b0000), .count(enable), .Q(counter_3_q[3:0]), .carry(counter_3_carry), .clk(count),
    .clr(clear));
  Hex_Digit_Display hex_digit_display_5 (.value(dcmp4_1_output[7:4]));  // open: dp
  Hex_Digit_Display hex_digit_display_6 (.value(dcmp4_1_output[3:0]));  // open: dp
  DCMP4 dcmp4_1 (.Clock(count), .Count(enable), .Clear(clear), .Output(dcmp4_1_output[3:0]), .Carry(dcmp4_1_carry));
  Hex_Digit_Display hex_digit_display_7 (.value(counter_3_q[7:4]));  // open: dp
  Hex_Digit_Display hex_digit_display_8 (.value(counter_3_q[3:0]));  // open: dp
  DCMP4 dcmp4_2 (.Clock(dcmp4_1_carry), .Count(enable), .Clear(clear), .Output(dcmp4_1_output[7:4]));  // open: Carry
  Counter #(.width(4), .max('hf), .trigger("falling")) counter_4 (
    .load(choise), .D(4'b0000), .count(enable), .Q(counter_3_q[7:4]), .clk(counter_3_carry), .clr(clear));  // open: carry
  // Probe on dcmp4_1_output
  // Probe on dcmp4_1_output
  // Probe on dcmp4_1_output
  // Probe on dcmp4_1_output
  // Probe on counter_3_q
  // Probe on counter_3_q
  // Probe on counter_3_q
  // Probe on counter_3_q
endmodule

module main0 (
  input  count,
  input  enable,
  input  clear,
  input  choice,
  input  in_5,
  input  [7:0] start
);

  wire counter_1_carry, counter_4_carry;
  wire [3:0] counter_1_q, counter_2_q, counter_2_q_2, counter_3_q, counter_4_q, counter_5_q, counter_5_q_2,
       counter_6_q;

  // Probe on start
  // Probe on start
  // Probe on start
  Hex_Digit_Display hex_digit_display_1 (.value(counter_3_q));  // open: dp
  Counter #(.width(4), .max('hf), .trigger("falling")) counter_1 (
    .load(choice), .D(start[3:0]), .count(enable), .Q(counter_1_q), .carry(counter_1_carry), .clk(count),
    .clr(clear));
  Hex_Digit_Display hex_digit_display_2 (.value(counter_2_q_2));  // open: dp
  Counter #(.trigger("falling")) counter_2 (
    .load(choice), .D(start), .count(enable), .Q({counter_2_q_2, counter_2_q}), .clk(count), .clr(clear));  // open: carry
  Hex_Digit_Display hex_digit_display_3 (.value(counter_1_q));  // open: dp
  Counter #(.width(4), .max('hf), .trigger("falling")) counter_3 (
    .load(choice), .D(start[7:4]), .count(enable), .Q(counter_3_q), .clk(counter_1_carry), .clr(clear));  // open: carry
  Hex_Digit_Display hex_digit_display_4 (.value(counter_2_q));  // open: dp
  // Probe on {counter_3_q, counter_1_q}
  // Probe on {counter_3_q, counter_1_q}
  // Probe on {counter_3_q, counter_1_q}
  // Probe on {counter_3_q, counter_1_q}
  // Probe on {counter_2_q_2, counter_2_q}
  // Probe on {counter_2_q_2, counter_2_q}
  // Probe on {counter_2_q_2, counter_2_q}
  // Probe on {counter_2_q_2, counter_2_q}
  Hex_Digit_Display hex_digit_display_5 (.value(counter_6_q));  // open: dp
  Counter #(.width(4), .max('hf)) counter_4 (
    .load(in_5), .D(start[3:0]), .count(enable), .Q(counter_4_q), .carry(counter_4_carry), .clk(count),
    .clr(clear));
  Hex_Digit_Display hex_digit_display_6 (.value(counter_5_q_2));  // open: dp
  Counter counter_5 (
    .load(in_5), .D(start), .count(enable), .Q({counter_5_q_2, counter_5_q}), .clk(count), .clr(clear));  // open: carry
  Hex_Digit_Display hex_digit_display_7 (.value(counter_4_q));  // open: dp
  Counter #(.width(4), .max('hf), .trigger("falling")) counter_6 (
    .load(in_5), .D(start[7:4]), .count(enable), .Q(counter_6_q), .clk(counter_4_carry), .clr(clear));  // open: carry
  Hex_Digit_Display hex_digit_display_8 (.value(counter_5_q));  // open: dp
  // Probe on {counter_6_q, counter_4_q}
  // Probe on {counter_6_q, counter_4_q}
  // Probe on {counter_6_q, counter_4_q}
  // Probe on {counter_6_q, counter_4_q}
  // Probe on {counter_5_q_2, counter_5_q}
  // Probe on {counter_5_q_2, counter_5_q}
  // Probe on {counter_5_q_2, counter_5_q}
  // Probe on {counter_5_q_2, counter_5_q}
endmodule

module main1 (
  input  count,
  input  enable,
  input  clear,
  input  choice,
  input  choice_2
);

  wire mcmp4_1_carry, mcmp4_3_carry;
  wire [3:0] counter_2_q, counter_2_q_2, mcmp4_1_output, mcmp4_2_output;
  wire [7:0] counter_1_q, mcmp4_3_output;

  MCMP4 mcmp4_1 (
    .count(enable), .clock(count), .Load(choice_2), .clear(clear), .carry(mcmp4_1_carry),
    .Output(mcmp4_1_output));
  Counter #(.trigger("falling")) counter_1 (
    .load(choice_2), .D({8{1'b0}}), .count(enable), .Q(counter_1_q), .clk(count), .clr(clear));  // open: carry
  Hex_Digit_Display hex_digit_display_1 (.value(mcmp4_2_output));  // open: dp
  Hex_Digit_Display hex_digit_display_2 (.value(mcmp4_1_output));  // open: dp
  Hex_Digit_Display hex_digit_display_3 (.value(counter_1_q[7:4]));  // open: dp
  Hex_Digit_Display hex_digit_display_4 (.value(counter_1_q[3:0]));  // open: dp
  MCMP4 mcmp4_2 (
    .count(count), .clock(mcmp4_1_carry), .Load(choice_2), .clear(clear), .Output(mcmp4_2_output));  // open: carry
  // Probe on {mcmp4_2_output, mcmp4_1_output}
  // Probe on {mcmp4_2_output, mcmp4_1_output}
  // Probe on {mcmp4_2_output, mcmp4_1_output}
  // Probe on {mcmp4_2_output, mcmp4_1_output}
  // Probe on counter_1_q
  // Probe on counter_1_q
  // Probe on counter_1_q
  // Probe on counter_1_q
  Hex_Digit_Display hex_digit_display_5 (.value(counter_2_q_2));  // open: dp
  Counter counter_2 (
    .load(choice), .D({8{1'b0}}), .count(count), .Q({counter_2_q_2, counter_2_q}), .clk(count), .clr(clear));  // open: carry
  Hex_Digit_Display hex_digit_display_6 (.value(mcmp4_3_output[7:4]));  // open: dp
  MCMP4 mcmp4_3 (
    .count(enable), .clock(count), .Load(choice), .clear(clear), .carry(mcmp4_3_carry),
    .Output(mcmp4_3_output[3:0]));
  Hex_Digit_Display hex_digit_display_7 (.value(counter_2_q));  // open: dp
  Hex_Digit_Display hex_digit_display_8 (.value(mcmp4_3_output[3:0]));  // open: dp
  MCMP4 mcmp4_4 (
    .count(enable), .clock(mcmp4_3_carry), .Load(choice), .clear(clear), .Output(mcmp4_3_output[7:4]));  // open: carry
  // Probe on {counter_2_q_2, counter_2_q}
  // Probe on {counter_2_q_2, counter_2_q}
  // Probe on {counter_2_q_2, counter_2_q}
  // Probe on {counter_2_q_2, counter_2_q}
  // Probe on mcmp4_3_output
  // Probe on mcmp4_3_output
  // Probe on mcmp4_3_output
  // Probe on mcmp4_3_output
endmodule

module main2 (
  input  count,
  input  enable,
  input  clear,
  input  choice,
  input  choice_2,
  input  [7:0] start
);

  wire cmp4d_1_carry, dcmp4d_1_carry;
  wire [3:0] cmp4d_1_output, cmp4d_2_output, counter_2_q, counter_2_q_2;
  wire [7:0] counter_1_q, dcmp4d_1_output;

  // Probe on start
  // Probe on start
  // Probe on start
  CMP4D cmp4d_1 (
    .Clock(count), .Count(enable), .Clear(clear), .Data(start[3:0]), .Load(choice_2),
    .Output(cmp4d_1_output), .Carry(cmp4d_1_carry));
  Counter #(.trigger("falling")) counter_1 (
    .load(choice_2), .D(start), .count(enable), .Q(counter_1_q), .clk(count), .clr(clear));  // open: carry
  Hex_Digit_Display hex_digit_display_1 (.value(cmp4d_2_output));  // open: dp
  Hex_Digit_Display hex_digit_display_2 (.value(cmp4d_1_output));  // open: dp
  Hex_Digit_Display hex_digit_display_3 (.value(counter_1_q[3:0]));  // open: dp
  Hex_Digit_Display hex_digit_display_4 (.value(counter_1_q[7:4]));  // open: dp
  CMP4D cmp4d_2 (
    .Clock(cmp4d_1_carry), .Count(count), .Clear(clear), .Data(start[7:4]), .Load(choice_2),
    .Output(cmp4d_2_output));  // open: Carry
  // Probe on {cmp4d_2_output, cmp4d_1_output}
  // Probe on {cmp4d_2_output, cmp4d_1_output}
  // Probe on {cmp4d_2_output, cmp4d_1_output}
  // Probe on {cmp4d_2_output, cmp4d_1_output}
  // Probe on counter_1_q
  // Probe on counter_1_q
  // Probe on counter_1_q
  // Probe on counter_1_q
  Hex_Digit_Display hex_digit_display_5 (.value(counter_2_q_2));  // open: dp
  Counter counter_2 (
    .load(choice), .D(start), .count(count), .Q({counter_2_q_2, counter_2_q}), .clk(count), .clr(clear));  // open: carry
  Hex_Digit_Display hex_digit_display_6 (.value(dcmp4d_1_output[7:4]));  // open: dp
  DCMP4D dcmp4d_1 (
    .Clock(count), .Count(enable), .Clear(clear), .Data(start[3:0]), .Load(choice),
    .Output(dcmp4d_1_output[3:0]), .Carry(dcmp4d_1_carry));
  Hex_Digit_Display hex_digit_display_7 (.value(counter_2_q));  // open: dp
  Hex_Digit_Display hex_digit_display_8 (.value(dcmp4d_1_output[3:0]));  // open: dp
  DCMP4D dcmp4d_2 (
    .Clock(dcmp4d_1_carry), .Count(enable), .Clear(clear), .Data(start[7:4]), .Load(choice),
    .Output(dcmp4d_1_output[7:4]));  // open: Carry
  // Probe on {counter_2_q_2, counter_2_q}
  // Probe on {counter_2_q_2, counter_2_q}
  // Probe on {counter_2_q_2, counter_2_q}
  // Probe on {counter_2_q_2, counter_2_q}
  // Probe on dcmp4d_1_output
  // Probe on dcmp4d_1_output
  // Probe on dcmp4d_1_output
  // Probe on dcmp4d_1_output
endmodule

module main3 (
  input  count,
  input  enable,
  input  clear,
  input  choice,
  input  choice_2,
  input  [7:0] start
);

  wire mcmp4d_1_carry, mcmp4d_3_carry;
  wire [3:0] counter_2_q, counter_2_q_2, mcmp4d_1_output, mcmp4d_2_output;
  wire [7:0] counter_1_q, mcmp4d_3_output;

  // Probe on start
  // Probe on start
  // Probe on start
  MCMP4D mcmp4d_1 (
    .count(enable), .clock(count), .Load(choice_2), .clear(clear), .carry(mcmp4d_1_carry),
    .Output(mcmp4d_1_output), .Data(start[3:0]));
  Counter #(.trigger("falling")) counter_1 (
    .load(choice_2), .D(start), .count(enable), .Q(counter_1_q), .clk(count), .clr(clear));  // open: carry
  Hex_Digit_Display hex_digit_display_1 (.value(mcmp4d_2_output));  // open: dp
  Hex_Digit_Display hex_digit_display_2 (.value(mcmp4d_1_output));  // open: dp
  Hex_Digit_Display hex_digit_display_3 (.value(counter_1_q[3:0]));  // open: dp
  Hex_Digit_Display hex_digit_display_4 (.value(counter_1_q[7:4]));  // open: dp
  MCMP4D mcmp4d_2 (
    .count(count), .clock(mcmp4d_1_carry), .Load(choice_2), .clear(clear), .Output(mcmp4d_2_output),
    .Data(start[7:4]));  // open: carry
  // Probe on {mcmp4d_2_output, mcmp4d_1_output}
  // Probe on {mcmp4d_2_output, mcmp4d_1_output}
  // Probe on {mcmp4d_2_output, mcmp4d_1_output}
  // Probe on {mcmp4d_2_output, mcmp4d_1_output}
  // Probe on counter_1_q
  // Probe on counter_1_q
  // Probe on counter_1_q
  // Probe on counter_1_q
  Hex_Digit_Display hex_digit_display_5 (.value(counter_2_q_2));  // open: dp
  Counter counter_2 (
    .load(choice), .D(start), .count(count), .Q({counter_2_q_2, counter_2_q}), .clk(count), .clr(clear));  // open: carry
  Hex_Digit_Display hex_digit_display_6 (.value(mcmp4d_3_output[7:4]));  // open: dp
  MCMP4D mcmp4d_3 (
    .count(enable), .clock(count), .Load(choice), .clear(clear), .carry(mcmp4d_3_carry),
    .Output(mcmp4d_3_output[3:0]), .Data(start[3:0]));
  Hex_Digit_Display hex_digit_display_7 (.value(counter_2_q));  // open: dp
  Hex_Digit_Display hex_digit_display_8 (.value(mcmp4d_3_output[3:0]));  // open: dp
  MCMP4D mcmp4d_4 (
    .count(enable), .clock(mcmp4d_3_carry), .Load(choice), .clear(clear), .Output(mcmp4d_3_output[7:4]),
    .Data(start[7:4]));  // open: carry
  // Probe on {counter_2_q_2, counter_2_q}
  // Probe on {counter_2_q_2, counter_2_q}
  // Probe on {counter_2_q_2, counter_2_q}
  // Probe on {counter_2_q_2, counter_2_q}
  // Probe on mcmp4d_3_output
  // Probe on mcmp4d_3_output
  // Probe on mcmp4d_3_output
  // Probe on mcmp4d_3_output
endmodule

module CMP4 (
  input  Clock,
  input  Count,
  input  Clear,
  output [3:0] Output,
  output Carry
);

  wire d_ff_1_qn, d_ff_2_qn, d_ff_3_qn, d_ff_4_qn;

  D_Flip_Flop #(.trigger("falling")) d_ff_1 (
    .clk(Clock), .D(d_ff_1_qn), .Q(Output[0]), .Qn(d_ff_1_qn), .preset(1'b0), .en(Count), .reset(Clear));
  D_Flip_Flop #(.trigger("falling")) d_ff_2 (
    .clk(Output[0]), .D(d_ff_2_qn), .Q(Output[1]), .Qn(d_ff_2_qn), .preset(1'b0), .en(Count), .reset(Clear));
  D_Flip_Flop #(.trigger("falling")) d_ff_3 (
    .clk(Output[1]), .D(d_ff_3_qn), .Q(Output[2]), .Qn(d_ff_3_qn), .preset(1'b0), .en(Count), .reset(Clear));
  D_Flip_Flop #(.trigger("falling")) d_ff_4 (
    .clk(Output[2]), .D(d_ff_4_qn), .Q(Carry), .Qn(d_ff_4_qn), .preset(1'b0), .en(Count), .reset(Clear));

  assign Output[3] = Carry;

  // Notes on the sheet:
  //   D0
  //   Q0
  //   D1
  //   Q2
  //   Q1
  //   D2
  //   Q3
  //   D3
endmodule

module DCMP4 (
  input  Clock,
  input  Count,
  input  Clear,
  output [3:0] Output,
  output Carry
);

  wire d_ff_1_qn, d_ff_2_qn, d_ff_3_qn, d_ff_4_qn;

  D_Flip_Flop d_ff_1 (
    .clk(Clock), .D(d_ff_1_qn), .Q(Output[0]), .Qn(d_ff_1_qn), .preset(1'b0), .en(Count), .reset(Clear));
  D_Flip_Flop d_ff_2 (
    .clk(Output[0]), .D(d_ff_2_qn), .Q(Output[1]), .Qn(d_ff_2_qn), .preset(1'b0), .en(Count), .reset(Clear));
  D_Flip_Flop d_ff_3 (
    .clk(Output[1]), .D(d_ff_3_qn), .Q(Output[2]), .Qn(d_ff_3_qn), .preset(1'b0), .en(Count), .reset(Clear));
  D_Flip_Flop d_ff_4 (
    .clk(Output[2]), .D(d_ff_4_qn), .Q(Carry), .Qn(d_ff_4_qn), .preset(1'b0), .en(Count), .reset(Clear));

  assign Output[3] = Carry;

  // Notes on the sheet:
  //   D0
  //   Q0
  //   D1
  //   Q1
  //   D2
  //   Q3
  //   Q2
  //   D3
endmodule

module CMP4D (
  input  Clock,
  input  Count,
  input  Clear,
  input  [3:0] Data,
  input  Load,
  output [3:0] Output,
  output Carry
);

  wire and_1_out, and_2_out, and_3_out, and_4_out, and_5_out, and_6_out, and_7_out, and_8_out, and_9_out,
       and_10_out, and_11_out, and_12_out, and_13_out, and_14_out, and_15_out, and_16_out, and_17_out,
       and_18_out, d_ff_1_qn, d_ff_2_qn, d_ff_3_qn, d_ff_4_qn, not_1_out, not_2_out, not_3_out, or_1_out,
       or_2_out, or_3_out, or_4_out, or_5_out, or_6_out, or_7_out, or_8_out;

  and and_1 (and_1_out, Clock, or_4_out);
  or or_1 (or_1_out, and_2_out, and_3_out);
  not not_1 (not_1_out, Clock);
  and and_2 (and_2_out, d_ff_1_qn, not_3_out);
  and and_3 (and_3_out, and_8_out, Data[0]);
  and and_4 (and_4_out, Clock, and_8_out);
  or or_2 (or_2_out, and_4_out, and_5_out);
  and and_5 (and_5_out, not_3_out, Output[0]);
  D_Flip_Flop #(.trigger("falling")) d_ff_1 (
    .clk(and_1_out), .D(or_1_out), .Q(Output[0]), .Qn(d_ff_1_qn), .preset(1'b0), .en(1'b1), .reset(Clear));
  or or_3 (or_3_out, and_6_out, and_7_out);
  and and_6 (and_6_out, d_ff_2_qn, not_3_out);
  and and_7 (and_7_out, and_8_out, Data[1]);
  not not_2 (not_2_out, Count);
  and and_8 (and_8_out, not_2_out, not_1_out, Load);
  or or_4 (or_4_out, and_8_out, Count);
  and and_9 (and_9_out, Clock, and_8_out);
  or or_5 (or_5_out, and_9_out, and_10_out);
  and and_10 (and_10_out, not_3_out, Output[1]);
  D_Flip_Flop #(.trigger("falling")) d_ff_2 (
    .clk(or_2_out), .D(or_3_out), .Q(Output[1]), .Qn(d_ff_2_qn), .preset(1'b0), .en(1'b1), .reset(Clear));
  or or_6 (or_6_out, and_11_out, and_12_out);
  and and_11 (and_11_out, d_ff_3_qn, not_3_out);
  and and_12 (and_12_out, and_8_out, Data[2]);
  and and_13 (and_13_out, Clock, and_8_out);
  or or_7 (or_7_out, and_13_out, and_14_out);
  and and_14 (and_14_out, not_3_out, Output[2]);
  D_Flip_Flop #(.trigger("falling")) d_ff_3 (
    .clk(or_5_out), .D(or_6_out), .Q(Output[2]), .Qn(d_ff_3_qn), .preset(1'b0), .en(1'b1), .reset(Clear));
  or or_8 (or_8_out, and_15_out, and_16_out);
  and and_15 (and_15_out, d_ff_4_qn, not_3_out);
  and and_16 (and_16_out, and_8_out, Data[3]);
  not not_3 (not_3_out, and_8_out);
  D_Flip_Flop #(.trigger("falling")) d_ff_4 (
    .clk(or_7_out), .D(or_8_out), .Q(Output[3]), .Qn(d_ff_4_qn), .preset(1'b0), .en(1'b1), .reset(Clear));
  and and_17 (and_17_out, Output[3], Count);
  and and_18 (and_18_out, Clock, and_8_out);
  or or_9 (Carry, and_17_out, and_18_out);
endmodule

module DCMP4D (
  input  Clock,
  input  Count,
  input  Clear,
  input  [3:0] Data,
  input  Load,
  output [3:0] Output,
  output Carry
);

  wire and_1_out, and_2_out, and_3_out, and_4_out, and_5_out, and_6_out, and_7_out, and_8_out, and_9_out,
       and_10_out, and_11_out, and_12_out, and_13_out, and_14_out, and_15_out, and_16_out, and_17_out,
       and_18_out, d_ff_1_qn, d_ff_2_qn, d_ff_3_qn, d_ff_4_qn, not_1_out, not_2_out, not_3_out, or_1_out,
       or_2_out, or_3_out, or_4_out, or_5_out, or_6_out, or_7_out, or_8_out;

  and and_1 (and_1_out, Clock, or_4_out);
  or or_1 (or_1_out, and_2_out, and_3_out);
  not not_1 (not_1_out, Clock);
  and and_2 (and_2_out, d_ff_1_qn, not_3_out);
  and and_3 (and_3_out, and_8_out, Data[0]);
  and and_4 (and_4_out, Clock, and_8_out);
  or or_2 (or_2_out, and_4_out, and_5_out);
  and and_5 (and_5_out, not_3_out, Output[0]);
  D_Flip_Flop d_ff_1 (
    .clk(and_1_out), .D(or_1_out), .Q(Output[0]), .Qn(d_ff_1_qn), .preset(1'b0), .en(1'b1), .reset(Clear));
  or or_3 (or_3_out, and_6_out, and_7_out);
  and and_6 (and_6_out, d_ff_2_qn, not_3_out);
  and and_7 (and_7_out, and_8_out, Data[1]);
  not not_2 (not_2_out, Count);
  and and_8 (and_8_out, not_2_out, not_1_out, Load);
  or or_4 (or_4_out, and_8_out, Count);
  and and_9 (and_9_out, Clock, and_8_out);
  or or_5 (or_5_out, and_9_out, and_10_out);
  and and_10 (and_10_out, not_3_out, Output[1]);
  D_Flip_Flop d_ff_2 (
    .clk(or_2_out), .D(or_3_out), .Q(Output[1]), .Qn(d_ff_2_qn), .preset(1'b0), .en(1'b1), .reset(Clear));
  or or_6 (or_6_out, and_11_out, and_12_out);
  and and_11 (and_11_out, d_ff_3_qn, not_3_out);
  and and_12 (and_12_out, and_8_out, Data[2]);
  and and_13 (and_13_out, Clock, and_8_out);
  or or_7 (or_7_out, and_13_out, and_14_out);
  and and_14 (and_14_out, not_3_out, Output[2]);
  D_Flip_Flop d_ff_3 (
    .clk(or_5_out), .D(or_6_out), .Q(Output[2]), .Qn(d_ff_3_qn), .preset(1'b0), .en(1'b1), .reset(Clear));
  or or_8 (or_8_out, and_15_out, and_16_out);
  and and_15 (and_15_out, d_ff_4_qn, not_3_out);
  and and_16 (and_16_out, and_8_out, Data[3]);
  not not_3 (not_3_out, and_8_out);
  D_Flip_Flop d_ff_4 (
    .clk(or_7_out), .D(or_8_out), .Q(Output[3]), .Qn(d_ff_4_qn), .preset(1'b0), .en(1'b1), .reset(Clear));
  and and_17 (and_17_out, Output[3], Count);
  and and_18 (and_18_out, Clock, and_8_out);
  or or_9 (Carry, and_17_out, and_18_out);
endmodule

module MCMP4 (
  input  count,
  input  clock,
  input  Load,
  input  clear,
  output carry,
  output [3:0] Output
);

  wire and_1_out, and_2_out, and_3_out, and_4_out, cmp4_1_carry, dcmp4_1_carry, not_1_out;
  wire [3:0] and_5_out, and_6_out, bit_extender_1_out, bit_extender_2_out, cmp4_1_output, dcmp4_1_output;

  not not_1 (not_1_out, Load);
  CMP4 cmp4_1 (.Clock(and_1_out), .Count(count), .Clear(clear), .Output(cmp4_1_output), .Carry(cmp4_1_carry));
  and and_1 (and_1_out, clock, not_1_out);
  DCMP4 dcmp4_1 (.Clock(and_2_out), .Count(count), .Clear(clear), .Output(dcmp4_1_output), .Carry(dcmp4_1_carry));
  and and_2 (and_2_out, clock, Load);
  and and_3 (and_3_out, cmp4_1_carry, not_1_out);
  and and_4 (and_4_out, dcmp4_1_carry, Load);
  assign bit_extender_1_out = {{3{not_1_out}}, not_1_out};  // Bit_Extender bit_extender_1
  assign bit_extender_2_out = {{3{Load}}, Load};  // Bit_Extender bit_extender_2
  or or_1 (carry, and_3_out, and_4_out);
  assign and_5_out = cmp4_1_output & bit_extender_1_out;  // AND_Gate and_5, 4 bits wide
  assign Output = and_5_out | and_6_out;  // OR_Gate or_2, 4 bits wide
  assign and_6_out = dcmp4_1_output & bit_extender_2_out;  // AND_Gate and_6, 4 bits wide
endmodule

module MCMP4D (
  input  count,
  input  clock,
  input  Load,
  input  clear,
  input  [3:0] Data,
  output carry,
  output [3:0] Output
);

  wire and_1_out, and_2_out, and_3_out, and_4_out, cmp4d_1_carry, dcmp4d_1_carry, not_1_out, not_2_out;
  wire [3:0] and_5_out, and_6_out, bit_extender_1_out, bit_extender_2_out, cmp4d_1_output, dcmp4d_1_output;

  not not_1 (not_1_out, Load);
  not not_2 (not_2_out, count);
  and and_1 (and_1_out, clock, not_1_out);
  and and_2 (and_2_out, clock, not_2_out, Load);
  CMP4D cmp4d_1 (
    .Clock(and_1_out), .Count(count), .Clear(clear), .Data(Data), .Load(Load), .Output(cmp4d_1_output),
    .Carry(cmp4d_1_carry));
  DCMP4D dcmp4d_1 (
    .Clock(and_2_out), .Count(count), .Clear(clear), .Data(Data), .Load(Load), .Output(dcmp4d_1_output),
    .Carry(dcmp4d_1_carry));
  and and_3 (and_3_out, cmp4d_1_carry, not_1_out);
  or or_1 (carry, and_3_out, and_4_out);
  and and_4 (and_4_out, dcmp4d_1_carry, Load);
  assign and_5_out = cmp4d_1_output & bit_extender_1_out;  // AND_Gate and_5, 4 bits wide
  assign bit_extender_1_out = {{3{not_1_out}}, not_1_out};  // Bit_Extender bit_extender_1
  assign and_6_out = dcmp4d_1_output & bit_extender_2_out;  // AND_Gate and_6, 4 bits wide
  assign bit_extender_2_out = {{3{Load}}, Load};  // Bit_Extender bit_extender_2
  assign Output = and_5_out | and_6_out;  // OR_Gate or_2, 4 bits wide
  // Probe on Output
endmodule
