// Logisim project 08_FLIP_FLOP_01_V.circ as structural Verilog: 19 circuits, main circuit main
module main (
  input  S,
  input  Clock,
  input  R,
  input  D,
  input  Clock_2,
  input  present,
  input  present_2,
  input  enable,
  input  enable_2,
  input  clear,
  input  clear_2,
  input  J,
  input  J_2,
  input  K,
  input  K_2,
  input  Clock_3,
  input  Clock_4,
  input  present_3,
  input  present_4,
  input  enable_3,
  input  enable_4,
  input  clear_3,
  input  clear_4,
  input  Clock_5,
  input  Clock_6,
  input  D_2,
  input  D_3,
  input  present_5,
  input  present_6,
  input  enable_5,
  input  enable_6,
  input  clear_5,
  input  clear_6,
  input  Clock_7,
  input  Clock_8,
  input  present_7,
  input  present_8,
  input  enable_7,
  input  enable_8,
  input  clear_7,
  input  clear_8,
  input  Clock_9,
  input  Clock_10,
  input  T,
  input  T_2,
  input  present_9,
  input  present_10,
  input  enable_9,
  input  enable_10,
  input  clear_9,
  input  clear_10,
  output out_52,
  output out_53,
  output out_54,
  output out_55,
  output out_56,
  output out_57,
  output out_58,
  output out_59,
  output out_60,
  output out_61,
  output out_62,
  output out_63,
  output out_64,
  output out_65,
  output out_66,
  output out_67,
  output out_68,
  output out_69,
  output out_70,
  output out_71
);

  S_R_Flip_Flop #(.trigger("high")) s_r_ff_1 (
    .S(S), .clk(Clock_2), .R(R), .Q(out_52), .preset(present), .reset(clear), .en(enable));  // open: Qn
  J_K_Flip_Flop #(.trigger("falling")) j_k_ff_1 (
    .J(J), .clk(Clock_3), .K(K), .Q(out_56), .preset(present_3), .en(enable_3), .reset(clear_3));  // open: Qn
  D_Flip_Flop #(.trigger("falling")) d_ff_1 (
    .clk(Clock_5), .D(D_2), .Q(out_60), .preset(present_5), .en(enable_5), .reset(clear_5));  // open: Qn
  T_Flip_Flop #(.trigger("falling")) t_ff_1 (
    .clk(Clock_7), .T(1'b1), .Q(out_64), .preset(present_7), .reset(clear_7), .en(enable_7));  // open: Qn
  T_Flip_Flop #(.trigger("falling")) t_ff_2 (
    .clk(Clock_9), .T(T), .Q(out_68), .preset(present_9), .reset(clear_9), .en(enable_9));  // open: Qn
  RSHE1 rshe1_1 (.Preset(present), .S(S), .H(Clock_2), .R(R), .Clear(clear), .Q(out_53), .Enable(enable));  // open: QN
  JKD jkd_1 (
    .J(J), .CLK(Clock_3), .K(K), .Q(out_57), .Preset(present_3), .Enable(enable_3), .Clear(clear_3));  // open: QN
  DD dd_1 (.D(D_2), .H(Clock_5), .Q(out_61), .Preset(present_5), .Enable(enable_5), .Clear(clear_5));  // open: QN
  TD td_1 (.Clock(Clock_7), .present(present_7), .enable(enable_7), .clear(clear_7), .Q(out_65));  // open: QN
  TLD tld_1 (.T(T), .present(present_9), .enable(enable_9), .clear(clear_9), .Q(out_69), .Clock(Clock_9));  // open: QN
  D_Flip_Flop #(.trigger("high")) d_ff_2 (
    .clk(Clock), .D(D), .Q(out_54), .preset(present_2), .en(enable_2), .reset(clear_2));  // open: Qn
  J_K_Flip_Flop j_k_ff_2 (
    .J(J_2), .clk(Clock_4), .K(K_2), .Q(out_58), .preset(present_4), .en(enable_4), .reset(clear_4));  // open: Qn
  D_Flip_Flop d_ff_3 (
    .clk(Clock_6), .D(D_3), .Q(out_62), .preset(present_6), .en(enable_6), .reset(clear_6));  // open: Qn
  T_Flip_Flop t_ff_3 (
    .clk(Clock_8), .T(1'b1), .Q(out_66), .preset(present_8), .reset(clear_8), .en(enable_8));  // open: Qn
  T_Flip_Flop t_ff_4 (
    .clk(Clock_10), .T(T_2), .Q(out_70), .preset(present_10), .reset(clear_10), .en(enable_10));  // open: Qn
  DE de_1 (.D(D), .H(Clock), .Q(out_55), .Preset(present_2), .Enable(enable_2), .Clear(clear_2));  // open: Q_Not
  JKM jkm_1 (
    .J(J_2), .CLK(Clock_4), .K(K_2), .Q(out_59), .Preset(present_4), .Enable(enable_4), .Clear(clear_4));  // open: QN
  DM dm_1 (.D(D_3), .Q(out_63), .H(Clock_6), .Preset(present_6), .Enable(enable_6), .Clear(clear_6));  // open: QN
  TM tm_1 (.Clock(Clock_8), .present(present_8), .enable(enable_8), .clear(clear_8), .Q(out_67));  // open: QN
  TLM tlm_1 (
    .T(T_2), .present(present_10), .enable(enable_10), .clear(clear_10), .Q(out_71), .clock(Clock_10));  // open: QN
endmodule

module RS (
  input  R,
  input  S,
  output Q,
  output Q_Not
);

  nor nor_1 (Q, R, Q_Not);
  nor nor_2 (Q_Not, Q, S);
endmodule

module RSEM (
  input  S,
  input  R,
  input  Preset,
  input  Enable,
  input  Clear,
  output Q,
  output QN
);

  wire pecm_1_ro, pecm_1_so;

  RS rs_1 (.R(pecm_1_ro), .Q(Q), .Q_Not(QN), .S(pecm_1_so));
  PECM pecm_1 (.Preset(Preset), .SI(S), .Enable(Enable), .RI(R), .Clear(Clear), .SO(pecm_1_so), .RO(pecm_1_ro));
endmodule

module RSEM2 (
  input  S,
  input  R,
  input  Preset,
  input  Enable,
  input  Clear,
  output Q,
  output QN
);

  wire and_1_out, and_2_out, or_1_out, or_2_out;

  and and_1 (and_1_out, S, Enable);
  and and_2 (and_2_out, Enable, R);
  or or_1 (or_1_out, Preset, and_1_out);
  or or_2 (or_2_out, and_2_out, Clear);
  RS rs_1 (.R(or_2_out), .Q(Q), .Q_Not(QN), .S(or_1_out));
endmodule

module RSE (
  input  S,
  input  R,
  input  Preset,
  input  Enable,
  input  Clear,
  output Q,
  output QN
);

  wire pecout_1_clear_out, pecout_1_enable_out, pecout_1_preset_out;

  PECOUT pecout_1 (
    .Preset(Preset), .Clear(Clear), .Enable(Enable), .Preset_out(pecout_1_preset_out),
    .Clear_out(pecout_1_clear_out), .Enable_out(pecout_1_enable_out));
  RSEM rsem_1 (
    .S(S), .R(R), .Preset(pecout_1_preset_out), .Enable(pecout_1_enable_out), .Clear(pecout_1_clear_out),
    .Q(Q), .QN(QN));
endmodule

module RSHEM (
  input  S,
  input  H,
  input  R,
  input  Preset,
  input  Enable,
  input  Clear,
  output Q,
  output QN
);

  wire and_1_out, and_2_out;

  and and_1 (and_1_out, S, H);
  and and_2 (and_2_out, H, R);
  RSEM rsem_1 (.S(and_1_out), .R(and_2_out), .Preset(Preset), .Enable(Enable), .Clear(Clear), .Q(Q), .QN(QN));
endmodule

module RSHE (
  input  S,
  input  H,
  input  R,
  input  Preset,
  input  Enable,
  input  Clear,
  output Q,
  output QN
);

  wire and_1_out, and_2_out;

  and and_1 (and_1_out, S, H);
  and and_2 (and_2_out, H, R);
  RSE rse_1 (.S(and_1_out), .R(and_2_out), .Preset(Preset), .Enable(Enable), .Clear(Clear), .Q(Q), .QN(QN));
endmodule

module RSHE1 (
  input  S,
  input  H,
  input  R,
  input  Preset,
  input  Enable,
  input  Clear,
  output Q,
  output QN
);

  wire pecout_1_clear_out, pecout_1_enable_out, pecout_1_preset_out;

  PECOUT pecout_1 (
    .Preset(Preset), .Clear(Clear), .Enable(Enable), .Preset_out(pecout_1_preset_out),
    .Clear_out(pecout_1_clear_out), .Enable_out(pecout_1_enable_out));
  RSHEM rshem_1 (
    .S(S), .H(H), .R(R), .Preset(pecout_1_preset_out), .Enable(pecout_1_enable_out),
    .Clear(pecout_1_clear_out), .Q(Q), .QN(QN));
endmodule

module DE (
  input  D,
  input  H,
  input  Preset,
  input  Enable,
  input  Clear,
  output Q,
  output Q_Not
);

  wire not_1_out;

  RSHE rshe_1 (.S(D), .Q(Q), .H(H), .QN(Q_Not), .R(not_1_out), .Preset(Preset), .Enable(Enable), .Clear(Clear));
  not not_1 (not_1_out, D);
endmodule

module JKD (
  input  J,
  input  CLK,
  input  K,
  input  Preset,
  input  Enable,
  input  Clear,
  output Q,
  output QN
);

  wire not_1_out, rshe_1_q, rshe_1_qn;

  not not_1 (not_1_out, CLK);
  RSHE rshe_1 (.S(J), .Q(rshe_1_q), .H(CLK), .QN(rshe_1_qn), .R(K), .Preset(Preset), .Enable(Enable), .Clear(Clear));
  RSHE rshe_2 (
    .S(rshe_1_q), .Q(Q), .H(not_1_out), .QN(QN), .R(rshe_1_qn), .Preset(Preset), .Enable(Enable),
    .Clear(Clear));
endmodule

module JKM (
  input  J,
  input  CLK,
  input  K,
  input  Preset,
  input  Enable,
  input  Clear,
  output Q,
  output QN
);

  wire not_1_out, rshe_1_q, rshe_1_qn;

  RSHE rshe_1 (
    .S(J), .Q(rshe_1_q), .H(not_1_out), .QN(rshe_1_qn), .R(K), .Preset(Preset), .Enable(Enable), .Clear(Clear));
  not not_1 (not_1_out, CLK);
  RSHE rshe_2 (.S(rshe_1_q), .Q(Q), .H(CLK), .QN(QN), .R(rshe_1_qn), .Preset(Preset), .Enable(Enable), .Clear(Clear));
endmodule

module DD (
  input  D,
  input  H,
  input  Preset,
  input  Enable,
  input  Clear,
  output Q,
  output QN
);

  wire not_1_out;

  not not_1 (not_1_out, D);
  JKD jkd_1 (.J(D), .CLK(H), .K(not_1_out), .Q(Q), .QN(QN), .Preset(Preset), .Enable(Enable), .Clear(Clear));
endmodule

module DM (
  input  D,
  input  H,
  input  Preset,
  input  Enable,
  input  Clear,
  output Q,
  output QN
);

  wire not_1_out;

  not not_1 (not_1_out, D);
  JKM jkm_1 (.J(D), .CLK(H), .K(not_1_out), .Q(Q), .QN(QN), .Preset(Preset), .Enable(Enable), .Clear(Clear));
endmodule

module TD (
  input  Clock,
  input  present,
  input  enable,
  input  clear,
  output Q,
  output QN
);

  DD dd_1 (.D(QN), .H(Clock), .Q(Q), .QN(QN), .Preset(present), .Enable(enable), .Clear(clear));
endmodule

module TM (
  input  Clock,
  input  present,
  input  enable,
  input  clear,
  output Q,
  output QN
);

  DM dm_1 (.D(QN), .Q(Q), .H(Clock), .QN(QN), .Preset(present), .Enable(enable), .Clear(clear));
endmodule

module TLD (
  input  Clock,
  input  T,
  input  present,
  input  enable,
  input  clear,
  output Q,
  output QN
);

  wire and_1_out, and_2_out;

  and and_1 (and_1_out, Clock, T);
  and and_2 (and_2_out, T, enable);
  DD dd_1 (.D(QN), .H(and_1_out), .Q(Q), .QN(QN), .Preset(present), .Enable(and_2_out), .Clear(clear));
endmodule

module TLM (
  input  clock,
  input  T,
  input  present,
  input  enable,
  input  clear,
  output Q,
  output QN
);

  wire and_1_out, and_2_out;

  and and_1 (and_1_out, clock, T);
  and and_2 (and_2_out, T, enable);
  DM dm_1 (.D(QN), .Q(Q), .H(and_1_out), .QN(QN), .Preset(present), .Enable(and_2_out), .Clear(clear));
endmodule

module PECOUT (
  input  Preset,
  input  Clear,
  input  Enable,
  output Preset_out,
  output Clear_out,
  output Enable_out
);

  wire nor_1_out, not_1_out;

  not not_1 (not_1_out, Clear);
  nor nor_1 (nor_1_out, Clear, Preset);
  and and_1 (Preset_out, not_1_out, Preset);
  and and_2 (Enable_out, nor_1_out, Enable);

  assign Clear_out = Clear;
endmodule

module PECM (
  input  Preset,
  input  SI,
  input  Enable,
  input  RI,
  input  Clear,
  output SO,
  output RO
);

  wire and_1_out, and_2_out;

  or or_1 (SO, Preset, and_1_out);
  and and_1 (and_1_out, SI, Enable);
  and and_2 (and_2_out, Enable, RI);
  or or_2 (RO, and_2_out, Clear);
endmodule
