// Logisim project 08_MEMORY.circ as structural Verilog: 4 circuits, main circuit main
module main (
  input  clear,
  input  enable,
  input  H,
  input  [3:0] D,
  input  [7:0] A,
  input  [7:0] DE,
  input  [1:0] A_2,
  input  [3:0] D_2,
  input  sel,
  input  H_2,
  input  ld,
  input  clr,
  input  clr_2,
  input  load,
  input  H_3,
  input  sel_2,
  input  str,
  input  [1:0] A_3,
  input  sel_3,
  output [7:0] DS
);

  wire not_1_out, ram4_1_select_data_0, ram4_1_select_data_1, ram4_1_select_data_2, ram4_1_select_data_3,
       rom4_1_select_data_0, rom4_1_select_data_1, rom4_1_select_data_2, rom4_1_select_data_3;
  wire [3:0] ram4_1_data, ram4_1_data_0, ram4_1_data_1, ram4_1_data_2, ram4_1_data_3, ram_1_data,
       reg4_1_output, register_1_q, rom4_1_data, rom4_1_data_0, rom4_1_data_1, rom4_1_data_2, rom4_1_data_3,
       rom_1_data;
  wire [7:0] ram_2_data;

  // Probe on D
  // Probe on D
  // Probe on D
  // Probe on D_2
  // Probe on D_2
  // Probe on D_2
  REG4 reg4_1 (.Data(D), .Clock(H), .Enable(enable), .Clear(clear), .Output(reg4_1_output));
  Hex_Digit_Display hex_digit_display_1 (.value(ram4_1_data_0), .dp(ram4_1_select_data_0));
  // Probe on reg4_1_output
  // Probe on reg4_1_output
  // Probe on reg4_1_output
  // Probe on reg4_1_output
  Hex_Digit_Display hex_digit_display_2 (.value(ram4_1_data_1), .dp(ram4_1_select_data_1));
  Hex_Digit_Display hex_digit_display_3 (.value(ram4_1_data_2), .dp(ram4_1_select_data_2));
  Register #(.width(4)) register_1 (.D(D), .en(enable), .Q(register_1_q), .clk(H), .clr(clear));
  Hex_Digit_Display hex_digit_display_4 (.value(ram4_1_data_3), .dp(ram4_1_select_data_3));
  RAM4 ram4_1 (
    .Input(D_2), .Store(str), .Address(A_2), .Load(load), .Select(sel_2), .Clock(H_3), .Clear(clr_2),
    .Data_0(ram4_1_data_0), .Data_1(ram4_1_data_1), .Data_2(ram4_1_data_2), .Data_3(ram4_1_data_3),
    .Data(ram4_1_data), .Select_data_0(ram4_1_select_data_0), .Select_data_1(ram4_1_select_data_1),
    .Select_data_2(ram4_1_select_data_2), .Select_data_3(ram4_1_select_data_3));
  Pull_Resistor pull_resistor_1 (.node(ram4_1_data));
  RAM #(.addrWidth(2), .dataWidth(4), .bus("separate")) ram_1 (
    .addr(A_2), .din(D_2), .data(ram_1_data), .str(str), .sel(sel_2), .clk(H_3), .ld(load), .clr(clr_2));
  Pull_Resistor pull_resistor_2 (.node(ram_1_data));
  // Probe on register_1_q
  // Probe on register_1_q
  // Probe on register_1_q
  // Probe on register_1_q
  // Probe on ram4_1_data
  // Probe on ram4_1_data
  // Probe on ram4_1_data
  // Probe on ram4_1_data
  // Probe on ram_1_data
  // Probe on ram_1_data
  // Probe on ram_1_data
  // Probe on ram_1_data
  Hex_Digit_Display hex_digit_display_5 (.value(rom4_1_data_1), .dp(rom4_1_select_data_1));
  Hex_Digit_Display hex_digit_display_6 (.value(rom4_1_data_0), .dp(rom4_1_select_data_0));
  RAM ram_2 (.addr(A), .data(ram_2_data), .sel(sel), .clk(H_2), .ld(ld), .clr(clr));
  Hex_Digit_Display hex_digit_display_7 (.value(rom4_1_data_2), .dp(rom4_1_select_data_2));
  Hex_Digit_Display hex_digit_display_8 (.value(rom4_1_data_3), .dp(rom4_1_select_data_3));
  ROM4 rom4_1 (
    .Select(sel_3), .Address(A_3), .Select_data_0(rom4_1_select_data_0),
    .Select_data_1(rom4_1_select_data_1), .Data_0(rom4_1_data_0), .Select_data_2(rom4_1_select_data_2),
    .Data_1(rom4_1_data_1), .Select_data_3(rom4_1_select_data_3), .Data_2(rom4_1_data_2),
    .Data_3(rom4_1_data_3), .Data(rom4_1_data));
  Pull_Resistor pull_resistor_3 (.node(rom4_1_data));
  // Probe on rom4_1_data
  // Probe on rom4_1_data
  // Probe on rom4_1_data
  // Probe on rom4_1_data
  ROM #(.addrWidth(2), .dataWidth(4)) rom_1 (.addr(A_3), .data(rom_1_data), .sel(sel_3));
  // Probe on rom_1_data
  // Probe on rom_1_data
  Pull_Resistor pull_resistor_4 (.node(rom_1_data));
  // Probe on rom_1_data
  // Probe on rom_1_data
  not not_1 (not_1_out, ld);
  Transistor #(.\type ("n"), .gate("br"), .width(8)) transistor_1 (.in(DE), .out(ram_2_data), .gate(not_1_out));
  Pull_Resistor pull_resistor_5 (.node(ram_2_data));
  Transistor #(.\type ("n"), .gate("br"), .width(8)) transistor_2 (.in(ram_2_data), .out(DS), .gate(ld));
  Pull_Resistor pull_resistor_6 (.node(DS));

  // Notes on the sheet:
  //   contents of rom_1 (hex, n*v repeats v):
  //   3 7 a f
endmodule

module REG4 (
  input  [3:0] Data,
  input  Clock,
  input  Enable,
  input  Clear,
  output [3:0] Output
);

  D_Flip_Flop d_ff_1 (.clk(Clock), .D(Data[3]), .Q(Output[3]), .preset(1'b0), .en(Enable), .reset(Clear));  // open: Qn
  D_Flip_Flop d_ff_2 (.clk(Clock), .D(Data[2]), .Q(Output[2]), .preset(1'b0), .en(Enable), .reset(Clear));  // open: Qn
  D_Flip_Flop d_ff_3 (.clk(Clock), .D(Data[1]), .Q(Output[1]), .preset(1'b0), .en(Enable), .reset(Clear));  // open: Qn
  D_Flip_Flop d_ff_4 (.clk(Clock), .D(Data[0]), .Q(Output[0]), .preset(1'b0), .en(Enable), .reset(Clear));  // open: Qn
endmodule

module RAM4 (
  input  [3:0] Input,
  input  Store,
  input  [1:0] Address,
  input  Load,
  input  Select,
  input  Clock,
  input  Clear,
  output Select_data_0,
  output [3:0] Data_0,
  output Select_data_1,
  output [3:0] Data_1,
  output Select_data_2,
  output [3:0] Data_2,
  output Select_data_3,
  output [3:0] Data_3,
  output [3:0] Data
);

  wire and_1_out, and_2_out, demultiplexer_1_out0, demultiplexer_1_out1, demultiplexer_1_out2,
       demultiplexer_1_out3;

  and and_1 (and_1_out, Store, Select);
  and and_2 (and_2_out, Load, Select);
  Decoder #(.select(2), .disabled(0)) decoder_1 (
    .out0(Select_data_0), .out1(Select_data_1), .out2(Select_data_2), .out3(Select_data_3), .sel(Address),
    .en(Select));
  Demultiplexer #(.select(2), .disabled(0)) demultiplexer_1 (
    .out0(demultiplexer_1_out0), .out1(demultiplexer_1_out1), .out2(demultiplexer_1_out2),
    .out3(demultiplexer_1_out3), .in(Clock), .sel(Address), .en(and_1_out));
  Register #(.width(4)) register_1 (.D(Input), .en(Select), .Q(Data_0), .clk(demultiplexer_1_out0), .clr(Clear));
  Register #(.width(4)) register_2 (.D(Input), .en(Select), .Q(Data_1), .clk(demultiplexer_1_out1), .clr(Clear));
  Register #(.width(4)) register_3 (.D(Input), .en(Select), .Q(Data_2), .clk(demultiplexer_1_out2), .clr(Clear));
  Register #(.width(4)) register_4 (.D(Input), .en(Select), .Q(Data_3), .clk(demultiplexer_1_out3), .clr(Clear));
  Multiplexer #(.select(2), .width(4), .disabled(0)) multiplexer_1 (
    .in0(Data_0), .in1(Data_1), .in2(Data_2), .in3(Data_3), .out(Data), .sel(Address), .en(and_2_out));

  // Notes on the sheet:
  //   DISPLAY
endmodule

module ROM4 (
  input  Select,
  input  [1:0] Address,
  output Select_data_0,
  output Select_data_1,
  output [3:0] Data_0,
  output Select_data_2,
  output [3:0] Data_1,
  output Select_data_3,
  output [3:0] Data_2,
  output [3:0] Data_3,
  output [3:0] Data
);

  Decoder #(.select(2), .disabled(0)) decoder_1 (
    .out0(Select_data_0), .out1(Select_data_1), .out2(Select_data_2), .out3(Select_data_3), .sel(Address),
    .en(Select));
  Multiplexer #(.select(2), .width(4), .disabled(0)) multiplexer_1 (
    .in0(4'b0011), .in1(4'b0111), .in2(4'b1010), .in3(4'b1111), .out(Data), .sel(Address), .en(Select));
  Pull_Resistor pull_resistor_1 (.node(Data));
  // Probe on 4'b0011
  // Probe on 4'b0011
  // Probe on 4'b0011
  // Probe on 4'b0111
  // Probe on 4'b0111
  // Probe on 4'b0111
  // Probe on 4'b1010
  // Probe on 4'b1010
  // Probe on 4'b1010
  // Probe on 4'b1111
  // Probe on 4'b1111
  // Probe on 4'b1111

  assign Data_0 = 4'b0011;
  assign Data_1 = 4'b0111;
  assign Data_2 = 4'b1010;
  assign Data_3 = 4'b1111;

  // Notes on the sheet:
  //   DISPLAY
endmodule
