// Logisim project 10_MEMORY_V.circ as structural Verilog: 5 circuits, main circuit main
module main (
  input  [1:0] A,
  input  [3:0] D,
  input  [7:0] A_2,
  input  [7:0] DE,
  input  sel,
  input  clr,
  input  H,
  input  load,
  input  ld,
  input  H_2,
  input  clr_2,
  input  sel_2,
  input  str,
  input  [1:0] A_3,
  input  sel_3,
  output [7:0] DS
);

  wire not_1_out, ram4_1_select_data_0, ram4_1_select_data_1, ram4_1_select_data_2, ram4_1_select_data_3,
       rom4_1_select_data_0, rom4_1_select_data_1, rom4_1_select_data_2, rom4_1_select_data_3;
  wire [3:0] ram4_1_data, ram4_1_data_0, ram4_1_data_1, ram4_1_data_2, ram4_1_data_3, ram4d_1_data,
       ram_1_data, rom4_1_data, rom4_1_data_0, rom4_1_data_1, rom4_1_data_2, rom4_1_data_3, rom4d_1_data,
       rom_1_data;
  wire [7:0] ram_2_data;

  // Probe on D
  // Probe on D
  // Probe on D
  Hex_Digit_Display hex_digit_display_1 (.value(ram4_1_data_0), .dp(ram4_1_select_data_0));
  Hex_Digit_Display hex_digit_display_2 (.value(ram4_1_data_1), .dp(ram4_1_select_data_1));
  Hex_Digit_Display hex_digit_display_3 (.value(ram4_1_data_3), .dp(ram4_1_select_data_3));
  Hex_Digit_Display hex_digit_display_4 (.value(ram4_1_data_2), .dp(ram4_1_select_data_2));
  RAM #(.addrWidth(2), .dataWidth(4), .bus("separate")) ram_1 (
    .addr(A), .din(D), .data(ram_1_data), .str(str), .sel(sel_2), .clk(H_2), .ld(load), .clr(clr));
  RAM4 ram4_1 (
    .Input(D), .Store(str), .Address(A), .Load(load), .Select(sel_2), .Clock(H_2), .Clear(clr),
    .Data_0(ram4_1_data_0), .Data_1(ram4_1_data_1), .Data_2(ram4_1_data_2), .Data_3(ram4_1_data_3),
    .Data(ram4_1_data), .Select_data_0(ram4_1_select_data_0), .Select_data_1(ram4_1_select_data_1),
    .Select_data_2(ram4_1_select_data_2), .Select_data_3(ram4_1_select_data_3));
  // Probe on ram4_1_data
  Pull_Resistor pull_resistor_1 (.node(ram4_1_data));
  // Probe on ram4_1_data
  // Probe on ram4_1_data
  // Probe on ram4_1_data
  // Probe on ram_1_data
  // Probe on ram_1_data
  Pull_Resistor pull_resistor_2 (.node(ram_1_data));
  // Probe on ram_1_data
  // Probe on ram_1_data
  RAM4D ram4d_1 (
    .Input(D), .Store(str), .Address(A), .Load(load), .Select(sel_2), .Clock(H_2), .Clear(clr),
    .Data(ram4d_1_data));
  // Probe on ram4d_1_data
  // Probe on ram4d_1_data
  Pull_Resistor pull_resistor_3 (.node(ram4d_1_data));
  // Probe on ram4d_1_data
  // Probe on ram4d_1_data
  Hex_Digit_Display hex_digit_display_5 (.value(rom4_1_data_1), .dp(rom4_1_select_data_1));
  Hex_Digit_Display hex_digit_display_6 (.value(rom4_1_data_0), .dp(rom4_1_select_data_0));
  RAM ram_2 (.addr(A_2), .data(ram_2_data), .sel(sel), .clk(H), .ld(ld), .clr(clr_2));
  Hex_Digit_Display hex_digit_display_7 (.value(rom4_1_data_3), .dp(rom4_1_select_data_3));
  Hex_Digit_Display hex_digit_display_8 (.value(rom4_1_data_2), .dp(rom4_1_select_data_2));
  ROM4 rom4_1 (
    .Select(sel_3), .Address(A_3), .Select_data_0(rom4_1_select_data_0),
    .Select_data_1(rom4_1_select_data_1), .Data_0(rom4_1_data_0), .Select_data_2(rom4_1_select_data_2),
    .Data_1(rom4_1_data_1), .Select_data_3(rom4_1_select_data_3), .Data_2(rom4_1_data_2),
    .Data_3(rom4_1_data_3), .Data(rom4_1_data));
  Pull_Resistor pull_resistor_4 (.node(rom4_1_data));
  ROM #(.addrWidth(2), .dataWidth(4)) rom_1 (.addr(A_3), .data(rom_1_data), .sel(sel_3));
  Pull_Resistor pull_resistor_5 (.node(rom_1_data));
  ROM4D rom4d_1 (.Address(A_3), .Select(sel_3), .Data(rom4d_1_data));
  Pull_Resistor pull_resistor_6 (.node(rom4d_1_data));
  // Probe on rom4_1_data
  // Probe on rom4_1_data
  // Probe on rom4_1_data
  // Probe on rom4_1_data
  // Probe on rom_1_data
  // Probe on rom_1_data
  // Probe on rom_1_data
  // Probe on rom_1_data
  // Probe on rom4d_1_data
  // Probe on rom4d_1_data
  // Probe on rom4d_1_data
  // Probe on rom4d_1_data
  // Probe on DE
  // Probe on DE
  // Probe on DE
  not not_1 (not_1_out, ld);
  Transistor #(.\type ("n"), .gate("br"), .width(8)) transistor_1 (.in(DE), .out(ram_2_data), .gate(not_1_out));
  Pull_Resistor pull_resistor_7 (.node(ram_2_data));
  // Probe on DS
  // Probe on DS
  // Probe on DS
  Transistor #(.\type ("n"), .gate("br"), .width(8)) transistor_2 (.in(ram_2_data), .out(DS), .gate(ld));
  Pull_Resistor pull_resistor_8 (.node(DS));

  // Notes on the sheet:
  //   contents of rom_1 (hex, n*v repeats v):
  //   3 7 a f
endmodule

module RAM4 (
  input  [3:0] Input,
  input  Store,
  input  [1:0] Address,
  input  Load,
  input  Select,
  input  Clock,
  input  Clear,
  output Select_data_0,
  output [3:0] Data_0,
  output Select_data_1,
  output [3:0] Data_1,
  output Select_data_2,
  output [3:0] Data_2,
  output Select_data_3,
  output [3:0] Data_3,
  output [3:0] Data
);

  wire and_1_out, and_2_out, demultiplexer_1_out0, demultiplexer_1_out1, demultiplexer_1_out2,
       demultiplexer_1_out3;

  and and_1 (and_1_out, Store, Select);
  and and_2 (and_2_out, Load, Select);
  Decoder #(.select(2), .disabled(0)) decoder_1 (
    .out0(Select_data_0), .out1(Select_data_1), .out2(Select_data_2), .out3(Select_data_3), .sel(Address),
    .en(Select));
  Demultiplexer #(.select(2), .disabled(0)) demultiplexer_1 (
    .out0(demultiplexer_1_out0), .out1(demultiplexer_1_out1), .out2(demultiplexer_1_out2),
    .out3(demultiplexer_1_out3), .in(Clock), .sel(Address), .en(and_1_out));
  Register #(.width(4)) register_1 (.D(Input), .en(Select), .Q(Data_0), .clk(demultiplexer_1_out0), .clr(Clear));
  Register #(.width(4)) register_2 (.D(Input), .en(Select), .Q(Data_1), .clk(demultiplexer_1_out1), .clr(Clear));
  Register #(.width(4)) register_3 (.D(Input), .en(Select), .Q(Data_2), .clk(demultiplexer_1_out2), .clr(Clear));
  Register #(.width(4)) register_4 (.D(Input), .en(Select), .Q(Data_3), .clk(demultiplexer_1_out3), .clr(Clear));
  Multiplexer #(.select(2), .width(4), .disabled(0)) multiplexer_1 (
    .in0(Data_0), .in1(Data_1), .in2(Data_2), .in3(Data_3), .out(Data), .sel(Address), .en(and_2_out));

  // Notes on the sheet:
  //   DISPLAY
endmodule

module ROM4 (
  input  Select,
  input  [1:0] Address,
  output Select_data_0,
  output Select_data_1,
  output [3:0] Data_0,
  output Select_data_2,
  output [3:0] Data_1,
  output Select_data_3,
  output [3:0] Data_2,
  output [3:0] Data_3,
  output [3:0] Data
);

  Decoder #(.select(2), .disabled(0)) decoder_1 (
    .out0(Select_data_0), .out1(Select_data_1), .out2(Select_data_2), .out3(Select_data_3), .sel(Address),
    .en(Select));
  Multiplexer #(.select(2), .width(4), .disabled(0)) multiplexer_1 (
    .in0(4'b0011), .in1(4'b0111), .in2(4'b1010), .in3(4'b1111), .out(Data), .sel(Address), .en(Select));
  Pull_Resistor pull_resistor_1 (.node(Data));
  // Probe on 4'b0011
  // Probe on 4'b0011
  // Probe on 4'b0011
  // Probe on 4'b0111
  // Probe on 4'b0111
  // Probe on 4'b0111
  // Probe on 4'b1010
  // Probe on 4'b1010
  // Probe on 4'b1010
  // Probe on 4'b1111
  // Probe on 4'b1111
  // Probe on 4'b1111

  assign Data_0 = 4'b0011;
  assign Data_1 = 4'b0111;
  assign Data_2 = 4'b1010;
  assign Data_3 = 4'b1111;

  // Notes on the sheet:
  //   DISPLAY
endmodule

module RAM4D (
  input  [3:0] Input,
  input  Store,
  input  [1:0] Address,
  input  Load,
  input  Select,
  input  Clock,
  input  Clear,
  output [3:0] Data
);

  wire and_1_out, and_2_out, demultiplexer_1_out0, demultiplexer_1_out1, demultiplexer_1_out2,
       demultiplexer_1_out3;
  wire [3:0] register_1_q, register_2_q, register_3_q, register_4_q;

  and and_1 (and_1_out, Store, Select);
  and and_2 (and_2_out, Load, Select);
  Demultiplexer #(.select(2), .disabled(0)) demultiplexer_1 (
    .out0(demultiplexer_1_out0), .out1(demultiplexer_1_out1), .out2(demultiplexer_1_out2),
    .out3(demultiplexer_1_out3), .in(Clock), .sel(Address), .en(and_1_out));
  Register #(.width(4)) register_1 (.D(Input), .en(Select), .Q(register_1_q), .clk(demultiplexer_1_out0), .clr(Clear));
  Register #(.width(4)) register_2 (.D(Input), .en(Select), .Q(register_2_q), .clk(demultiplexer_1_out1), .clr(Clear));
  Register #(.width(4)) register_3 (.D(Input), .en(Select), .Q(register_3_q), .clk(demultiplexer_1_out2), .clr(Clear));
  Register #(.width(4)) register_4 (.D(Input), .en(Select), .Q(register_4_q), .clk(demultiplexer_1_out3), .clr(Clear));
  Multiplexer #(.select(2), .width(4), .disabled(0)) multiplexer_1 (
    .in0(register_1_q), .in1(register_2_q), .in2(register_3_q), .in3(register_4_q), .out(Data),
    .sel(Address), .en(and_2_out));
endmodule

module ROM4D (
  input  [1:0] Address,
  input  Select,
  output [3:0] Data
);

  Multiplexer #(.select(2), .width(4), .disabled(0)) multiplexer_1 (
    .in0(4'b0011), .in1(4'b0111), .in2(4'b1010), .in3(4'b1111), .out(Data), .sel(Address), .en(Select));
  Pull_Resistor pull_resistor_1 (.node(Data));
endmodule
