// Logisim project 11_RAND_V.circ as structural Verilog: 19 circuits, main circuit main
module main (
  input  H,
  input  Enable,
  input  [3:0] in_3,
  input  [7:0] MAX,
  input  [7:0] MIN,
  input  Clock,
  input  Enable_2,
  input  Clear,
  output [15:0] Output,
  output Clock_out
);

  wire random_2_p5, random_3_p4, srand8_2_clock_out, srand8_3_clock_out;
  wire [3:0] random_1_out, sram4m_1_output, srand4_1_output, srand4s_1_output, sranm4b_1_output;
  wire [7:0] randm_1_output, srand8_1_output, sranmm_1_o;

  // Probe on MAX
  // Probe on MAX
  // Probe on MAX
  // Probe on MIN
  // Probe on MIN
  // Probe on MIN
  Random #(.width(4)) random_1 (.clk(H), .next(Enable), .out(random_1_out), .clr(1'b0));
  SRAND4 srand4_1 (.Clear(1'b0), .Enable(Enable), .Clock(H), .Output(srand4_1_output));  // open: Clock_out
  SRAND8 srand8_1 (.Clear(1'b0), .Enable(Enable), .Clock(H), .Output(srand8_1_output));  // open: Clock_out
  RANDM randm_1 (.H(H), .Enable(Enable), .Max(MAX), .Output(randm_1_output));  // open: def
  SRANMM sranmm_1 (.Max(MAX), .Min(MIN), .H(H), .Enable(Enable), .O(sranmm_1_o));
  SRAND8 srand8_2 (
    .Clear(Clear), .Enable(Enable_2), .Clock(Clock), .Output(Output[7:0]), .Clock_out(srand8_2_clock_out));
  // Probe on random_1_out
  // Probe on random_1_out
  // Probe on random_1_out
  // Probe on random_1_out
  // Probe on srand4_1_output
  // Probe on srand4_1_output
  // Probe on srand4_1_output
  // Probe on srand4_1_output
  // Probe on srand8_1_output
  // Probe on srand8_1_output
  // Probe on srand8_1_output
  // Probe on srand8_1_output
  // Probe on randm_1_output
  // Probe on randm_1_output
  // Probe on randm_1_output
  // Probe on randm_1_output
  // Probe on sranmm_1_o
  // Probe on sranmm_1_o
  // Probe on sranmm_1_o
  // Probe on sranmm_1_o
  SRAND8 srand8_3 (
    .Clear(Clear), .Enable(Enable_2), .Clock(srand8_2_clock_out), .Output(Output[15:8]),
    .Clock_out(srand8_3_clock_out));
  // Probe on Output
  // Probe on Output
  or or_1 (Clock_out, srand8_3_clock_out, srand8_2_clock_out);
  SRAM4M sram4m_1 (.Clear(1'b0), .Enable(Enable), .Clock(H), .Output(sram4m_1_output));  // open: Clock_out
  SRAND4S srand4s_1 (.Clear(1'b0), .Enable(Enable), .Clock(H), .Output(srand4s_1_output));  // open: Clock_out
  SRANM4B sranm4b_1 (
    .Clear(1'b0), .Enable(Enable), .Clock(H), .Output(sranm4b_1_output), .MAX(in_3));  // open: Clock_out
  // Random random_2: pin names not known; wires that end beside it: H, Enable, MAX, MIN, random_2_p5
  // Probe on sram4m_1_output
  // Probe on sram4m_1_output
  // Probe on sram4m_1_output
  // Probe on sram4m_1_output
  // Probe on srand4s_1_output
  // Probe on srand4s_1_output
  // Probe on srand4s_1_output
  // Probe on srand4s_1_output
  // Probe on sranm4b_1_output
  // Probe on sranm4b_1_output
  // Probe on sranm4b_1_output
  // Probe on sranm4b_1_output
  // Random random_3: pin names not known; wires that end beside it: H, Enable, MAX, random_3_p4
  // Probe on random_3_p4
  // Probe on random_3_p4
  // Probe on random_3_p4
  // Probe on random_3_p4
  // Probe on random_2_p5
  // Probe on random_2_p5
  // Probe on random_2_p5
  // Probe on random_2_p5

  // Notes on the sheet:
  //   RANDM
  //   other_chip8.circ
  //   Other.jar
  //   Other.jar
endmodule

module SRAND4 (
  input  Clear,
  input  Enable,
  input  Clock,
  output Clock_out,
  output [3:0] Output
);

  wire and_1_out, not_1_out, not_2_out, not_3_out, not_4_out, or_1_out, xor_1_out;

  or or_1 (or_1_out, xor_1_out, and_1_out);
  and and_1 (and_1_out, not_1_out, not_2_out, not_3_out, not_4_out);
  D_Flip_Flop d_ff_1 (.clk(Clock), .D(or_1_out), .Q(Output[0]), .preset(1'b0), .en(Enable), .reset(Clear));  // open: Qn
  not not_1 (not_1_out, Output[3]);
  not not_2 (not_2_out, Output[2]);
  not not_3 (not_3_out, Output[1]);
  not not_4 (not_4_out, Output[0]);
  xor xor_1 (xor_1_out, Clock_out, Output[1]);
  D_Flip_Flop d_ff_2 (
    .clk(Clock), .D(Output[0]), .Q(Output[1]), .preset(1'b0), .en(Enable), .reset(Clear));  // open: Qn
  D_Flip_Flop d_ff_3 (
    .clk(Clock), .D(Output[1]), .Q(Output[2]), .preset(1'b0), .en(Enable), .reset(Clear));  // open: Qn
  D_Flip_Flop d_ff_4 (
    .clk(Clock), .D(Output[2]), .Q(Output[3]), .preset(1'b0), .en(Enable), .reset(Clear));  // open: Qn
  D_Flip_Flop d_ff_5 (
    .clk(Clock), .D(Output[3]), .Q(Clock_out), .preset(1'b0), .en(Enable), .reset(Clear));  // open: Qn
  // Probe on Output
  // Probe on Output

  // Notes on the sheet:
  //   E
  //   Q0
  //   Q1
  //   Q1
  //   Q2
  //   Q3
  //   Q4
endmodule

module SRAM4M (
  input  Clear,
  input  Enable,
  input  Clock,
  output Clock_out,
  output [3:0] Output
);

  wire nor_1_out, or_1_out, xor_1_out;

  or or_1 (or_1_out, xor_1_out, nor_1_out);
  nor nor_1 (nor_1_out, Output[3], Output[2], Output[1], Output[0]);
  D_Flip_Flop d_ff_1 (.clk(Clock), .D(or_1_out), .Q(Output[0]), .preset(1'b0), .en(Enable), .reset(Clear));  // open: Qn
  xor xor_1 (xor_1_out, Clock_out, Output[1]);
  D_Flip_Flop d_ff_2 (
    .clk(Clock), .D(Output[0]), .Q(Output[1]), .preset(1'b0), .en(Enable), .reset(Clear));  // open: Qn
  D_Flip_Flop d_ff_3 (
    .clk(Clock), .D(Output[1]), .Q(Output[2]), .preset(1'b0), .en(Enable), .reset(Clear));  // open: Qn
  D_Flip_Flop d_ff_4 (
    .clk(Clock), .D(Output[2]), .Q(Output[3]), .preset(1'b0), .en(Enable), .reset(Clear));  // open: Qn
  D_Flip_Flop d_ff_5 (
    .clk(Clock), .D(Output[3]), .Q(Clock_out), .preset(1'b0), .en(Enable), .reset(Clear));  // open: Qn
  // Probe on Output
  // Probe on Output

  // Notes on the sheet:
  //   E
  //   Q0
  //   Q1
  //   Q1
  //   Q2
  //   Q3
  //   Q4
endmodule

module SRAND4S (
  input  Clear,
  input  Enable,
  input  Clock,
  output Clock_out,
  output [3:0] Output
);

  wire cstate_1_out;

  D_Flip_Flop d_ff_1 (
    .clk(Clock), .D(cstate_1_out), .Q(Output[0]), .preset(1'b0), .en(Enable), .reset(Clear));  // open: Qn
  D_Flip_Flop d_ff_2 (
    .clk(Clock), .D(Output[0]), .Q(Output[1]), .preset(1'b0), .en(Enable), .reset(Clear));  // open: Qn
  D_Flip_Flop d_ff_3 (
    .clk(Clock), .D(Output[1]), .Q(Output[2]), .preset(1'b0), .en(Enable), .reset(Clear));  // open: Qn
  D_Flip_Flop d_ff_4 (
    .clk(Clock), .D(Output[2]), .Q(Output[3]), .preset(1'b0), .en(Enable), .reset(Clear));  // open: Qn
  CSTATE cstate_1 (
    .IN0(Output[0]), .IN1(Output[1]), .IN2(Output[2]), .IN3(Output[3]), .IN4(Clock_out), .Out(cstate_1_out));
  D_Flip_Flop d_ff_5 (
    .clk(Clock), .D(Output[3]), .Q(Clock_out), .preset(1'b0), .en(Enable), .reset(Clear));  // open: Qn
  // Probe on Output
  // Probe on Output

  // Notes on the sheet:
  //   E
  //   Q0
  //   Q1
  //   Q2
  //   Q3
  //   Q4
endmodule

module CSTATE (
  input  IN0,
  input  IN1,
  input  IN2,
  input  IN3,
  input  IN4,
  output Out
);

  wire nor_1_out, xor_1_out;

  xor xor_1 (xor_1_out, IN1, IN4);
  nor nor_1 (nor_1_out, IN0, IN1, IN2, IN3);
  or or_1 (Out, nor_1_out, xor_1_out);

  // Notes on the sheet:
  //   O0
  //   O1
endmodule

module SISO (
  input  Clear,
  input  Enable,
  input  Clock,
  output Clock_out,
  output [3:0] Output
);

  D_Flip_Flop d_ff_1 (.clk(Clock), .D(1'b1), .Q(Output[0]), .preset(1'b0), .en(Enable), .reset(Clear));  // open: Qn
  D_Flip_Flop d_ff_2 (
    .clk(Clock), .D(Output[0]), .Q(Output[1]), .preset(1'b0), .en(Enable), .reset(Clear));  // open: Qn
  D_Flip_Flop d_ff_3 (
    .clk(Clock), .D(Output[1]), .Q(Output[2]), .preset(1'b0), .en(Enable), .reset(Clear));  // open: Qn
  D_Flip_Flop d_ff_4 (
    .clk(Clock), .D(Output[2]), .Q(Output[3]), .preset(1'b0), .en(Enable), .reset(Clear));  // open: Qn
  D_Flip_Flop d_ff_5 (
    .clk(Clock), .D(Output[3]), .Q(Clock_out), .preset(1'b0), .en(Enable), .reset(Clear));  // open: Qn
  // Probe on Output
  // Probe on Output

  // Notes on the sheet:
  //   E0
  //   Registre à décalage
endmodule

module SISO2 (
  input  Clear,
  input  Enable,
  input  Clock,
  output Clock_out,
  output [3:0] Output
);

  wire d_ff_1_q, d_ff_1_qn;

  D_Flip_Flop d_ff_1 (
    .clk(Clock), .D(d_ff_1_qn), .Q(d_ff_1_q), .Qn(d_ff_1_qn), .preset(1'b0), .en(Enable), .reset(Clear));
  D_Flip_Flop d_ff_2 (.clk(Clock), .D(d_ff_1_q), .Q(Output[0]), .preset(1'b0), .en(Enable), .reset(Clear));  // open: Qn
  D_Flip_Flop d_ff_3 (
    .clk(Clock), .D(Output[0]), .Q(Output[1]), .preset(1'b0), .en(Enable), .reset(Clear));  // open: Qn
  D_Flip_Flop d_ff_4 (
    .clk(Clock), .D(Output[1]), .Q(Output[2]), .preset(1'b0), .en(Enable), .reset(Clear));  // open: Qn
  D_Flip_Flop d_ff_5 (
    .clk(Clock), .D(Output[2]), .Q(Output[3]), .preset(1'b0), .en(Enable), .reset(Clear));  // open: Qn
  D_Flip_Flop d_ff_6 (
    .clk(Clock), .D(Output[3]), .Q(Clock_out), .preset(1'b0), .en(Enable), .reset(Clear));  // open: Qn
  // Probe on Output
  // Probe on Output

  // Notes on the sheet:
  //   DT
  //   E
endmodule

module SRAND8 (
  input  Clock,
  input  Enable,
  input  Clear,
  output [7:0] Output,
  output Clock_out
);

  wire sram4m_1_clock_out, sram4m_2_clock_out;

  SRAM4M sram4m_1 (.Clear(Clear), .Enable(Enable), .Clock(Clock), .Clock_out(sram4m_1_clock_out), .Output(Output[3:0]));
  SRAM4M sram4m_2 (
    .Clear(Clear), .Enable(Enable), .Clock(sram4m_1_clock_out), .Clock_out(sram4m_2_clock_out),
    .Output(Output[7:4]));
  or or_1 (Clock_out, sram4m_2_clock_out, sram4m_1_clock_out);
  // Probe on Output
  // Probe on Output
endmodule

module SRANMM (
  input  [7:0] Max,
  input  [7:0] Min,
  input  H,
  input  Enable,
  output [7:0] O
);

  wire [7:0] bit_extender_3_out, randm_1_output;
  wire [8:0] adder_1_out, bit_extender_1_out, bit_extender_2_out, bit_extender_4_out, subtractor_1_out;

  assign bit_extender_1_out = {{1{1'b0}}, Max};  // Bit_Extender bit_extender_1
  assign bit_extender_2_out = {{1{1'b0}}, Min};  // Bit_Extender bit_extender_2
  Subtractor #(.width(9)) subtractor_1 (
    .a(bit_extender_1_out), .b(bit_extender_2_out), .out(subtractor_1_out), .bin(1'b0));  // open: bout
  Bit_Extender #(.in_width(9), .out_width(8)) bit_extender_3 (.in(subtractor_1_out), .out(bit_extender_3_out));
  RANDM randm_1 (.H(H), .Enable(Enable), .Max(bit_extender_3_out), .Output(randm_1_output));  // open: def
  assign bit_extender_4_out = {{1{1'b0}}, randm_1_output};  // Bit_Extender bit_extender_4
  Adder #(.width(9)) adder_1 (
    .a(bit_extender_4_out), .b(bit_extender_2_out), .out(adder_1_out), .cin(1'b0));  // open: cout
  Bit_Extender #(.in_width(9), .out_width(8)) bit_extender_5 (.in(adder_1_out), .out(O));

  // Notes on the sheet:
  //   RANDM
  //   other_chip8.circ
endmodule

module MASK (
  input  [7:0] mask,
  input  [7:0] \input ,
  output [7:0] Output
);

  // Probe on Output
  assign Output = mask & \input ;  // AND_Gate and_1, 8 bits wide
endmodule

module MMASK4B (
  input  [3:0] Max,
  output [3:0] Output
);

  wire coder_1_p5;
  wire [1:0] coder_1_p7;
  wire [3:0] decoder_1_out0, subtractor_1_out;

  // Probe on Max
  // Coder coder_1: pin names not known; wires that end beside it: Max[0], Max[1], Max[2], Max[3], coder_1_p5, 1'b1, coder_1_p7
  Decoder #(.select(2), .disabled(0)) decoder_1 (
    .out0(decoder_1_out0[0]), .out1(decoder_1_out0[1]), .out2(decoder_1_out0[2]), .out3(decoder_1_out0[3]),
    .sel(coder_1_p7), .en(coder_1_p5));
  // Probe on coder_1_p7
  // Probe on decoder_1_out0
  // Probe on decoder_1_out0
  Subtractor #(.width(4)) subtractor_1 (
    .a(decoder_1_out0), .b(4'b0001), .out(subtractor_1_out), .bin(1'b0));  // open: bout
  // Probe on subtractor_1_out
  // Probe on subtractor_1_out
  assign Output = subtractor_1_out | 4'b0001;  // OR_Gate or_1, 4 bits wide
  // Probe on Output

  // Notes on the sheet:
  //   I0
  //   OD0
  //   Mask creation
  //   OS0
  //   O0
endmodule

module RVM4B (
  input  [3:0] Input,
  input  [3:0] Max,
  output [3:0] Output
);

  wire comparator_1_gt;
  wire [3:0] and_1_out, and_2_out, and_3_out, bit_extender_1_out, mmask4b_1_output, not_1_out;

  // Probe on Input
  // Probe on Max
  Comparator #(.width(4), .mode("unsigned")) comparator_1 (.a(Input), .b(Max), .gt(comparator_1_gt));  // open: eq, lt
  MMASK4B mmask4b_1 (.Max(Max), .Output(mmask4b_1_output));
  assign not_1_out = ~bit_extender_1_out;  // NOT_Gate not_1, 4 bits wide
  assign bit_extender_1_out = {{3{comparator_1_gt}}, comparator_1_gt};  // Bit_Extender bit_extender_1
  assign and_1_out = Input & mmask4b_1_output;  // AND_Gate and_1, 4 bits wide
  // Probe on mmask4b_1_output
  // Probe on mmask4b_1_output
  // Probe on and_2_out
  // Probe on and_2_out
  assign and_2_out = not_1_out & Input;  // AND_Gate and_2, 4 bits wide
  assign and_3_out = bit_extender_1_out & and_1_out;  // AND_Gate and_3, 4 bits wide
  // Probe on and_1_out
  // Probe on and_1_out
  // Probe on Output
  assign Output = and_2_out | and_3_out;  // OR_Gate or_1, 4 bits wide
  // Probe on and_3_out
  // Probe on and_3_out

  // Notes on the sheet:
  //   if (Input <= Max) =>>> Input
  //   if(Input > Max)
  //   OI0
endmodule

module SRANM4B (
  input  Clock,
  input  Enable,
  input  Clear,
  input  [3:0] MAX,
  output [3:0] Output,
  output Clock_out
);

  wire [3:0] sram4m_1_output;

  RVM4B rvm4b_1 (.Input(sram4m_1_output), .Max(MAX), .Output(Output));
  SRAM4M sram4m_1 (.Clear(Clear), .Enable(Enable), .Clock(Clock), .Clock_out(Clock_out), .Output(sram4m_1_output));
endmodule

module MISRA4B (
  input  [3:0] MAX,
  input  [3:0] MIN,
  input  Clock,
  input  Enable,
  input  Clear,
  output [3:0] Output,
  output Clock_out
);

  wire [3:0] sranm4b_1_output, subtractor_1_out;

  Subtractor #(.width(4)) subtractor_1 (.a(MAX), .b(MIN), .out(subtractor_1_out), .bin(1'b0));  // open: bout
  SRANM4B sranm4b_1 (
    .Clear(Clear), .Enable(Enable), .Clock(Clock), .Clock_out(Clock_out), .Output(sranm4b_1_output),
    .MAX(subtractor_1_out));
  Adder #(.width(4)) adder_1 (.a(MIN), .b(sranm4b_1_output), .out(Output), .cin(1'b0));  // open: cout
endmodule

module MSRABB (
  input  [3:0] max,
  input  horloge,
  input  enable,
  input  clear,
  output [3:0] ouput,
  output output_c
);

  wire rvm24b_1_output;

  RVM24B rvm24b_1 (.Input(ouput), .Max(max), .Clear(clear), .Clock(horloge), .Enable(enable), .Output(rvm24b_1_output));
  SRAM4M sram4m_1 (.Clear(clear), .Enable(enable), .Clock(rvm24b_1_output), .Clock_out(output_c), .Output(ouput));
endmodule

module DBZER (
  input  IN0,
  input  IN1,
  input  IN2,
  input  IN3,
  input  E,
  input  IN4,
  input  in_7,
  input  in_8,
  input  in_9,
  output out_10
);

  wire and_1_out, d_ff_1_q, d_ff_1_qn, nor_1_out;

  nor nor_1 (nor_1_out, IN0, IN1, IN2, IN3);
  D_Flip_Flop d_ff_1 (
    .clk(and_1_out), .D(d_ff_1_qn), .Q(d_ff_1_q), .Qn(d_ff_1_qn), .preset(in_7), .en(in_8), .reset(out_10));
  and and_1 (and_1_out, nor_1_out, E, IN4);
  or or_1 (out_10, in_9, d_ff_1_q);
endmodule

module SRAM04B (
  input  Clear,
  input  Enable,
  input  Clock,
  output Clock_out,
  output [3:0] Output
);

  wire cstate_1_out, dbzer_1_out_10;

  D_Flip_Flop d_ff_1 (
    .clk(Clock), .D(cstate_1_out), .Q(Output[0]), .preset(1'b0), .en(Enable), .reset(dbzer_1_out_10));  // open: Qn
  D_Flip_Flop d_ff_2 (
    .clk(Clock), .D(Output[0]), .Q(Output[1]), .preset(1'b0), .en(Enable), .reset(dbzer_1_out_10));  // open: Qn
  D_Flip_Flop d_ff_3 (
    .clk(Clock), .D(Output[1]), .Q(Output[2]), .preset(1'b0), .en(Enable), .reset(dbzer_1_out_10));  // open: Qn
  D_Flip_Flop d_ff_4 (
    .clk(Clock), .D(Output[2]), .Q(Output[3]), .preset(1'b0), .en(Enable), .reset(dbzer_1_out_10));  // open: Qn
  DBZER dbzer_1 (
    .IN1(Output[1]), .IN2(Output[2]), .IN3(Output[3]), .IN0(Output[0]), .IN4(Clock_out), .in_7(1'b0),
    .in_8(Enable), .in_9(Clear), .out_10(dbzer_1_out_10), .E(cstate_1_out));
  CSTATE cstate_1 (
    .IN0(Output[0]), .IN1(Output[1]), .IN2(Output[2]), .IN3(Output[3]), .IN4(Clock_out), .Out(cstate_1_out));
  D_Flip_Flop d_ff_5 (
    .clk(Clock), .D(Output[3]), .Q(Clock_out), .preset(1'b0), .en(Enable), .reset(dbzer_1_out_10));  // open: Qn
  // Probe on Output
  // Probe on Output

  // Notes on the sheet:
  //   E
  //   Q0
  //   Q1
  //   Q2
  //   Q3
  //   Q4
endmodule

module RVM24B (
  input  [3:0] Input,
  input  [3:0] Max,
  input  Clear,
  input  Clock,
  input  Enable,
  output Output
);

  wire and_2_out, comparator_1_gt, d_ff_1_q, d_ff_1_qn, not_1_out, or_1_out, or_2_out;
  wire [3:0] and_1_out, bit_extender_1_out, bit_extender_2_out, or_3_out;

  or or_1 (or_1_out, Max[0], Max[1], Max[2], Max[3]);
  not not_1 (not_1_out, or_1_out);
  assign and_1_out = Max & bit_extender_1_out;  // AND_Gate and_1, 4 bits wide
  assign bit_extender_1_out = {{3{or_1_out}}, or_1_out};  // Bit_Extender bit_extender_1
  assign bit_extender_2_out = {{3{not_1_out}}, not_1_out};  // Bit_Extender bit_extender_2
  or or_2 (or_2_out, Clear, and_2_out);
  and and_2 (and_2_out, Clock, d_ff_1_q);
  Comparator #(.width(4), .mode("unsigned")) comparator_1 (
    .a(Input), .b(or_3_out), .gt(comparator_1_gt));  // open: eq, lt
  assign or_3_out = and_1_out | bit_extender_2_out;  // OR_Gate or_3, 4 bits wide
  D_Flip_Flop #(.trigger("high")) d_ff_1 (
    .clk(comparator_1_gt), .D(d_ff_1_qn), .Q(d_ff_1_q), .Qn(d_ff_1_qn), .preset(1'b0), .en(Enable),
    .reset(or_2_out));
  and and_3 (Output, d_ff_1_qn, Clock);
endmodule

module SRAMM4B (
  input  [3:0] MAX,
  input  [3:0] MIN,
  input  Clock,
  input  Enable,
  input  Clear,
  output [3:0] Output,
  output Clock_out
);

  wire [3:0] sranm4b_1_output, subtractor_1_out;

  Subtractor #(.width(4)) subtractor_1 (.a(MAX), .b(MIN), .out(subtractor_1_out), .bin(1'b0));  // open: bout
  SRANM4B sranm4b_1 (
    .Clear(Clear), .Enable(Enable), .Clock(Clock), .Clock_out(Clock_out), .Output(sranm4b_1_output),
    .MAX(subtractor_1_out));
  Adder #(.width(4)) adder_1 (.a(MIN), .b(sranm4b_1_output), .out(Output), .cin(1'b0));  // open: cout
endmodule
