// Logisim project 12_mini_clavier_pc.circ as structural Verilog: 10 circuits, main circuit mini_clavier
module cl_hexa (
);

  wire _0_out, _1_out, _2_out, _3_out, _4_out, _5_out, _6_out, _7_out, _8_out, _9_out, A_out, B_out,
       button_1_out, button_2_out, button_3_out, button_4_out, C_out, coder_1_p17, coder_1_p19, coder_2_p18,
       coder_2_p20, coder_3_p17, D_out, decoder_1_out0, decoder_1_out1, decoder_1_out2, decoder_1_out3,
       decoder_1_out4, decoder_1_out5, decoder_1_out6, decoder_1_out7, decoder_1_out8, decoder_1_out9,
       decoder_1_out10, decoder_1_out11, decoder_1_out12, decoder_1_out13, decoder_1_out14, decoder_1_out15,
       E_out, F_out, keyboard_1_p2, keyboard_3_p1, keyboard_3_p5, keyboard_3_p10;
  wire [3:0] coder_1_p18, coder_2_p19, coder_3_p18, keyboard_1_p1, keyboard_3_p9, register_1_q, register_2_q,
       register_3_q, register_4_q;
  wire [15:0] _0_3_out, coder_2_p1;

  Button _0 (.out(_0_out));
  Button _1 (.out(_1_out));
  Button _2 (.out(_2_out));
  Button _3 (.out(_3_out));
  Button _4 (.out(_4_out));
  Button _5 (.out(_5_out));
  Button _6 (.out(_6_out));
  Button _7 (.out(_7_out));
  Button _8 (.out(_8_out));
  Button _9 (.out(_9_out));
  Button A (.out(A_out));
  Button B (.out(B_out));
  Button C (.out(C_out));
  Button D (.out(D_out));
  Button E (.out(E_out));
  Button F (.out(F_out));
  // Keyboard keyboard_1: pin names not known; wires that end beside it: keyboard_1_p1, keyboard_1_p2
  // Probe on keyboard_1_p1
  // Coder coder_1: pin names not known; wires that end beside it: _0_out, _1_out, _2_out, _3_out, _4_out, _5_out, _6_out, _7_out, _8_out, _9_out, A_out, B_out, C_out, D_out, E_out, F_out, coder_1_p17, coder_1_p18, coder_1_p19, coder_1_p19, coder_1_p19, coder_1_p19
  Button button_1 (.out(button_1_out));
  Decoder #(.select(4), .disabled(0)) decoder_1 (
    .out0(decoder_1_out0), .out1(decoder_1_out1), .out2(decoder_1_out2), .out3(decoder_1_out3),
    .out4(decoder_1_out4), .out5(decoder_1_out5), .out6(decoder_1_out6), .out7(decoder_1_out7),
    .out8(decoder_1_out8), .out9(decoder_1_out9), .out10(decoder_1_out10), .out11(decoder_1_out11),
    .out12(decoder_1_out12), .out13(decoder_1_out13), .out14(decoder_1_out14), .out15(decoder_1_out15),
    .sel(keyboard_1_p1), .en(keyboard_1_p2));
  LED led_1 (.in(register_1_q[0]));
  LED led_2 (.in(register_1_q[1]));
  LED led_3 (.in(register_1_q[2]));
  LED led_4 (.in(register_1_q[3]));
  LED led_5 (.in(coder_1_p17));
  Register #(.width(4)) register_1 (
    .D(coder_1_p18), .en(1'b1), .Q(register_1_q), .clk(coder_1_p17), .clr(button_1_out));
  LED _0_2 (.in(decoder_1_out0));
  LED _1_2 (.in(decoder_1_out1));
  LED _2_2 (.in(decoder_1_out2));
  LED _3_2 (.in(decoder_1_out3));
  LED _4_2 (.in(decoder_1_out4));
  LED _5_2 (.in(decoder_1_out5));
  LED _6_2 (.in(decoder_1_out6));
  LED _7_2 (.in(decoder_1_out7));
  LED _8_2 (.in(decoder_1_out8));
  LED _9_2 (.in(decoder_1_out9));
  LED A_2 (.in(decoder_1_out10));
  LED B_2 (.in(decoder_1_out11));
  LED C_2 (.in(decoder_1_out12));
  LED D_2 (.in(decoder_1_out13));
  LED E_2 (.in(decoder_1_out14));
  LED F_2 (.in(decoder_1_out15));
  Button _1_3 (.out(_0_3_out[1]));
  Button _4_3 (.out(_0_3_out[4]));
  Button _7_3 (.out(_0_3_out[7]));
  Button A_3 (.out(_0_3_out[10]));
  Button _3_3 (.out(_0_3_out[3]));
  Button _2_3 (.out(_0_3_out[2]));
  Button _5_3 (.out(_0_3_out[5]));
  Button _6_3 (.out(_0_3_out[6]));
  Button _8_3 (.out(_0_3_out[8]));
  Button _9_3 (.out(_0_3_out[9]));
  Button _0_3 (.out(_0_3_out[0]));
  Button B_3 (.out(_0_3_out[11]));
  // Keyboard keyboard_2: pin names not known
  // Keyboard keyboard_3: pin names not known; wires that end beside it: keyboard_3_p1, keyboard_3_p1, keyboard_3_p1, keyboard_3_p1, keyboard_3_p5, keyboard_3_p5, keyboard_3_p5, keyboard_3_p5, keyboard_3_p9, keyboard_3_p10
  Button C_3 (.out(_0_3_out[12]));
  Button D_3 (.out(_0_3_out[13]));
  Button E_3 (.out(_0_3_out[14]));
  Button F_3 (.out(_0_3_out[15]));
  // Probe on keyboard_3_p9
  // Coder coder_2: pin names not known; wires that end beside it: coder_2_p1, coder_2_p1[0], coder_2_p1[1], coder_2_p1[2], coder_2_p1[3], coder_2_p1[4], coder_2_p1[5], coder_2_p1[6], coder_2_p1[7], coder_2_p1[8], coder_2_p1[9], coder_2_p1[10], coder_2_p1[11], coder_2_p1[12], coder_2_p1[13], coder_2_p1[14], coder_2_p1[15], coder_2_p18, coder_2_p19, coder_2_p20, coder_2_p20, coder_2_p20, coder_2_p20
  Button button_2 (.out(button_2_out));
  Button button_3 (.out(button_3_out));
  Register #(.width(4)) register_2 (
    .D(keyboard_3_p9), .en(1'b1), .Q(register_2_q), .clk(keyboard_3_p10), .clr(button_2_out));
  Button button_4 (.out(button_4_out));
  Register #(.width(4)) register_3 (
    .D(coder_2_p19), .en(1'b1), .Q(register_3_q), .clk(coder_2_p18), .clr(button_3_out));
  LED led_6 (.in(register_2_q[0]));
  LED led_7 (.in(register_2_q[1]));
  LED led_8 (.in(register_2_q[2]));
  LED led_9 (.in(register_2_q[3]));
  LED led_10 (.in(keyboard_3_p10));
  // Coder coder_3: pin names not known; wires that end beside it: _0_3_out[0], _0_3_out[1], _0_3_out[2], _0_3_out[3], _0_3_out[4], _0_3_out[5], _0_3_out[6], _0_3_out[7], _0_3_out[8], _0_3_out[9], _0_3_out[10], _0_3_out[11], _0_3_out[12], _0_3_out[13], _0_3_out[14], _0_3_out[15], coder_3_p17, coder_3_p18
  Register #(.width(4)) register_4 (
    .D(coder_3_p18), .en(1'b1), .Q(register_4_q), .clk(coder_3_p17), .clr(button_4_out));
  LED led_11 (.in(register_3_q[0]));
  LED led_12 (.in(register_3_q[1]));
  LED led_13 (.in(register_3_q[2]));
  LED led_14 (.in(register_3_q[3]));
  LED led_15 (.in(coder_2_p18));
  LED led_16 (.in(register_4_q[0]));
  LED led_17 (.in(register_4_q[1]));
  LED led_18 (.in(register_4_q[2]));
  LED led_19 (.in(register_4_q[3]));
  LED led_20 (.in(coder_3_p17));

  // Notes on the sheet:
  //   5
  //   binary
  //   Other.jar
  //   1
  //   Other.jar
  //   no binary
  //   Other.jar
  //   binary
  //   Other.jar
  //   4
  //   2
  //   Other.jar
  //   Other.jar
  //   3
endmodule

module cl_num (
);

  wire _0_out, _1_out, _2_out, _3_out, _4_out, _5_out, _6_out, _7_out, _8_out, _9_out, button_1_out,
       button_2_out, button_3_out, button_4_out, coder_1_p11, coder_1_p13, coder_2_p11, coder_3_p11,
       decoder_1_out0, decoder_1_out1, decoder_1_out2, decoder_1_out3, decoder_1_out4, decoder_1_out5,
       decoder_1_out6, decoder_1_out7, decoder_1_out8, decoder_1_out9, keyboard_1_p2, keyboard_2_p1,
       keyboard_3_p1, keyboard_3_p5, keyboard_3_p10;
  wire [3:0] coder_1_p12, coder_2_p12, coder_3_p12, keyboard_1_p1, keyboard_3_p9, register_1_q, register_2_q,
       register_3_q, register_4_q;
  wire [9:0] _0_3_out, keyboard_2_p5;

  Button _0 (.out(_0_out));
  Button _1 (.out(_1_out));
  Button _2 (.out(_2_out));
  Button _3 (.out(_3_out));
  Button _4 (.out(_4_out));
  Button _5 (.out(_5_out));
  Button _6 (.out(_6_out));
  Button _7 (.out(_7_out));
  Button _8 (.out(_8_out));
  Button _9 (.out(_9_out));
  // Keyboard keyboard_1: pin names not known; wires that end beside it: keyboard_1_p1, keyboard_1_p2
  // Probe on keyboard_1_p1
  // Coder coder_1: pin names not known; wires that end beside it: _0_out, _1_out, _2_out, _3_out, _4_out, _5_out, _6_out, _7_out, _8_out, _9_out, coder_1_p11, coder_1_p12, coder_1_p13, coder_1_p13, coder_1_p13, coder_1_p13
  Button button_1 (.out(button_1_out));
  Decoder #(.select(4), .disabled(0)) decoder_1 (
    .out0(decoder_1_out0), .out1(decoder_1_out1), .out2(decoder_1_out2), .out3(decoder_1_out3),
    .out4(decoder_1_out4), .out5(decoder_1_out5), .out6(decoder_1_out6), .out7(decoder_1_out7),
    .out8(decoder_1_out8), .out9(decoder_1_out9), .sel(keyboard_1_p1), .en(keyboard_1_p2));  // open: out10, out11, out12, out13, out14, out15
  Register #(.width(4)) register_1 (
    .D(coder_1_p12), .en(1'b1), .Q(register_1_q), .clk(coder_1_p11), .clr(button_1_out));
  LED _0_2 (.in(decoder_1_out0));
  LED _1_2 (.in(decoder_1_out1));
  LED _2_2 (.in(decoder_1_out2));
  LED _3_2 (.in(decoder_1_out3));
  LED _4_2 (.in(decoder_1_out4));
  LED _5_2 (.in(decoder_1_out5));
  LED _6_2 (.in(decoder_1_out6));
  LED _7_2 (.in(decoder_1_out7));
  LED _8_2 (.in(decoder_1_out8));
  LED _9_2 (.in(decoder_1_out9));
  LED led_1 (.in(register_1_q[0]));
  LED led_2 (.in(register_1_q[1]));
  LED led_3 (.in(register_1_q[2]));
  LED led_4 (.in(register_1_q[3]));
  LED led_5 (.in(coder_1_p11));
  Button _7_3 (.out(_0_3_out[7]));
  Button _4_3 (.out(_0_3_out[4]));
  Button _1_3 (.out(_0_3_out[1]));
  Button _9_3 (.out(_0_3_out[9]));
  Button _8_3 (.out(_0_3_out[8]));
  Button _5_3 (.out(_0_3_out[5]));
  Button _6_3 (.out(_0_3_out[6]));
  Button _3_3 (.out(_0_3_out[3]));
  Button _2_3 (.out(_0_3_out[2]));
  Button _0_3 (.out(_0_3_out[0]));
  // Keyboard keyboard_2: pin names not known; wires that end beside it: keyboard_2_p1, keyboard_2_p1, keyboard_2_p1, keyboard_2_p1, keyboard_2_p5
  // Keyboard keyboard_3: pin names not known; wires that end beside it: keyboard_3_p1, keyboard_3_p1, keyboard_3_p1, keyboard_3_p1, keyboard_3_p5, keyboard_3_p5, keyboard_3_p5, keyboard_3_p5, keyboard_3_p9, keyboard_3_p10
  // Probe on keyboard_3_p9
  // Coder coder_2: pin names not known; wires that end beside it: keyboard_2_p5[0], keyboard_2_p5[1], keyboard_2_p5[2], keyboard_2_p5[3], keyboard_2_p5[4], keyboard_2_p5[5], keyboard_2_p5[6], keyboard_2_p5[7], keyboard_2_p5[8], keyboard_2_p5[9], coder_2_p11, coder_2_p12
  Button button_2 (.out(button_2_out));
  // Coder coder_3: pin names not known; wires that end beside it: _0_3_out[0], _0_3_out[1], _0_3_out[2], _0_3_out[3], _0_3_out[4], _0_3_out[5], _0_3_out[6], _0_3_out[7], _0_3_out[8], _0_3_out[9], coder_3_p11, coder_3_p12
  Button button_3 (.out(button_3_out));
  Button button_4 (.out(button_4_out));
  Register #(.width(4)) register_2 (
    .D(keyboard_3_p9), .en(1'b1), .Q(register_2_q), .clk(keyboard_3_p10), .clr(button_2_out));
  Register #(.width(4)) register_3 (
    .D(coder_3_p12), .en(1'b1), .Q(register_3_q), .clk(coder_3_p11), .clr(button_3_out));
  Register #(.width(4)) register_4 (
    .D(coder_2_p12), .en(1'b1), .Q(register_4_q), .clk(coder_2_p11), .clr(button_4_out));
  LED led_6 (.in(register_3_q[0]));
  LED led_7 (.in(register_3_q[1]));
  LED led_8 (.in(register_3_q[2]));
  LED led_9 (.in(register_3_q[3]));
  LED led_10 (.in(coder_3_p11));
  LED led_11 (.in(register_4_q[0]));
  LED led_12 (.in(register_4_q[1]));
  LED led_13 (.in(register_4_q[2]));
  LED led_14 (.in(register_4_q[3]));
  LED led_15 (.in(coder_2_p11));
  LED led_16 (.in(register_2_q[0]));
  LED led_17 (.in(register_2_q[1]));
  LED led_18 (.in(register_2_q[2]));
  LED led_19 (.in(register_2_q[3]));
  LED led_20 (.in(keyboard_3_p10));

  // Notes on the sheet:
  //   5
  //   binary
  //   Other.jar
  //   1
  //   Other.jar
  //   no binary
  //   Other.jar
  //   binary
  //   Other.jar
  //   2
  //   4
  //   Other.jar
  //   Other.jar
  //   3
endmodule

module cl_azerty (
);

  wire A_out, B_out, button_1_out, button_2_out, button_3_out, button_4_out, button_5_out, C_out,
       coder_1_p28, coder_1_p30, coder_2_p28, coder_3_p29, D_out, E_out, F_out, G_out, H_out, I_out, J_out,
       K_out, keyboard_3_p1, keyboard_3_p5, L_out, M_out, N_out, O_out, P_out, Q_out, R_out, S_out, T_out,
       U_out, undriven_2, undriven_4, V_out, W_out, X_out, Y_out, Z_out;
  wire [4:0] coder_1_p29, coder_2_p29, coder_3_p30, register_1_q, register_2_q, register_3_q, register_4_q,
       register_5_q, undriven, undriven_3;
  wire [26:0] coder_3_p1;
  wire [26:1] A_2_out;

  Button A (.out(A_out));
  Button B (.out(B_out));
  Button C (.out(C_out));
  Button D (.out(D_out));
  Button E (.out(E_out));
  Button F (.out(F_out));
  Button G (.out(G_out));
  Button H (.out(H_out));
  Button I (.out(I_out));
  Button J (.out(J_out));
  Button K (.out(K_out));
  Button L (.out(L_out));
  Button M (.out(M_out));
  Button N (.out(N_out));
  Button O (.out(O_out));
  Button P (.out(P_out));
  Button Q (.out(Q_out));
  Button R (.out(R_out));
  Button S (.out(S_out));
  Button T (.out(T_out));
  Button U (.out(U_out));
  Button V (.out(V_out));
  Button W (.out(W_out));
  Button X (.out(X_out));
  Button Y (.out(Y_out));
  Button Z (.out(Z_out));
  // Keyboard keyboard_1: pin names not known
  // Keyboard keyboard_2: pin names not known
  // Coder coder_1: pin names not known; wires that end beside it: 1'b0, A_out, B_out, C_out, D_out, E_out, F_out, G_out, H_out, I_out, J_out, K_out, L_out, M_out, N_out, O_out, P_out, Q_out, R_out, S_out, T_out, U_out, V_out, W_out, X_out, Y_out, Z_out, coder_1_p28, coder_1_p29, coder_1_p30, coder_1_p30, coder_1_p30, coder_1_p30
  Button button_1 (.out(button_1_out));
  LED led_1 (.in(register_1_q[0]));
  LED led_2 (.in(register_1_q[1]));
  LED led_3 (.in(register_1_q[2]));
  LED led_4 (.in(register_1_q[3]));
  LED led_5 (.in(register_1_q[4]));
  LED led_6 (.in(coder_1_p28));
  Register #(.width(5)) register_1 (
    .D(coder_1_p29), .en(1'b1), .Q(register_1_q), .clk(coder_1_p28), .clr(button_1_out));
  Button button_2 (.out(button_2_out));
  Button button_3 (.out(button_3_out));
  Button A_2 (.out(A_2_out[1]));
  LED led_7 (.in(register_2_q[0]));
  LED led_8 (.in(register_2_q[1]));
  LED led_9 (.in(register_2_q[2]));
  LED led_10 (.in(register_2_q[3]));
  LED led_11 (.in(register_2_q[4]));
  Register #(.width(5)) register_2 (.D(undriven), .en(1'b1), .Q(register_2_q), .clk(undriven_2), .clr(button_2_out));
  LED led_12 (.in(undriven_2));
  LED led_13 (.in(register_3_q[0]));
  LED led_14 (.in(register_3_q[1]));
  LED led_15 (.in(register_3_q[2]));
  LED led_16 (.in(register_3_q[3]));
  LED led_17 (.in(register_3_q[4]));
  Register #(.width(5)) register_3 (.D(undriven_3), .en(1'b1), .Q(register_3_q), .clk(undriven_4), .clr(button_3_out));
  LED led_18 (.in(undriven_4));
  Button Z_2 (.out(A_2_out[26]));
  Button Q_2 (.out(A_2_out[17]));
  Button W_2 (.out(A_2_out[23]));
  Button E_2 (.out(A_2_out[5]));
  Button S_2 (.out(A_2_out[19]));
  Button D_2 (.out(A_2_out[4]));
  Button X_2 (.out(A_2_out[24]));
  Button T_2 (.out(A_2_out[20]));
  Button R_2 (.out(A_2_out[18]));
  Button F_2 (.out(A_2_out[6]));
  Button C_2 (.out(A_2_out[3]));
  Button Y_2 (.out(A_2_out[25]));
  Button G_2 (.out(A_2_out[7]));
  Button B_2 (.out(A_2_out[2]));
  Button V_2 (.out(A_2_out[22]));
  // Keyboard keyboard_3: pin names not known; wires that end beside it: keyboard_3_p1, keyboard_3_p1, keyboard_3_p1, keyboard_3_p1, keyboard_3_p5, keyboard_3_p5, keyboard_3_p5, keyboard_3_p5
  Button U_2 (.out(A_2_out[21]));
  Button H_2 (.out(A_2_out[8]));
  Button J_2 (.out(A_2_out[10]));
  Button N_2 (.out(A_2_out[14]));
  Button O_2 (.out(A_2_out[15]));
  Button I_2 (.out(A_2_out[9]));
  Button K_2 (.out(A_2_out[11]));
  Button P_2 (.out(A_2_out[16]));
  Button L_2 (.out(A_2_out[12]));
  Button M_2 (.out(A_2_out[13]));
  // Coder coder_2: pin names not known; wires that end beside it: 1'b0, A_2_out[1], A_2_out[2], A_2_out[3], A_2_out[4], A_2_out[5], A_2_out[6], A_2_out[7], A_2_out[8], A_2_out[9], A_2_out[10], A_2_out[11], A_2_out[12], A_2_out[13], A_2_out[14], A_2_out[15], A_2_out[16], A_2_out[17], A_2_out[18], A_2_out[19], A_2_out[20], A_2_out[21], A_2_out[22], A_2_out[23], A_2_out[24], A_2_out[25], A_2_out[26], coder_2_p28, coder_2_p29
  Button button_4 (.out(button_4_out));
  // Coder coder_3: pin names not known; wires that end beside it: coder_3_p1, coder_3_p1[0], coder_3_p1[1], coder_3_p1[2], coder_3_p1[3], coder_3_p1[4], coder_3_p1[5], coder_3_p1[6], coder_3_p1[7], coder_3_p1[8], coder_3_p1[9], coder_3_p1[10], coder_3_p1[11], coder_3_p1[12], coder_3_p1[13], coder_3_p1[14], coder_3_p1[15], coder_3_p1[16], coder_3_p1[17], coder_3_p1[18], coder_3_p1[19], coder_3_p1[20], coder_3_p1[21], coder_3_p1[22], coder_3_p1[23], coder_3_p1[24], coder_3_p1[25], coder_3_p1[26], coder_3_p29, coder_3_p30
  Register #(.width(5)) register_4 (
    .D(coder_2_p29), .en(1'b1), .Q(register_4_q), .clk(coder_2_p28), .clr(button_4_out));
  Register #(.width(5)) register_5 (
    .D(coder_3_p30), .en(1'b1), .Q(register_5_q), .clk(coder_3_p29), .clr(button_5_out));
  Button button_5 (.out(button_5_out));
  LED led_19 (.in(register_4_q[0]));
  LED led_20 (.in(register_4_q[1]));
  LED led_21 (.in(register_4_q[2]));
  LED led_22 (.in(register_4_q[3]));
  LED led_23 (.in(register_4_q[4]));
  LED led_24 (.in(coder_2_p28));
  LED led_25 (.in(register_5_q[0]));
  LED led_26 (.in(register_5_q[1]));
  LED led_27 (.in(register_5_q[2]));
  LED led_28 (.in(register_5_q[3]));
  LED led_29 (.in(register_5_q[4]));
  LED led_30 (.in(coder_3_p29));

  // Notes on the sheet:
  //   Other.jar
  //   Other.jar
  //   4
  //   4
  //   1
  //   Other.jar
  //   binary
  //   binary
  //   Other.jar
  //   3
  //   no binary
  //   Other.jar
  //   2
  //   Other.jar
endmodule

module cl_real (
);

  wire button_1_out, clock_1_out, keyboard_1_avail;
  wire [6:0] keyboard_1_data, register_1_q;

  Keyboard keyboard_1 (
    .clk(clock_1_out), .re(1'b1), .clr(button_1_out), .avail(keyboard_1_avail), .data(keyboard_1_data));
  Clock clock_1 (.out(clock_1_out));
  Button button_1 (.out(button_1_out));
  TTY tty_1 (.data(keyboard_1_data), .clk(keyboard_1_avail), .we(1'b1), .clr(button_1_out));
  Register #(.width(7)) register_1 (
    .D(keyboard_1_data), .en(1'b1), .Q(register_1_q), .clk(keyboard_1_avail), .clr(button_1_out));
  // Probe on register_1_q
  // Probe on register_1_q
  // Probe on register_1_q
  // Probe on register_1_q

  // Notes on the sheet:
  //   ASCII
endmodule

module cl_num_ascii (
);

  wire button_1_out, button_2_out, keyboard_1_p2, keyboard_2_p1, keyboard_2_p3, keyboard_2_p8, keyboard_2_p9;
  wire [3:0] keyboard_1_p1;
  wire [6:0] and_1_out, bit_extender_1_out, bit_extender_2_out, keyboard_2_p7, or_1_out, register_1_q,
       register_2_q;

  // Keyboard keyboard_1: pin names not known; wires that end beside it: keyboard_1_p1, keyboard_1_p2
  Button button_1 (.out(button_1_out));
  TTY #(.trigger("falling")) tty_1 (.data(and_1_out), .clk(keyboard_1_p2), .we(1'b1), .clr(button_1_out));
  assign bit_extender_1_out = {{3{1'b0}}, keyboard_1_p1};  // Bit_Extender bit_extender_1
  assign bit_extender_2_out = {{6{keyboard_1_p2}}, keyboard_1_p2};  // Bit_Extender bit_extender_2
  assign and_1_out = bit_extender_2_out & or_1_out;  // AND_Gate and_1, 7 bits wide
  assign or_1_out = bit_extender_1_out | 7'b0110000;  // OR_Gate or_1, 7 bits wide
  Register #(.width(7), .trigger("falling")) register_1 (
    .D(and_1_out), .en(1'b1), .Q(register_1_q), .clk(keyboard_1_p2), .clr(button_1_out));
  LED led_1 (.in(register_1_q[6]));
  LED led_2 (.in(register_1_q[5]));
  LED led_3 (.in(register_1_q[4]));
  LED led_4 (.in(register_1_q[2]));
  LED led_5 (.in(register_1_q[3]));
  LED led_6 (.in(register_1_q[1]));
  LED led_7 (.in(register_1_q[0]));
  Button button_2 (.out(button_2_out));
  // Keyboard keyboard_2: pin names not known; wires that end beside it: keyboard_2_p1, keyboard_2_p1, keyboard_2_p3, keyboard_2_p3, keyboard_2_p3, keyboard_2_p3, keyboard_2_p7, keyboard_2_p8, keyboard_2_p9, keyboard_2_p9
  TTY tty_2 (.data(keyboard_2_p7), .clk(keyboard_2_p8), .we(1'b1), .clr(button_2_out));
  Register #(.width(7)) register_2 (
    .D(keyboard_2_p7), .en(1'b1), .Q(register_2_q), .clk(keyboard_2_p8), .clr(button_2_out));
  LED led_8 (.in(register_2_q[6]));
  LED led_9 (.in(register_2_q[5]));
  LED led_10 (.in(register_2_q[4]));
  LED led_11 (.in(register_2_q[3]));
  LED led_12 (.in(register_2_q[2]));
  LED led_13 (.in(register_2_q[1]));
  LED led_14 (.in(register_2_q[0]));

  // Notes on the sheet:
  //   Other.jar
  //   1
  //   binary
  //   2
  //   ASCII
  //   Other.jar
  //   0x30 = 0b 011 0000
  //   0x0F = 0b 000 1111
endmodule

module cl_azerty_ascii (
);

  wire button_1_out, button_2_out, button_3_out, button_4_out, keyboard_1_p1, keyboard_3_p1, keyboard_3_p3,
       keyboard_3_p5, keyboard_3_p7, keyboard_3_p9, keyboard_3_p11, keyboard_3_p12, keyboard_3_p14,
       keyboard_3_p16, keyboard_3_p18, keyboard_3_p20, keyboard_3_p21, keyboard_3_p22, keyboard_3_p25,
       keyboard_3_p26, keyboard_3_p29, keyboard_3_p30, keyboard_3_p31, keyboard_4_p1, keyboard_4_p3,
       keyboard_4_p7, undriven_2, undriven_4, undriven_6, undriven_8;
  wire [4:0] undriven, undriven_7;
  wire [6:0] and_1_out, and_2_out, bit_extender_1_out, bit_extender_2_out, bit_extender_3_out,
       bit_extender_4_out, or_1_out, or_2_out, or_3_out, register_1_q, register_2_q, register_3_q,
       register_4_q, undriven_3, undriven_5;

  // Keyboard keyboard_1: pin names not known; wires that end beside it: keyboard_1_p1, keyboard_1_p1
  // Keyboard keyboard_2: pin names not known; wires that end beside it: keyboard_1_p1, keyboard_1_p1
  Button button_1 (.out(button_1_out));
  Button button_2 (.out(button_2_out));
  TTY tty_1 (.data(undriven_3), .clk(undriven_2), .we(1'b1), .clr(button_1_out));
  TTY #(.trigger("falling")) tty_2 (.data(and_1_out), .clk(undriven_4), .we(1'b1), .clr(button_2_out));
  assign bit_extender_1_out = {{2{1'b0}}, undriven};  // Bit_Extender bit_extender_1
  Register #(.width(7)) register_1 (.D(undriven_3), .en(1'b1), .Q(register_1_q), .clk(undriven_2), .clr(button_1_out));
  LED led_1 (.in(register_1_q[6]));
  LED led_2 (.in(register_1_q[5]));
  assign bit_extender_2_out = {{6{undriven_4}}, undriven_4};  // Bit_Extender bit_extender_2
  assign and_1_out = bit_extender_2_out & or_1_out;  // AND_Gate and_1, 7 bits wide
  assign or_1_out = bit_extender_1_out | 7'b1000000;  // OR_Gate or_1, 7 bits wide
  LED led_3 (.in(register_1_q[3]));
  LED led_4 (.in(register_1_q[4]));
  LED led_5 (.in(register_1_q[2]));
  Register #(.width(7), .trigger("falling")) register_2 (
    .D(and_1_out), .en(1'b1), .Q(register_2_q), .clk(undriven_4), .clr(button_2_out));
  LED led_6 (.in(register_1_q[1]));
  LED led_7 (.in(register_1_q[0]));
  LED led_8 (.in(register_2_q[6]));
  LED led_9 (.in(register_2_q[5]));
  // Keyboard keyboard_3: pin names not known; wires that end beside it: keyboard_3_p1, keyboard_3_p1, keyboard_3_p3, keyboard_3_p3, keyboard_3_p5, keyboard_3_p5, keyboard_3_p7, keyboard_3_p7, keyboard_3_p9, keyboard_3_p9, keyboard_3_p11, keyboard_3_p12, keyboard_3_p12, keyboard_3_p14, keyboard_3_p14, keyboard_3_p16, keyboard_3_p16, keyboard_3_p18, keyboard_3_p18, keyboard_3_p20, keyboard_3_p21, keyboard_3_p22, keyboard_3_p21, keyboard_3_p22, keyboard_3_p25, keyboard_3_p26, keyboard_3_p25, keyboard_3_p26, keyboard_3_p29, keyboard_3_p30, keyboard_3_p31, keyboard_3_p29, keyboard_3_p30, keyboard_3_p31, keyboard_3_p31, keyboard_3_p31
  // Keyboard keyboard_4: pin names not known; wires that end beside it: keyboard_4_p1, keyboard_4_p1, keyboard_4_p3, keyboard_4_p3, keyboard_4_p1, keyboard_4_p1, keyboard_4_p7, keyboard_3_p11, keyboard_4_p7, keyboard_3_p20, keyboard_4_p7, keyboard_4_p7
  LED led_10 (.in(register_2_q[2]));
  LED led_11 (.in(register_2_q[1]));
  LED led_12 (.in(register_2_q[3]));
  LED led_13 (.in(register_2_q[4]));
  LED led_14 (.in(register_2_q[0]));
  Button button_3 (.out(button_3_out));
  Button button_4 (.out(button_4_out));
  TTY #(.trigger("falling")) tty_3 (.data(or_2_out), .clk(undriven_6), .we(1'b1), .clr(button_3_out));
  TTY #(.trigger("falling")) tty_4 (.data(and_2_out), .clk(undriven_8), .we(1'b1), .clr(button_4_out));
  assign bit_extender_3_out = {{2{1'b0}}, undriven_7};  // Bit_Extender bit_extender_3
  assign or_2_out = 7'b0100000 | undriven_5;  // OR_Gate or_2, 7 bits wide
  assign bit_extender_4_out = {{6{undriven_8}}, undriven_8};  // Bit_Extender bit_extender_4
  assign and_2_out = bit_extender_4_out & or_3_out;  // AND_Gate and_2, 7 bits wide
  assign or_3_out = bit_extender_3_out | 7'b1100000;  // OR_Gate or_3, 7 bits wide
  Register #(.width(7), .trigger("falling")) register_3 (
    .D(or_2_out), .en(1'b1), .Q(register_3_q), .clk(undriven_6), .clr(button_3_out));
  LED led_15 (.in(register_3_q[6]));
  Register #(.width(7), .trigger("falling")) register_4 (
    .D(and_2_out), .en(1'b1), .Q(register_4_q), .clk(undriven_8), .clr(button_4_out));
  LED led_16 (.in(register_3_q[5]));
  LED led_17 (.in(register_3_q[3]));
  LED led_18 (.in(register_3_q[4]));
  LED led_19 (.in(register_4_q[5]));
  LED led_20 (.in(register_4_q[6]));
  LED led_21 (.in(register_3_q[0]));
  LED led_22 (.in(register_3_q[1]));
  LED led_23 (.in(register_3_q[2]));
  LED led_24 (.in(register_4_q[3]));
  LED led_25 (.in(register_4_q[4]));
  LED led_26 (.in(register_4_q[1]));
  LED led_27 (.in(register_4_q[2]));
  LED led_28 (.in(register_4_q[0]));

  // Notes on the sheet:
  //   0x1F = 0b 001 1111
  //   0x40 = 0b 100 0000
  //   0x20 = 0b 010 0000
  //   0x60 = 0b 110 0000
  //   Other.jar
  //   Other.jar
  //   1
  //   binary
  //   2
  //   AZERTY
  //   AZERTY
  //   ASCII
  //   Other.jar
  //   Other.jar
  //   2.5
  //   binary
  //   3
  //   ASCII
  //   azerty
  //   azerty
endmodule

module cl_azerty_maj_min (
);

  wire button_1_out, button_2_out, inter_1_p1, inter_1_p2, inter_1_p3, inter_2_p2, inter_2_p3, or_1_out,
       or_2_out, SHIFT_2_out, SHIFT_out, upd_1_leduppercase, uppercase_1_p5, VERR_2_out, VERR_out;
  wire [6:0] inter_2_p1, register_1_q, register_2_q, upd_1_output, uppercase_1_p6;

  // Keyboard keyboard_1: pin names not known
  // Keyboard keyboard_2: pin names not known
  Button button_1 (.out(button_1_out));
  Button VERR (.out(VERR_out));
  Button SHIFT (.out(SHIFT_out));
  // Inter inter_1: pin names not known; wires that end beside it: inter_1_p1, inter_1_p2, inter_1_p3
  Button button_2 (.out(button_2_out));
  Button VERR_2 (.out(VERR_2_out));
  Button SHIFT_2 (.out(SHIFT_2_out));
  // Inter inter_2: pin names not known; wires that end beside it: inter_2_p1, inter_2_p2, inter_2_p3
  TTY #(.trigger("falling")) tty_1 (.data(uppercase_1_p6), .clk(inter_1_p2), .we(1'b1), .clr(button_1_out));
  or or_1 (or_1_out, SHIFT_out, inter_1_p3);
  TTY #(.trigger("falling")) tty_2 (.data(upd_1_output), .clk(inter_2_p2), .we(1'b1), .clr(button_2_out));
  or or_2 (or_2_out, SHIFT_2_out, inter_2_p3);
  // Uppercase uppercase_1: pin names not known; wires that end beside it: VERR_out, or_1_out, inter_1_p1, inter_1_p2, uppercase_1_p5, uppercase_1_p6
  UPD upd_1 (
    .Verr(VERR_2_out), .Shift(or_2_out), .Input(inter_2_p1), .LedUppercase(upd_1_leduppercase),
    .Output(upd_1_output), .Enable(inter_2_p2));
  LED led_1 (.in(uppercase_1_p5));
  Register #(.width(7), .trigger("falling")) register_1 (
    .D(uppercase_1_p6), .en(1'b1), .Q(register_1_q), .clk(inter_1_p2), .clr(button_1_out));
  LED led_2 (.in(upd_1_leduppercase));
  Register #(.width(7), .trigger("falling")) register_2 (
    .D(upd_1_output), .en(1'b1), .Q(register_2_q), .clk(inter_2_p2), .clr(button_2_out));
  LED led_3 (.in(register_1_q[3]));
  LED led_4 (.in(register_1_q[4]));
  LED led_5 (.in(register_1_q[5]));
  LED led_6 (.in(register_1_q[6]));
  LED led_7 (.in(register_2_q[4]));
  LED led_8 (.in(register_2_q[6]));
  LED led_9 (.in(register_2_q[5]));
  LED led_10 (.in(register_2_q[3]));
  LED led_11 (.in(register_1_q[0]));
  LED led_12 (.in(register_1_q[2]));
  LED led_13 (.in(register_1_q[1]));
  LED led_14 (.in(register_2_q[0]));
  LED led_15 (.in(register_2_q[1]));
  LED led_16 (.in(register_2_q[2]));

  // Notes on the sheet:
  //   Other.jar
  //   Other.jar
  //   ASCII
  //   ASCII
  //   Other.jar
  //   other_chip8.circ
endmodule

module mini_clavier (
);

  wire BS_out, button_1_out, keyboard_2_p1, keyboard_2_p2, LF_out, or_1_out, SHIFT_out, SP_out,
       uppercase_1_p5, VERR_out;
  wire [6:0] fct_1_s, keyboard_2_p3, or_2_out, uppercase_1_p6;
  wire [7:0] register_1_q;

  Button button_1 (.out(button_1_out));
  Button VERR (.out(VERR_out));
  Button SHIFT (.out(SHIFT_out));
  TTY #(.cols(28)) tty_1 (.data(or_2_out), .clk(or_1_out), .we(1'b1), .clr(button_1_out));
  LED caps (.in(uppercase_1_p5));
  // Keyboard keyboard_1: pin names not known
  Button SP (.out(SP_out));
  Register register_1 (.D({1'b0, or_2_out}), .en(1'b1), .Q(register_1_q), .clk(or_1_out), .clr(button_1_out));
  Button BS (.out(BS_out));
  Button LF (.out(LF_out));
  // Probe on register_1_q
  // Probe on register_1_q
  // Probe on register_1_q
  // Probe on register_1_q
  // Keyboard keyboard_2: pin names not known; wires that end beside it: keyboard_2_p1, keyboard_2_p2, keyboard_2_p3
  FCT fct_1 (.BS(BS_out), .LF(LF_out), .SP(SP_out), .S(fct_1_s));
  // Uppercase uppercase_1: pin names not known; wires that end beside it: VERR_out, SHIFT_out, keyboard_2_p1, keyboard_2_p2, uppercase_1_p5, uppercase_1_p6
  LED led_1 (.in(register_1_q[5]));
  LED led_2 (.in(register_1_q[6]));
  LED led_3 (.in(register_1_q[7]));
  LED led_4 (.in(register_1_q[4]));
  LED led_5 (.in(register_1_q[1]));
  LED led_6 (.in(register_1_q[2]));
  LED led_7 (.in(register_1_q[3]));
  LED led_8 (.in(register_1_q[0]));
  or or_1 (or_1_out, or_2_out[0], or_2_out[1], or_2_out[2], or_2_out[3], or_2_out[4], or_2_out[5], or_2_out[6]);
  assign or_2_out = keyboard_2_p3 | fct_1_s | uppercase_1_p6;  // OR_Gate or_2, 7 bits wide

  // Notes on the sheet:
  //   Other.jar
  //   ASCII
  //   ASCII
  //   Other.jar
  //   Other.jar
  //   ASCII
endmodule

module joystick (
);

  wire decoder_1_out0, decoder_3_out0, decoder_4_out0;
  wire [3:0] joystick_1_x, joystick_1_y, joystick_2_x, joystick_2_y, joystick_3_x, joystick_3_y;
  wire [14:0] decoder_1_out15, decoder_2_out1, decoder_3_out15, decoder_4_out15, demultiplexer_1_out1,
       demultiplexer_1_out2, demultiplexer_1_out3, demultiplexer_1_out4, demultiplexer_1_out5,
       demultiplexer_1_out6, demultiplexer_1_out7, demultiplexer_1_out8, demultiplexer_1_out9,
       demultiplexer_1_out10, demultiplexer_1_out11, demultiplexer_1_out12, demultiplexer_1_out13,
       demultiplexer_1_out14, demultiplexer_1_out15, demultiplexer_2_out1, demultiplexer_2_out2,
       demultiplexer_2_out3, demultiplexer_2_out4, demultiplexer_2_out5, demultiplexer_2_out6,
       demultiplexer_2_out7, demultiplexer_2_out8, demultiplexer_2_out9, demultiplexer_2_out10,
       demultiplexer_2_out11, demultiplexer_2_out12, demultiplexer_2_out13, demultiplexer_2_out14,
       demultiplexer_2_out15, demultiplexer_3_out1, demultiplexer_3_out2, demultiplexer_3_out3,
       demultiplexer_3_out4, demultiplexer_3_out5, demultiplexer_3_out6, demultiplexer_3_out7,
       demultiplexer_3_out8, demultiplexer_3_out9, demultiplexer_3_out10, demultiplexer_3_out11,
       demultiplexer_3_out12, demultiplexer_3_out13, demultiplexer_3_out14, demultiplexer_3_out15;

  // Probe on joystick_1_y
  // Probe on joystick_1_y
  // Probe on joystick_1_y
  // Probe on joystick_1_y
  // Probe on joystick_1_x
  // Probe on joystick_1_x
  // Probe on joystick_1_x
  // Probe on joystick_1_x
  Joystick joystick_1 (.x(joystick_1_x), .y(joystick_1_y));
  Decoder #(.select(4), .enable("false")) decoder_1 (
    .out0(decoder_1_out0), .out1(decoder_1_out15[14]), .out2(decoder_1_out15[13]),
    .out3(decoder_1_out15[12]), .out4(decoder_1_out15[11]), .out5(decoder_1_out15[10]),
    .out6(decoder_1_out15[9]), .out7(decoder_1_out15[8]), .out8(decoder_1_out15[7]),
    .out9(decoder_1_out15[6]), .out10(decoder_1_out15[5]), .out11(decoder_1_out15[4]),
    .out12(decoder_1_out15[3]), .out13(decoder_1_out15[2]), .out14(decoder_1_out15[1]),
    .out15(decoder_1_out15[0]), .sel(joystick_1_y));
  DotMatrix #(.matrixcols(15), .matrixrows(15)) dotmatrix_1 (
    .col0(demultiplexer_1_out1), .col1(demultiplexer_1_out2), .col2(demultiplexer_1_out3),
    .col3(demultiplexer_1_out4), .col4(demultiplexer_1_out5), .col5(demultiplexer_1_out6),
    .col6(demultiplexer_1_out7), .col7(demultiplexer_1_out8), .col8(demultiplexer_1_out9),
    .col9(demultiplexer_1_out10), .col10(demultiplexer_1_out11), .col11(demultiplexer_1_out12),
    .col12(demultiplexer_1_out13), .col13(demultiplexer_1_out14), .col14(demultiplexer_1_out15));
  Decoder #(.select(4), .enable("false")) decoder_2 (
    .out1(decoder_2_out1[0]), .out2(decoder_2_out1[1]), .out3(decoder_2_out1[2]), .out4(decoder_2_out1[3]),
    .out5(decoder_2_out1[4]), .out6(decoder_2_out1[5]), .out7(decoder_2_out1[6]), .out8(decoder_2_out1[7]),
    .out9(decoder_2_out1[8]), .out10(decoder_2_out1[9]), .out11(decoder_2_out1[10]),
    .out12(decoder_2_out1[11]), .out13(decoder_2_out1[12]), .out14(decoder_2_out1[13]),
    .out15(decoder_2_out1[14]), .sel(joystick_1_x));  // open: out0
  Demultiplexer #(.select(4), .width(15), .enable("false")) demultiplexer_1 (
    .out1(demultiplexer_1_out1), .out2(demultiplexer_1_out2), .out3(demultiplexer_1_out3),
    .out4(demultiplexer_1_out4), .out5(demultiplexer_1_out5), .out6(demultiplexer_1_out6),
    .out7(demultiplexer_1_out7), .out8(demultiplexer_1_out8), .out9(demultiplexer_1_out9),
    .out10(demultiplexer_1_out10), .out11(demultiplexer_1_out11), .out12(demultiplexer_1_out12),
    .out13(demultiplexer_1_out13), .out14(demultiplexer_1_out14), .out15(demultiplexer_1_out15),
    .in(decoder_1_out15), .sel(joystick_1_x));  // open: out0
  // Probe on decoder_2_out1
  // Probe on decoder_2_out1
  // Probe on decoder_2_out1
  // Probe on decoder_2_out1
  // Probe on decoder_1_out15
  // Probe on decoder_1_out15
  // Probe on decoder_1_out15
  // Probe on decoder_1_out15
  Joystick joystick_2 (.x(joystick_2_x), .y(joystick_2_y));
  Joystick joystick_3 (.x(joystick_3_x), .y(joystick_3_y));
  Decoder #(.select(4), .enable("false")) decoder_3 (
    .out0(decoder_3_out0), .out1(decoder_3_out15[14]), .out2(decoder_3_out15[13]),
    .out3(decoder_3_out15[12]), .out4(decoder_3_out15[11]), .out5(decoder_3_out15[10]),
    .out6(decoder_3_out15[9]), .out7(decoder_3_out15[8]), .out8(decoder_3_out15[7]),
    .out9(decoder_3_out15[6]), .out10(decoder_3_out15[5]), .out11(decoder_3_out15[4]),
    .out12(decoder_3_out15[3]), .out13(decoder_3_out15[2]), .out14(decoder_3_out15[1]),
    .out15(decoder_3_out15[0]), .sel(joystick_2_y));
  Decoder #(.select(4), .enable("false")) decoder_4 (
    .out0(decoder_4_out0), .out1(decoder_4_out15[14]), .out2(decoder_4_out15[13]),
    .out3(decoder_4_out15[12]), .out4(decoder_4_out15[11]), .out5(decoder_4_out15[10]),
    .out6(decoder_4_out15[9]), .out7(decoder_4_out15[8]), .out8(decoder_4_out15[7]),
    .out9(decoder_4_out15[6]), .out10(decoder_4_out15[5]), .out11(decoder_4_out15[4]),
    .out12(decoder_4_out15[3]), .out13(decoder_4_out15[2]), .out14(decoder_4_out15[1]),
    .out15(decoder_4_out15[0]), .sel(joystick_3_y));
  DotMatrix #(.matrixcols(15), .matrixrows(15)) dotmatrix_2 (
    .col0(demultiplexer_3_out1), .col1(demultiplexer_3_out2), .col2(demultiplexer_3_out3),
    .col3(demultiplexer_3_out4), .col4(demultiplexer_3_out5), .col5(demultiplexer_3_out6),
    .col6(demultiplexer_3_out7), .col7(demultiplexer_3_out8), .col8(demultiplexer_3_out9),
    .col9(demultiplexer_3_out10), .col10(demultiplexer_3_out11), .col11(demultiplexer_3_out12),
    .col12(demultiplexer_3_out13), .col13(demultiplexer_3_out14), .col14(demultiplexer_3_out15));
  DotMatrix #(.matrixcols(15), .matrixrows(15)) dotmatrix_3 (
    .col0(demultiplexer_2_out1), .col1(demultiplexer_2_out2), .col2(demultiplexer_2_out3),
    .col3(demultiplexer_2_out4), .col4(demultiplexer_2_out5), .col5(demultiplexer_2_out6),
    .col6(demultiplexer_2_out7), .col7(demultiplexer_2_out8), .col8(demultiplexer_2_out9),
    .col9(demultiplexer_2_out10), .col10(demultiplexer_2_out11), .col11(demultiplexer_2_out12),
    .col12(demultiplexer_2_out13), .col13(demultiplexer_2_out14), .col14(demultiplexer_2_out15));
  Demultiplexer #(.select(4), .width(15), .enable("false")) demultiplexer_2 (
    .out1(demultiplexer_2_out1), .out2(demultiplexer_2_out2), .out3(demultiplexer_2_out3),
    .out4(demultiplexer_2_out4), .out5(demultiplexer_2_out5), .out6(demultiplexer_2_out6),
    .out7(demultiplexer_2_out7), .out8(demultiplexer_2_out8), .out9(demultiplexer_2_out9),
    .out10(demultiplexer_2_out10), .out11(demultiplexer_2_out11), .out12(demultiplexer_2_out12),
    .out13(demultiplexer_2_out13), .out14(demultiplexer_2_out14), .out15(demultiplexer_2_out15),
    .in(decoder_4_out15), .sel(joystick_3_x));  // open: out0
  Demultiplexer #(.select(4), .width(15), .enable("false")) demultiplexer_3 (
    .out1(demultiplexer_3_out1), .out2(demultiplexer_3_out2), .out3(demultiplexer_3_out3),
    .out4(demultiplexer_3_out4), .out5(demultiplexer_3_out5), .out6(demultiplexer_3_out6),
    .out7(demultiplexer_3_out7), .out8(demultiplexer_3_out8), .out9(demultiplexer_3_out9),
    .out10(demultiplexer_3_out10), .out11(demultiplexer_3_out11), .out12(demultiplexer_3_out12),
    .out13(demultiplexer_3_out13), .out14(demultiplexer_3_out14), .out15(demultiplexer_3_out15),
    .in(decoder_3_out15), .sel(joystick_2_x));  // open: out0
endmodule

module FCT (
  input  BS,
  input  LF,
  input  SP,
  output [6:0] S
);

  wire [6:0] and_1_out, and_2_out, and_3_out, bit_extender_1_out, bit_extender_2_out, bit_extender_3_out;

  assign bit_extender_1_out = {{6{BS}}, BS};  // Bit_Extender bit_extender_1
  assign bit_extender_2_out = {{6{LF}}, LF};  // Bit_Extender bit_extender_2
  assign bit_extender_3_out = {{6{SP}}, SP};  // Bit_Extender bit_extender_3
  assign and_1_out = bit_extender_1_out & 7'b0001000;  // AND_Gate and_1, 7 bits wide
  assign and_2_out = bit_extender_2_out & 7'b0001010;  // AND_Gate and_2, 7 bits wide
  assign and_3_out = bit_extender_3_out & 7'b0100000;  // AND_Gate and_3, 7 bits wide
  assign S = and_1_out | and_2_out | and_3_out;  // OR_Gate or_1, 7 bits wide
endmodule
