// Logisim project 12_screen_color.circ as structural Verilog: 6 circuits, main circuit main_pixel_color
module main_pixel_color (
  input  [7:0] in_1,
  input  [7:0] in_2,
  input  [7:0] in_3
);

  wire colorpixel_1_clear_2, colorpixel_1_clock, decoder_1_out0, decoder_1_out1, decoder_1_out2,
       decoder_1_out3, or_1_out, screencolor_1_p1, screencolor_1_p2;
  wire [1:0] DC;
  wire [2:0] CL;
  wire [3:0] pixelxy_1_x_2;
  wire [4:0] colorpixel_1_inputy;
  wire [23:0] CB, CG, CI, CO, CR;
  wire [31:0] pixelxy_1_y_2;

  Hex_Digit_Display hex_digit_display_1 (.value(CI[23:20]));  // open: dp
  LED led_1 (.in(decoder_1_out0));
  LED led_2 (.in(decoder_1_out1));
  LED led_3 (.in(decoder_1_out2));
  LED led_4 (.in(decoder_1_out3));
  or or_1 (or_1_out, decoder_1_out0, decoder_1_out1, decoder_1_out2, decoder_1_out3);
  LED led_5 (.in(or_1_out));
  Hex_Digit_Display hex_digit_display_2 (.value(CI[19:16]));  // open: dp
  Hex_Digit_Display hex_digit_display_3 (.value(CI[15:12]));  // open: dp
  Hex_Digit_Display hex_digit_display_4 (.value(CI[7:4]));  // open: dp
  Hex_Digit_Display hex_digit_display_5 (.value(CI[11:8]));  // open: dp
  Decoder #(.select(2), .enable("false")) decoder_1 (
    .out0(decoder_1_out0), .out1(decoder_1_out1), .out2(decoder_1_out2), .out3(decoder_1_out3), .sel(DC));
  // Probe on in_1
  // Probe on in_1
  // Probe on CR
  // Probe on in_2
  // Probe on in_2
  // Probe on CG
  // Probe on in_3
  // Probe on in_3
  // Probe on CB
  // Probe on CI
  // Probe on CI
  // Probe on CO
  // Probe on CO
  Hex_Digit_Display hex_digit_display_6 (.value(CI[3:0]));  // open: dp
  Button RW (.out(CL[0]));
  Button u_CO (.out(CL[1]));
  Button u_CL (.out(CL[2]));
  colorToRGB colortorgb_1 (.in_1({in_3, in_2, in_1}), .out_2(CR), .out_3(CG), .out_4(CB));
  colorPixel colorpixel_1 (
    .Blue(in_3), .Green(in_2), .Red(in_1), .Row(CL[0]), .Column(CL[1]), .Clear(CL[2]), .Input(CO),
    .InputX(DC), .InputY(colorpixel_1_inputy), .Clock(colorpixel_1_clock), .Clear_2(colorpixel_1_clear_2),
    .Color(CI));
  DotMatrix #(.inputtype("row"), .matrixcols(4), .matrixrows(1)) dotmatrix_1 (.row0(pixelxy_1_x_2));
  // ScreenColor screencolor_1: pin names not known; wires that end beside it: screencolor_1_p1, screencolor_1_p2, screencolor_1_p1, screencolor_1_p2, screencolor_1_p2, screencolor_1_p1
  // Probe on DC
  // Probe on colorpixel_1_inputy
  DotMatrix #(.matrixcols(1), .matrixrows(32)) dotmatrix_2 (.col0(pixelxy_1_y_2));
  pixelXY pixelxy_1 (.X(DC), .Y(colorpixel_1_inputy), .X_2(pixelxy_1_x_2), .Y_2(pixelxy_1_y_2));

  // Other names for the same wires on the sheet: C[23:0] = {in_3, in_2, in_1}; R[7:0] = in_1; G[7:0] = in_2;
  //   B[7:0] = in_3

  // Notes on the sheet:
  //   R
  //   G
  //   B
  //   C
  //   C
  //   R G B C
endmodule

module main_image_color (
);

  wire button_1_out, clock_1_out, imageromscreen_1_p4, imageromscreen_1_p5, imageromscreen_1_p6,
       imageromscreen_1_p7;
  wire [15:0] imageromscreen_1_p8;
  wire [23:0] rom_1_data;

  Button button_1 (.out(button_1_out));
  Clock clock_1 (.out(clock_1_out));
  // ScreenColor screencolor_1: pin names not known
  ROM #(.addrWidth(16), .dataWidth(24)) rom_1 (.addr(imageromscreen_1_p8), .data(rom_1_data), .sel(1'b1));
  // ImageRomScreen imageromscreen_1: pin names not known; wires that end beside it: rom_1_data, button_1_out, clock_1_out, imageromscreen_1_p4, imageromscreen_1_p5, imageromscreen_1_p6, imageromscreen_1_p7, imageromscreen_1_p8, imageromscreen_1_p5, imageromscreen_1_p4, clock_1_out

  // Notes on the sheet:
  //   contents of rom_1 (hex, n*v repeats v):
  //   e8 74 17*ffffff fdfdfd fdfdfd fbfbfb fafafa f8f8f8 f5f5f5 f3f3f3 f1f1f1 efefef ededed ededed ededed
  //   ebebeb ebebeb ededed ededed ededed efefef f1f1f1 f3f3f3 f5f5f5 f7f7f7 f9f9f9 fbfbfb fcfcfc fdfdfd
  //   88*ffffff fdfdfd fdfdfd fbfbfb f8f8f8 f5f5f5 f3f3f3 f0f0f0 eceae8 e3cab5 e4af81 e79c5a eb9346 ee8d36
  //   ef8b30 ef8b2e ee8d35 eb9145 e59855 dea677 d6b99f d5ccc3 e4e4e4 eaeaea ededed f1f1f1 f4f4f4 f7f7f7
  //   f9f9f9 fbfbfb fdfdfd fefefe 83*ffffff fdfdfd fdfdfd fbfbfb f7f7f7 f5f5f5 f0f0f0 ebe2db e7ae7f ec8e3a
  //   f68611 f78805 fa8e07 fb920b fb950b fb960d fb960d fb950b fb930b fb9109 fb8d07 fb8a05 fa8705 f68411
  //   ec8b32 da9e6b cfbcac dbdada e6e6e6 eeeeee f2f2f2 f5f5f5 f9f9f9 fbfbfb fdfdfd fefefe 80*ffffff fdfdfd
  //   fbfbfb f8f8f8 f5f5f5 f0f0f0 e9c7aa eb903d f78407 fa8d07 fa960b fd9d0f fea312 fea616 ffa718 ffaa1b
  //   ffaa1b ffa719 ffa719 ffa416 ffa112 ff9e0f ff9c0d fe990a fd9508 fd9206 fb8a05 fa8607 e68b35 d1a988
  //   d2d0ce e0e0e0 ededed f2f2f2 f6f6f6 f9f9f9 fbfbfb fdfdfd 77*ffffff fdfdfd fdfdfd fafafa f6f6f6 f2f2f2
  //   ebc9ae ef8a31 f78707 fb920b fb9d11 fea516 ffac1b ffaf1e ffb321 ffb422 ffb724 ffb525 ffb425 ffb325
  //   ffaf22 ffad1e ffaa19 ffa714 ffa612 ffa410 ffa210 ffa10c ff9f0d fe990a fe9206 fb8a05 eb8a29 cfa986
  //   cecdcc e1e1e1 eeeeee f3f3f3 f7f7f7 fbfbfb fdfdfd fefefe 74*ffffff fdfdfd fbfbfb f8f8f8 f4f4f4 ede7e3
  //   eb9348 f78505 fb920d fd9f11 fea718 ffaf1c ffb422 ffb825 ffbd28 ffbd2a ffbd2b ffbe2c ffbd2c ffba2c
  //   ffb72b ffb328 ffb124 ffac1e ffaa19 ffaa16 ffa714 ffa712 ffa710 ffa710 ffa710 ffa40e ffa00d fd9708
  //   fb8b03 e38c3a c7b7a9 d0d0d0 e9e9e9 f0f0f0 f5f5f5 f9f9f9 fcfcfc fdfdfd 72*ffffff fdfdfd fbfbfb f8f8f8
  //   f2f2f2 ebc09a f38213 fa8e09 fd9d0f fea718 ffaf1e ffb722 ffbb25 ffbd2a ffc02a ffc22e ffc22e ffc330
  //   ffc232 ffbe30 ffbb2f ffb72e ffb32a ffae27 ffab1f ffa81b ffa716 ffa716 ffa812 ffaa12 ffad12 ffad14
  //   ffad14 ffad12 ffa80e fea20d fb9508 f6890f cd996a c8c8c8 dfdfdf eeeeee f4f4f4 f8f8f8 fcfcfc fdfdfd
  //   70*ffffff fdfdfd fbfbfb f7f7f7 f2f2f2 eda167 f78405 fb950d fea314 ffad1c ffb41f ffba22 ffc02c ffc437
  //   ffc740 ffca42 ffc940 ffc738 ffc432 ffc030 ffbd30 ffb82e ffb32b ffad28 ffa824 ffa51e ffa118 ffa116
  //   ffa314 ffa612 ffa812 ffad14 ffb114 ffb314 ffb516 ffb414 ffb112 ffab10 fe9e08 fb9005 dc924a bfbab7
  //   d7d7d7 ececec f2f2f2 f8f8f8 fbfbfb fdfdfd 68*ffffff fdfdfd fbfbfb f6f6f6 f0f0f0 ee9347 f78707 fb9a0f
  //   fea718 ffb11b ffb821 ffc23a ffcd57 ffd267 ffd46c ffd669 ffd160 ffcf57 ffcc4e ffc740 ffc032 ffbb2f
  //   ffb52e ffaf2a ffa927 ffa423 ff9f1d ff9d18 ff9c12 ff9d10 ffa110 ffa610 ffac12 ffb214 ffb716 ffbb16
  //   ffbd15 ffbd15 ffb816 ffb214 fda60c fb9305 e38d38 bdb6b0 d1d1d1 ebebeb f2f2f2 f8f8f8 fbfbfb fdfdfd
  //   56*ffffff fefefe 9*ffffff fdfdfd fbfbfb f7f7f7 f0f0f0 ee8f3d f98907 fb9c11 ffaa18 ffb21b ffc03b
  //   ffd16a ffda84 ffda83 ffd779 ffdb74 ffd368 ffd262 ffcf57 ffcc4e ffc847 ffbf36 ffb92e ffb32c ffac2a
  //   ffa624 ff9f20 ff9a19 ff9714 ff9611 ff970f ff9b0d ffa10f ffa70e ffae12 ffb714 ffbd17 ffc117 ffc319
  //   ffc219 ffbd15 ffb712 ffaa0c fb9706 e68d31 bcb5ae d2d2d2 ebebeb f2f2f2 f8f8f8 fcfcfc fdfdfd 23*ffffff
  //   fefefe 4*fdfdfd fefefe 22*ffffff fdfdfd fdfdfd fbfbfb fbfbfb fafafa fbfbfb fbfbfb fdfdfd fdfdfd
  //   4*ffffff fdfdfd fbfbfb f8f8f8 f2f2f2 ee944a f98905 fd9d11 ffaa16 ffb421 ffca5e ffdc90 ffdf93 ffdc87
  //   ffda7f ffdf7c deb559 7e5819 d8c06b ffdb66 ffc94c ffc546 ffbf37 ffb82e ffb22b ffa928 ffa224 ff9c1e
  //   ff9616 ff9311 ff930d ff930a ff970d ff9d0d ffa40e ffac10 ffb314 ffbb17 ffc217 ffc619 ffc71a ffc71a
  //   ffc117 ffb814 ffab0c fb9806 e28d39 bcb9b5 d3d3d3 ebebeb f3f3f3 f8f8f8 fcfcfc fefefe 20*ffffff fefefe
  //   fdfdfd fcfcfc fafafa f9f9f9 f9f9f9 fafafa fbfbfb fcfcfc fefefe 19*ffffff fdfdfd fbfbfb f8f8f8 f6f6f6
  //   f4f4f4 f4f4f4 f4f4f4 f6f6f6 f9f9f9 fbfbfb 4*ffffff fdfdfd f8f8f8 f2f2f2 eea367 f78705 fb9c11 ffa812
  //   ffb82c ffd47d ffe2a4 ffdf98 ffdd8f ffdc86 ffe084 e9c268 704608 6c4408 ebd981 ffd760 ffc94c ffc546
  //   ffbe37 ffb82e ffb12b ffa828 ffa124 ff9a1e ff9416 ff910f ff900d ff910a ff950a ff9c0a ffa30c ffac10
  //   ffb412 ffbd15 ffc217 ffc819 ffcc1a ffcd1a ffcc1a ffc417 ffb914 ffac0e fb9606 db924a bababa d9d9d9
  //   ececec f4f4f4 f9f9f9 fcfcfc fefefe 18*ffffff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
  //   Other.jar
  //   Other.jar
endmodule

module main_2_images_colors (
  input  in_1
);

  wire CLE_out, CLI_out, clock_1_out, imageromscreen_1_p4, imageromscreen_1_p5, imageromscreen_1_p6,
       imageromscreen_1_p7;
  wire [15:0] demultiplexer_1_out0, demultiplexer_1_out1, imageromscreen_1_p8;
  wire [23:0] imageromscreen_1_p1, rom_1_data, rom_2_data;

  Button CLI (.out(CLI_out));
  Button CLE (.out(CLE_out));
  Clock clock_1 (.out(clock_1_out));
  Demultiplexer #(.width(16), .enable("false")) demultiplexer_1 (
    .out0(demultiplexer_1_out0), .out1(demultiplexer_1_out1), .in(imageromscreen_1_p8), .sel(in_1));
  // ImageRomScreen imageromscreen_1: pin names not known; wires that end beside it: imageromscreen_1_p1, CLI_out, clock_1_out, imageromscreen_1_p4, imageromscreen_1_p5, imageromscreen_1_p6, imageromscreen_1_p7, imageromscreen_1_p8
  ROM #(.addrWidth(16), .dataWidth(24)) rom_1 (.addr(demultiplexer_1_out0), .data(rom_1_data), .sel(1'b1));
  ROM #(.addrWidth(16), .dataWidth(24)) rom_2 (.addr(demultiplexer_1_out1), .data(rom_2_data), .sel(1'b1));
  Multiplexer #(.width(24), .enable("false")) multiplexer_1 (
    .in0(rom_1_data), .in1(rom_2_data), .out(imageromscreen_1_p1), .sel(in_1));
  // ScreenColor screencolor_1: pin names not known

  // Notes on the sheet:
  //   Other.jar
  //   contents of rom_1 (hex, n*v repeats v):
  //   100 80 a0e2f a0929 a0828 b1d3e a2a4a b4668 a1e3f a0b2a a0b2b a3056 90c2d a0e2f a0f2f b1030 a1031
  //   b1131 a1334 b1434 b1436 a1636 a1739 b1739 a5e85 b4168 a1737 a0c2c b193b a1131 a1536 a3a63 b2043
  //   a1939 b1e41 b102f a1737 b2144 a0c2c a183a a1c3e a1435 b2e55 a2244 a1130 a2043 b1334 a2448 b3760
  //   a1031 a1536 a4168 a1132 b1e41 a2448 a183a a0f2f a1b3f a0f2f a1638 a0f2f a1739 a0e2f a1738 b0f30
  //   a0e2e b3058 a2245 a1f41 b0f2f b193b b2348 a2145 a0f2f b102f a1638 a0f30 a1536 a1032 a1434 a1234
  //   91233 a1536 a1c3d b1e3f a4c76 b416c a345e a294f a1534 a1638 a1737 b0f2f a1739 a0f2e a1636 b0f30
  //   a1233 b1333 a0e2e a2b4d b1232 b1c3f a2045 a1f42 a1e41 a264a a2245 b0727 b0827 b0827 a1030 b0f30
  //   a0b2c b0928 a0b2b a1435 a1030 a0a2a a0727 b0f2f a1132 a0c2c b0928 b0827 a2447 a1030 b0f2f b0e2f
  //   b0e2f a0e2e a0929 a0928 a2d53 b4065 a6d95 92d50 a0c2b a0b2b a2649 90b2d a0e2f a0f2f a1030 a1031
  //   b1030 a1132 b1435 b1437 91637 a1739 b1739 b4f71 a3355 a193b a1130 a1c3f a1131 a1939 a4775 a1a3d
  //   a183b b1c3f a0e2f a183a b2c52 a0c2c a2044 a294c b1d3e a5481 b4b6e a1232 a274d b1233 b264b a4d7b
  //   a1132 a183a a5e8a a1031 92144 b284e a1839 a0f2f a1c3f b0f2f b1639 a0f2f a1839 a0f2f b1739 a0f30
  //   a0f2f b3059 a2448 b1f42 b0f2f a1a3c a254a a2145 a1030 a102f a1738 a1030 b1636 a1132 a1435 b1234
  //   a1233 a1636 a1031 a365d a507e a4a78 a3d69 b345c a1232 a0f2f a1738 b1030 a1739 a0f2f a1636 b0f30
  //   a1333 b1333 a0e2e b2b4e b1232 a1b3e a2349 b2448 b3c61 a264b a2347 b0827 b0827 b0827 a0f30 b0f2f
  //   a0b2c b0928 a0b2b a1435 a0f30 a0a2a a0727 b0f30 a1232 a0c2c b0928 b0828 a1f40 a1637 b0e2f b0e2f
  //   b0e2f b0d2f a0929 a0828 a2549 a3959 b5e82 a2648 a0b2b a0b2a a2a4f a0c2d a0e2f a0f2f a1031 a1031
  //   90d2c a0d2d b1233 b1437 91638 a1739 a1839 b577d b385c b1132 b1232 b2348 b1637 a1d3f b5c88 a2346
  //   a1e40 a2b50 b1030 c2145 a345d b0d2e b2d52 a2c53 a2e50 c6e9b a5477 a1838 b3861 91a3c b4066 b7bab
  //   b2142 b294d a709d a1334 a2f55 b2d54 a1739 a0f2f b1d40 a0f2f b1739 a102f a183a a0f2f a1839 b0f30
  //   a0f2f a3159 b1739 a1c3f a1535 a1637 b1d40 a2145 a0f30 a1030 a1739 a1030 b1637 91231 a1535 a1234
  //   a1333 a1536 a0f2f b2c51 b436e a3c67 b3760 a1b3c b0f2f a0f30 a1738 a1030 a1839 a0f2f a1637 a0f2f
  //   a1334 b1333 a0e2f b2d4f a1132 b1e41 a254a a2449 b3e66 a274b a2548 b0828 b0827 b0827 a0f30 a0f2f
  //   a0b2c b0828 a0b2b a1435 a0f30 a0a2a a0727 b0f30 a1232 a0c2d a0828 b0827 a0d2d a2446 b0e2f b0e2f
  //   b0e2f a0a2b a0929 a0928 b2345 a3556 a587b a2445 b0c2b a0b2b b2d53 a0c2d a0e2f a0f2f a1031 b1032
  //   90d2d a0d2e b1333 b1636 91638 a1839 a1839 b5e80 b3c61 a0f2f 90c2c a294f a1233 a1838 a375e b1334
  //   a1737 a1737 a0c2b 9102f b2242 90b2a a1333 b2143 b2245 b5281 b4a6f a1333 b2243 a1130 a1f3f b5478
  //   b1939 a1c3e a5278 a1232 b2a50 a355c a193a a0f2f b1d41 b0f30 a183a a1030 a183b a0f2f a183a b0f30
  //   b0f2e a315a a1f43 b1e42 b1a3c a183a a2246 a2246 a1030 a1030 a183a a1031 a1737 a1232 91636 91335
  //   b1232 a1637 a0f2f a1233 a1b3d a2043 a1536 a0e2e a0f31 a1030 a183a a1030 a183a a0f2f a1738 b0f30
  //   a1435 b1334 a0f2e b1736 a1131 b1739 a1a3b a1c3f b1a3b a2549 a264a b0929 b0827 b0827 a0f2f a1030
  //   a0c2c a0928 a0b2b a1536 a0f30 a0a2a a0727 b1030 a1232 a0c2d b0929 a0726 a0a2a b2245 b0e2f b0e2f
  //   b0e2f a0929 a0929 a0829 a3056 b476c b769f b3056 a0c2b a0a2b b2549 a0c2d a0f2f a0f2f a1031 b1133
  //   b1133 a1233 a1535 b1636 91638 a1839 a1839 b4d6e a2e50 a0f30 a0c2d a1f42 b1132 b2548 b5888 a1c3e
  //   a1a3c a1b3d a0d2d a1434 b1f42 b0b2b a1c3e a2d53 a1f42 a5f8e a5678 b1233 b1e41 a1130 a2042 b5782
  //   b1c3d a3056 b79a5 a1232 a2347 a2e55 a1334 a1332 b1e41 a1032 a183a a1131 a1a3c a1030 a193b a1031
  //   a0f2e a315a a2b52 b173a a0d2e a193c a2247 a1e40 a1131 a1130 b193b a1132 a1839 a1233 a1334 b1536
  //   b1131 a1334 a1435 a1231 b1030 a1031 a1132 b1937 c4467 a1030 a183a a1031 b193a a0f30 a1839 a1030
  //   b1535 a1435 a0f2f a1030 90d2e a0d2d a0e2d a0d2d a0d2d a1d3d b274b b0c2a b0827 b0827 a0f2f a0f2f
  //   a0c2c a0828 a0b2b a1536 a0f30 a0b2a b0828 a1030 a1333 a0d2d b0929 b0727 b0b2b a1636 b1a3a a0e2f
  //   b0e2f a0929 a0929 a0728 a1535 a1e3e a314f b1737 a0d2d a0d2e a355e 90c2c a0f2f a0f2f b1031 b1133
  //   a1233 a1334 a1535 b1636 91638 a1739 a1839 b698e a466b a0f30 a0e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
  //   contents of rom_2 (hex, n*v repeats v):
  //   100 8 cee6f2 cee6f2 cee6f0 cfe7f1 cfe7f1 d0e8f2 d0e8f2 cfe7f1 cee6f0 d0e6f1 cee6f2 cee6f0 cfe8ef
  //   cfe7f1 cee4f2 cfe7f1 cee6f0 cfe7f1 cfe8ef cfe7f1 d0e6f1 d0e6f1 cfe7f3 cee5f3 cee6f0 cde8f1 bcd3d9
  //   707b7f 677075 bbcdd7 cee6f2 cee5f3 cee6f0 cfe7f1 aec1c8 52575a 414548 abbcc4 cfe5f0 cfe7f1 cee6f2
  //   cde8f1 9bacb3 393a3e 17181a 97a6ab cee6f2 cfe7f1 cee6f2 cee6f2 b7cad1 a4b6ba a1b3b7 b7cad1 cfe7f1
  //   cee5f3 cee6f0 cfe7f1 cee6f0 cfe7f1 cee6f2 cee6f2 cee6f2 cee6f0 cee6f0 cfe7f1 d0e6f1 cfe7f3 d0e6f1
  //   d1e7f2 cfe7f1 cee6f2 a1c7da 9fc5d8 a0c5d8 9fc5d8 9fc5da 9fc5d8 9fc5d8 9fc4de abcbe4 edf8fe eff8ff
  //   edf8fe edf8fe eef9ff edf8fe accbe7 b4cfe2 feffff 5*ffffff b7d2e7 b3cde4 feffff ffffff fdfdfd ebebeb
  //   e1e1e1 ffffff b8d0e8 b1cde3 feffff e0e0e0 d4d4d6 cccccc ffffff fffdfe b8d1e7 b8d2e3 feffff d6d6d6
  //   f1f1f1 d8dad9 fefefe ffffff b8d1e7 bad1e3 feffff fdfdfd e4e4e4 fcfcfc ffffff ffffff b8d0e8 bad1e1
  //   feffff fefefe 4*ffffff b8d1e7 bbd2e4 feffff ffffff f3f3f3 ffffff ffffff ffffff b8d0e8 b2cce3 feffff
  //   fefefe bdbdbd cdcdcd ededed ffffff b8d1e7 b3cee3 feffff ffffff dadada c0c0c0 d9d9d9 ffffff b7d2e7
  //   b3cee1 feffff ffffff eeeeee 9f9f9f bbbbbb fefefe b8d1e7 b4cfe0 feffff ffffff e3e3e3 d4d4d4 dbdbdb
  //   ffffff b7d1e8 b4cfe2 feffff ffffff f2f2f2 b9b9b9 eaeaea ffffff b7d2e7 b5cfe0 feffff ffffff ededed
  //   cfcfcf e5e5e5 ffffff b7d2e7 b6cddf feffff ffffff e6e6e6 d0d0d0 f1f1f1 ffffff b8d0e8 b4cfe2 feffff
  //   ffffff eeeeee e4e4e4 f5f5f5 ffffff bad0e7 b4cfe2 fdfffe ffffff ececec b9b9b9 eaeaea ffffff b9cfe6
  //   b5cfe0 feffff ffffff dedede eaeaea dedede ffffff b8d0e8 b5cee2 feffff ffffff efefef e3e3e3 f5f5f5
  //   ffffff b7d1e8 b4cfe2 feffff ffffff f1f1f1 d0d0d0 cfcfcf fefefe b8d1e7 b4cfe2 feffff ffffff e7e7e7
  //   cecece e0e0e0 ffffff b8d1e7 b4cfe2 feffff ffffff ececec cdcdcd e4e4e4 ffffff b7d0e6 b5d0e3 feffff
  //   ffffff f1f1f1 c7c7c7 ededed ffffff b8d1e7 b5d0e3 feffff ffffff f4f4f4 d5d5d5 dadada ffffff b8d1e7
  //   b3cee1 feffff ffffff e7e7e7 939393 dedede ffffff b8d1e7 b5d0e3 feffff ffffff efefef f6f6f6 ffffff
  //   ffffff b8d1e7 b5d0e3 feffff ffffff f2f2f2 d0d0d0 f0f0f0 ffffff b8d1e7 b4cfe2 feffff ffffff eaeaea
  //   c6c6c6 f2f2f2 ffffff b8d1e7 b4cfe2 feffff ffffff e9e9e9 d1d1d1 e1e1e1 ffffff b8d1e7 b4cfe2 feffff
  //   ffffff eaeaea c8c8c8 e1e1e1 ffffff b8d1e7 b6d1e4 feffff ffffff c9c9c9 cbcbcb e5e5e5 ffffff b7d0e6
  //   b4cfe2 feffff ffffff e7e7e7 cecece efefef ffffff b8d1e7 b4cfe2 feffff ffffff ececec b7b7b7 e4e4e4
  //   ffffff b8d1e7 b3cee1 feffff ffffff eeeeee bebebe e5e5e5 ffffff b8d1e7 b3cee1 feffff ffffff e8e8e8
  //   c9c9c9 f6f6f6 ffffff b8d1e7 b5d0e3 feffff ffffff e1e1e1 e9e9e9 d8d8d8 ffffff b8d1e7 b4cfe2 feffff
  //   ffffff c8c8c8 cdcdcd efefef ffffff b8d1e7 b4cfe2 feffff ffffff f1f1f1 bababa efefef ffffff b8d1e7
  //   b5d0e3 feffff ffffff e4e4e4 b8b8b8 d8d8d8 ffffff b8d1e7 b5d0e3 feffff ffffff eeeeee b7b7b7 eaeaea
  //   ffffff b8d1e7 b4cfe2 feffff ffffff f0f0f0 fbfbfb ffffff ffffff b8d1e7 b5d0e3 feffff 5*ffffff b8d1e7
  //   b4cfe2 feffff 5*ffffff b8d1e7 b4cfe2 feffff 5*ffffff b8d1e7 b4cfe2 feffff 5*ffffff b8d1e7 b5d0e3
  //   feffff 5*ffffff b8d1e7 b4cfe2 feffff 5*ffffff b8d1e7 b4cfe2 feffff 5*ffffff b8d1e7 b4cfe2 feffff
  //   5*ffffff b8d1e7 b4cfe2 feffff 5*ffffff b8d1e7 b4cfe2 feffff 5*ffffff b8d1e7 b4cfe2 feffff 5*ffffff
  //   b8d1e7 b4cfe2 feffff 5*ffffff b8d1e7 b4cfe2 feffff 5*ffffff b8d1e7 b4cfe2 feffff 5*ffffff b8d1e7
  //   b4cfe2 feffff 5*ffffff b8d1e7 b4cfe2 feffff 5*ffffff b8d1e7 b4cfe2 feffff 5*ffffff b8d1e7 b4cfe2
  //   feffff 5*ffffff b8d1e7 b4cfe2 feffff 5*ffffff b8d1e7 b4cfe2 feffff 5*ffffff b8d1e7 b4cfe2 feffff
  //   5*ffffff b8d1e7 b4cfe4 feffff ffffff fefefe ffffff ffffff ffffff b9d2e8 b3d0e2 feffff ffffff fefefe
  //   ffffff ffffff ffffff b8d0e8 b4cfe2 feffff 4*ffffff feffff b7d1e8 b5d0e3 feffff 5*ffffff b7d2e5
  //   b5d0e3 ffffff ffffff feffff feffff ffffff ffffff b7d2e5 adcde2 f1faff 4*f1fbfd f2f9ff aecee7 98c1df
  //   98c1dd 98c1dd 98c1dd 97c3de 99c2de 98c1dd 93c0df c2e0eb c3e1eb c2e0eb c2e0eb c3e1ec c3e1ec c3e1eb
  //   c3e1ec c3e1ec c2e0eb c3e1ec c2e0eb c0e0eb c2e0eb c2e0eb c3e1ec c4e2ed c4e0eb c8d7d0 d1ddc9 d2deca
  //   caddd9 c2e0eb c2e0eb c4e0ec c4e1e9 cfb97f fad56a afb38e a3b8b1 c0e0ef c3e1ec c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
  //   Other.jar
endmodule

module colorToRGB (
  input  [23:0] in_1,
  output [23:0] out_2,
  output [23:0] out_3,
  output [23:0] out_4
);

  assign out_2 = 24'hff0000 & in_1;  // AND_Gate and_1, 24 bits wide
  assign out_3 = 24'hff00 & in_1;  // AND_Gate and_2, 24 bits wide
  assign out_4 = 24'hff & in_1;  // AND_Gate and_3, 24 bits wide
endmodule

module colorPixel (
  input  [7:0] Red,
  input  [7:0] Green,
  input  [7:0] Blue,
  input  Row,
  input  Column,
  input  Clear,
  output [23:0] Color,
  output [23:0] Input,
  output [1:0] InputX,
  output [4:0] InputY,
  output Clock,
  output Clear_2
);

  wire d_ff_1_q, d_ff_1_qn;
  wire [23:0] colortorgb_1_out_2, colortorgb_1_out_3, colortorgb_1_out_4;

  Counter #(.width(2), .max('h3), .trigger("falling")) counter_1 (
    .load(1'b0), .D(2'b00), .count(1'b1), .Q(InputX), .clk(d_ff_1_q), .clr(Clear));  // open: carry
  D_Flip_Flop d_ff_1 (
    .clk(Column), .D(d_ff_1_qn), .Q(d_ff_1_q), .Qn(d_ff_1_qn), .preset(1'b0), .en(1'b1), .reset(Clear));
  colorToRGB colortorgb_1 (
    .in_1({Red, Green, Blue}), .out_2(colortorgb_1_out_2), .out_3(colortorgb_1_out_3),
    .out_4(colortorgb_1_out_4));
  Multiplexer #(.select(2), .width(24), .enable("false")) multiplexer_1 (
    .in0(colortorgb_1_out_2), .in1(colortorgb_1_out_3), .in2(colortorgb_1_out_4), .in3({Red, Green, Blue}),
    .out(Input), .sel(InputX));
  Counter #(.width(5), .max('h1f)) counter_2 (
    .load(1'b0), .D({5{1'b0}}), .count(1'b1), .Q(InputY), .clk(Row), .clr(Clear));  // open: carry

  assign Clear_2 = Clear;
  assign Clock = Column;
  assign Color = {Red, Green, Blue};
endmodule

module pixelXY (
  input  [1:0] X,
  input  [4:0] Y,
  output [3:0] X_2,
  output [31:0] Y_2
);

  Decoder #(.select(2), .enable("false")) decoder_1 (
    .out0(X_2[3]), .out1(X_2[2]), .out2(X_2[1]), .out3(X_2[0]), .sel(X));
  Decoder #(.select(5), .enable("false")) decoder_2 (
    .out0(Y_2[31]), .out1(Y_2[30]), .out2(Y_2[29]), .out3(Y_2[28]), .out4(Y_2[27]), .out5(Y_2[26]),
    .out6(Y_2[25]), .out7(Y_2[24]), .out8(Y_2[23]), .out9(Y_2[22]), .out10(Y_2[21]), .out11(Y_2[20]),
    .out12(Y_2[19]), .out13(Y_2[18]), .out14(Y_2[17]), .out15(Y_2[16]), .out16(Y_2[15]), .out17(Y_2[14]),
    .out18(Y_2[13]), .out19(Y_2[12]), .out20(Y_2[11]), .out21(Y_2[10]), .out22(Y_2[9]), .out23(Y_2[8]),
    .out24(Y_2[7]), .out25(Y_2[6]), .out26(Y_2[5]), .out27(Y_2[4]), .out28(Y_2[3]), .out29(Y_2[2]),
    .out30(Y_2[1]), .out31(Y_2[0]), .sel(Y));
endmodule
