// Logisim project 13_screen_black.circ as structural Verilog: 5 circuits, main circuit main_led_matrix
module main_led_matrix (
  input  [31:0] in_1,
  input  [7:0] in_2,
  input  [7:0] in_3,
  input  [7:0] in_4,
  input  [7:0] in_5
);

  DotMatrix #(.matrixcols(4), .matrixrows(8)) dotmatrix_1 (.col0(in_2), .col1(in_3), .col2(in_4), .col3(in_5));
  DotMatrix #(.matrixcols(8), .matrixrows(1)) dotmatrix_2 (
    .col0(in_1[31]), .col1(in_1[30]), .col2(in_1[29]), .col3(in_1[28]), .col4(in_1[27]), .col5(in_1[26]),
    .col6(in_1[25]), .col7(in_1[24]));
  DotMatrix #(.matrixcols(8), .matrixrows(1)) dotmatrix_3 (
    .col0(in_1[23]), .col1(in_1[22]), .col2(in_1[21]), .col3(in_1[20]), .col4(in_1[19]), .col5(in_1[18]),
    .col6(in_1[17]), .col7(in_1[16]));
  DotMatrix #(.matrixcols(8), .matrixrows(1)) dotmatrix_4 (
    .col0(in_1[15]), .col1(in_1[14]), .col2(in_1[13]), .col3(in_1[12]), .col4(in_1[11]), .col5(in_1[10]),
    .col6(in_1[9]), .col7(in_1[8]));
  DotMatrix #(.matrixcols(8), .matrixrows(1)) dotmatrix_5 (
    .col0(in_1[7]), .col1(in_1[6]), .col2(in_1[5]), .col3(in_1[4]), .col4(in_1[3]), .col5(in_1[2]),
    .col6(in_1[1]), .col7(in_1[0]));
  DotMatrix #(.inputtype("row"), .matrixcols(8), .matrixrows(4)) dotmatrix_6 (
    .row0(in_1[31:24]), .row1(in_1[23:16]), .row2(in_1[15:8]), .row3(in_1[7:0]));
  LED led_1 (.in(in_1[29]));
  LED led_2 (.in(in_1[30]));
  LED led_3 (.in(in_1[31]));
  LED led_4 (.in(in_1[23]));
  LED led_5 (.in(in_1[21]));
  LED led_6 (.in(in_1[22]));
  LED led_7 (.in(in_1[15]));
  LED led_8 (.in(in_1[13]));
  LED led_9 (.in(in_1[14]));
  LED led_10 (.in(in_1[6]));
  LED led_11 (.in(in_1[5]));
  LED led_12 (.in(in_1[7]));
  LED led_13 (.in(in_1[27]));
  LED led_14 (.in(in_1[26]));
  LED led_15 (.in(in_1[25]));
  LED led_16 (.in(in_1[28]));
  LED led_17 (.in(in_1[19]));
  LED led_18 (.in(in_1[17]));
  LED led_19 (.in(in_1[18]));
  LED led_20 (.in(in_1[20]));
  LED led_21 (.in(in_1[11]));
  LED led_22 (.in(in_1[9]));
  LED led_23 (.in(in_1[12]));
  LED led_24 (.in(in_1[10]));
  LED led_25 (.in(in_1[4]));
  LED led_26 (.in(in_1[1]));
  LED led_27 (.in(in_1[3]));
  LED led_28 (.in(in_1[2]));
  LED led_29 (.in(in_1[24]));
  LED led_30 (.in(in_1[16]));
  LED led_31 (.in(in_1[8]));
  LED led_32 (.in(in_1[0]));

  // Notes on the sheet:
  //   LED Matrix (line)
  //   LED Matrix
  //   LED Matrix (LEDS)
endmodule

module main_screen_column (
  input  E,
  input  [4:0] Y,
  input  X,
  input  I,
  input  [4:0] Y_2,
  input  E_2,
  input  H,
  input  [2:0] X_2,
  input  [4:0] Y_3,
  input  H_2,
  input  I_2,
  input  E_3,
  input  H_3,
  input  I_3,
  input  [31:0] in_15,
  input  [31:0] in_16,
  input  [31:0] in_17,
  input  [31:0] in_18,
  input  [31:0] in_19,
  input  [31:0] in_20,
  input  [31:0] in_21,
  input  [31:0] in_22
);

  wire CL_2_out, CL_3_out, CL_out, decoder_1_out0, decoder_1_out1;
  wire [31:0] l32_1_o, l32_2_o, l32_3_o, lc8_1_o0, lc8_1_o1, lc8_1_o2, lc8_1_o3, lc8_1_o4, lc8_1_o5,
       lc8_1_o6, lc8_1_o7;

  Button CL (.out(CL_out));
  DotMatrix #(.matrixcols(1), .matrixrows(32)) dotmatrix_1 (.col0(l32_1_o));
  L32 l32_1 (.E(E), .L(Y), .I(I), .H(H), .CL(CL_out), .O(l32_1_o));
  Decoder #(.disabled(0)) decoder_1 (.out0(decoder_1_out0), .out1(decoder_1_out1), .sel(X), .en(E_2));
  Button CL_2 (.out(CL_2_out));
  L32 l32_2 (.E(decoder_1_out0), .L(Y_3), .I(I_2), .H(H_3), .CL(CL_2_out), .O(l32_2_o));
  L32 l32_3 (.E(decoder_1_out1), .L(Y_3), .I(I_2), .H(H_3), .CL(CL_2_out), .O(l32_3_o));
  DotMatrix #(.matrixcols(2), .matrixrows(32)) dotmatrix_2 (.col0(l32_2_o), .col1(l32_3_o));
  Button CL_3 (.out(CL_3_out));
  DotMatrix #(.matrixcols(8), .matrixrows(32)) dotmatrix_3 (
    .col0(lc8_1_o0), .col1(lc8_1_o1), .col2(lc8_1_o2), .col3(lc8_1_o3), .col4(lc8_1_o4), .col5(lc8_1_o5),
    .col6(lc8_1_o6), .col7(lc8_1_o7));
  LC8 lc8_1 (
    .Enable(E_3), .X(X_2), .Y(Y_2), .I(I_3), .H(H_2), .CL(CL_3_out), .O0(lc8_1_o0), .O1(lc8_1_o1),
    .O2(lc8_1_o2), .O3(lc8_1_o3), .O4(lc8_1_o4), .O5(lc8_1_o5), .O6(lc8_1_o6), .O7(lc8_1_o7));
  DotMatrix #(.matrixcols(8), .matrixrows(32)) dotmatrix_4 (
    .col0(in_15), .col1(in_16), .col2(in_17), .col3(in_18), .col4(in_19), .col5(in_20), .col6(in_21),
    .col7(in_22));

  // Notes on the sheet:
  //   other_chip8_lib.circ
  //   other_chip8_lib.circ
  //   other_chip8_lib.circ
endmodule

module main_screen_column_2 (
  input  [4:0] Y,
  input  [4:0] X,
  input  H,
  input  E,
  input  I
);

  wire CL_out;
  wire [31:0] lc32_1_o0, lc32_1_out_8, lc32_1_out_9, lc32_1_out_10, lc32_1_out_11, lc32_1_out_12,
       lc32_1_out_13, lc32_1_out_14, lc32_1_out_15, lc32_1_out_16, lc32_1_out_17, lc32_1_out_18,
       lc32_1_out_19, lc32_1_out_20, lc32_1_out_21, lc32_1_out_22, lc32_1_out_23, lc32_1_out_24,
       lc32_1_out_25, lc32_1_out_26, lc32_1_out_27, lc32_1_out_28, lc32_1_out_29, lc32_1_out_30,
       lc32_1_out_31, lc32_1_out_32, lc32_1_out_33, lc32_1_out_34, lc32_1_out_35, lc32_1_out_36,
       lc32_1_out_37, lc32_1_out_38;

  Button CL (.out(CL_out));
  LC32 lc32_1 (
    .enable(E), .X(X), .Y(Y), .H(H), .I(I), .C(CL_out), .O0(lc32_1_o0), .out_8(lc32_1_out_8),
    .out_9(lc32_1_out_9), .out_10(lc32_1_out_10), .out_11(lc32_1_out_11), .out_12(lc32_1_out_12),
    .out_13(lc32_1_out_13), .out_14(lc32_1_out_14), .out_15(lc32_1_out_15), .out_16(lc32_1_out_16),
    .out_17(lc32_1_out_17), .out_18(lc32_1_out_18), .out_19(lc32_1_out_19), .out_20(lc32_1_out_20),
    .out_21(lc32_1_out_21), .out_22(lc32_1_out_22), .out_23(lc32_1_out_23), .out_24(lc32_1_out_24),
    .out_25(lc32_1_out_25), .out_26(lc32_1_out_26), .out_27(lc32_1_out_27), .out_28(lc32_1_out_28),
    .out_29(lc32_1_out_29), .out_30(lc32_1_out_30), .out_31(lc32_1_out_31), .out_32(lc32_1_out_32),
    .out_33(lc32_1_out_33), .out_34(lc32_1_out_34), .out_35(lc32_1_out_35), .out_36(lc32_1_out_36),
    .out_37(lc32_1_out_37), .out_38(lc32_1_out_38));
  DotMatrix #(.matrixcols(8), .matrixrows(32)) dotmatrix_1 (
    .col0(lc32_1_o0), .col1(lc32_1_out_8), .col2(lc32_1_out_9), .col3(lc32_1_out_10), .col4(lc32_1_out_11),
    .col5(lc32_1_out_12), .col6(lc32_1_out_13), .col7(lc32_1_out_14));
  DotMatrix #(.matrixcols(8), .matrixrows(32)) dotmatrix_2 (
    .col0(lc32_1_out_15), .col1(lc32_1_out_16), .col2(lc32_1_out_17), .col3(lc32_1_out_18),
    .col4(lc32_1_out_19), .col5(lc32_1_out_20), .col6(lc32_1_out_21), .col7(lc32_1_out_22));
  DotMatrix #(.matrixcols(8), .matrixrows(32)) dotmatrix_3 (
    .col0(lc32_1_out_23), .col1(lc32_1_out_24), .col2(lc32_1_out_25), .col3(lc32_1_out_26),
    .col4(lc32_1_out_27), .col5(lc32_1_out_28), .col6(lc32_1_out_29), .col7(lc32_1_out_30));
  DotMatrix #(.matrixcols(8), .matrixrows(32)) dotmatrix_4 (
    .col0(lc32_1_out_31), .col1(lc32_1_out_32), .col2(lc32_1_out_33), .col3(lc32_1_out_34),
    .col4(lc32_1_out_35), .col5(lc32_1_out_36), .col6(lc32_1_out_37), .col7(lc32_1_out_38));
  DotMatrix #(.matrixcols(32), .matrixrows(32)) dotmatrix_5 (
    .col0(lc32_1_o0), .col1(lc32_1_out_8), .col2(lc32_1_out_9), .col3(lc32_1_out_10), .col4(lc32_1_out_11),
    .col5(lc32_1_out_12), .col6(lc32_1_out_13), .col7(lc32_1_out_14), .col8(lc32_1_out_15),
    .col9(lc32_1_out_16), .col10(lc32_1_out_17), .col11(lc32_1_out_18), .col12(lc32_1_out_19),
    .col13(lc32_1_out_20), .col14(lc32_1_out_21), .col15(lc32_1_out_22), .col16(lc32_1_out_23),
    .col17(lc32_1_out_24), .col18(lc32_1_out_25), .col19(lc32_1_out_26), .col20(lc32_1_out_27),
    .col21(lc32_1_out_28), .col22(lc32_1_out_29), .col23(lc32_1_out_30), .col24(lc32_1_out_31),
    .col25(lc32_1_out_32), .col26(lc32_1_out_33), .col27(lc32_1_out_34), .col28(lc32_1_out_35),
    .col29(lc32_1_out_36), .col30(lc32_1_out_37), .col31(lc32_1_out_38));

  // Notes on the sheet:
  //   other_chip8_lib.circ
endmodule

module main_screen_black (
  input  [4:0] Y,
  input  [5:0] X,
  input  H,
  input  E,
  input  I
);

  wire CL_out;
  wire [31:0] lc64_1_out_7, lc64_1_out_8, lc64_1_out_9, lc64_1_out_10, lc64_1_out_11, lc64_1_out_12,
       lc64_1_out_13, lc64_1_out_14, lc64_1_out_15, lc64_1_out_16, lc64_1_out_17, lc64_1_out_18,
       lc64_1_out_19, lc64_1_out_20, lc64_1_out_21, lc64_1_out_22, lc64_1_out_23, lc64_1_out_24,
       lc64_1_out_25, lc64_1_out_26, lc64_1_out_27, lc64_1_out_28, lc64_1_out_29, lc64_1_out_30,
       lc64_1_out_31, lc64_1_out_32, lc64_1_out_33, lc64_1_out_34, lc64_1_out_35, lc64_1_out_36,
       lc64_1_out_37, lc64_1_out_38, lc64_1_out_39, lc64_1_out_40, lc64_1_out_41, lc64_1_out_42,
       lc64_1_out_43, lc64_1_out_44, lc64_1_out_45, lc64_1_out_46, lc64_1_out_47, lc64_1_out_48,
       lc64_1_out_49, lc64_1_out_50, lc64_1_out_51, lc64_1_out_52, lc64_1_out_53, lc64_1_out_54,
       lc64_1_out_55, lc64_1_out_56, lc64_1_out_57, lc64_1_out_58, lc64_1_out_59, lc64_1_out_60,
       lc64_1_out_61, lc64_1_out_62, lc64_1_out_63, lc64_1_out_64, lc64_1_out_65, lc64_1_out_66,
       lc64_1_out_67, lc64_1_out_68, lc64_1_out_69, lc64_1_out_70;

  // ScreenColor screencolor_1: pin names not known
  Button CL (.out(CL_out));
  DotMatrix #(.matrixcols(32), .matrixrows(32)) dotmatrix_1 (
    .col0(lc64_1_out_7), .col1(lc64_1_out_8), .col2(lc64_1_out_9), .col3(lc64_1_out_10),
    .col4(lc64_1_out_11), .col5(lc64_1_out_12), .col6(lc64_1_out_13), .col7(lc64_1_out_14),
    .col8(lc64_1_out_15), .col9(lc64_1_out_16), .col10(lc64_1_out_17), .col11(lc64_1_out_18),
    .col12(lc64_1_out_19), .col13(lc64_1_out_20), .col14(lc64_1_out_21), .col15(lc64_1_out_22),
    .col16(lc64_1_out_23), .col17(lc64_1_out_24), .col18(lc64_1_out_25), .col19(lc64_1_out_26),
    .col20(lc64_1_out_27), .col21(lc64_1_out_28), .col22(lc64_1_out_29), .col23(lc64_1_out_30),
    .col24(lc64_1_out_31), .col25(lc64_1_out_32), .col26(lc64_1_out_33), .col27(lc64_1_out_34),
    .col28(lc64_1_out_35), .col29(lc64_1_out_36), .col30(lc64_1_out_37), .col31(lc64_1_out_38));
  LC64 lc64_1 (
    .E(E), .X(X), .Y(Y), .H(H), .I(I), .C(CL_out), .out_7(lc64_1_out_7), .out_8(lc64_1_out_8),
    .out_9(lc64_1_out_9), .out_10(lc64_1_out_10), .out_11(lc64_1_out_11), .out_12(lc64_1_out_12),
    .out_13(lc64_1_out_13), .out_14(lc64_1_out_14), .out_15(lc64_1_out_15), .out_16(lc64_1_out_16),
    .out_17(lc64_1_out_17), .out_18(lc64_1_out_18), .out_19(lc64_1_out_19), .out_20(lc64_1_out_20),
    .out_21(lc64_1_out_21), .out_22(lc64_1_out_22), .out_23(lc64_1_out_23), .out_24(lc64_1_out_24),
    .out_25(lc64_1_out_25), .out_26(lc64_1_out_26), .out_27(lc64_1_out_27), .out_28(lc64_1_out_28),
    .out_29(lc64_1_out_29), .out_30(lc64_1_out_30), .out_31(lc64_1_out_31), .out_32(lc64_1_out_32),
    .out_33(lc64_1_out_33), .out_34(lc64_1_out_34), .out_35(lc64_1_out_35), .out_36(lc64_1_out_36),
    .out_37(lc64_1_out_37), .out_38(lc64_1_out_38), .out_39(lc64_1_out_39), .out_40(lc64_1_out_40),
    .out_41(lc64_1_out_41), .out_42(lc64_1_out_42), .out_43(lc64_1_out_43), .out_44(lc64_1_out_44),
    .out_45(lc64_1_out_45), .out_46(lc64_1_out_46), .out_47(lc64_1_out_47), .out_48(lc64_1_out_48),
    .out_49(lc64_1_out_49), .out_50(lc64_1_out_50), .out_51(lc64_1_out_51), .out_52(lc64_1_out_52),
    .out_53(lc64_1_out_53), .out_54(lc64_1_out_54), .out_55(lc64_1_out_55), .out_56(lc64_1_out_56),
    .out_57(lc64_1_out_57), .out_58(lc64_1_out_58), .out_59(lc64_1_out_59), .out_60(lc64_1_out_60),
    .out_61(lc64_1_out_61), .out_62(lc64_1_out_62), .out_63(lc64_1_out_63), .out_64(lc64_1_out_64),
    .out_65(lc64_1_out_65), .out_66(lc64_1_out_66), .out_67(lc64_1_out_67), .out_68(lc64_1_out_68),
    .out_69(lc64_1_out_69), .out_70(lc64_1_out_70));
  DotMatrix #(.matrixcols(32), .matrixrows(32)) dotmatrix_2 (
    .col0(lc64_1_out_39), .col1(lc64_1_out_40), .col2(lc64_1_out_41), .col3(lc64_1_out_42),
    .col4(lc64_1_out_43), .col5(lc64_1_out_44), .col6(lc64_1_out_45), .col7(lc64_1_out_46),
    .col8(lc64_1_out_47), .col9(lc64_1_out_48), .col10(lc64_1_out_49), .col11(lc64_1_out_50),
    .col12(lc64_1_out_51), .col13(lc64_1_out_52), .col14(lc64_1_out_53), .col15(lc64_1_out_54),
    .col16(lc64_1_out_55), .col17(lc64_1_out_56), .col18(lc64_1_out_57), .col19(lc64_1_out_58),
    .col20(lc64_1_out_59), .col21(lc64_1_out_60), .col22(lc64_1_out_61), .col23(lc64_1_out_62),
    .col24(lc64_1_out_63), .col25(lc64_1_out_64), .col26(lc64_1_out_65), .col27(lc64_1_out_66),
    .col28(lc64_1_out_67), .col29(lc64_1_out_68), .col30(lc64_1_out_69), .col31(lc64_1_out_70));

  // Notes on the sheet:
  //   Other.jar
  //   other_chip8.circ
endmodule

module main_image_black (
);

  wire button_1_out, clock_1_out, igrb_1_igd, igrb_1_ob, imageromscreen_1_p4, imageromscreen_1_p5,
       imageromscreen_1_p6, imageromscreen_1_p7;
  wire [4:0] igrb_1_oy;
  wire [5:0] igrb_1_ox;
  wire [11:0] igrb_1_or, imageromscreen_1_p8;
  wire [23:0] rom_1_data, rom_2_data;

  // Probe on igrb_1_or
  Clock clock_1 (.out(clock_1_out));
  Button button_1 (.out(button_1_out));
  // ScreenColor screencolor_1: pin names not known
  ROM #(.addrWidth(12), .dataWidth(24)) rom_1 (.addr(igrb_1_or), .data(rom_1_data), .sel(1'b1));
  IGRB igrb_1 (
    .I(rom_1_data), .CL(button_1_out), .H(clock_1_out), .OX(igrb_1_ox), .OY(igrb_1_oy), .IGD(igrb_1_igd),
    .OR(igrb_1_or), .OB(igrb_1_ob));
  // Probe on igrb_1_or
  // Probe on igrb_1_or
  // Probe on igrb_1_or
  // Probe on igrb_1_or
  // Probe on imageromscreen_1_p8
  // ScreenColor screencolor_2: pin names not known
  ROM #(.addrWidth(12), .dataWidth(24)) rom_2 (.addr(imageromscreen_1_p8), .data(rom_2_data), .sel(1'b1));
  // ImageRomScreen imageromscreen_1: pin names not known; wires that end beside it: rom_2_data, button_1_out, clock_1_out, imageromscreen_1_p4, imageromscreen_1_p5, imageromscreen_1_p6, imageromscreen_1_p7, imageromscreen_1_p8, imageromscreen_1_p5, imageromscreen_1_p4, clock_1_out, imageromscreen_1_p7, imageromscreen_1_p6, button_1_out
  // Probe on imageromscreen_1_p8
  // Probe on imageromscreen_1_p8
  // Probe on imageromscreen_1_p8
  // Probe on imageromscreen_1_p8

  // Notes on the sheet:
  //   Other.jar
  //   contents of rom_1 (hex, n*v repeats v):
  //   40 20 121*0 6*ffffff 26*0 ffffff 0 0 ffffff 28*0 ffffff 0 0 ffffff 17*0 ffffff ffffff ffffff 8*0
  //   ffffff 0 0 ffffff 16*0 6*ffffff 7*0 ffffff ffffff 16*0 ffffff ffffff 0 0 0 ffffff ffffff ffffff 23*0
  //   ffffff ffffff 6*0 ffffff ffffff 5*0 4*ffffff 12*0 ffffff ffffff 8*0 ffffff ffffff 0 0 0 ffffff 4*0
  //   ffffff 11*0 ffffff 10*0 ffffff 0 0 0 ffffff 4*0 ffffff 11*0 ffffff 10*0 ffffff 0 0 0 ffffff 4*0
  //   ffffff 0 0 6*ffffff 0 0 0 ffffff 10*0 ffffff 4*0 ffffff 0 0 ffffff 8*0 ffffff 0 0 0 ffffff ffffff
  //   ffffff 6*0 ffffff ffffff ffffff 16*0 ffffff 4*0 ffffff ffffff 6*0 ffffff ffffff 4*0 ffffff 12*0
  //   ffffff 18*0 ffffff 12*0 ffffff 0 0 0 ffffff 10*0 ffffff 0 0 0 6*ffffff 11*0 12*ffffff 0 0 0 ffffff
  //   7*0 5*ffffff 4*0 12*ffffff 0 0 0 ffffff 12*0 ffffff 0 0 0 ffffff 4*0 ffffff 5*0 ffffff 16*0 ffffff
  //   8*0 ffffff 9*0 6*ffffff 7*0 ffffff 8*0 ffffff 9*0 ffffff 0 0 ffffff 4*0 5*ffffff 9*0 ffffff 9*0
  //   ffffff 0 0 ffffff 18*0 ffffff 9*0 ffffff 0 0 ffffff ffffff 0 0 0 6*ffffff 0 0 0 ffffff 4*0 ffffff
  //   5*0 ffffff 4*0 ffffff ffffff 0 0 ffffff 0 0 ffffff 4*0 ffffff 0 0 0 12*ffffff 11*0 ffffff 4*0 ffffff
  //   0 0 0 12*ffffff 4*0 4*ffffff 0 0 0 ffffff 4*0 ffffff 0 0 0 ffffff 10*0 ffffff 0 0 0 ffffff 4*0
  //   ffffff 0 0 0 4*ffffff 19*0 ffffff 4*0 ffffff 11*0 ffffff 10*0 ffffff 0 0 0 ffffff 4*0 ffffff 0 0 0
  //   4*ffffff 4*0 12*ffffff 4*0 4*ffffff 0 0 0 ffffff 4*0 ffffff 0 0 0 12*ffffff 11*0 ffffff 4*0 ffffff 0
  //   0 0 ffffff 10*0 ffffff 0 0 0 6*ffffff 0 0 ffffff 4*0 ffffff 18*0 ffffff ffffff 7*0 4*ffffff 4*0
  //   ffffff 10*0 ffffff 5*0 ffffff ffffff 13*0 12*ffffff 7*0 ffffff ffffff 0 0 ffffff ffffff 7*0
  //   12*ffffff 0 0 0 6*ffffff 4*0 ffffff ffffff 5*0 ffffff 4*0 ffffff 5*0 ffffff 15*0 ffffff ffffff 0 0 0
  //   ffffff 4*0 ffffff 9*0 ffffff 4*0 ffffff 4*0 ffffff ffffff 5*0 ffffff 4*0 ffffff 9*0 6*ffffff 0 0
  //   ffffff ffffff 7*0 ffffff ffffff 0 0 ffffff ffffff 9*0 ffffff 4*0 ffffff 12*0 4*ffffff 18*0 ffffff
  //   4*0 ffffff 5*0 ffffff ffffff 12*0 4*ffffff 0 0 0 6*ffffff 18*0 ffffff 4*0 ffffff 0 0 ffffff 4*0
  //   ffffff 8*0 ffffff ffffff 8*0 ffffff 4*0 ffffff 16*0 ffffff ffffff 8*0 ffffff 0 0 0 ffffff ffffff 0 0
  //   0 4*ffffff 9*0 ffffff ffffff 9*0 5*ffffff 0 0 ffffff 4*0 ffffff 8*0 ffffff ffffff 16*0 ffffff 4*0
  //   ffffff 18*0 5*ffffff 0 0 0 ffffff 4*0 ffffff 5*0 ffffff ffffff 0 0 0 ffffff ffffff ffffff 10*0
  //   ffffff 0 0 0 ffffff 0 0 ffffff 5*0 4*ffffff 0 5*ffffff 9*0 ffffff 11*0 ffffff ffffff 0 0 ffffff
  //   ffffff ffffff 0 0 0 ffffff ffffff 8*0 ffffff 11*0 ffffff 4*0 ffffff 5*0 ffffff 0 0 0 5*ffffff 12*0
  //   ffffff 4*0 ffffff 5*0 ffffff 20*0 ffffff ffffff 0 0 ffffff ffffff ffffff 0 0 0 ffffff ffffff 0 0 0
  //   6*ffffff 12*0 4*ffffff 0 5*ffffff 4*0 ffffff 0 0 ffffff 0 ffffff 13*0 ffffff ffffff 0 0 0 ffffff
  //   ffffff ffffff 5*0 ffffff 0 0 ffffff 0 ffffff 26*0 ffffff 0 0 ffffff 0 ffffff 26*0 ffffff 4*0 ffffff
  //   other_chip8.circ
  //   Other.jar
  //   contents of rom_2 (hex, n*v repeats v):
  //   40 20 121*0 6*ffffff 26*0 ffffff 0 0 ffffff 28*0 ffffff 0 0 ffffff 17*0 ffffff ffffff ffffff 8*0
  //   ffffff 0 0 ffffff 16*0 6*ffffff 7*0 ffffff ffffff 16*0 ffffff ffffff 0 0 0 ffffff ffffff ffffff 23*0
  //   ffffff ffffff 6*0 ffffff ffffff 5*0 4*ffffff 12*0 ffffff ffffff 8*0 ffffff ffffff 0 0 0 ffffff 4*0
  //   ffffff 11*0 ffffff 10*0 ffffff 0 0 0 ffffff 4*0 ffffff 11*0 ffffff 10*0 ffffff 0 0 0 ffffff 4*0
  //   ffffff 0 0 6*ffffff 0 0 0 ffffff 10*0 ffffff 4*0 ffffff 0 0 ffffff 8*0 ffffff 0 0 0 ffffff ffffff
  //   ffffff 6*0 ffffff ffffff ffffff 16*0 ffffff 4*0 ffffff ffffff 6*0 ffffff ffffff 4*0 ffffff 12*0
  //   ffffff 18*0 ffffff 12*0 ffffff 0 0 0 ffffff 10*0 ffffff 0 0 0 6*ffffff 11*0 12*ffffff 0 0 0 ffffff
  //   7*0 5*ffffff 4*0 12*ffffff 0 0 0 ffffff 12*0 ffffff 0 0 0 ffffff 4*0 ffffff 5*0 ffffff 16*0 ffffff
  //   8*0 ffffff 9*0 6*ffffff 7*0 ffffff 8*0 ffffff 9*0 ffffff 0 0 ffffff 4*0 5*ffffff 9*0 ffffff 9*0
  //   ffffff 0 0 ffffff 18*0 ffffff 9*0 ffffff 0 0 ffffff ffffff 0 0 0 6*ffffff 0 0 0 ffffff 4*0 ffffff
  //   5*0 ffffff 4*0 ffffff ffffff 0 0 ffffff 0 0 ffffff 4*0 ffffff 0 0 0 12*ffffff 11*0 ffffff 4*0 ffffff
  //   0 0 0 12*ffffff 4*0 4*ffffff 0 0 0 ffffff 4*0 ffffff 0 0 0 ffffff 10*0 ffffff 0 0 0 ffffff 4*0
  //   ffffff 0 0 0 4*ffffff 19*0 ffffff 4*0 ffffff 11*0 ffffff 10*0 ffffff 0 0 0 ffffff 4*0 ffffff 0 0 0
  //   4*ffffff 4*0 12*ffffff 4*0 4*ffffff 0 0 0 ffffff 4*0 ffffff 0 0 0 12*ffffff 11*0 ffffff 4*0 ffffff 0
  //   0 0 ffffff 10*0 ffffff 0 0 0 6*ffffff 0 0 ffffff 4*0 ffffff 18*0 ffffff ffffff 7*0 4*ffffff 4*0
  //   ffffff 10*0 ffffff 5*0 ffffff ffffff 13*0 12*ffffff 7*0 ffffff ffffff 0 0 ffffff ffffff 7*0
  //   12*ffffff 0 0 0 6*ffffff 4*0 ffffff ffffff 5*0 ffffff 4*0 ffffff 5*0 ffffff 15*0 ffffff ffffff 0 0 0
  //   ffffff 4*0 ffffff 9*0 ffffff 4*0 ffffff 4*0 ffffff ffffff 5*0 ffffff 4*0 ffffff 9*0 6*ffffff 0 0
  //   ffffff ffffff 7*0 ffffff ffffff 0 0 ffffff ffffff 9*0 ffffff 4*0 ffffff 12*0 4*ffffff 18*0 ffffff
  //   4*0 ffffff 5*0 ffffff ffffff 12*0 4*ffffff 0 0 0 6*ffffff 18*0 ffffff 4*0 ffffff 0 0 ffffff 4*0
  //   ffffff 8*0 ffffff ffffff 8*0 ffffff 4*0 ffffff 16*0 ffffff ffffff 8*0 ffffff 0 0 0 ffffff ffffff 0 0
  //   0 4*ffffff 9*0 ffffff ffffff 9*0 5*ffffff 0 0 ffffff 4*0 ffffff 8*0 ffffff ffffff 16*0 ffffff 4*0
  //   ffffff 18*0 5*ffffff 0 0 0 ffffff 4*0 ffffff 5*0 ffffff ffffff 0 0 0 ffffff ffffff ffffff 10*0
  //   ffffff 0 0 0 ffffff 0 0 ffffff 5*0 4*ffffff 0 5*ffffff 9*0 ffffff 11*0 ffffff ffffff 0 0 ffffff
  //   ffffff ffffff 0 0 0 ffffff ffffff 8*0 ffffff 11*0 ffffff 4*0 ffffff 5*0 ffffff 0 0 0 5*ffffff 12*0
  //   ffffff 4*0 ffffff 5*0 ffffff 20*0 ffffff ffffff 0 0 ffffff ffffff ffffff 0 0 0 ffffff ffffff 0 0 0
  //   6*ffffff 12*0 4*ffffff 0 5*ffffff 4*0 ffffff 0 0 ffffff 0 ffffff 13*0 ffffff ffffff 0 0 0 ffffff
  //   ffffff ffffff 5*0 ffffff 0 0 ffffff 0 ffffff 26*0 ffffff 0 0 ffffff 0 ffffff 26*0 ffffff 4*0 ffffff
  //   Other.jar
endmodule
