// Logisim project 14_C8_02_collision.circ as structural Verilog: 4 circuits, main circuit main_collision
module main_collision (
  input  [4:0] Y,
  input  [5:0] X,
  input  H,
  input  E,
  input  I,
  input  C,
  output out_7,
  output out_8,
  output out_9
);

  // ScreenColor screencolor_1: pin names not known
  COLC64 colc64_1 (.Enable(E), .X(X), .Y(Y), .I(I), .H(H), .CL(C), .OS(out_7));
  // Collision collision_1: pin names not known; wires that end beside it: Y, X, H, E, I, C, out_8, Y, X, H, E, I, C
  COLC64_2 colc64_2_1 (.Enable(E), .OS(out_9), .X(X), .Y(Y), .I(I), .H(H), .CL(C));
endmodule

module colorToRGB (
  input  [23:0] in_1,
  output [23:0] out_2,
  output [23:0] out_3,
  output [23:0] out_4
);

  assign out_2 = 24'hff0000 & in_1;  // AND_Gate and_1, 24 bits wide
  assign out_3 = 24'hff00 & in_1;  // AND_Gate and_2, 24 bits wide
  assign out_4 = 24'hff & in_1;  // AND_Gate and_3, 24 bits wide
endmodule

module colorPixel (
  input  [7:0] Red,
  input  [7:0] Green,
  input  [7:0] Blue,
  input  Row,
  input  Column,
  input  Clear,
  output [23:0] Color,
  output [23:0] Input,
  output [1:0] InputX,
  output [4:0] InputY,
  output Clock,
  output Clear_2
);

  wire d_ff_1_q, d_ff_1_qn;
  wire [23:0] colortorgb_1_out_2, colortorgb_1_out_3, colortorgb_1_out_4;

  Counter #(.width(2), .max('h3), .trigger("falling")) counter_1 (
    .load(1'b0), .D(2'b00), .count(1'b1), .Q(InputX), .clk(d_ff_1_q), .clr(Clear));  // open: carry
  D_Flip_Flop d_ff_1 (
    .clk(Column), .D(d_ff_1_qn), .Q(d_ff_1_q), .Qn(d_ff_1_qn), .preset(1'b0), .en(1'b1), .reset(Clear));
  colorToRGB colortorgb_1 (
    .in_1({Red, Green, Blue}), .out_2(colortorgb_1_out_2), .out_3(colortorgb_1_out_3),
    .out_4(colortorgb_1_out_4));
  Multiplexer #(.select(2), .width(24), .enable("false")) multiplexer_1 (
    .in0(colortorgb_1_out_2), .in1(colortorgb_1_out_3), .in2(colortorgb_1_out_4), .in3({Red, Green, Blue}),
    .out(Input), .sel(InputX));
  Counter #(.width(5), .max('h1f)) counter_2 (
    .load(1'b0), .D({5{1'b0}}), .count(1'b1), .Q(InputY), .clk(Row), .clr(Clear));  // open: carry

  assign Clear_2 = Clear;
  assign Clock = Column;
  assign Color = {Red, Green, Blue};
endmodule

module pixelXY (
  input  [1:0] X,
  input  [4:0] Y,
  output [3:0] X_2,
  output [31:0] Y_2
);

  Decoder #(.select(2), .enable("false")) decoder_1 (
    .out0(X_2[3]), .out1(X_2[2]), .out2(X_2[1]), .out3(X_2[0]), .sel(X));
  Decoder #(.select(5), .enable("false")) decoder_2 (
    .out0(Y_2[31]), .out1(Y_2[30]), .out2(Y_2[29]), .out3(Y_2[28]), .out4(Y_2[27]), .out5(Y_2[26]),
    .out6(Y_2[25]), .out7(Y_2[24]), .out8(Y_2[23]), .out9(Y_2[22]), .out10(Y_2[21]), .out11(Y_2[20]),
    .out12(Y_2[19]), .out13(Y_2[18]), .out14(Y_2[17]), .out15(Y_2[16]), .out16(Y_2[15]), .out17(Y_2[14]),
    .out18(Y_2[13]), .out19(Y_2[12]), .out20(Y_2[11]), .out21(Y_2[10]), .out22(Y_2[9]), .out23(Y_2[8]),
    .out24(Y_2[7]), .out25(Y_2[6]), .out26(Y_2[5]), .out27(Y_2[4]), .out28(Y_2[3]), .out29(Y_2[2]),
    .out30(Y_2[1]), .out31(Y_2[0]), .sel(Y));
endmodule
