// Logisim project 15_C8_01_transf.circ as structural Verilog: 1 circuit, main circuit main
module main (
  input  E,
  input  CL,
  input  [7:0] D,
  input  [11:0] A,
  input  STR,
  input  SEL,
  output [7:0] RAM,
  output out_8,
  output [7:0] RAM_2,
  output out_10
);

  wire clock_1_out, transferram_1_p10, transferram_1_p14, transferram_1_p15, transferram_1_p16,
       transferram_1_p17, transferram_1_p19, trfc_1_clearra, trfc_1_er, trfc_1_erg, trfc_1_hra,
       trfc_1_selrao, trfc_1_strrao;
  wire [7:0] rom_1_data, rom_2_data, transferram_1_p11, transferram_1_p13, transferram_1_p20, trfc_1_drao;
  wire [8:0] transferram_1_p9, trfc_1_ar;
  wire [11:0] transferram_1_p12, transferram_1_p18, trfc_1_arao, trfc_1_arg;

  Clock clock_1 (.out(clock_1_out));
  // TransferRam transferram_1: pin names not known; wires that end beside it: clock_1_out, E, CL, D, A, STR, SEL, 12'h100, transferram_1_p9, transferram_1_p10, transferram_1_p11, transferram_1_p12, transferram_1_p13, transferram_1_p14, transferram_1_p15, transferram_1_p16, transferram_1_p17, transferram_1_p18, transferram_1_p19, transferram_1_p20, out_10
  TRFC trfc_1 (
    .enable(E), .clear(CL), .DRAI(D), .ARAI(A), .strRAI(STR), .selRAI(SEL), .AR(trfc_1_ar), .ER(trfc_1_er),
    .ARAO(trfc_1_arao), .DRAO(trfc_1_drao), .strRAO(trfc_1_strrao), .SelRAO(trfc_1_selrao), .HRA(trfc_1_hra),
    .clearRA(trfc_1_clearra), .ARG(trfc_1_arg), .ERG(trfc_1_erg), .DRG(rom_2_data), .DR(rom_1_data),
    .H(clock_1_out), .EM(out_8), .MAX(12'h100));
  ROM #(.addrWidth(9)) rom_1 (.addr(trfc_1_ar), .data(rom_1_data), .sel(trfc_1_er));
  RAM #(.addrWidth(12), .bus("separate")) ram_1 (
    .addr(trfc_1_arao), .din(trfc_1_drao), .data(RAM), .str(trfc_1_strrao), .sel(trfc_1_selrao),
    .clk(trfc_1_hra), .ld(1'b1), .clr(trfc_1_clearra));
  ROM #(.addrWidth(12)) rom_2 (.addr(trfc_1_arg), .data(rom_2_data), .sel(trfc_1_erg));
  ROM #(.addrWidth(9)) rom_3 (.addr(transferram_1_p9), .data(transferram_1_p11), .sel(transferram_1_p10));
  RAM #(.addrWidth(12), .bus("separate")) u_ram_2 (
    .addr(transferram_1_p12), .din(transferram_1_p13), .data(RAM_2), .str(transferram_1_p14),
    .sel(transferram_1_p15), .clk(transferram_1_p16), .ld(1'b1), .clr(transferram_1_p17));
  ROM #(.addrWidth(12)) rom_4 (.addr(transferram_1_p18), .data(transferram_1_p20), .sel(transferram_1_p19));

  // Notes on the sheet:
  //   MAX
  //   other_chip8.circ
  //   Other.jar
  //   ROM CHIP8
  //   contents of rom_1 (hex, n*v repeats v):
  //   12 0 12 0 f0 90 90 90 f0 20 60 20 20 70 f0 10 f0 80 f0 f0 10 f0 10 f0 90 90 f0 10 10 f0 80 f0 10 f0
  //   f0 80 f0 90 f0 f0 10 20 40 40 f0 90 f0 90 f0 f0 90 f0 10 f0 f0 90 f0 90 90 e0 90 e0 90 e0 f0 80 80
  //   80 f0 e0 90 90 90 e0 f0 80 f0 80 f0 f0 80 f0 80 80
  //   ROM GAME
  //   contents of rom_2 (hex, n*v repeats v):
  //   6a 2 6b c 6c 3f 6d c a2 ea da b6 dc d6 6e 0 22 d4 66 3 68 2 60 60 f0 15 f0 7 30 0 12 1a c7 17 77 8
  //   69 ff a2 f0 d6 71 a2 ea da b6 dc d6 60 1 e0 a1 7b fe 60 4 e0 a1 7b 2 60 1f 8b 2 da b6 8d 70 c0 a 7d
  //   fe 40 0 7d 2 60 0 60 1f 8d 2 dc d6 a2 f0 d6 71 86 84 87 94 60 3f 86 2 61 1f 87 12 46 2 12 78 46 3f
  //   12 82 47 1f 69 ff 47 0 69 1 d6 71 12 2a 68 2 63 1 80 70 80 b5 12 8a 68 fe 63 a 80 70 80 d5 3f 1 12
  //   a2 61 2 80 15 3f 1 12 ba 80 15 3f 1 12 c8 80 15 3f 1 12 c2 60 20 f0 18 22 d4 8e 34 22 d4 66 3e 33 1
  //   66 3 68 fe 33 1 68 2 12 16 79 ff 49 fe 69 ff 12 c8 79 1 49 2 69 1 60 4 f0 18 76 1 46 40 76 fe 12 6c
  //   a2 f2 fe 33 f2 65 f1 29 64 14 65 0 d4 55 74 15 f2 29 d4 55 0 ee
  //   ROM CHIP8
  //   contents of rom_3 (hex, n*v repeats v):
  //   12 0 12 0 f0 90 90 90 f0 20 60 20 20 70 f0 10 f0 80 f0 f0 10 f0 10 f0 90 90 f0 10 10 f0 80 f0 10 f0
  //   f0 80 f0 90 f0 f0 10 20 40 40 f0 90 f0 90 f0 f0 90 f0 10 f0 f0 90 f0 90 90 e0 90 e0 90 e0 f0 80 80
  //   80 f0 e0 90 90 90 e0 f0 80 f0 80 f0 f0 80 f0 80 80
  //   ROM GAME
  //   contents of rom_4 (hex, n*v repeats v):
  //   6a 2 6b c 6c 3f 6d c a2 ea da b6 dc d6 6e 0 22 d4 66 3 68 2 60 60 f0 15 f0 7 30 0 12 1a c7 17 77 8
  //   69 ff a2 f0 d6 71 a2 ea da b6 dc d6 60 1 e0 a1 7b fe 60 4 e0 a1 7b 2 60 1f 8b 2 da b6 8d 70 c0 a 7d
  //   fe 40 0 7d 2 60 0 60 1f 8d 2 dc d6 a2 f0 d6 71 86 84 87 94 60 3f 86 2 61 1f 87 12 46 2 12 78 46 3f
  //   12 82 47 1f 69 ff 47 0 69 1 d6 71 12 2a 68 2 63 1 80 70 80 b5 12 8a 68 fe 63 a 80 70 80 d5 3f 1 12
  //   a2 61 2 80 15 3f 1 12 ba 80 15 3f 1 12 c8 80 15 3f 1 12 c2 60 20 f0 18 22 d4 8e 34 22 d4 66 3e 33 1
  //   66 3 68 fe 33 1 68 2 12 16 79 ff 49 fe 69 ff 12 c8 79 1 49 2 69 1 60 4 f0 18 76 1 46 40 76 fe 12 6c
  //   a2 f2 fe 33 f2 65 f1 29 64 14 65 0 d4 55 74 15 f2 29 d4 55 0 ee
endmodule
