// Logisim project 15_C8_carte_graphic.circ as structural Verilog: 3 circuits, main circuit main_image_data_black
module main_image_data_black (
  input  [5:0] AL,
  input  [4:0] AC,
  input  Store,
  input  D,
  input  M,
  output DO,
  output ENDI,
  output DO_2,
  output ENDI_2
);

  wire clock_1_out, graf_1_clear, graf_1_dis, graf_1_enable, graf_1_h_2, graf_lsi_1_clear, graf_lsi_1_dis,
       graf_lsi_1_enable, graf_lsi_1_h_2, R_out;
  wire [4:0] graf_1_ac_2, graf_lsi_1_ac_2;
  wire [5:0] graf_1_al_2, graf_lsi_1_al_2;

  Clock clock_1 (.out(clock_1_out));
  Button R (.out(R_out));
  GRAF_lsi graf_lsi_1 (
    .DO(DO), .AL(AL), .AL_2(graf_lsi_1_al_2), .AC(AC), .AC_2(graf_lsi_1_ac_2), .E(1'b1), .M(M),
    .clear(graf_lsi_1_clear), .R(R_out), .Enable(graf_lsi_1_enable), .D(D), .DIS(graf_lsi_1_dis),
    .H_2(graf_lsi_1_h_2), .H(clock_1_out), .Store(Store), .ENDI(ENDI));
  GRAF graf_1 (
    .DO(DO_2), .AL(AL), .AL_2(graf_1_al_2), .AC(AC), .AC_2(graf_1_ac_2), .E(1'b1), .M(M),
    .clear(graf_1_clear), .R(R_out), .Enable(graf_1_enable), .D(D), .DIS(graf_1_dis), .H_2(graf_1_h_2),
    .H(clock_1_out), .Store(Store), .ENDI(ENDI_2));
  // ScreenColor screencolor_1: pin names not known
  // ScreenColor screencolor_2: pin names not known

  // Notes on the sheet:
  //   E
  //   Other.jar
  //   other_chip8.circ
  //   Other.jar
  //   Other.jar
endmodule

module GRAF_lsi (
  input  [5:0] AL,
  input  [4:0] AC,
  input  Store,
  input  D,
  input  H,
  input  R,
  input  M,
  input  E,
  output clear,
  output DIS,
  output Enable,
  output H_2,
  output [4:0] AC_2,
  output [5:0] AL_2,
  output DO,
  output ENDI
);

  wire colc64_2_1_os, igrb_1_igd, igrb_1_ob, igsc_1_ck_i, igsc_1_cl_i;
  wire [4:0] igrb_1_oy;
  wire [5:0] igrb_1_ox;
  wire [11:0] igrb_1_or;
  wire [23:0] rom_1_data;

  IGSC igsc_1 (
    .DOS(colc64_2_1_os), .AL(AL), .AC(AC), .M(M), .E(E), .D(D), .H(H), .R(R), .Store(Store), .DO(DO),
    .AL_2(AL_2), .AC_2(AC_2), .clear(clear), .Enable(Enable), .DIS(DIS), .H_2(H_2), .ENDI(ENDI),
    .CL_I(igsc_1_cl_i), .CK_I(igsc_1_ck_i), .AC_I(igrb_1_ox), .AL_I(igrb_1_oy), .D_I(igrb_1_ob),
    .ENDI_I(igrb_1_igd));
  ROM #(.addrWidth(12), .dataWidth(24)) rom_1 (.addr(igrb_1_or), .data(rom_1_data), .sel(1'b1));
  IGRB igrb_1 (
    .I(rom_1_data), .CL(igsc_1_cl_i), .H(igsc_1_ck_i), .OX(igrb_1_ox), .OY(igrb_1_oy), .IGD(igrb_1_igd),
    .OR(igrb_1_or), .OB(igrb_1_ob));
  COLC64_2 colc64_2_1 (.Enable(Enable), .OS(colc64_2_1_os), .X(AL_2), .Y(AC_2), .I(DIS), .H(H_2), .CL(clear));

  // Notes on the sheet:
  //   contents of rom_1 (hex, n*v repeats v):
  //   40 20 121*0 6*ffffff 26*0 ffffff 0 0 ffffff 28*0 ffffff 0 0 ffffff 17*0 ffffff ffffff ffffff 8*0
  //   ffffff 0 0 ffffff 16*0 6*ffffff 7*0 ffffff ffffff 16*0 ffffff ffffff 0 0 0 ffffff ffffff ffffff 23*0
  //   ffffff ffffff 6*0 ffffff ffffff 5*0 4*ffffff 12*0 ffffff ffffff 8*0 ffffff ffffff 0 0 0 ffffff 4*0
  //   ffffff 11*0 ffffff 10*0 ffffff 0 0 0 ffffff 4*0 ffffff 11*0 ffffff 10*0 ffffff 0 0 0 ffffff 4*0
  //   ffffff 0 0 6*ffffff 0 0 0 ffffff 10*0 ffffff 4*0 ffffff 0 0 ffffff 8*0 ffffff 0 0 0 ffffff ffffff
  //   ffffff 6*0 ffffff ffffff ffffff 16*0 ffffff 4*0 ffffff ffffff 6*0 ffffff ffffff 4*0 ffffff 12*0
  //   ffffff 18*0 ffffff 12*0 ffffff 0 0 0 ffffff 10*0 ffffff 0 0 0 6*ffffff 11*0 12*ffffff 0 0 0 ffffff
  //   7*0 5*ffffff 4*0 12*ffffff 0 0 0 ffffff 12*0 ffffff 0 0 0 ffffff 4*0 ffffff 5*0 ffffff 16*0 ffffff
  //   8*0 ffffff 9*0 6*ffffff 7*0 ffffff 8*0 ffffff 9*0 ffffff 0 0 ffffff 4*0 5*ffffff 9*0 ffffff 9*0
  //   ffffff 0 0 ffffff 18*0 ffffff 9*0 ffffff 0 0 ffffff ffffff 0 0 0 6*ffffff 0 0 0 ffffff 4*0 ffffff
  //   5*0 ffffff 4*0 ffffff ffffff 0 0 ffffff 0 0 ffffff 4*0 ffffff 0 0 0 12*ffffff 11*0 ffffff 4*0 ffffff
  //   0 0 0 12*ffffff 4*0 4*ffffff 0 0 0 ffffff 4*0 ffffff 0 0 0 ffffff 10*0 ffffff 0 0 0 ffffff 4*0
  //   ffffff 0 0 0 4*ffffff 19*0 ffffff 4*0 ffffff 11*0 ffffff 10*0 ffffff 0 0 0 ffffff 4*0 ffffff 0 0 0
  //   4*ffffff 4*0 12*ffffff 4*0 4*ffffff 0 0 0 ffffff 4*0 ffffff 0 0 0 12*ffffff 11*0 ffffff 4*0 ffffff 0
  //   0 0 ffffff 10*0 ffffff 0 0 0 6*ffffff 0 0 ffffff 4*0 ffffff 18*0 ffffff ffffff 7*0 4*ffffff 4*0
  //   ffffff 10*0 ffffff 5*0 ffffff ffffff 13*0 12*ffffff 7*0 ffffff ffffff 0 0 ffffff ffffff 7*0
  //   12*ffffff 0 0 0 6*ffffff 4*0 ffffff ffffff 5*0 ffffff 4*0 ffffff 5*0 ffffff 15*0 ffffff ffffff 0 0 0
  //   ffffff 4*0 ffffff 9*0 ffffff 4*0 ffffff 4*0 ffffff ffffff 5*0 ffffff 4*0 ffffff 9*0 6*ffffff 0 0
  //   ffffff ffffff 7*0 ffffff ffffff 0 0 ffffff ffffff 9*0 ffffff 4*0 ffffff 12*0 4*ffffff 18*0 ffffff
  //   4*0 ffffff 5*0 ffffff ffffff 12*0 4*ffffff 0 0 0 6*ffffff 18*0 ffffff 4*0 ffffff 0 0 ffffff 4*0
  //   ffffff 8*0 ffffff ffffff 8*0 ffffff 4*0 ffffff 16*0 ffffff ffffff 8*0 ffffff 0 0 0 ffffff ffffff 0 0
  //   0 4*ffffff 9*0 ffffff ffffff 9*0 5*ffffff 0 0 ffffff 4*0 ffffff 8*0 ffffff ffffff 16*0 ffffff 4*0
  //   ffffff 18*0 5*ffffff 0 0 0 ffffff 4*0 ffffff 5*0 ffffff ffffff 0 0 0 ffffff ffffff ffffff 10*0
  //   ffffff 0 0 0 ffffff 0 0 ffffff 5*0 4*ffffff 0 5*ffffff 9*0 ffffff 11*0 ffffff ffffff 0 0 ffffff
  //   ffffff ffffff 0 0 0 ffffff ffffff 8*0 ffffff 11*0 ffffff 4*0 ffffff 5*0 ffffff 0 0 0 5*ffffff 12*0
  //   ffffff 4*0 ffffff 5*0 ffffff 20*0 ffffff ffffff 0 0 ffffff ffffff ffffff 0 0 0 ffffff ffffff 0 0 0
  //   6*ffffff 12*0 4*ffffff 0 5*ffffff 4*0 ffffff 0 0 ffffff 0 ffffff 13*0 ffffff ffffff 0 0 0 ffffff
  //   ffffff ffffff 5*0 ffffff 0 0 ffffff 0 ffffff 26*0 ffffff 0 0 ffffff 0 ffffff 26*0 ffffff 4*0 ffffff
endmodule

module GRAF (
  input  [5:0] AL,
  input  [4:0] AC,
  input  Store,
  input  D,
  input  H,
  input  R,
  input  M,
  input  E,
  output clear,
  output DIS,
  output Enable,
  output H_2,
  output [4:0] AC_2,
  output [5:0] AL_2,
  output DO,
  output ENDI
);

  wire imagescreen_1_p11, imagescreen_1_p12, imagescreen_1_p19, imagescreen_1_p20, imagescreen_1_p21,
       imagescreen_1_p22, imagescreen_1_p23;
  wire [11:0] imageromscreen_1_p8;
  wire [23:0] rom_1_data;

  // ImageScreen imagescreen_1: pin names not known; wires that end beside it: AL, AC, Store, D, DO, H, R, M, E, ENDI, imagescreen_1_p11, imagescreen_1_p12, clear, DIS, Enable, H_2, AC_2, AL_2, imagescreen_1_p19, imagescreen_1_p20, imagescreen_1_p21, imagescreen_1_p22, imagescreen_1_p23
  ROM #(.addrWidth(12), .dataWidth(24)) rom_1 (.addr(imageromscreen_1_p8), .data(rom_1_data), .sel(1'b1));
  // ImageRomScreen imageromscreen_1: pin names not known; wires that end beside it: rom_1_data, imagescreen_1_p11, imagescreen_1_p12, imagescreen_1_p21, imagescreen_1_p20, imagescreen_1_p22, imagescreen_1_p23, imageromscreen_1_p8
  // Collision collision_1: pin names not known; wires that end beside it: AL_2, AC_2, H_2, Enable, DIS, clear, imagescreen_1_p19

  // Notes on the sheet:
  //   contents of rom_1 (hex, n*v repeats v):
  //   40 20 121*0 6*ffffff 26*0 ffffff 0 0 ffffff 28*0 ffffff 0 0 ffffff 17*0 ffffff ffffff ffffff 8*0
  //   ffffff 0 0 ffffff 16*0 6*ffffff 7*0 ffffff ffffff 16*0 ffffff ffffff 0 0 0 ffffff ffffff ffffff 23*0
  //   ffffff ffffff 6*0 ffffff ffffff 5*0 4*ffffff 12*0 ffffff ffffff 8*0 ffffff ffffff 0 0 0 ffffff 4*0
  //   ffffff 11*0 ffffff 10*0 ffffff 0 0 0 ffffff 4*0 ffffff 11*0 ffffff 10*0 ffffff 0 0 0 ffffff 4*0
  //   ffffff 0 0 6*ffffff 0 0 0 ffffff 10*0 ffffff 4*0 ffffff 0 0 ffffff 8*0 ffffff 0 0 0 ffffff ffffff
  //   ffffff 6*0 ffffff ffffff ffffff 16*0 ffffff 4*0 ffffff ffffff 6*0 ffffff ffffff 4*0 ffffff 12*0
  //   ffffff 18*0 ffffff 12*0 ffffff 0 0 0 ffffff 10*0 ffffff 0 0 0 6*ffffff 11*0 12*ffffff 0 0 0 ffffff
  //   7*0 5*ffffff 4*0 12*ffffff 0 0 0 ffffff 12*0 ffffff 0 0 0 ffffff 4*0 ffffff 5*0 ffffff 16*0 ffffff
  //   8*0 ffffff 9*0 6*ffffff 7*0 ffffff 8*0 ffffff 9*0 ffffff 0 0 ffffff 4*0 5*ffffff 9*0 ffffff 9*0
  //   ffffff 0 0 ffffff 18*0 ffffff 9*0 ffffff 0 0 ffffff ffffff 0 0 0 6*ffffff 0 0 0 ffffff 4*0 ffffff
  //   5*0 ffffff 4*0 ffffff ffffff 0 0 ffffff 0 0 ffffff 4*0 ffffff 0 0 0 12*ffffff 11*0 ffffff 4*0 ffffff
  //   0 0 0 12*ffffff 4*0 4*ffffff 0 0 0 ffffff 4*0 ffffff 0 0 0 ffffff 10*0 ffffff 0 0 0 ffffff 4*0
  //   ffffff 0 0 0 4*ffffff 19*0 ffffff 4*0 ffffff 11*0 ffffff 10*0 ffffff 0 0 0 ffffff 4*0 ffffff 0 0 0
  //   4*ffffff 4*0 12*ffffff 4*0 4*ffffff 0 0 0 ffffff 4*0 ffffff 0 0 0 12*ffffff 11*0 ffffff 4*0 ffffff 0
  //   0 0 ffffff 10*0 ffffff 0 0 0 6*ffffff 0 0 ffffff 4*0 ffffff 18*0 ffffff ffffff 7*0 4*ffffff 4*0
  //   ffffff 10*0 ffffff 5*0 ffffff ffffff 13*0 12*ffffff 7*0 ffffff ffffff 0 0 ffffff ffffff 7*0
  //   12*ffffff 0 0 0 6*ffffff 4*0 ffffff ffffff 5*0 ffffff 4*0 ffffff 5*0 ffffff 15*0 ffffff ffffff 0 0 0
  //   ffffff 4*0 ffffff 9*0 ffffff 4*0 ffffff 4*0 ffffff ffffff 5*0 ffffff 4*0 ffffff 9*0 6*ffffff 0 0
  //   ffffff ffffff 7*0 ffffff ffffff 0 0 ffffff ffffff 9*0 ffffff 4*0 ffffff 12*0 4*ffffff 18*0 ffffff
  //   4*0 ffffff 5*0 ffffff ffffff 12*0 4*ffffff 0 0 0 6*ffffff 18*0 ffffff 4*0 ffffff 0 0 ffffff 4*0
  //   ffffff 8*0 ffffff ffffff 8*0 ffffff 4*0 ffffff 16*0 ffffff ffffff 8*0 ffffff 0 0 0 ffffff ffffff 0 0
  //   0 4*ffffff 9*0 ffffff ffffff 9*0 5*ffffff 0 0 ffffff 4*0 ffffff 8*0 ffffff ffffff 16*0 ffffff 4*0
  //   ffffff 18*0 5*ffffff 0 0 0 ffffff 4*0 ffffff 5*0 ffffff ffffff 0 0 0 ffffff ffffff ffffff 10*0
  //   ffffff 0 0 0 ffffff 0 0 ffffff 5*0 4*ffffff 0 5*ffffff 9*0 ffffff 11*0 ffffff ffffff 0 0 ffffff
  //   ffffff ffffff 0 0 0 ffffff ffffff 8*0 ffffff 11*0 ffffff 4*0 ffffff 5*0 ffffff 0 0 0 5*ffffff 12*0
  //   ffffff 4*0 ffffff 5*0 ffffff 20*0 ffffff ffffff 0 0 ffffff ffffff ffffff 0 0 0 ffffff ffffff 0 0 0
  //   6*ffffff 12*0 4*ffffff 0 5*ffffff 4*0 ffffff 0 0 ffffff 0 ffffff 13*0 ffffff ffffff 0 0 0 ffffff
  //   ffffff ffffff 5*0 ffffff 0 0 ffffff 0 ffffff 26*0 ffffff 0 0 ffffff 0 ffffff 26*0 ffffff 4*0 ffffff
endmodule
