// Logisim project 15_C8_dec.circ as structural Verilog: 7 circuits, main circuit main
module main (
  input  in_1,
  input  [15:0] in_2,
  output _00E0,
  output _00EE,
  output _0NNN,
  output _1NNN,
  output _2NNN,
  output _3XKK,
  output _4XKK,
  output _5XY0,
  output _6XKK,
  output _7XKK,
  output _8XY0,
  output _8XY1,
  output _8XY2,
  output _8XY3,
  output _8XY4,
  output _8XY5,
  output _8X06,
  output _8XY7,
  output _8X0E,
  output _9XY0,
  output ANNN,
  output BNNN,
  output CXKK,
  output DXYK,
  output EX9E,
  output EXA1,
  output FX07,
  output FX0A,
  output FX15,
  output FX18,
  output FX1E,
  output FX29,
  output FX33,
  output FX55,
  output FX65,
  output [7:0] KK,
  output [3:0] K,
  output [3:0] AX,
  output [3:0] AY,
  output [11:0] NNN
);

  DEC dec_1 (
    .enable(in_1), .opcode(in_2), .AX(AX), .AY(AY), .K(K), .KK(KK), .NNN(NNN), ._00E0(_00E0), ._00EE(_00EE),
    ._0NNN(_0NNN), ._1NNN(_1NNN), ._2NNN(_2NNN), .ANNN(ANNN), .BNNN(BNNN), ._3XKK(_3XKK), ._4XKK(_4XKK),
    ._6XKK(_6XKK), ._7XKK(_7XKK), .CXKK(CXKK), ._5XY0(_5XY0), ._8XY0(_8XY0), ._8XY1(_8XY1), ._8XY2(_8XY2),
    ._8XY3(_8XY3), ._8XY4(_8XY4), ._8XY5(_8XY5), ._8XY7(_8XY7), ._9XY0(_9XY0), .DXYK(DXYK), ._8X06(_8X06),
    ._8X0E(_8X0E), .EX9E(EX9E), .EXA1(EXA1), .FX07(FX07), .FX0A(FX0A), .FX15(FX15), .FX18(FX18), .FX1E(FX1E),
    .FX29(FX29), .FX33(FX33), .FX55(FX55), .FX65(FX65));
  // Probe on NNN
  // Probe on NNN
  // Probe on NNN
  // Probe on KK
  // Probe on KK
  // Probe on KK
  // Probe on K
  // Probe on K
  // Probe on K
  // Probe on AX
  // Probe on AX
  // Probe on AX
  // Probe on AY
  // Probe on AY
  // Probe on AY
endmodule

module DEC (
  input  enable,
  input  [15:0] opcode,
  output _00E0,
  output _00EE,
  output _0NNN,
  output _1NNN,
  output _2NNN,
  output ANNN,
  output BNNN,
  output _3XKK,
  output _4XKK,
  output _6XKK,
  output _7XKK,
  output CXKK,
  output _5XY0,
  output _8XY0,
  output _8XY1,
  output _8XY2,
  output _8XY3,
  output _8XY4,
  output _8XY5,
  output _8XY7,
  output _9XY0,
  output DXYK,
  output _8X06,
  output _8X0E,
  output EX9E,
  output EXA1,
  output FX07,
  output FX0A,
  output FX15,
  output FX18,
  output FX1E,
  output FX29,
  output FX33,
  output FX55,
  output FX65,
  output [3:0] AX,
  output [3:0] AY,
  output [3:0] K,
  output [7:0] KK,
  output [11:0] NNN
);

  wire opnnn_1_kk, opnnn_1_nnn, opnnn_1_x, opx_1_x, opxy_1_xy, or_1_out, or_2_out;
  wire [15:0] decop_1_decode0, decop_1_decode1, decop_1_decode2, decop_1_decode3;

  DECOP decop_1 (
    .enable(enable), .opcode(opcode), .decode3(decop_1_decode3), .decode2(decop_1_decode2),
    .decode1(decop_1_decode1), .decode0(decop_1_decode0));
  OPNNN opnnn_1 (
    .decode3(decop_1_decode3), .decode2(decop_1_decode2), .decode1(decop_1_decode1),
    .decode0(decop_1_decode0), ._00E0(_00E0), ._00EE(_00EE), ._0NNN(_0NNN), ._1NNN(_1NNN), ._2NNN(_2NNN),
    .ANNN(ANNN), .BNNN(BNNN), ._3XKK(_3XKK), ._4XKK(_4XKK), ._6XKK(_6XKK), ._7XKK(_7XKK), .CXKK(CXKK),
    .NNN(opnnn_1_nnn), .KK(opnnn_1_kk), .X(opnnn_1_x));
  OPXY opxy_1 (
    .decode3(decop_1_decode3), .decode2(decop_1_decode2), .decode1(decop_1_decode1),
    .decode0(decop_1_decode0), ._5XY0(_5XY0), ._8XY0(_8XY0), ._8XY1(_8XY1), ._8XY2(_8XY2), ._8XY3(_8XY3),
    ._8XY4(_8XY4), ._8XY5(_8XY5), ._8XY7(_8XY7), ._9XY0(_9XY0), .DXYK(DXYK), .XY(opxy_1_xy));
  OPX opx_1 (
    .decode3(decop_1_decode3), .decode2(decop_1_decode2), .decode1(decop_1_decode1),
    .decode0(decop_1_decode0), ._8X06(_8X06), ._8X0E(_8X0E), .EX9E(EX9E), .EXA1(EXA1), .FX07(FX07),
    .FX0A(FX0A), .FX15(FX15), .FX18(FX18), .FX1E(FX1E), .FX29(FX29), .FX33(FX33), .FX55(FX55), .FX65(FX65),
    .X(opx_1_x));
  or or_1 (or_1_out, opnnn_1_x, DXYK, opxy_1_xy, opx_1_x);
  or or_2 (or_2_out, DXYK, opxy_1_xy);
  OPDATA opdata_1 (
    .opcode(opcode), .X(or_1_out), .Y(or_2_out), .K(DXYK), .KK(opnnn_1_kk), .NNN(opnnn_1_nnn), .AX(AX),
    .AY(AY), .K_2(K), .KK_2(KK), .NNN_2(NNN));
endmodule

module DECOP (
  input  enable,
  input  [15:0] opcode,
  output [15:0] decode3,
  output [15:0] decode2,
  output [15:0] decode1,
  output [15:0] decode0
);

  Decoder #(.select(4)) decoder_1 (
    .out0(decode3[0]), .out1(decode3[1]), .out2(decode3[2]), .out3(decode3[3]), .out4(decode3[4]),
    .out5(decode3[5]), .out6(decode3[6]), .out7(decode3[7]), .out8(decode3[8]), .out9(decode3[9]),
    .out10(decode3[10]), .out11(decode3[11]), .out12(decode3[12]), .out13(decode3[13]), .out14(decode3[14]),
    .out15(decode3[15]), .sel(opcode[15:12]), .en(enable));
  Decoder #(.select(4)) decoder_2 (
    .out0(decode2[0]), .out1(decode2[1]), .out2(decode2[2]), .out3(decode2[3]), .out4(decode2[4]),
    .out5(decode2[5]), .out6(decode2[6]), .out7(decode2[7]), .out8(decode2[8]), .out9(decode2[9]),
    .out10(decode2[10]), .out11(decode2[11]), .out12(decode2[12]), .out13(decode2[13]), .out14(decode2[14]),
    .out15(decode2[15]), .sel(opcode[11:8]), .en(enable));
  Decoder #(.select(4)) decoder_3 (
    .out0(decode1[0]), .out1(decode1[1]), .out2(decode1[2]), .out3(decode1[3]), .out4(decode1[4]),
    .out5(decode1[5]), .out6(decode1[6]), .out7(decode1[7]), .out8(decode1[8]), .out9(decode1[9]),
    .out10(decode1[10]), .out11(decode1[11]), .out12(decode1[12]), .out13(decode1[13]), .out14(decode1[14]),
    .out15(decode1[15]), .sel(opcode[7:4]), .en(enable));
  Decoder #(.select(4)) decoder_4 (
    .out0(decode0[0]), .out1(decode0[1]), .out2(decode0[2]), .out3(decode0[3]), .out4(decode0[4]),
    .out5(decode0[5]), .out6(decode0[6]), .out7(decode0[7]), .out8(decode0[8]), .out9(decode0[9]),
    .out10(decode0[10]), .out11(decode0[11]), .out12(decode0[12]), .out13(decode0[13]), .out14(decode0[14]),
    .out15(decode0[15]), .sel(opcode[3:0]), .en(enable));
  Pull_Resistor pull_resistor_1 (.node(decode3));
  Pull_Resistor pull_resistor_2 (.node(decode2));
  Pull_Resistor pull_resistor_3 (.node(decode1));
  Pull_Resistor pull_resistor_4 (.node(decode0));
endmodule

module OPNNN (
  input  [15:0] decode3,
  input  [15:0] decode2,
  input  [15:0] decode1,
  input  [15:0] decode0,
  output _00E0,
  output _00EE,
  output _0NNN,
  output _1NNN,
  output _2NNN,
  output ANNN,
  output BNNN,
  output _3XKK,
  output _4XKK,
  output _6XKK,
  output _7XKK,
  output CXKK,
  output NNN,
  output KK,
  output X
);

  wire and_1_out, nor_1_out;

  and and_1 (and_1_out, decode3[0], decode2[0], decode1[14]);
  and and_2 (_00E0, decode0[0], and_1_out);
  and and_3 (_00EE, and_1_out, decode0[14]);
  and and_4 (_0NNN, nor_1_out, decode3[0]);
  nor nor_1 (nor_1_out, _00E0, _00EE);
  or or_1 (NNN, _0NNN, decode3[1], decode3[2], decode3[10], decode3[11]);
  or or_2 (KK, decode3[3], decode3[4], decode3[6], decode3[7], decode3[12]);

  assign _1NNN = decode3[1];
  assign _2NNN = decode3[2];
  assign _3XKK = decode3[3];
  assign _4XKK = decode3[4];
  assign _6XKK = decode3[6];
  assign _7XKK = decode3[7];
  assign ANNN = decode3[10];
  assign BNNN = decode3[11];
  assign CXKK = decode3[12];
  assign X = KK;
endmodule

module OPXY (
  input  [15:0] decode3,
  input  [15:0] decode2,
  input  [15:0] decode1,
  input  [15:0] decode0,
  output _5XY0,
  output _8XY0,
  output _8XY1,
  output _8XY2,
  output _8XY3,
  output _8XY4,
  output _8XY5,
  output _8XY7,
  output _9XY0,
  output DXYK,
  output XY
);

  and and_1 (_5XY0, decode3[5], decode0[0]);
  and and_2 (_8XY0, decode3[8], decode0[0]);
  and and_3 (_8XY1, decode3[8], decode0[1]);
  and and_4 (_8XY2, decode3[8], decode0[2]);
  and and_5 (_8XY3, decode3[8], decode0[3]);
  and and_6 (_8XY4, decode3[8], decode0[4]);
  and and_7 (_8XY5, decode3[8], decode0[5]);
  and and_8 (_8XY7, decode3[8], decode0[7]);
  and and_9 (_9XY0, decode3[9], decode0[0]);
  or or_1 (XY, decode3[13], _9XY0, _8XY7, _8XY5, _8XY4, _8XY3, _8XY2, _8XY1, _8XY0, _5XY0);

  assign DXYK = decode3[13];
endmodule

module OPX (
  input  [15:0] decode3,
  input  [15:0] decode2,
  input  [15:0] decode1,
  input  [15:0] decode0,
  output _8X06,
  output _8X0E,
  output EX9E,
  output EXA1,
  output FX07,
  output FX0A,
  output FX15,
  output FX18,
  output FX1E,
  output FX29,
  output FX33,
  output FX55,
  output FX65,
  output X
);

  and and_1 (_8X06, decode3[8], decode1[0], decode0[6]);
  and and_2 (_8X0E, decode3[8], decode1[0], decode0[14]);
  and and_3 (EX9E, decode3[14], decode1[9], decode0[14]);
  and and_4 (EXA1, decode3[14], decode1[10], decode0[1]);
  and and_5 (FX07, decode3[15], decode1[0], decode0[7]);
  and and_6 (FX0A, decode3[15], decode1[0], decode0[10]);
  and and_7 (FX15, decode3[15], decode1[1], decode0[5]);
  and and_8 (FX18, decode1[1], decode0[8], decode3[15]);
  and and_9 (FX1E, decode3[15], decode0[14], decode1[1]);
  and and_10 (FX29, decode3[15], decode1[2], decode0[9]);
  and and_11 (FX33, decode3[15], decode1[3], decode0[3]);
  and and_12 (FX55, decode3[15], decode1[5], decode0[5]);
  and and_13 (FX65, decode3[15], decode1[6], decode0[5]);
  or or_1 (X, _8X06, _8X0E, EX9E, EXA1, FX07, FX0A, FX15, FX18, FX1E, FX29, FX33, FX55, FX65);
endmodule

module OPDATA (
  input  [15:0] opcode,
  input  X,
  input  Y,
  input  K,
  input  KK,
  input  NNN,
  output [3:0] AX,
  output [3:0] AY,
  output [3:0] K_2,
  output [7:0] KK_2,
  output [11:0] NNN_2
);

  wire [3:0] bit_extender_1_out, bit_extender_2_out, bit_extender_3_out, bit_extender_4_out,
       bit_extender_5_out;

  assign bit_extender_1_out = {{3{X}}, X};  // Bit_Extender bit_extender_1
  assign bit_extender_2_out = {{3{Y}}, Y};  // Bit_Extender bit_extender_2
  assign bit_extender_3_out = {{3{K}}, K};  // Bit_Extender bit_extender_3
  assign bit_extender_4_out = {{3{KK}}, KK};  // Bit_Extender bit_extender_4
  assign bit_extender_5_out = {{3{NNN}}, NNN};  // Bit_Extender bit_extender_5
  assign AX = opcode[11:8] & bit_extender_1_out;  // AND_Gate and_1, 4 bits wide
  assign AY = opcode[7:4] & bit_extender_2_out;  // AND_Gate and_2, 4 bits wide
  assign K_2 = opcode[3:0] & bit_extender_3_out;  // AND_Gate and_3, 4 bits wide
  assign KK_2[3:0] = opcode[3:0] & bit_extender_4_out;  // AND_Gate and_4, 4 bits wide
  assign KK_2[7:4] = opcode[7:4] & bit_extender_4_out;  // AND_Gate and_5, 4 bits wide
  assign NNN_2[3:0] = opcode[3:0] & bit_extender_5_out;  // AND_Gate and_6, 4 bits wide
  assign NNN_2[7:4] = opcode[7:4] & bit_extender_5_out;  // AND_Gate and_7, 4 bits wide
  assign NNN_2[11:8] = opcode[11:8] & bit_extender_5_out;  // AND_Gate and_8, 4 bits wide
endmodule
