// Logisim project 15_C8_dec2.circ as structural Verilog: 6 circuits, main circuit DEC
module DEC (
  input  enable,
  input  [15:0] opcode,
  output [11:0] OPNNN,
  output [9:0] OPXY,
  output [12:0] OPX,
  output [3:0] AX,
  output [3:0] AY,
  output [3:0] K,
  output [7:0] KK,
  output [11:0] NNN
);

  wire X0, X1, X2;
  wire [4:0] D;
  wire [31:0] D01, D23;

  DECOP decop_1 (
    .enable(enable), .opcode(opcode), .decode3(D23[31:16]), .decode2(D23[15:0]), .decode1(D01[31:16]),
    .decode0(D01[15:0]));
  or or_1 (D[0], X0, X1, X2);
  OPNNN opnnn_1 (
    .decode3(D23[31:16]), .decode2(D23[15:0]), .decode1(D01[31:16]), .decode0(D01[15:0]), .NNN(D[4]),
    .KK(D[3]), .Data(OPNNN), .X(X0));
  OPXY opxy_1 (
    .decode3(D23[31:16]), .decode2(D23[15:0]), .decode1(D01[31:16]), .decode0(D01[15:0]), .Y(D[1]),
    .out_5(OPXY), .K(D[2]), .X(X1));
  OPX opx_1 (.decode3(D23[31:16]), .decode2(D23[15:0]), .decode1(D01[31:16]), .decode0(D01[15:0]), .X(X2), .data(OPX));
  OPDATA opdata_1 (
    .opcode(opcode), .X(D[0]), .Y(D[1]), .K(D[2]), .KK(D[3]), .NNN(D[4]), .AX(AX), .AY(AY), .K_2(K),
    .KK_2(KK), .NNN_2(NNN));

  // Other names for the same wires on the sheet: Y1 = D[1]; K1 = D[2]; KK0 = D[3]; NNN_t = D[4]; OP[15:0] = opcode
endmodule

module DECOP (
  input  [15:0] opcode,
  input  enable,
  output [15:0] decode2,
  output [15:0] decode3,
  output [15:0] decode0,
  output [15:0] decode1
);

  Decoder #(.select(4)) decoder_1 (
    .out0(decode2[0]), .out1(decode2[1]), .out2(decode2[2]), .out3(decode2[3]), .out4(decode2[4]),
    .out5(decode2[5]), .out6(decode2[6]), .out7(decode2[7]), .out8(decode2[8]), .out9(decode2[9]),
    .out10(decode2[10]), .out11(decode2[11]), .out12(decode2[12]), .out13(decode2[13]), .out14(decode2[14]),
    .out15(decode2[15]), .sel(opcode[11:8]), .en(enable));
  Decoder #(.select(4)) decoder_2 (
    .out0(decode0[0]), .out1(decode0[1]), .out2(decode0[2]), .out3(decode0[3]), .out4(decode0[4]),
    .out5(decode0[5]), .out6(decode0[6]), .out7(decode0[7]), .out8(decode0[8]), .out9(decode0[9]),
    .out10(decode0[10]), .out11(decode0[11]), .out12(decode0[12]), .out13(decode0[13]), .out14(decode0[14]),
    .out15(decode0[15]), .sel(opcode[3:0]), .en(enable));
  Pull_Resistor pull_resistor_1 (.node(decode2));
  Pull_Resistor pull_resistor_2 (.node(decode0));
  Decoder #(.select(4)) decoder_3 (
    .out0(decode3[0]), .out1(decode3[1]), .out2(decode3[2]), .out3(decode3[3]), .out4(decode3[4]),
    .out5(decode3[5]), .out6(decode3[6]), .out7(decode3[7]), .out8(decode3[8]), .out9(decode3[9]),
    .out10(decode3[10]), .out11(decode3[11]), .out12(decode3[12]), .out13(decode3[13]), .out14(decode3[14]),
    .out15(decode3[15]), .sel(opcode[15:12]), .en(enable));
  Decoder #(.select(4)) decoder_4 (
    .out0(decode1[0]), .out1(decode1[1]), .out2(decode1[2]), .out3(decode1[3]), .out4(decode1[4]),
    .out5(decode1[5]), .out6(decode1[6]), .out7(decode1[7]), .out8(decode1[8]), .out9(decode1[9]),
    .out10(decode1[10]), .out11(decode1[11]), .out12(decode1[12]), .out13(decode1[13]), .out14(decode1[14]),
    .out15(decode1[15]), .sel(opcode[7:4]), .en(enable));
  Pull_Resistor pull_resistor_3 (.node(decode3));
  Pull_Resistor pull_resistor_4 (.node(decode1));

  // Other names for the same wires on the sheet: E = enable; O0[3:0] = opcode[3:0]; O1[3:0] = opcode[7:4];
  //   O2[3:0] = opcode[11:8]; O3[3:0] = opcode[15:12]
endmodule

module OPNNN (
  input  [15:0] decode3,
  input  [15:0] decode2,
  input  [15:0] decode1,
  input  [15:0] decode0,
  output [11:0] Data,
  output NNN,
  output KK,
  output X
);

  wire and_2_out, nor_1_out;

  and and_1 (Data[0], decode0[0], and_2_out);
  and and_2 (and_2_out, decode3[0], decode2[0], decode1[14]);
  and and_3 (Data[1], and_2_out, decode0[14]);
  and and_4 (Data[2], nor_1_out, decode3[0]);
  nor nor_1 (nor_1_out, Data[0], Data[1]);
  or or_1 (NNN, Data[2], decode3[1], decode3[2], decode3[10], decode3[11]);
  or or_2 (KK, decode3[3], decode3[4], decode3[6], decode3[7], decode3[12]);

  assign Data[11:3] = {decode3[12:10], decode3[7:6], decode3[4:1]};
  assign X = KK;

  // Other names for the same wires on the sheet: _00E0 = Data[0]; _00EE = Data[1]; _0NNN = Data[2];
  //   _1NNN = decode3[1]; _2NNN = decode3[2]; _3XKK = decode3[3]; _4XKK = decode3[4]; _6XKK = decode3[6];
  //   _7XKK = decode3[7]; ANNN = decode3[10]; BNNN = decode3[11]; CXKK = decode3[12]
endmodule

module OPXY (
  input  [15:0] decode3,
  input  [15:0] decode2,
  input  [15:0] decode1,
  input  [15:0] decode0,
  output [9:0] out_5,
  output Y,
  output X,
  output K
);

  and and_1 (out_5[0], decode3[5], decode0[0]);
  and and_2 (out_5[1], decode3[8], decode0[0]);
  and and_3 (out_5[2], decode3[8], decode0[1]);
  and and_4 (out_5[3], decode3[8], decode0[2]);
  and and_5 (out_5[4], decode3[8], decode0[3]);
  and and_6 (out_5[5], decode3[8], decode0[4]);
  and and_7 (out_5[6], decode3[8], decode0[5]);
  and and_8 (out_5[7], decode3[8], decode0[7]);
  and and_9 (out_5[8], decode3[9], decode0[0]);
  or or_1 (X, decode3[13], out_5[8], out_5[7], out_5[6], out_5[5], out_5[4], out_5[3], out_5[2], out_5[1], out_5[0]);

  assign K = decode3[13];
  assign out_5[9] = decode3[13];
  assign Y = X;

  // Other names for the same wires on the sheet: _5XY0 = out_5[0]; _8XY0 = out_5[1]; _8XY1 = out_5[2];
  //   _8XY2 = out_5[3]; _8XY3 = out_5[4]; _8XY4 = out_5[5]; _8XY5 = out_5[6]; _8XY7 = out_5[7]; _9XY0 = out_5[8];
  //   DXYK = decode3[13]
endmodule

module OPX (
  input  [15:0] decode3,
  input  [15:0] decode2,
  input  [15:0] decode1,
  input  [15:0] decode0,
  output [12:0] data,
  output X
);

  and and_1 (data[0], decode3[8], decode1[0], decode0[6]);
  and and_2 (data[1], decode3[8], decode1[0], decode0[14]);
  and and_3 (data[2], decode3[14], decode1[9], decode0[14]);
  and and_4 (data[3], decode3[14], decode1[10], decode0[1]);
  and and_5 (data[4], decode3[15], decode1[0], decode0[7]);
  and and_6 (data[5], decode3[15], decode1[0], decode0[10]);
  and and_7 (data[6], decode3[15], decode1[1], decode0[5]);
  and and_8 (data[7], decode1[1], decode0[8], decode3[15]);
  and and_9 (data[8], decode3[15], decode0[14], decode1[1]);
  and and_10 (data[9], decode3[15], decode1[2], decode0[9]);
  and and_11 (data[10], decode3[15], decode1[3], decode0[3]);
  and and_12 (data[11], decode3[15], decode1[5], decode0[5]);
  and and_13 (data[12], decode3[15], decode1[6], decode0[5]);
  or or_1 (X, data[0], data[1], data[2], data[3], data[4], data[5], data[6], data[7], data[8], data[9], data[10], data[11], data[12]);

  // Other names for the same wires on the sheet: _8X06 = data[0]; _8X0E = data[1]; EX9E = data[2]; EXA1 = data[3];
  //   FX07 = data[4]; FX0A = data[5]; FX15 = data[6]; FX18 = data[7]; FX1E = data[8]; FX29 = data[9]; FX33 = data[10];
  //   FX55 = data[11]; FX65 = data[12]
endmodule

module OPDATA (
  input  [15:0] opcode,
  input  X,
  input  Y,
  input  K,
  input  KK,
  input  NNN,
  output [3:0] AX,
  output [3:0] AY,
  output [3:0] K_2,
  output [7:0] KK_2,
  output [11:0] NNN_2
);

  wire [3:0] bit_extender_1_out, bit_extender_2_out, bit_extender_3_out, bit_extender_4_out,
       bit_extender_5_out;

  assign bit_extender_1_out = {{3{X}}, X};  // Bit_Extender bit_extender_1
  assign bit_extender_2_out = {{3{Y}}, Y};  // Bit_Extender bit_extender_2
  assign bit_extender_3_out = {{3{K}}, K};  // Bit_Extender bit_extender_3
  assign bit_extender_4_out = {{3{KK}}, KK};  // Bit_Extender bit_extender_4
  assign bit_extender_5_out = {{3{NNN}}, NNN};  // Bit_Extender bit_extender_5
  assign AX = opcode[11:8] & bit_extender_1_out;  // AND_Gate and_1, 4 bits wide
  assign AY = opcode[7:4] & bit_extender_2_out;  // AND_Gate and_2, 4 bits wide
  assign K_2 = opcode[3:0] & bit_extender_3_out;  // AND_Gate and_3, 4 bits wide
  assign KK_2[3:0] = opcode[3:0] & bit_extender_4_out;  // AND_Gate and_4, 4 bits wide
  assign KK_2[7:4] = opcode[7:4] & bit_extender_4_out;  // AND_Gate and_5, 4 bits wide
  assign NNN_2[3:0] = opcode[3:0] & bit_extender_5_out;  // AND_Gate and_6, 4 bits wide
  assign NNN_2[7:4] = opcode[7:4] & bit_extender_5_out;  // AND_Gate and_7, 4 bits wide
  assign NNN_2[11:8] = opcode[11:8] & bit_extender_5_out;  // AND_Gate and_8, 4 bits wide
endmodule
