// Logisim project 17_C8_other.circ as structural Verilog: 3 circuits, main circuit loadR
module main (
  input  C,
  input  E,
  input  H,
  input  [11:0] A,
  input  [7:0] D,
  input  S,
  input  H_2,
  input  C_2,
  output out_9
);

  wire loadr_1_spc;
  wire [7:0] ram_1_data;
  wire [11:0] and_1_out, and_2_out, bit_extender_1_out, loadr_1_pc_2, not_1_out, or_1_out, register_1_q;
  wire [15:0] loadr_1_opcode;

  assign bit_extender_1_out = {{11{S}}, S};  // Bit_Extender bit_extender_1
  // Probe on loadr_1_opcode
  loadR loadr_1 (
    .DR(ram_1_data), .enable(E), .H(H), .clear(C), .PC(or_1_out), .opcode(loadr_1_opcode), .\end (out_9),
    .SPC(loadr_1_spc), .PC_2(loadr_1_pc_2));
  assign and_1_out = A & bit_extender_1_out;  // AND_Gate and_1, 12 bits wide
  assign and_2_out = register_1_q & not_1_out;  // AND_Gate and_2, 12 bits wide
  assign not_1_out = ~bit_extender_1_out;  // NOT_Gate not_1, 12 bits wide
  Register #(.width(12)) register_1 (.D(loadr_1_pc_2), .en(loadr_1_spc), .Q(register_1_q), .clk(H), .clr(C));
  assign or_1_out = and_1_out | and_2_out;  // OR_Gate or_1, 12 bits wide
  RAM #(.addrWidth(12), .bus("separate")) ram_1 (
    .addr(or_1_out), .din(D), .data(ram_1_data), .str(S), .sel(E), .clk(H_2), .ld(loadr_1_spc), .clr(C_2));
endmodule

module loadR (
  input  [7:0] DR,
  input  enable,
  input  H,
  input  clear,
  input  [11:0] PC,
  output [15:0] opcode,
  output \end ,
  output SPC,
  output [11:0] PC_2
);

  wire and_1_out, and_4_out, and_6_out, not_1_out, not_2_out, not_3_out;
  wire [1:0] counter_1_q;
  wire [7:0] and_2_out, and_3_out, bit_extender_1_out, bit_extender_2_out, register_1_q;
  wire [11:0] adder_1_out, bit_extender_3_out;

  assign bit_extender_1_out = {{7{and_6_out}}, and_6_out};  // Bit_Extender bit_extender_1
  assign bit_extender_2_out = {{7{and_4_out}}, and_4_out};  // Bit_Extender bit_extender_2
  and and_1 (and_1_out, H, enable, not_1_out);
  assign and_2_out = bit_extender_1_out & DR;  // AND_Gate and_2, 8 bits wide
  assign and_3_out = DR & bit_extender_2_out;  // AND_Gate and_3, 8 bits wide
  Counter #(.width(2), .max('h3)) counter_1 (
    .load(1'b0), .D(2'b00), .count(enable), .Q(counter_1_q), .clk(and_1_out), .clr(clear));  // open: carry
  not not_1 (not_1_out, \end );
  or or_1 (SPC, and_4_out, and_6_out);
  Adder #(.width(12)) adder_1 (.a(PC), .b(12'h1), .out(adder_1_out), .cin(1'b0));  // open: cout
  Register register_1 (.D(and_3_out), .en(and_4_out), .Q(register_1_q), .clk(and_1_out), .clr(clear));
  and and_4 (and_4_out, counter_1_q[0], not_2_out);
  not not_2 (not_2_out, counter_1_q[1]);
  Comparator #(.width(2)) comparator_1 (.a(counter_1_q), .b(2'b11), .eq(\end ));  // open: gt, lt
  assign bit_extender_3_out = {{11{SPC}}, SPC};  // Bit_Extender bit_extender_3
  Register #(.width(16)) register_2 (
    .D({register_1_q, and_2_out}), .en(and_6_out), .Q(opcode), .clk(and_1_out), .clr(clear));
  not not_3 (not_3_out, counter_1_q[0]);
  assign PC_2 = adder_1_out & bit_extender_3_out;  // AND_Gate and_5, 12 bits wide
  and and_6 (and_6_out, not_3_out, counter_1_q[1]);
endmodule

module MA (
  input  MA,
  input  RESET,
  output LedM,
  output MA_2,
  output R
);

  wire d_ff_1_qn, not_1_out;

  or or_1 (R, not_1_out, RESET);
  D_Flip_Flop d_ff_1 (.clk(MA), .D(d_ff_1_qn), .Q(LedM), .Qn(d_ff_1_qn), .preset(1'b0), .en(1'b1), .reset(1'b0));
  not not_1 (not_1_out, LedM);

  assign MA_2 = LedM;

  // Notes on the sheet:
  //   MARCHE / ARRET
endmodule
