// Logisim project 18_C8_aluH.circ as structural Verilog: 6 circuits, main circuit aluHexDec
module main (
  input  [7:0] VX,
  input  [11:0] I,
  input  H,
  input  sel,
  input  LD,
  input  CLR
);

  wire aluhexdec_1_sr;
  wire [7:0] aluhexdec_1_dr, ram_1_data;
  wire [11:0] aluhexdec_1_ar, and_1_out, and_2_out, bit_extender_1_out, not_1_out, or_1_out;

  // Probe on VX
  // Probe on VX
  // Probe on VX
  // Probe on VX
  aluHexDec aluhexdec_1 (
    .VX(VX), .I(I), .H(H), .enable(sel), .DR(aluhexdec_1_dr), .SR(aluhexdec_1_sr), .AR(aluhexdec_1_ar));  // open: out_8
  assign not_1_out = ~bit_extender_1_out;  // NOT_Gate not_1, 12 bits wide
  assign bit_extender_1_out = {{11{aluhexdec_1_sr}}, aluhexdec_1_sr};  // Bit_Extender bit_extender_1
  assign and_1_out = I & not_1_out;  // AND_Gate and_1, 12 bits wide
  assign and_2_out = aluhexdec_1_ar & bit_extender_1_out;  // AND_Gate and_2, 12 bits wide
  RAM #(.addrWidth(12), .bus("separate")) ram_1 (
    .addr(or_1_out), .din(aluhexdec_1_dr), .data(ram_1_data), .str(aluhexdec_1_sr), .sel(sel), .clk(H),
    .ld(LD), .clr(CLR));
  assign or_1_out = and_1_out | and_2_out;  // OR_Gate or_1, 12 bits wide
  // Probe on ram_1_data
  // Probe on ram_1_data
  // Probe on ram_1_data
  // Probe on ram_1_data
endmodule

module aluHexDec (
  input  [7:0] VX,
  input  [11:0] I,
  input  enable,
  input  H,
  output [7:0] DR,
  output [11:0] AR,
  output SR,
  output out_8
);

  wire savram_1_sel_hundred, savram_1_sel_ten, savram_1_sel_unit, tmphex_1_save;
  wire [1:0] tmphex_1_sel;
  wire [7:0] and_1_out, and_2_out, and_3_out, bit_extender_1_out, bit_extender_2_out, bit_extender_3_out,
       hexadec_1_output_hundred, hexadec_1_output_ten, hexadec_1_output_unit;

  tmpHex tmphex_1 (.enable(enable), .H(H), .save(tmphex_1_save), .Sel(tmphex_1_sel), .\end (out_8));
  hexadec hexadec_1 (
    .VX(VX), .Output_hundred(hexadec_1_output_hundred), .Output_unit(hexadec_1_output_unit),
    .Output_ten(hexadec_1_output_ten));
  savRam savram_1 (
    .I(I), .enable(enable), .Sel(tmphex_1_sel), .AR(AR), .Sel_unit(savram_1_sel_unit),
    .Sel_ten(savram_1_sel_ten), .Sel_hundred(savram_1_sel_hundred));
  assign bit_extender_1_out = {{7{savram_1_sel_hundred}}, savram_1_sel_hundred};  // Bit_Extender bit_extender_1
  assign bit_extender_2_out = {{7{savram_1_sel_ten}}, savram_1_sel_ten};  // Bit_Extender bit_extender_2
  assign bit_extender_3_out = {{7{savram_1_sel_unit}}, savram_1_sel_unit};  // Bit_Extender bit_extender_3
  or or_1 (SR, savram_1_sel_hundred, savram_1_sel_ten, savram_1_sel_unit, tmphex_1_save);
  assign and_1_out = hexadec_1_output_hundred & bit_extender_1_out;  // AND_Gate and_1, 8 bits wide
  assign and_2_out = hexadec_1_output_ten & bit_extender_2_out;  // AND_Gate and_2, 8 bits wide
  assign and_3_out = hexadec_1_output_unit & bit_extender_3_out;  // AND_Gate and_3, 8 bits wide
  assign DR = and_1_out | and_2_out | and_3_out;  // OR_Gate or_2, 8 bits wide
endmodule

module hexadec (
  input  [7:0] VX,
  output [7:0] Output_hundred,
  output [7:0] Output_ten,
  output [7:0] Output_unit
);

  wire [7:0] divider_1_out;

  Divider divider_1 (.a(VX), .b(8'ha), .out(divider_1_out), .upper({8{1'b0}}), .rem(Output_unit));
  Divider divider_2 (.a(divider_1_out), .b(8'ha), .out(Output_hundred), .upper({8{1'b0}}), .rem(Output_ten));
endmodule

module savRam (
  input  [11:0] I,
  input  enable,
  input  [1:0] Sel,
  output [11:0] AR,
  output Sel_unit,
  output Sel_ten,
  output Sel_hundred
);

  wire [11:0] adder_1_out, adder_2_out, and_1_out, and_2_out, and_3_out, bit_extender_1_out,
       bit_extender_2_out, bit_extender_3_out;

  Adder #(.width(12)) adder_1 (.a(12'h1), .b(I), .out(adder_1_out), .cin(1'b0));  // open: cout
  Decoder #(.select(2), .disabled(0)) decoder_1 (
    .out0(Sel_hundred), .out1(Sel_ten), .out2(Sel_unit), .sel(Sel), .en(enable));  // open: out3
  Adder #(.width(12)) adder_2 (.a(adder_1_out), .b(12'h1), .out(adder_2_out), .cin(1'b0));  // open: cout
  assign bit_extender_1_out = {{11{Sel_hundred}}, Sel_hundred};  // Bit_Extender bit_extender_1
  assign bit_extender_2_out = {{11{Sel_ten}}, Sel_ten};  // Bit_Extender bit_extender_2
  assign bit_extender_3_out = {{11{Sel_unit}}, Sel_unit};  // Bit_Extender bit_extender_3
  assign and_1_out = I & bit_extender_1_out;  // AND_Gate and_1, 12 bits wide
  assign and_2_out = adder_1_out & bit_extender_2_out;  // AND_Gate and_2, 12 bits wide
  assign AR = and_1_out | and_2_out | and_3_out;  // OR_Gate or_1, 12 bits wide
  assign and_3_out = adder_2_out & bit_extender_3_out;  // AND_Gate and_3, 12 bits wide
endmodule

module tmpHex (
  input  enable,
  input  H,
  output save,
  output [1:0] Sel,
  output \end 
);

  wire and_1_out, and_2_out, comparator_1_eq, comparator_1_gt, comparator_1_lt, not_1_out;
  wire [7:0] counter_1_q;

  and and_1 (and_1_out, enable, comparator_1_lt);
  not not_1 (not_1_out, enable);
  Counter counter_1 (
    .load(1'b0), .D({8{1'b0}}), .count(and_1_out), .Q(counter_1_q), .clk(and_2_out), .clr(not_1_out));  // open: carry
  and and_2 (and_2_out, H, comparator_1_lt);
  Comparator #(.width(6)) comparator_1 (
    .a(counter_1_q[7:2]), .b(6'b000011), .gt(comparator_1_gt), .eq(comparator_1_eq), .lt(comparator_1_lt));
  or or_1 (save, counter_1_q[0], counter_1_q[1]);
  Bit_Extender #(.in_width(6), .out_width(2)) bit_extender_1 (.in(counter_1_q[7:2]), .out(Sel));
  or or_2 (\end , comparator_1_gt, comparator_1_eq);
endmodule

module hexatest (
  input  in_1,
  input  in_2
);

  wire and_1_out, and_2_out, or_1_out, or_2_out;
  wire [3:0] counter_1_q, counter_2_q;
  wire [7:0] counter_4_q, divider_1_out, divider_1_rem, divider_2_out, divider_2_rem;

  Counter #(.width(4), .max('hf)) counter_1 (
    .load(1'b0), .D(4'b0000), .count(1'b1), .Q(counter_1_q), .clk(in_1), .clr(or_1_out));  // open: carry
  or or_1 (or_1_out, and_1_out, in_2);
  Counter #(.width(4), .max('hf)) counter_2 (
    .load(1'b0), .D(4'b0000), .count(1'b1), .Q(counter_2_q), .clk(or_1_out), .clr(or_2_out));  // open: carry
  or or_2 (or_2_out, and_2_out, in_2);
  Counter #(.width(4), .max('hf)) counter_3 (
    .load(1'b0), .D(4'b0000), .count(1'b1), .clk(or_2_out), .clr(in_2));  // open: Q, carry
  Counter counter_4 (.load(1'b0), .D({8{1'b0}}), .count(1'b1), .Q(counter_4_q), .clk(in_1), .clr(in_2));  // open: carry
  // Probe on counter_4_q
  and and_1 (and_1_out, counter_1_q[1], counter_1_q[3]);
  and and_2 (and_2_out, counter_2_q[1], counter_2_q[3]);
  Divider divider_1 (.a(counter_4_q), .b(8'ha), .out(divider_1_out), .upper({8{1'b0}}), .rem(divider_1_rem));
  Divider divider_2 (.a(divider_1_out), .b(8'ha), .out(divider_2_out), .upper({8{1'b0}}), .rem(divider_2_rem));
  // Probe on divider_2_out
  // Probe on divider_2_rem
  // Probe on divider_1_rem
endmodule
