// Logisim project 19_C8_reg.circ as structural Verilog: 6 circuits, main circuit main
module main (
  input  [7:0] DE,
  input  [7:0] DM,
  input  storeM,
  input  [3:0] AX,
  input  storeX,
  input  loadX,
  input  [3:0] AY,
  input  loadY,
  input  H,
  input  select,
  input  clear,
  output [7:0] D0,
  output [7:0] DX,
  output [7:0] DY,
  output [7:0] D0_2,
  output [7:0] DX_2,
  output [7:0] DY_2
);

  wire [7:0] regi16d_1_r8_b, regi16d_1_r8_b_2, regi16d_1_r8_b_3, regi16d_1_r8_b_4, regi16d_1_rc_f,
       regi16d_1_rc_f_2, regi16d_1_rc_f_3, regi16d_1_rc_f_4;
  wire [31:0] regi16d_1_r0_3, regi16d_1_r4_7;

  // Probe on DE
  // Probe on DE
  // Probe on DE
  // Probe on DM
  // Probe on DM
  // Probe on DM
  REGI16 regi16_1 (
    .DE(DE), .AX(AX), .AY(AY), .H(H), .storeX(storeX), .loadX(loadX), .loadY(loadY), .select(select),
    .clear(clear), .DX(DX), .DY(DY), .D0(D0), .DM(DM), .storeM(storeM));
  REGI16D regi16d_1 (
    .DE(DE), .AX(AX), .AY(AY), .H(H), .storeX(storeX), .loadX(loadX), .loadY(loadY), .select(select),
    .clear(clear), .DX(DX_2), .DY(DY_2), .R0_3(regi16d_1_r0_3), .R4_7(regi16d_1_r4_7),
    .R8_B({regi16d_1_r8_b_4, regi16d_1_r8_b_3, regi16d_1_r8_b_2, regi16d_1_r8_b}),
    .RC_F({regi16d_1_rc_f_4, regi16d_1_rc_f_3, regi16d_1_rc_f_2, regi16d_1_rc_f}), .D0(D0_2), .DM(DM),
    .storeM(storeM));
  // Probe on regi16d_1_r0_3[7:0]
  // Probe on regi16d_1_r0_3[7:0]
  // Probe on regi16d_1_r0_3[7:0]
  // Probe on regi16d_1_r0_3[7:0]
  // Probe on regi16d_1_r0_3[15:8]
  // Probe on regi16d_1_r0_3[15:8]
  // Probe on regi16d_1_r0_3[15:8]
  // Probe on regi16d_1_r0_3[15:8]
  // Probe on regi16d_1_r0_3[23:16]
  // Probe on regi16d_1_r0_3[23:16]
  // Probe on regi16d_1_r0_3[23:16]
  // Probe on regi16d_1_r0_3[23:16]
  // Probe on regi16d_1_r0_3[31:24]
  // Probe on regi16d_1_r0_3[31:24]
  // Probe on regi16d_1_r0_3[31:24]
  // Probe on regi16d_1_r0_3[31:24]
  // Probe on regi16d_1_r4_7[7:0]
  // Probe on regi16d_1_r4_7[7:0]
  // Probe on regi16d_1_r4_7[7:0]
  // Probe on regi16d_1_r4_7[7:0]
  // Probe on regi16d_1_r4_7[15:8]
  // Probe on regi16d_1_r4_7[15:8]
  // Probe on regi16d_1_r4_7[15:8]
  // Probe on regi16d_1_r4_7[15:8]
  // Probe on regi16d_1_r4_7[23:16]
  // Probe on regi16d_1_r4_7[23:16]
  // Probe on regi16d_1_r4_7[23:16]
  // Probe on regi16d_1_r4_7[23:16]
  // Probe on regi16d_1_r4_7[31:24]
  // Probe on regi16d_1_r4_7[31:24]
  // Probe on regi16d_1_r4_7[31:24]
  // Probe on regi16d_1_r4_7[31:24]
  // Probe on regi16d_1_r8_b
  // Probe on regi16d_1_r8_b
  // Probe on regi16d_1_r8_b
  // Probe on regi16d_1_r8_b
  // Probe on regi16d_1_r8_b_2
  // Probe on regi16d_1_r8_b_2
  // Probe on regi16d_1_r8_b_2
  // Probe on regi16d_1_r8_b_2
  // Probe on regi16d_1_r8_b_3
  // Probe on regi16d_1_r8_b_3
  // Probe on regi16d_1_r8_b_3
  // Probe on regi16d_1_r8_b_3
  // Probe on regi16d_1_r8_b_4
  // Probe on regi16d_1_r8_b_4
  // Probe on regi16d_1_r8_b_4
  // Probe on regi16d_1_r8_b_4
  // Probe on regi16d_1_rc_f
  // Probe on regi16d_1_rc_f
  // Probe on regi16d_1_rc_f
  // Probe on regi16d_1_rc_f
  // Probe on regi16d_1_rc_f_2
  // Probe on regi16d_1_rc_f_2
  // Probe on regi16d_1_rc_f_2
  // Probe on regi16d_1_rc_f_2
  // Probe on regi16d_1_rc_f_3
  // Probe on regi16d_1_rc_f_3
  // Probe on regi16d_1_rc_f_3
  // Probe on regi16d_1_rc_f_3
  // Probe on regi16d_1_rc_f_4
  // Probe on regi16d_1_rc_f_4
  // Probe on regi16d_1_rc_f_4
  // Probe on regi16d_1_rc_f_4

  // Notes on the sheet:
  //   DE
  //   DM
  //   D0
  //   D1
  //   D2
  //   D3
  //   D4
  //   D5
  //   D6
  //   D7
  //   D8
  //   D9
  //   DA
  //   DB
  //   DC
  //   DD
  //   DE
  //   DF
endmodule

module REGI16 (
  input  [7:0] DE,
  input  H,
  input  select,
  input  clear,
  input  storeX,
  input  loadX,
  input  loadY,
  input  [3:0] AX,
  input  [3:0] AY,
  input  [7:0] DM,
  input  storeM,
  output [7:0] D0,
  output [7:0] DX,
  output [7:0] DY
);

  wire decoder_1_out0, decoder_1_out1, decoder_1_out2, decoder_1_out3, decoder_2_out0, decoder_2_out1,
       decoder_2_out2, decoder_2_out3, decoder_3_out0, decoder_3_out1, decoder_3_out2, decoder_3_out3;
  wire [7:0] reg4_1_dx, reg4_1_dy, reg4_2_dx, reg4_2_dy, reg4_3_dx, reg4_3_dy, reg4_4_dx, reg4_4_dy;

  Decoder #(.select(2), .disabled(0)) decoder_1 (
    .out0(decoder_1_out0), .out1(decoder_1_out1), .out2(decoder_1_out2), .out3(decoder_1_out3),
    .sel(AX[3:2]), .en(storeX));
  Decoder #(.select(2), .disabled(0)) decoder_2 (
    .out0(decoder_2_out0), .out1(decoder_2_out1), .out2(decoder_2_out2), .out3(decoder_2_out3),
    .sel(AX[3:2]), .en(loadX));
  Decoder #(.select(2), .disabled(0)) decoder_3 (
    .out0(decoder_3_out0), .out1(decoder_3_out1), .out2(decoder_3_out2), .out3(decoder_3_out3),
    .sel(AY[3:2]), .en(loadY));
  REG4 reg4_1 (
    .DE(DE), .AX(AX[1:0]), .AY(AY[1:0]), .H(H), .storeX(decoder_1_out0), .loadX(decoder_2_out0),
    .loadY(decoder_3_out0), .select(select), .clear(clear), .DM({8{1'b0}}), .storeM(1'b0), .D0(D0),
    .DX(reg4_1_dx), .DY(reg4_1_dy));
  REG4 reg4_2 (
    .DE(DE), .AX(AX[1:0]), .AY(AY[1:0]), .H(H), .storeX(decoder_1_out1), .loadX(decoder_2_out1),
    .loadY(decoder_3_out1), .select(select), .clear(clear), .DM({8{1'b0}}), .storeM(1'b0), .DX(reg4_2_dx),
    .DY(reg4_2_dy));  // open: D0
  REG4 reg4_3 (
    .DE(DE), .AX(AX[1:0]), .AY(AY[1:0]), .H(H), .storeX(decoder_1_out2), .loadX(decoder_2_out2),
    .loadY(decoder_3_out2), .select(select), .clear(clear), .DM({8{1'b0}}), .storeM(1'b0), .DX(reg4_3_dx),
    .DY(reg4_3_dy));  // open: D0
  REG4 reg4_4 (
    .DE(DE), .AX(AX[1:0]), .AY(AY[1:0]), .H(H), .storeX(decoder_1_out3), .loadX(decoder_2_out3),
    .loadY(decoder_3_out3), .select(select), .clear(clear), .DM(DM), .storeM(storeM), .DX(reg4_4_dx),
    .DY(reg4_4_dy));  // open: D0
  assign DX = reg4_1_dx | reg4_2_dx | reg4_3_dx | reg4_4_dx;  // OR_Gate or_1, 8 bits wide
  assign DY = reg4_2_dy | reg4_1_dy | reg4_3_dy | reg4_4_dy;  // OR_Gate or_2, 8 bits wide
endmodule

module REG4 (
  input  [7:0] DE,
  input  [1:0] AX,
  input  [1:0] AY,
  input  H,
  input  storeX,
  input  loadX,
  input  loadY,
  input  select,
  input  clear,
  input  [7:0] DM,
  input  storeM,
  output [7:0] D0,
  output [7:0] DX,
  output [7:0] DY
);

  wire and_1_out, and_2_out, and_3_out, and_6_out, and_7_out, demultiplexer_1_out0, demultiplexer_1_out1,
       demultiplexer_1_out2, demultiplexer_1_out3, not_2_out, or_2_out;
  wire [7:0] and_4_out, and_5_out, bit_extender_1_out, not_1_out, or_1_out, register_2_q, register_3_q,
       register_4_q;

  // Probe on DE
  and and_1 (and_1_out, storeX, select);
  and and_2 (and_2_out, loadX, select);
  and and_3 (and_3_out, loadY, select);
  // Probe on DM
  assign bit_extender_1_out = {{7{storeM}}, storeM};  // Bit_Extender bit_extender_1
  Demultiplexer #(.select(2), .disabled(0)) demultiplexer_1 (
    .out0(demultiplexer_1_out0), .out1(demultiplexer_1_out1), .out2(demultiplexer_1_out2),
    .out3(demultiplexer_1_out3), .in(H), .sel(AX), .en(and_1_out));
  assign and_4_out = DE & not_1_out;  // AND_Gate and_4, 8 bits wide
  assign not_1_out = ~bit_extender_1_out;  // NOT_Gate not_1, 8 bits wide
  assign and_5_out = DM & bit_extender_1_out;  // AND_Gate and_5, 8 bits wide
  not not_2 (not_2_out, storeM);
  assign or_1_out = and_4_out | and_5_out;  // OR_Gate or_1, 8 bits wide
  and and_6 (and_6_out, demultiplexer_1_out3, not_2_out);
  or or_2 (or_2_out, and_6_out, and_7_out);
  and and_7 (and_7_out, storeM, H);
  Register register_1 (.D(DE), .en(select), .Q(D0), .clk(demultiplexer_1_out0), .clr(clear));
  Register register_2 (.D(DE), .en(select), .Q(register_2_q), .clk(demultiplexer_1_out1), .clr(clear));
  Register register_3 (.D(DE), .en(select), .Q(register_3_q), .clk(demultiplexer_1_out2), .clr(clear));
  Register register_4 (.D(or_1_out), .en(select), .Q(register_4_q), .clk(or_2_out), .clr(clear));
  // Probe on D0
  // Probe on DX
  Multiplexer #(.select(2), .width(8), .disabled(0)) multiplexer_1 (
    .in0(D0), .in1(register_2_q), .in2(register_3_q), .in3(register_4_q), .out(DX), .sel(AX), .en(and_2_out));
  // Probe on DY
  Multiplexer #(.select(2), .width(8), .disabled(0)) multiplexer_2 (
    .in0(D0), .in1(register_2_q), .in2(register_3_q), .in3(register_4_q), .out(DY), .sel(AY), .en(and_3_out));
endmodule

module REGI16D (
  input  [7:0] DE,
  input  H,
  input  select,
  input  clear,
  input  storeX,
  input  loadX,
  input  loadY,
  input  [3:0] AX,
  input  [3:0] AY,
  input  [7:0] DM,
  input  storeM,
  output [7:0] D0,
  output [7:0] DX,
  output [7:0] DY,
  output [31:0] R0_3,
  output [31:0] R4_7,
  output [31:0] R8_B,
  output [31:0] RC_F
);

  wire decoder_1_out0, decoder_1_out1, decoder_1_out2, decoder_1_out3, decoder_2_out0, decoder_2_out1,
       decoder_2_out2, decoder_2_out3, decoder_3_out0, decoder_3_out1, decoder_3_out2, decoder_3_out3;
  wire [7:0] reg4d_1_dx, reg4d_1_dy, reg4d_2_dx, reg4d_2_dy, reg4d_3_dx, reg4d_3_dy, reg4d_4_dx, reg4d_4_dy;

  Decoder #(.select(2), .disabled(0)) decoder_1 (
    .out0(decoder_1_out0), .out1(decoder_1_out1), .out2(decoder_1_out2), .out3(decoder_1_out3),
    .sel(AX[3:2]), .en(storeX));
  Decoder #(.select(2), .disabled(0)) decoder_2 (
    .out0(decoder_2_out0), .out1(decoder_2_out1), .out2(decoder_2_out2), .out3(decoder_2_out3),
    .sel(AX[3:2]), .en(loadX));
  Decoder #(.select(2), .disabled(0)) decoder_3 (
    .out0(decoder_3_out0), .out1(decoder_3_out1), .out2(decoder_3_out2), .out3(decoder_3_out3),
    .sel(AY[3:2]), .en(loadY));
  REG4D reg4d_1 (
    .DE(DE), .AX(AX[1:0]), .AY(AY[1:0]), .H(H), .storeX(decoder_1_out0), .loadX(decoder_2_out0),
    .loadY(decoder_3_out0), .select(select), .clear(clear), .DM({8{1'b0}}), .storeM(1'b0), .D0(D0),
    .DX(reg4d_1_dx), .DY(reg4d_1_dy), .D0_3(R0_3));
  REG4D reg4d_2 (
    .DE(DE), .AX(AX[1:0]), .AY(AY[1:0]), .H(H), .storeX(decoder_1_out1), .loadX(decoder_2_out1),
    .loadY(decoder_3_out1), .select(select), .clear(clear), .DM({8{1'b0}}), .storeM(1'b0), .DX(reg4d_2_dx),
    .DY(reg4d_2_dy), .D0_3(R4_7));  // open: D0
  REG4D reg4d_3 (
    .DE(DE), .AX(AX[1:0]), .AY(AY[1:0]), .H(H), .storeX(decoder_1_out2), .loadX(decoder_2_out2),
    .loadY(decoder_3_out2), .select(select), .clear(clear), .DM({8{1'b0}}), .storeM(1'b0), .DX(reg4d_3_dx),
    .DY(reg4d_3_dy), .D0_3(R8_B));  // open: D0
  REG4D reg4d_4 (
    .DE(DE), .AX(AX[1:0]), .AY(AY[1:0]), .H(H), .storeX(decoder_1_out3), .loadX(decoder_2_out3),
    .loadY(decoder_3_out3), .select(select), .clear(clear), .DM(DM), .storeM(storeM), .DX(reg4d_4_dx),
    .DY(reg4d_4_dy), .D0_3(RC_F));  // open: D0
  assign DX = reg4d_1_dx | reg4d_2_dx | reg4d_3_dx | reg4d_4_dx;  // OR_Gate or_1, 8 bits wide
  assign DY = reg4d_2_dy | reg4d_1_dy | reg4d_3_dy | reg4d_4_dy;  // OR_Gate or_2, 8 bits wide
endmodule

module REG4D (
  input  [7:0] DE,
  input  [1:0] AX,
  input  [1:0] AY,
  input  H,
  input  storeX,
  input  loadX,
  input  loadY,
  input  select,
  input  clear,
  input  [7:0] DM,
  input  storeM,
  output [7:0] D0,
  output [7:0] DX,
  output [7:0] DY,
  output [31:0] D0_3
);

  wire and_1_out, and_2_out, and_3_out, and_6_out, and_7_out, demultiplexer_1_out0, demultiplexer_1_out1,
       demultiplexer_1_out2, demultiplexer_1_out3, not_2_out, or_2_out;
  wire [7:0] and_4_out, and_5_out, bit_extender_1_out, not_1_out, or_1_out;

  and and_1 (and_1_out, storeX, select);
  and and_2 (and_2_out, loadX, select);
  and and_3 (and_3_out, loadY, select);
  assign bit_extender_1_out = {{7{storeM}}, storeM};  // Bit_Extender bit_extender_1
  Demultiplexer #(.select(2), .disabled(0)) demultiplexer_1 (
    .out0(demultiplexer_1_out0), .out1(demultiplexer_1_out1), .out2(demultiplexer_1_out2),
    .out3(demultiplexer_1_out3), .in(H), .sel(AX), .en(and_1_out));
  assign and_4_out = DE & not_1_out;  // AND_Gate and_4, 8 bits wide
  assign not_1_out = ~bit_extender_1_out;  // NOT_Gate not_1, 8 bits wide
  assign and_5_out = DM & bit_extender_1_out;  // AND_Gate and_5, 8 bits wide
  not not_2 (not_2_out, storeM);
  assign or_1_out = and_4_out | and_5_out;  // OR_Gate or_1, 8 bits wide
  and and_6 (and_6_out, demultiplexer_1_out3, not_2_out);
  or or_2 (or_2_out, and_6_out, and_7_out);
  and and_7 (and_7_out, storeM, H);
  Register register_1 (.D(DE), .en(select), .Q(D0), .clk(demultiplexer_1_out0), .clr(clear));
  Register register_2 (.D(DE), .en(select), .Q(D0_3[15:8]), .clk(demultiplexer_1_out1), .clr(clear));
  Register register_3 (.D(DE), .en(select), .Q(D0_3[23:16]), .clk(demultiplexer_1_out2), .clr(clear));
  Register register_4 (.D(or_1_out), .en(select), .Q(D0_3[31:24]), .clk(or_2_out), .clr(clear));
  Multiplexer #(.select(2), .width(8), .disabled(0)) multiplexer_1 (
    .in0(D0), .in1(D0_3[15:8]), .in2(D0_3[23:16]), .in3(D0_3[31:24]), .out(DX), .sel(AX), .en(and_2_out));
  Multiplexer #(.select(2), .width(8), .disabled(0)) multiplexer_2 (
    .in0(D0), .in1(D0_3[15:8]), .in2(D0_3[23:16]), .in3(D0_3[31:24]), .out(DY), .sel(AY), .en(and_3_out));

  assign D0_3[7:0] = D0;
endmodule

module REGI_DB (
  input  [7:0] DE,
  input  [3:0] AX,
  input  [3:0] AY,
  input  H,
  input  storeX,
  input  loadX,
  input  loadY,
  input  select,
  input  clear,
  input  [7:0] EDF,
  input  storeF,
  output [7:0] D0,
  output [31:0] R0_3,
  output [7:0] DX,
  output [31:0] R4_7,
  output [7:0] DY,
  output [31:0] R8_B,
  output [31:0] RC_F
);

  wire and_1_out, and_2_out, and_3_out, and_6_out, and_7_out, demultiplexer_2_out0, demultiplexer_2_out1,
       demultiplexer_2_out2, demultiplexer_2_out3, demultiplexer_2_out4, demultiplexer_2_out5,
       demultiplexer_2_out6, demultiplexer_2_out7, demultiplexer_2_out8, demultiplexer_2_out9,
       demultiplexer_2_out10, demultiplexer_2_out11, demultiplexer_2_out12, demultiplexer_2_out13,
       demultiplexer_2_out14, demultiplexer_2_out15, not_2_out, or_2_out;
  wire [7:0] and_4_out, and_5_out, bit_extender_1_out, demultiplexer_1_out0, demultiplexer_1_out1,
       demultiplexer_1_out2, demultiplexer_1_out3, demultiplexer_1_out4, demultiplexer_1_out5,
       demultiplexer_1_out6, demultiplexer_1_out7, demultiplexer_1_out8, demultiplexer_1_out9,
       demultiplexer_1_out10, demultiplexer_1_out11, demultiplexer_1_out12, demultiplexer_1_out13,
       demultiplexer_1_out14, demultiplexer_1_out15, not_1_out, or_1_out;

  and and_1 (and_1_out, storeX, select);
  and and_2 (and_2_out, loadX, select);
  and and_3 (and_3_out, loadY, select);
  Demultiplexer #(.select(4), .width(8), .disabled(0)) demultiplexer_1 (
    .out0(demultiplexer_1_out0), .out1(demultiplexer_1_out1), .out2(demultiplexer_1_out2),
    .out3(demultiplexer_1_out3), .out4(demultiplexer_1_out4), .out5(demultiplexer_1_out5),
    .out6(demultiplexer_1_out6), .out7(demultiplexer_1_out7), .out8(demultiplexer_1_out8),
    .out9(demultiplexer_1_out9), .out10(demultiplexer_1_out10), .out11(demultiplexer_1_out11),
    .out12(demultiplexer_1_out12), .out13(demultiplexer_1_out13), .out14(demultiplexer_1_out14),
    .out15(demultiplexer_1_out15), .in(DE), .sel(AX), .en(and_1_out));
  Demultiplexer #(.select(4), .disabled(0)) demultiplexer_2 (
    .out0(demultiplexer_2_out0), .out1(demultiplexer_2_out1), .out2(demultiplexer_2_out2),
    .out3(demultiplexer_2_out3), .out4(demultiplexer_2_out4), .out5(demultiplexer_2_out5),
    .out6(demultiplexer_2_out6), .out7(demultiplexer_2_out7), .out8(demultiplexer_2_out8),
    .out9(demultiplexer_2_out9), .out10(demultiplexer_2_out10), .out11(demultiplexer_2_out11),
    .out12(demultiplexer_2_out12), .out13(demultiplexer_2_out13), .out14(demultiplexer_2_out14),
    .out15(demultiplexer_2_out15), .in(H), .sel(AX), .en(and_1_out));
  assign bit_extender_1_out = {{7{storeF}}, storeF};  // Bit_Extender bit_extender_1
  assign not_1_out = ~bit_extender_1_out;  // NOT_Gate not_1, 8 bits wide
  assign and_4_out = EDF & bit_extender_1_out;  // AND_Gate and_4, 8 bits wide
  assign and_5_out = demultiplexer_1_out15 & not_1_out;  // AND_Gate and_5, 8 bits wide
  assign or_1_out = and_5_out | and_4_out;  // OR_Gate or_1, 8 bits wide
  not not_2 (not_2_out, storeF);
  and and_6 (and_6_out, demultiplexer_2_out15, not_2_out);
  and and_7 (and_7_out, storeF, H);
  or or_2 (or_2_out, and_6_out, and_7_out);
  Register register_1 (.D(demultiplexer_1_out0), .en(select), .Q(D0), .clk(demultiplexer_2_out0), .clr(clear));
  Register register_2 (.D(demultiplexer_1_out1), .en(select), .Q(R0_3[15:8]), .clk(demultiplexer_2_out1), .clr(clear));
  Register register_3 (.D(demultiplexer_1_out2), .en(select), .Q(R0_3[23:16]), .clk(demultiplexer_2_out2), .clr(clear));
  Register register_4 (.D(demultiplexer_1_out3), .en(select), .Q(R0_3[31:24]), .clk(demultiplexer_2_out3), .clr(clear));
  Register register_5 (.D(demultiplexer_1_out4), .en(select), .Q(R4_7[7:0]), .clk(demultiplexer_2_out4), .clr(clear));
  Register register_6 (.D(demultiplexer_1_out5), .en(select), .Q(R4_7[15:8]), .clk(demultiplexer_2_out5), .clr(clear));
  Register register_7 (.D(demultiplexer_1_out6), .en(select), .Q(R4_7[23:16]), .clk(demultiplexer_2_out6), .clr(clear));
  Register register_8 (.D(demultiplexer_1_out7), .en(select), .Q(R4_7[31:24]), .clk(demultiplexer_2_out7), .clr(clear));
  Register register_9 (.D(demultiplexer_1_out8), .en(select), .Q(R8_B[7:0]), .clk(demultiplexer_2_out8), .clr(clear));
  Register register_10 (.D(demultiplexer_1_out9), .en(select), .Q(R8_B[15:8]), .clk(demultiplexer_2_out9), .clr(clear));
  Register register_11 (
    .D(demultiplexer_1_out10), .en(select), .Q(R8_B[23:16]), .clk(demultiplexer_2_out10), .clr(clear));
  Register register_12 (
    .D(demultiplexer_1_out11), .en(select), .Q(R8_B[31:24]), .clk(demultiplexer_2_out11), .clr(clear));
  Register register_13 (
    .D(demultiplexer_1_out12), .en(select), .Q(RC_F[7:0]), .clk(demultiplexer_2_out12), .clr(clear));
  Register register_14 (
    .D(demultiplexer_1_out13), .en(select), .Q(RC_F[15:8]), .clk(demultiplexer_2_out13), .clr(clear));
  Register register_15 (
    .D(demultiplexer_1_out14), .en(select), .Q(RC_F[23:16]), .clk(demultiplexer_2_out14), .clr(clear));
  Register register_16 (.D(or_1_out), .en(select), .Q(RC_F[31:24]), .clk(or_2_out), .clr(clear));
  Multiplexer #(.select(4), .width(8), .disabled(0)) multiplexer_1 (
    .in0(D0), .in1(R0_3[15:8]), .in2(R0_3[23:16]), .in3(R0_3[31:24]), .in4(R4_7[7:0]), .in5(R4_7[15:8]),
    .in6(R4_7[23:16]), .in7(R4_7[31:24]), .in8(R8_B[7:0]), .in9(R8_B[15:8]), .in10(R8_B[23:16]),
    .in11(R8_B[31:24]), .in12(RC_F[7:0]), .in13(RC_F[15:8]), .in14(RC_F[23:16]), .in15(RC_F[31:24]),
    .out(DX), .sel(AX), .en(and_2_out));
  Multiplexer #(.select(4), .width(8), .disabled(0)) multiplexer_2 (
    .in0(D0), .in1(R0_3[15:8]), .in2(R0_3[23:16]), .in3(R0_3[31:24]), .in4(R4_7[7:0]), .in5(R4_7[15:8]),
    .in6(R4_7[23:16]), .in7(R4_7[31:24]), .in8(R8_B[7:0]), .in9(R8_B[15:8]), .in10(R8_B[23:16]),
    .in11(R8_B[31:24]), .in12(RC_F[7:0]), .in13(RC_F[15:8]), .in14(RC_F[23:16]), .in15(RC_F[31:24]),
    .out(DY), .sel(AY), .en(and_3_out));

  assign R0_3[7:0] = D0;
endmodule
