// Logisim project 20_C8_aluG.circ as structural Verilog: 11 circuits, main circuit main
module main (
  input  enable,
  input  C,
  input  M
);

  wire alu_g_1_nc, alu_g_1_scstore, alu_g_1_sscp, alu_g_1_svf, and_1_out, citestg_1_end, clock_1_out,
       graf_lsi_1_p5, graf_lsi_1_p10, graf_lsi_1_p11, graf_lsi_1_p12, graf_lsi_1_p13, graf_lsi_1_p14,
       graf_lsi_1_p15, not_1_out, not_2_out;
  wire [3:0] citestg_1_k;
  wire [4:0] alu_g_1_scy;
  wire [5:0] alu_g_1_scx;
  wire [7:0] alu_g_1_df, citestg_1_dr, citestg_1_vx, citestg_1_vy;
  wire [11:0] alu_g_1_ar, citestg_1_i;

  Clock clock_1 (.out(clock_1_out));
  and and_1 (and_1_out, enable, not_1_out, not_2_out);
  citestg citestg_1 (
    .H(not_2_out), .Clear(C), .Enable(and_1_out), .Address(alu_g_1_ar), .VX(citestg_1_vx), .VY(citestg_1_vy),
    .DR(citestg_1_dr), .K(citestg_1_k), .I(citestg_1_i), .\end (citestg_1_end));
  not not_1 (not_1_out, citestg_1_end);
  Counter counter_1 (.load(1'b0), .D({8{1'b0}}), .count(1'b1), .clk(not_2_out), .clr(C));  // open: Q, carry
  not not_2 (not_2_out, alu_g_1_nc);
  // ScreenColor screencolor_1: pin names not known
  Register register_1 (.D(alu_g_1_df), .en(and_1_out), .clk(alu_g_1_svf), .clr(C));  // open: Q
  ALU_G alu_g_1 (
    .VX(citestg_1_vx), .VY(citestg_1_vy), .B1(citestg_1_k), .I(citestg_1_i), .DR(citestg_1_dr),
    .SCP(graf_lsi_1_p5), .enable(and_1_out), .H(clock_1_out), .SCX(alu_g_1_scx), .SCY(alu_g_1_scy),
    .NC(alu_g_1_nc), .AR(alu_g_1_ar), .SCstore(alu_g_1_scstore), .SSCP(alu_g_1_sscp), .SVF(alu_g_1_svf),
    .DF(alu_g_1_df));  // open: C
  // GRAF_lsi graf_lsi_1: pin names not known; wires that end beside it: alu_g_1_scx, alu_g_1_scy, alu_g_1_scstore, alu_g_1_sscp, graf_lsi_1_p5, clock_1_out, C, M, and_1_out, graf_lsi_1_p10, graf_lsi_1_p11, graf_lsi_1_p12, graf_lsi_1_p13, graf_lsi_1_p14, graf_lsi_1_p15, graf_lsi_1_p15, graf_lsi_1_p14, graf_lsi_1_p13, graf_lsi_1_p12, graf_lsi_1_p11, graf_lsi_1_p10
endmodule

module main2 (
  input  [7:0] VX,
  input  [7:0] VY,
  input  [11:0] I,
  input  enable,
  input  C,
  input  M
);

  wire alu_g_1_scstore, alu_g_1_sscp, alu_g_1_svf, clock_1_out, graf_lsi_1_p5, graf_lsi_1_p10,
       graf_lsi_1_p11, graf_lsi_1_p12, graf_lsi_1_p13, graf_lsi_1_p14, graf_lsi_1_p15;
  wire [4:0] alu_g_1_scy;
  wire [5:0] alu_g_1_scx;
  wire [7:0] alu_g_1_df, rom_1_data;
  wire [11:0] alu_g_1_ar;

  Clock clock_1 (.out(clock_1_out));
  // ScreenColor screencolor_1: pin names not known
  ROM #(.addrWidth(12)) rom_1 (.addr(alu_g_1_ar), .data(rom_1_data), .sel(enable));
  ALU_G alu_g_1 (
    .VX(VX), .VY(VY), .B1(4'b1111), .I(I), .DR(rom_1_data), .SCP(graf_lsi_1_p5), .enable(enable),
    .H(clock_1_out), .SCX(alu_g_1_scx), .SCY(alu_g_1_scy), .AR(alu_g_1_ar), .SCstore(alu_g_1_scstore),
    .SSCP(alu_g_1_sscp), .SVF(alu_g_1_svf), .DF(alu_g_1_df));  // open: NC, C
  Register register_1 (.D(alu_g_1_df), .en(enable), .clk(alu_g_1_svf), .clr(C));  // open: Q
  // GRAF_lsi graf_lsi_1: pin names not known; wires that end beside it: alu_g_1_scx, alu_g_1_scy, alu_g_1_scstore, alu_g_1_sscp, graf_lsi_1_p5, clock_1_out, C, M, enable, graf_lsi_1_p10, graf_lsi_1_p11, graf_lsi_1_p12, graf_lsi_1_p13, graf_lsi_1_p14, graf_lsi_1_p15, graf_lsi_1_p15, graf_lsi_1_p14, graf_lsi_1_p13, graf_lsi_1_p12, graf_lsi_1_p11, graf_lsi_1_p10

  // Notes on the sheet:
  //   contents of rom_1 (hex, n*v repeats v):
  //   ff 81 99 9*a5 99 81 ff 0 ff 81 89 99 a9 7*89 bd 81 ff 0 ff 81 99 a5 85 85 89 89 91 91 a1 a1 bd 81 ff
  //   0 ff 81 99 a5 85 85 85 99 85 85 85 a5 99 81 ff 0 ff 81 85 89 89 91 91 a1 a9 a9 bd 89 89 81 ff 0 ff
  //   81 bd 4*a1 b9 85 85 85 a5 99 81 ff 0 ff 81 99 a5 a1 a1 a1 b9 4*a5 99 81 ff 0 ff 81 b9 85 85 89 89 89
  //   91 91 a1 a1 a1 81 ff 0 ff 81 99 4*a5 99 4*a5 99 81 ff 0 ff 81 99 4*a5 9d 85 85 85 a5 99 81 ff
endmodule

module main3 (
  input  [7:0] VX,
  input  [7:0] VY,
  input  [11:0] I,
  input  [7:0] in_4,
  input  [3:0] in_5,
  input  enable,
  input  C,
  input  M
);

  wire alu_g_1_scstore, alu_g_1_sscp, alu_g_1_svf, clock_1_out, graf_lsi_1_p5, graf_lsi_1_p10,
       graf_lsi_1_p11, graf_lsi_1_p12, graf_lsi_1_p13, graf_lsi_1_p14, graf_lsi_1_p15;
  wire [4:0] alu_g_1_scy;
  wire [5:0] alu_g_1_scx;
  wire [7:0] alu_g_1_df;

  Clock clock_1 (.out(clock_1_out));
  // ScreenColor screencolor_1: pin names not known
  ALU_G alu_g_1 (
    .VX(VX), .VY(VY), .B1(in_5), .I(I), .DR(in_4), .SCP(graf_lsi_1_p5), .enable(enable), .H(clock_1_out),
    .SCX(alu_g_1_scx), .SCY(alu_g_1_scy), .SCstore(alu_g_1_scstore), .SSCP(alu_g_1_sscp), .SVF(alu_g_1_svf),
    .DF(alu_g_1_df));  // open: NC, AR, C
  Register register_1 (.D(alu_g_1_df), .en(enable), .clk(alu_g_1_svf), .clr(C));  // open: Q
  // GRAF_lsi graf_lsi_1: pin names not known; wires that end beside it: alu_g_1_scx, alu_g_1_scy, alu_g_1_scstore, alu_g_1_sscp, graf_lsi_1_p5, clock_1_out, C, M, enable, graf_lsi_1_p10, graf_lsi_1_p11, graf_lsi_1_p12, graf_lsi_1_p13, graf_lsi_1_p14, graf_lsi_1_p15, graf_lsi_1_p15, graf_lsi_1_p14, graf_lsi_1_p13, graf_lsi_1_p12, graf_lsi_1_p11, graf_lsi_1_p10
endmodule

module ALU_G (
  input  [7:0] VX,
  input  [7:0] VY,
  input  [3:0] B1,
  input  [11:0] I,
  input  [7:0] DR,
  input  SCP,
  input  enable,
  input  H,
  output [5:0] SCX,
  output [4:0] SCY,
  output NC,
  output [11:0] AR,
  output SCstore,
  output SSCP,
  output C,
  output SVF,
  output [7:0] DF
);

  wire and_1_out, cylpix_1_end, not_1_out, not_2_out;
  wire [1:0] cylpix_1_v1;
  wire [3:0] caljk_1_j, caljk_1_k;

  and and_1 (and_1_out, enable, not_2_out);
  not not_1 (not_1_out, enable);
  CALXY calxy_1 (.VX(VX), .J(caljk_1_j), .VY(VY), .K(caljk_1_k), .SCX(SCX), .SCY(SCY));
  CALJK caljk_1 (
    .enable(enable), .H(H), .clear(not_1_out), .b1(B1), .K(caljk_1_k), .J(caljk_1_j), .\end (NC),
    .E1(cylpix_1_end));
  CALP calp_1 (
    .I(I), .K(caljk_1_k), .DR(DR), .enable(enable), .J(caljk_1_j), .SCP(SCP), .AR(AR), .SCstore(SCstore),
    .SSCP(SSCP), .CF(SVF), .DF(DF), .C(C), .SJ(cylpix_1_v1));
  CYLPIX cylpix_1 (.enable(and_1_out), .clear(not_1_out), .H(H), .V1(cylpix_1_v1), .\end (cylpix_1_end));
  not not_2 (not_2_out, NC);

  // Notes on the sheet:
  //   VX: pull=down
  //   B1: pull=down
  //   enable: pull=down
  //   SCP: pull=down
  //   VY: pull=down
  //   H: pull=down
  //   I: pull=down
  //   DR: pull=down
endmodule

module CALJK (
  input  E1,
  input  enable,
  input  H,
  input  clear,
  input  [3:0] b1,
  output [3:0] K,
  output [3:0] J,
  output \end 
);

  wire and_1_out, and_2_out, and_3_out, and_4_out, and_5_out, and_6_out, comparator_1_lt, comparator_2_eq,
       comparator_2_lt, d_ff_1_q, not_1_out, or_1_out, or_2_out;
  wire [3:0] bit_extender_1_out, bit_extender_2_out, counter_2_q;
  wire [4:0] bit_extender_3_out, bit_extender_4_out, counter_1_q;

  and and_1 (and_1_out, E1, enable);
  and and_2 (and_2_out, enable, comparator_1_lt);
  and and_3 (and_3_out, comparator_1_lt, or_1_out, H);
  and and_4 (and_4_out, comparator_1_lt, d_ff_1_q);
  and and_5 (and_5_out, not_1_out, and_1_out, and_4_out, comparator_2_lt);
  and and_6 (and_6_out, comparator_2_lt, and_4_out, H);
  Counter #(.width(5), .max('h1f)) counter_1 (
    .load(1'b0), .D({5{1'b0}}), .count(and_2_out), .Q(counter_1_q), .clk(and_3_out), .clr(clear));  // open: carry
  or or_1 (or_1_out, clear, comparator_2_eq);
  D_Flip_Flop #(.trigger("falling")) d_ff_1 (
    .clk(H), .D(1'b1), .Q(d_ff_1_q), .preset(1'b0), .en(and_1_out), .reset(or_2_out));  // open: Qn
  or or_2 (or_2_out, clear, comparator_2_eq);
  Counter #(.width(4), .max('hf)) counter_2 (
    .load(1'b0), .D(4'b0000), .count(and_5_out), .Q(counter_2_q), .clk(and_6_out), .clr(or_1_out));  // open: carry
  assign bit_extender_1_out = {{3{comparator_1_lt}}, comparator_1_lt};  // Bit_Extender bit_extender_1
  Bit_Extender #(.in_width(5), .out_width(4)) bit_extender_2 (.in(counter_1_q), .out(bit_extender_2_out));
  assign K = bit_extender_1_out & bit_extender_2_out;  // AND_Gate and_7, 4 bits wide
  assign J = bit_extender_1_out & counter_2_q;  // AND_Gate and_8, 4 bits wide
  Comparator #(.width(5)) comparator_1 (
    .a(counter_1_q), .b(bit_extender_3_out), .eq(\end ), .lt(comparator_1_lt));  // open: gt
  assign bit_extender_3_out = {{1{1'b0}}, b1};  // Bit_Extender bit_extender_3
  not not_1 (not_1_out, \end );
  assign bit_extender_4_out = {{1{1'b0}}, counter_2_q};  // Bit_Extender bit_extender_4
  Comparator #(.width(5)) comparator_2 (
    .a(bit_extender_4_out), .b(5'b01000), .eq(comparator_2_eq), .lt(comparator_2_lt));  // open: gt

  // Notes on the sheet:
  //   E1: pull=down
  //   clear: pull=down
  //   enable: pull=down
  //   b1: pull=down
  //   H: pull=down
endmodule

module CALXY (
  input  [7:0] VX,
  input  [3:0] J,
  input  [7:0] VY,
  input  [3:0] K,
  output [5:0] SCX,
  output [4:0] SCY
);

  wire [7:0] adder_1_out, adder_2_out, bit_extender_1_out, bit_extender_2_out;
  wire [8:0] bit_extender_3_out, bit_extender_4_out, divider_1_rem, divider_2_rem;

  assign bit_extender_1_out = {{4{1'b0}}, J};  // Bit_Extender bit_extender_1
  assign bit_extender_2_out = {{4{1'b0}}, K};  // Bit_Extender bit_extender_2
  Adder adder_1 (.a(VX), .b(bit_extender_1_out), .out(adder_1_out), .cin(1'b0));  // open: cout
  Adder adder_2 (.a(VY), .b(bit_extender_2_out), .out(adder_2_out), .cin(1'b0));  // open: cout
  assign bit_extender_3_out = {{1{1'b0}}, adder_1_out};  // Bit_Extender bit_extender_3
  assign bit_extender_4_out = {{1{1'b0}}, adder_2_out};  // Bit_Extender bit_extender_4
  Divider #(.width(9)) divider_1 (
    .a(bit_extender_3_out), .b(9'h40), .upper({9{1'b0}}), .rem(divider_1_rem));  // open: out
  // Probe on 9'h40
  Divider #(.width(9)) divider_2 (
    .a(bit_extender_4_out), .b(9'h20), .upper({9{1'b0}}), .rem(divider_2_rem));  // open: out
  // Probe on 9'h20
  Bit_Extender #(.in_width(9), .out_width(6)) bit_extender_5 (.in(divider_1_rem), .out(SCX));
  Bit_Extender #(.in_width(9), .out_width(5)) bit_extender_6 (.in(divider_2_rem), .out(SCY));

  // Notes on the sheet:
  //   VX: pull=down
  //   J: pull=down
  //   K: pull=down
  //   VY: pull=down
endmodule

module CALP (
  input  [11:0] I,
  input  [3:0] K,
  input  [7:0] DR,
  input  enable,
  input  [3:0] J,
  input  [1:0] SJ,
  input  SCP,
  output [11:0] AR,
  output SCstore,
  output SSCP,
  output C,
  output CF,
  output [7:0] DF
);

  wire adder_2_cout, adder_2_out, and_1_out, and_2_out, and_5_out, d_ff_1_qn, not_1_out, recpix_1_out_4,
       recpix_1_out_5;
  wire [11:0] bit_extender_1_out;

  and and_1 (and_1_out, enable, recpix_1_out_4);
  RECPIX recpix_1 (.SJ(SJ), .Enable(enable), .out_5(recpix_1_out_5), .out_4(recpix_1_out_4), .SCP(SCP));
  assign bit_extender_1_out = {{8{1'b0}}, K};  // Bit_Extender bit_extender_1
  not not_1 (not_1_out, enable);
  Adder #(.width(12)) adder_1 (.a(I), .b(bit_extender_1_out), .out(AR), .cin(1'b0));  // open: cout
  INIMRP inimrp_1 (.DR(DR), .enable(and_1_out), .J(J), .S(SCstore));
  Adder #(.width(1)) adder_2 (.a(SCstore), .b(recpix_1_out_5), .out(adder_2_out), .cin(1'b0), .cout(adder_2_cout));
  and and_2 (and_2_out, C, d_ff_1_qn);
  D_Flip_Flop d_ff_1 (
    .clk(and_2_out), .D(d_ff_1_qn), .Q(CF), .Qn(d_ff_1_qn), .preset(1'b0), .en(enable), .reset(not_1_out));
  and and_3 (SSCP, SCstore, adder_2_out);
  and and_4 (C, SCstore, adder_2_cout);
  and and_5 (and_5_out, CF, enable);
  assign DF = {{7{1'b0}}, and_5_out};  // Bit_Extender bit_extender_2

  // Notes on the sheet:
  //   enable: pull=down
  //   K: pull=down
  //   SJ: pull=down
  //   DR: pull=down
  //   I: pull=down
  //   J: pull=down
  //   SCP: pull=down
endmodule

module RECPIX (
  input  [1:0] SJ,
  input  Enable,
  input  SCP,
  output out_4,
  output out_5
);

  wire and_2_out, and_3_out, and_4_out, and_5_out, not_1_out, not_2_out, not_3_out, not_4_out, or_1_out;
  wire [1:0] and_1_out, bit_extender_1_out;

  assign and_1_out = SJ & bit_extender_1_out;  // AND_Gate and_1, 2 bits wide
  assign bit_extender_1_out = {{1{Enable}}, Enable};  // Bit_Extender bit_extender_1
  not not_1 (not_1_out, and_1_out[1]);
  not not_2 (not_2_out, and_1_out[0]);
  not not_3 (not_3_out, Enable);
  and and_2 (and_2_out, and_1_out[0], not_1_out);
  or or_1 (or_1_out, and_2_out, not_3_out);
  and and_3 (and_3_out, not_2_out, and_1_out[1]);
  and and_4 (and_4_out, and_1_out[0], and_1_out[1]);
  not not_4 (not_4_out, or_1_out);
  or or_2 (out_4, and_4_out, and_5_out);
  and and_5 (and_5_out, not_4_out, out_4);
  D_Flip_Flop d_ff_1 (.clk(and_3_out), .D(SCP), .Q(out_5), .preset(1'b0), .en(Enable), .reset(or_1_out));  // open: Qn

  // Notes on the sheet:
  //   SJ: pull=down
  //   Enable: pull=down
  //   SCP: pull=down
endmodule

module CYLPIX (
  input  enable,
  input  clear,
  input  H,
  output [1:0] V1,
  output \end 
);

  wire and_1_out, or_1_out;
  wire [1:0] and_3_out, and_4_out, bit_extender_1_out, not_1_out;
  wire [3:0] counter_1_q;

  or or_1 (or_1_out, clear, and_1_out);
  Counter #(.width(4), .max('hf)) counter_1 (
    .load(1'b0), .D(4'b0000), .count(enable), .Q(counter_1_q), .clk(H), .clr(or_1_out));  // open: carry
  and and_1 (and_1_out, counter_1_q[1], counter_1_q[2]);
  assign bit_extender_1_out = {{1{counter_1_q[2]}}, counter_1_q[2]};  // Bit_Extender bit_extender_1
  assign not_1_out = ~bit_extender_1_out;  // NOT_Gate not_1, 2 bits wide
  and and_2 (\end , counter_1_q[2], counter_1_q[0]);
  assign and_3_out = 2'b01 & bit_extender_1_out;  // AND_Gate and_3, 2 bits wide
  assign V1 = and_3_out | and_4_out;  // OR_Gate or_2, 2 bits wide
  assign and_4_out = not_1_out & counter_1_q[1:0];  // AND_Gate and_4, 2 bits wide
endmodule

module INIMRP (
  input  [7:0] DR,
  input  enable,
  input  [3:0] J,
  output S
);

  wire and_1_out, and_2_out, and_3_out, and_4_out, and_5_out, and_6_out, and_7_out, and_8_out,
       decoder_1_out0, decoder_1_out1, decoder_1_out2, decoder_1_out3, decoder_1_out4, decoder_1_out5,
       decoder_1_out6, decoder_1_out7;
  wire [2:0] bit_extender_1_out;

  Decoder #(.select(3)) decoder_1 (
    .out0(decoder_1_out0), .out1(decoder_1_out1), .out2(decoder_1_out2), .out3(decoder_1_out3),
    .out4(decoder_1_out4), .out5(decoder_1_out5), .out6(decoder_1_out6), .out7(decoder_1_out7),
    .sel(bit_extender_1_out), .en(enable));
  Pull_Resistor pull_resistor_1 (.node(decoder_1_out1));
  Pull_Resistor pull_resistor_2 (.node(decoder_1_out2));
  Pull_Resistor pull_resistor_3 (.node(decoder_1_out0));
  Pull_Resistor pull_resistor_4 (.node(decoder_1_out3));
  Bit_Extender #(.in_width(4), .out_width(3)) bit_extender_1 (.in(J), .out(bit_extender_1_out));
  Pull_Resistor pull_resistor_5 (.node(decoder_1_out6));
  Pull_Resistor pull_resistor_6 (.node(decoder_1_out4));
  Pull_Resistor pull_resistor_7 (.node(decoder_1_out5));
  Pull_Resistor pull_resistor_8 (.node(decoder_1_out7));
  and and_1 (and_1_out, DR[0], decoder_1_out7);
  and and_2 (and_2_out, DR[1], decoder_1_out6);
  and and_3 (and_3_out, DR[2], decoder_1_out5);
  and and_4 (and_4_out, DR[3], decoder_1_out4);
  and and_5 (and_5_out, DR[4], decoder_1_out3);
  and and_6 (and_6_out, DR[5], decoder_1_out2);
  and and_7 (and_7_out, DR[6], decoder_1_out1);
  and and_8 (and_8_out, DR[7], decoder_1_out0);
  or or_1 (S, and_1_out, and_2_out, and_3_out, and_4_out, and_5_out, and_6_out, and_7_out, and_8_out);

  // Notes on the sheet:
  //   J: pull=down
  //   enable: pull=down
  //   DR: pull=down
endmodule

module citestg (
  input  H,
  input  Clear,
  input  Enable,
  input  [11:0] Address,
  output \end ,
  output [7:0] VX,
  output [7:0] VY,
  output [7:0] DR,
  output [3:0] K,
  output [11:0] I
);

  wire and_1_out, and_2_out, or_1_out, or_2_out, or_3_out;
  wire [1:0] counter_2_q;
  wire [3:0] and_3_out, and_4_out, bit_extender_1_out, counter_1_q, counter_3_q, not_1_out;

  or or_1 (or_1_out, counter_1_q[3], Clear);
  Counter #(.width(4), .max('hf)) counter_1 (
    .load(1'b0), .D(4'b0000), .count(1'b1), .Q(counter_1_q), .clk(H), .clr(or_1_out));  // open: carry
  Counter #(.width(2), .max('h3)) counter_2 (
    .load(1'b0), .D(2'b00), .count(1'b1), .Q(counter_2_q), .clk(or_1_out), .clr(or_2_out));  // open: carry
  or or_2 (or_2_out, and_2_out, Clear);
  Counter #(.width(4), .max('hf)) counter_3 (
    .load(1'b0), .D(4'b0000), .count(1'b1), .Q(counter_3_q), .clk(H), .clr(or_3_out));  // open: carry
  and and_1 (and_1_out, counter_3_q[1], counter_3_q[3]);
  or or_3 (or_3_out, and_1_out, Clear);
  and and_2 (and_2_out, counter_2_q[0], counter_2_q[1]);
  ROM #(.addrWidth(4)) rom_1 (.addr(counter_1_q), .data(VX), .sel(Enable));
  ROM #(.addrWidth(2)) rom_2 (.addr(counter_2_q), .data(VY), .sel(Enable));
  ROM #(.addrWidth(12)) rom_3 (.addr(Address), .data(DR), .sel(Enable));
  ROM #(.addrWidth(4), .dataWidth(12)) rom_4 (.addr(counter_3_q), .data(I), .sel(Enable));
  D_Flip_Flop d_ff_1 (.clk(and_2_out), .D(1'b1), .Q(\end ), .preset(1'b0), .en(Enable), .reset(Clear));  // open: Qn
  assign bit_extender_1_out = {{3{counter_2_q[1]}}, counter_2_q[1]};  // Bit_Extender bit_extender_1
  assign and_3_out = 4'b0010 & bit_extender_1_out;  // AND_Gate and_3, 4 bits wide
  assign and_4_out = 4'b1111 & not_1_out;  // AND_Gate and_4, 4 bits wide
  assign not_1_out = ~bit_extender_1_out;  // NOT_Gate not_1, 4 bits wide
  assign K = and_3_out | and_4_out;  // OR_Gate or_4, 4 bits wide

  // Notes on the sheet:
  //   contents of rom_1 (hex, n*v repeats v):
  //   0 8 10 18 20 28 30 38
  //   contents of rom_2 (hex, n*v repeats v):
  //   0 f 1e
  //   contents of rom_3 (hex, n*v repeats v):
  //   ff 81 99 9*a5 99 81 ff 0 ff 81 89 99 a9 7*89 bd 81 ff 0 ff 81 99 a5 85 85 89 89 91 91 a1 a1 bd 81 ff
  //   0 ff 81 99 a5 85 85 85 99 85 85 85 a5 99 81 ff 0 ff 81 85 89 89 91 91 a1 a9 a9 bd 89 89 81 ff 0 ff
  //   81 bd 4*a1 b9 85 85 85 a5 99 81 ff 0 ff 81 99 a5 a1 a1 a1 b9 4*a5 99 81 ff 0 ff 81 b9 85 85 89 89 89
  //   91 91 a1 a1 a1 81 ff 0 ff 81 99 4*a5 99 4*a5 99 81 ff 0 ff 81 99 4*a5 9d 85 85 85 a5 99 81 ff
  //   contents of rom_4 (hex, n*v repeats v):
  //   0 10 20 30 40 50 60 70 80 90
endmodule
