// Logisim project 21_C8_aluOt.circ as structural Verilog: 3 circuits, main circuit SAVD
module main (
  input  in_1,
  input  in_2,
  input  in_3,
  input  in_4,
  input  in_5,
  input  [3:0] in_6,
  input  in_7
);

  wire cpm_1_end, savd_1_s;
  wire [7:0] cpm_1_t0;

  SAVD savd_1 (.H(in_1), .T(in_2), .clear(in_3), .S(savd_1_s));
  CPM cpm_1 (
    .enable(in_4), .H(in_5), .NC(in_6), .EC(in_7), .T0(cpm_1_t0[0]), .T1(cpm_1_t0[1]), .T2(cpm_1_t0[2]),
    .T3(cpm_1_t0[3]), .T4(cpm_1_t0[4]), .T5(cpm_1_t0[5]), .T6(cpm_1_t0[6]), .T7(cpm_1_t0[7]),
    .\end (cpm_1_end));
  // Probe on savd_1_s
  // Probe on cpm_1_t0
  // Probe on cpm_1_end
endmodule

module SAVD (
  input  H,
  input  T,
  input  clear,
  output S
);

  wire d_ff_1_q, d_ff_1_qn, d_ff_2_q, d_ff_2_qn, or_1_out;

  D_Flip_Flop #(.trigger("falling")) d_ff_1 (
    .clk(H), .D(d_ff_1_qn), .Q(d_ff_1_q), .Qn(d_ff_1_qn), .preset(1'b0), .en(T), .reset(or_1_out));
  D_Flip_Flop d_ff_2 (.clk(H), .D(d_ff_2_qn), .Q(d_ff_2_q), .Qn(d_ff_2_qn), .preset(1'b0), .en(T), .reset(clear));
  or or_1 (or_1_out, d_ff_2_q, clear);
  and and_1 (S, d_ff_1_q, T);
endmodule

module CPM (
  input  enable,
  input  H,
  input  [3:0] NC,
  input  EC,
  output T0,
  output T1,
  output T2,
  output T3,
  output T4,
  output T5,
  output T6,
  output T7,
  output \end 
);

  wire and_1_out, and_2_out, and_3_out, comparator_1_eq, comparator_2_gt, comparator_2_lt, not_1_out,
       not_2_out, or_1_out;
  wire [3:0] counter_1_q;

  not not_1 (not_1_out, enable);
  and and_1 (and_1_out, H, and_3_out);
  and and_2 (and_2_out, enable, and_3_out);
  and and_3 (and_3_out, not_2_out, EC);
  Counter #(.width(4), .max('hf)) counter_1 (
    .load(1'b0), .D(4'b0000), .count(and_2_out), .Q(counter_1_q), .clk(and_1_out), .clr(not_1_out));  // open: carry
  Decoder #(.select(3), .disabled(0)) decoder_1 (
    .out0(T0), .out1(T1), .out2(T2), .out3(T3), .out4(T4), .out5(T5), .out6(T6), .out7(T7),
    .sel(counter_1_q[2:0]), .en(enable));
  Comparator #(.width(4)) comparator_1 (.a(counter_1_q), .b(NC), .eq(comparator_1_eq));  // open: gt, lt
  not not_2 (not_2_out, comparator_1_eq);
  or or_1 (or_1_out, comparator_2_gt, comparator_2_lt);
  Comparator #(.width(4)) comparator_2 (
    .a(counter_1_q), .b(4'b0000), .gt(comparator_2_gt), .lt(comparator_2_lt));  // open: eq
  and and_4 (\end , comparator_1_eq, or_1_out, enable);
endmodule
