// Logisim project 21_C8_aluS.circ as structural Verilog: 5 circuits, main circuit ALU_S
module main (
  input  clear,
  input  [7:0] in_2,
  input  H,
  input  E,
  output out_5
);

  wire alu_s_1_end, alu_s_1_select, and_1_out, and_2_out, d_ff_1_q, d_ff_1_qn, not_1_out, or_1_out;
  wire [1:0] counter_1_q;
  wire [15:0] alu_s_1_output, register_1_q;

  and and_1 (and_1_out, alu_s_1_end, not_1_out, E, H);
  ALU_S alu_s_1 (
    .VX(in_2), .T1(counter_1_q[0]), .Input(register_1_q), .T2(counter_1_q[1]), .H(H),
    .Output(alu_s_1_output), .select(alu_s_1_select), .sound(out_5), .END(alu_s_1_end));
  Counter #(.width(2), .max('h3)) counter_1 (
    .load(1'b0), .D(2'b00), .count(1'b1), .Q(counter_1_q), .clk(and_1_out), .clr(or_1_out));  // open: carry
  or or_1 (or_1_out, clear, and_2_out);
  not not_1 (not_1_out, d_ff_1_q);
  Register #(.width(16)) register_1 (.D(alu_s_1_output), .en(alu_s_1_select), .Q(register_1_q), .clk(H), .clr(clear));
  and and_2 (and_2_out, counter_1_q[1], counter_1_q[0]);
  D_Flip_Flop d_ff_1 (
    .clk(and_2_out), .D(d_ff_1_qn), .Q(d_ff_1_q), .Qn(d_ff_1_qn), .preset(1'b0), .en(E), .reset(clear));
endmodule

module ALU_S (
  input  [7:0] VX,
  input  T1,
  input  [15:0] Input,
  input  T2,
  input  H,
  output [15:0] Output,
  output select,
  output sound,
  output END
);

  wire sound_1_select;
  wire [15:0] sound_1_output;

  CMPVS cmpvs_1 (.VX(VX), .Input(sound_1_output), .newValue(T1), .SCMPSON(sound_1_select), .Output(Output));
  Sound sound_1 (
    .Input(Input), .enable(T2), .H(H), .Output(sound_1_output), .sound(sound), .select(sound_1_select),
    .END(END));
  or or_1 (select, T1, sound_1_select);
endmodule

module CMPVS (
  input  [7:0] VX,
  input  [15:0] Input,
  input  newValue,
  input  SCMPSON,
  output [15:0] Output
);

  wire [15:0] and_1_out, and_2_out, bit_extender_1_out, bit_extender_2_out, bit_extender_3_out,
       multiplier_1_out;

  assign bit_extender_1_out = {{8{1'b0}}, VX};  // Bit_Extender bit_extender_1
  Multiplier #(.width(16)) multiplier_1 (
    .a(bit_extender_1_out), .b(16'h20), .out(multiplier_1_out), .cin({16{1'b0}}));  // open: cout
  assign bit_extender_2_out = {{15{newValue}}, newValue};  // Bit_Extender bit_extender_2
  assign bit_extender_3_out = {{15{SCMPSON}}, SCMPSON};  // Bit_Extender bit_extender_3
  assign and_1_out = multiplier_1_out & bit_extender_2_out;  // AND_Gate and_1, 16 bits wide
  assign and_2_out = Input & bit_extender_3_out;  // AND_Gate and_2, 16 bits wide
  assign Output = and_1_out | and_2_out;  // OR_Gate or_1, 16 bits wide
endmodule

module Sound (
  input  [15:0] Input,
  input  enable,
  input  H,
  output [15:0] Output,
  output sound,
  output END,
  output select
);

  wire tmp_s_1_output;

  Comparator #(.width(16)) comparator_1 (.a(Input), .b({16{1'b0}}), .gt(sound), .eq(END));  // open: lt
  TMP_S tmp_s_1 (.enable(enable), .H(H), .Output(tmp_s_1_output));
  Subtractor #(.width(16)) subtractor_1 (.a(Input), .b(16'h1), .out(Output), .bin(1'b0));  // open: bout
  and and_1 (select, sound, tmp_s_1_output);
endmodule

module TMP_S (
  input  enable,
  input  H,
  output Output
);

  wire and_1_out, comparator_1_eq, comparator_1_lt, not_1_out;
  wire [15:0] counter_1_q;

  Counter #(.width(16), .max('hffff)) counter_1 (
    .load(1'b0), .D({16{1'b0}}), .count(enable), .Q(counter_1_q), .clk(and_1_out), .clr(not_1_out));  // open: carry
  not not_1 (not_1_out, enable);
  and and_1 (and_1_out, H, comparator_1_lt);
  Comparator #(.width(16)) comparator_1 (
    .a(counter_1_q), .b({16{1'b0}}), .eq(comparator_1_eq), .lt(comparator_1_lt));  // open: gt
  and and_2 (Output, enable, comparator_1_eq);
endmodule
