// Logisim project 25_C8_alu2.circ as structural Verilog: 11 circuits, main circuit main
module main (
  input  [3:0] in_1,
  input  [3:0] in_2,
  input  [7:0] in_3,
  input  [7:0] in_4,
  input  in_5,
  input  in_6,
  input  in_7,
  output [3:0] out_8,
  output [3:0] out_9,
  output [3:0] out_10,
  output [3:0] out_11,
  output [7:0] out_12,
  output [7:0] out_13,
  output out_14,
  output out_15,
  output [3:0] out_16,
  output [3:0] out_17,
  output [7:0] out_18,
  output out_19
);

  wire cpm_1_p5, cpm_2_p5, cpm_3_p5, n8xy1_1_ec, n8xy1_1_svx, n8xy2_1_ec, n8xy2_1_svx, n8xy3_1_ec,
       n8xy3_1_svx;
  wire [3:0] n8xy1_1_nc, n8xy2_1_nc, n8xy3_1_nc;
  wire [7:0] register_1_q, register_2_q, register_3_q;

  _8XY1 u_8xy1_1 (
    .Y(in_1), .X(in_2), .VY(in_3), .VX(in_4), .T1(cpm_1_p5), .enable(in_5), .AY(out_8), .AX(out_10),
    .VX_2(out_12), .SVX(n8xy1_1_svx), .EC(n8xy1_1_ec), .NC(n8xy1_1_nc), .H(in_6));
  // CPM cpm_1: pin names not known; wires that end beside it: in_5, in_6, n8xy1_1_nc, n8xy1_1_ec, cpm_1_p5, out_14
  _8XY3 u_8xy3_1 (
    .Y(in_1), .X(in_2), .VY(in_3), .VX(in_4), .T1(cpm_2_p5), .enable(in_5), .AY(out_16), .AX(out_17),
    .VX_2(out_18), .SVX(n8xy3_1_svx), .EC(n8xy3_1_ec), .NC(n8xy3_1_nc), .H(in_6));
  // CPM cpm_2: pin names not known; wires that end beside it: in_5, in_6, n8xy3_1_nc, n8xy3_1_ec, cpm_2_p5, out_19
  Register register_1 (.D(out_12), .en(in_5), .Q(register_1_q), .clk(n8xy1_1_svx), .clr(in_7));
  // Probe on register_1_q
  Register register_2 (.D(out_18), .en(in_5), .Q(register_2_q), .clk(n8xy3_1_svx), .clr(in_7));
  // Probe on register_2_q
  _8XY2 u_8xy2_1 (
    .Y(in_1), .X(in_2), .VY(in_3), .VX(in_4), .T1(cpm_3_p5), .enable(in_5), .AY(out_9), .AX(out_11),
    .VX_2(out_13), .SVX(n8xy2_1_svx), .EC(n8xy2_1_ec), .NC(n8xy2_1_nc), .H(in_6));
  // CPM cpm_3: pin names not known; wires that end beside it: in_5, in_6, n8xy2_1_nc, n8xy2_1_ec, cpm_3_p5, out_15
  Register register_3 (.D(out_13), .en(in_5), .Q(register_3_q), .clk(n8xy2_1_svx), .clr(in_7));
  // Probe on register_3_q

  // Other names for the same wires on the sheet: C = in_7; E = in_5; H = in_6; VX[7:0] = in_3; VY[7:0] = in_4;
  //   X[3:0] = in_2; Y[3:0] = in_1

  // Notes on the sheet:
  //   OR
  //   XOR
  //   AND
endmodule

module ALU2 (
  input  [3:0] X,
  input  [7:0] VX,
  input  [3:0] Y,
  input  [7:0] VY,
  input  _8X06,
  input  _8X0E,
  input  _8XY0,
  input  _8XY1,
  input  _8XY2,
  input  _8XY3,
  input  _8XY4,
  input  _8XY5,
  input  _8XY7,
  input  T1,
  input  H,
  output [3:0] AY,
  output [7:0] VF,
  output SVF,
  output [3:0] AX,
  output [7:0] VX_2,
  output SVX,
  output EC,
  output [3:0] NC
);

  wire n8x0e_1_ec, n8x0e_1_svf, n8x0e_1_svx, n8x06_1_ec, n8x06_1_svf, n8x06_1_svx, n8xy0_1_ec, n8xy0_1_svx,
       n8xy1_1_ec, n8xy1_1_svx, n8xy2_1_ec, n8xy2_1_svx, n8xy3_1_ec, n8xy3_1_svx, n8xy4_1_ec, n8xy4_1_svf,
       n8xy4_1_svx, n8xy5_1_ec, n8xy5_1_svf, n8xy5_1_svx, n8xy7_1_ec, n8xy7_1_svf, n8xy7_1_svx;
  wire [3:0] n8x0e_1_ax, n8x0e_1_nc, n8x06_1_ax, n8x06_1_nc, n8xy0_1_ax, n8xy0_1_ay, n8xy0_1_nc, n8xy1_1_ax,
       n8xy1_1_ay, n8xy1_1_nc, n8xy2_1_ax, n8xy2_1_ay, n8xy2_1_nc, n8xy3_1_ax, n8xy3_1_ay, n8xy3_1_nc,
       n8xy4_1_ax, n8xy4_1_ay, n8xy4_1_nc, n8xy5_1_ax, n8xy5_1_ay, n8xy5_1_nc, n8xy7_1_ax, n8xy7_1_ay,
       n8xy7_1_nc;
  wire [7:0] n8x0e_1_vf, n8x0e_1_vx_2, n8x06_1_vf, n8x06_1_vx_2, n8xy0_1_vx, n8xy1_1_vx_2, n8xy2_1_vx_2,
       n8xy3_1_vx_2, n8xy4_1_vf, n8xy4_1_vx_2, n8xy5_1_vf, n8xy5_1_vx_2, n8xy7_1_vf, n8xy7_1_vx_2;

  _8X06 u_8x06_1 (
    .X(X), .VX(VX), .T1(T1), .enable(_8X06), .AX(n8x06_1_ax), .VF(n8x06_1_vf), .SVF(n8x06_1_svf),
    .VX_2(n8x06_1_vx_2), .SVX(n8x06_1_svx), .EC(n8x06_1_ec), .NC(n8x06_1_nc), .H(H));
  _8X0E u_8x0e_1 (
    .X(X), .VX(VX), .T1(T1), .enable(_8X0E), .AX(n8x0e_1_ax), .VF(n8x0e_1_vf), .SVF(n8x0e_1_svf),
    .VX_2(n8x0e_1_vx_2), .SVX(n8x0e_1_svx), .EC(n8x0e_1_ec), .NC(n8x0e_1_nc), .H(H));
  _8XY0 u_8xy0_1 (
    .Y(Y), .X(X), .VY(VY), .T1(T1), .enable(_8XY0), .AY(n8xy0_1_ay), .AX(n8xy0_1_ax), .VX(n8xy0_1_vx),
    .SVX(n8xy0_1_svx), .EC(n8xy0_1_ec), .NC(n8xy0_1_nc), .H(H));
  _8XY1 u_8xy1_1 (
    .Y(Y), .X(X), .VY(VY), .VX(VX), .T1(T1), .enable(_8XY1), .AY(n8xy1_1_ay), .AX(n8xy1_1_ax),
    .VX_2(n8xy1_1_vx_2), .SVX(n8xy1_1_svx), .EC(n8xy1_1_ec), .NC(n8xy1_1_nc), .H(H));
  _8XY2 u_8xy2_1 (
    .Y(Y), .X(X), .VY(VY), .VX(VX), .T1(T1), .enable(_8XY2), .AY(n8xy2_1_ay), .AX(n8xy2_1_ax),
    .VX_2(n8xy2_1_vx_2), .SVX(n8xy2_1_svx), .EC(n8xy2_1_ec), .NC(n8xy2_1_nc), .H(H));
  _8XY3 u_8xy3_1 (
    .Y(Y), .X(X), .VY(VY), .VX(VX), .T1(T1), .enable(_8XY3), .AY(n8xy3_1_ay), .AX(n8xy3_1_ax),
    .VX_2(n8xy3_1_vx_2), .SVX(n8xy3_1_svx), .EC(n8xy3_1_ec), .NC(n8xy3_1_nc), .H(H));
  _8XY4 u_8xy4_1 (
    .Y(Y), .X(X), .VY(VY), .VX(VX), .T1(T1), .enable(_8XY4), .AY(n8xy4_1_ay), .AX(n8xy4_1_ax),
    .VF(n8xy4_1_vf), .SVF(n8xy4_1_svf), .VX_2(n8xy4_1_vx_2), .SVX(n8xy4_1_svx), .EC(n8xy4_1_ec),
    .NC(n8xy4_1_nc), .H(H));
  _8XY5 u_8xy5_1 (
    .Y(Y), .X(X), .VY(VY), .VX(VX), .T1(T1), .enable(_8XY5), .AY(n8xy5_1_ay), .AX(n8xy5_1_ax),
    .VF(n8xy5_1_vf), .SVF(n8xy5_1_svf), .VX_2(n8xy5_1_vx_2), .SVX(n8xy5_1_svx), .EC(n8xy5_1_ec),
    .NC(n8xy5_1_nc), .H(H));
  _8XY7 u_8xy7_1 (
    .Y(Y), .X(X), .VY(VY), .VX(VX), .T1(T1), .enable(_8XY7), .AY(n8xy7_1_ay), .AX(n8xy7_1_ax),
    .VF(n8xy7_1_vf), .SVF(n8xy7_1_svf), .VX_2(n8xy7_1_vx_2), .SVX(n8xy7_1_svx), .EC(n8xy7_1_ec),
    .NC(n8xy7_1_nc), .H(H));
  assign AY = n8xy0_1_ay | n8xy1_1_ay | n8xy2_1_ay | n8xy3_1_ay | n8xy4_1_ay | n8xy5_1_ay | n8xy7_1_ay;  // OR_Gate or_1, 4 bits wide
  assign VF = n8x06_1_vf | n8x0e_1_vf | n8xy4_1_vf | n8xy5_1_vf | n8xy7_1_vf;  // OR_Gate or_2, 8 bits wide
  or or_3 (SVF, n8x06_1_svf, n8x0e_1_svf, n8xy4_1_svf, n8xy5_1_svf, n8xy7_1_svf);
  assign AX = n8x06_1_ax | n8x0e_1_ax | n8xy0_1_ax | n8xy1_1_ax | n8xy2_1_ax | n8xy3_1_ax | n8xy4_1_ax | n8xy5_1_ax | n8xy7_1_ax;  // OR_Gate or_4, 4 bits wide
  assign VX_2 = n8x06_1_vx_2 | n8x0e_1_vx_2 | n8xy0_1_vx | n8xy1_1_vx_2 | n8xy2_1_vx_2 | n8xy3_1_vx_2 | n8xy4_1_vx_2 | n8xy5_1_vx_2 | n8xy7_1_vx_2;  // OR_Gate or_5, 8 bits wide
  or or_6 (SVX, n8x06_1_svx, n8x0e_1_svx, n8xy0_1_svx, n8xy1_1_svx, n8xy2_1_svx, n8xy3_1_svx, n8xy4_1_svx, n8xy5_1_svx, n8xy7_1_svx);
  or or_7 (EC, n8x06_1_ec, n8x0e_1_ec, n8xy0_1_ec, n8xy1_1_ec, n8xy2_1_ec, n8xy3_1_ec, n8xy4_1_ec, n8xy5_1_ec, n8xy7_1_ec);
  assign NC = n8x06_1_nc | n8x0e_1_nc | n8xy0_1_nc | n8xy1_1_nc | n8xy2_1_nc | n8xy3_1_nc | n8xy4_1_nc | n8xy5_1_nc | n8xy7_1_nc;  // OR_Gate or_8, 4 bits wide
endmodule

module _8X06 (
  input  [3:0] X,
  input  [7:0] VX,
  input  H,
  input  T1,
  input  enable,
  output [3:0] AX,
  output [7:0] VF,
  output SVF,
  output [7:0] VX_2,
  output SVX,
  output EC,
  output [3:0] NC
);

  wire and_1_out, bit_extender_1_out, not_1_out, savd_2_p5;
  wire [3:0] bit_extender_4_out, bit_extender_5_out;
  wire [7:0] bit_extender_2_out, bit_extender_3_out, shifter_1_out;

  Bit_Extender #(.out_width(1)) bit_extender_1 (.in(VX), .out(bit_extender_1_out));
  Shifter #(.shift("lr")) shifter_1 (.in(VX), .\dist (3'b001), .out(shifter_1_out));
  and and_1 (and_1_out, T1, enable);
  assign bit_extender_2_out = {{7{1'b0}}, bit_extender_1_out};  // Bit_Extender bit_extender_2
  not not_1 (not_1_out, enable);
  assign bit_extender_3_out = {{7{and_1_out}}, and_1_out};  // Bit_Extender bit_extender_3
  assign bit_extender_4_out = {{3{enable}}, enable};  // Bit_Extender bit_extender_4
  assign VF = bit_extender_2_out & bit_extender_3_out;  // AND_Gate and_2, 8 bits wide
  assign VX_2 = shifter_1_out & bit_extender_3_out;  // AND_Gate and_3, 8 bits wide
  and and_4 (EC, 1'b1, enable);
  assign NC = 4'b0011 & bit_extender_4_out;  // AND_Gate and_5, 4 bits wide
  assign bit_extender_5_out = {{3{enable}}, enable};  // Bit_Extender bit_extender_5
  // SAVD savd_1: pin names not known; wires that end beside it: H, and_1_out, not_1_out, SVF
  // SAVD savd_2: pin names not known; wires that end beside it: H, and_1_out, not_1_out, SVX, savd_2_p5
  assign AX = X & bit_extender_5_out;  // AND_Gate and_6, 4 bits wide

  // Notes on the sheet:
  //   8xy6 - [  Vx>>=1             ] - SHR Vx {, Vy}
  //   Stores the least significant bit of VX in VF and then shifts VX to the right by 1.
endmodule

module _8X0E (
  input  [3:0] X,
  input  [7:0] VX,
  input  H,
  input  T1,
  input  enable,
  output [3:0] AX,
  output [7:0] VF,
  output SVF,
  output [7:0] VX_2,
  output SVX,
  output EC,
  output [3:0] NC
);

  wire and_1_out, not_1_out, savd_2_p5;
  wire [3:0] bit_extender_3_out, bit_extender_4_out;
  wire [7:0] bit_extender_1_out, bit_extender_2_out, shifter_1_out;

  Shifter shifter_1 (.in(VX), .\dist (3'b001), .out(shifter_1_out));
  and and_1 (and_1_out, T1, enable);
  assign bit_extender_1_out = {{7{1'b0}}, VX[7]};  // Bit_Extender bit_extender_1
  not not_1 (not_1_out, enable);
  assign VF = bit_extender_1_out & bit_extender_2_out;  // AND_Gate and_2, 8 bits wide
  assign VX_2 = shifter_1_out & bit_extender_2_out;  // AND_Gate and_3, 8 bits wide
  assign bit_extender_2_out = {{7{and_1_out}}, and_1_out};  // Bit_Extender bit_extender_2
  assign bit_extender_3_out = {{3{enable}}, enable};  // Bit_Extender bit_extender_3
  and and_4 (EC, 1'b1, enable);
  assign NC = 4'b0011 & bit_extender_3_out;  // AND_Gate and_5, 4 bits wide
  assign AX = X & bit_extender_4_out;  // AND_Gate and_6, 4 bits wide
  assign bit_extender_4_out = {{3{enable}}, enable};  // Bit_Extender bit_extender_4
  // SAVD savd_1: pin names not known; wires that end beside it: H, and_1_out, not_1_out, SVF
  // SAVD savd_2: pin names not known; wires that end beside it: H, and_1_out, not_1_out, SVX, savd_2_p5

  // Notes on the sheet:
  //   8xyE - [  Vx<<=1             ] - SHL Vx {, Vy}
  //   Stores the most significant bit of VX in VF and then shifts VX to the left by 1.
endmodule

module _8XY0 (
  input  [3:0] Y,
  input  [3:0] X,
  input  [7:0] VY,
  input  H,
  input  T1,
  input  enable,
  output [3:0] AY,
  output [3:0] AX,
  output [7:0] VX,
  output SVX,
  output EC,
  output [3:0] NC
);

  wire and_2_out, not_1_out, savd_1_p5;
  wire [3:0] bit_extender_2_out, bit_extender_3_out, bit_extender_4_out;
  wire [7:0] bit_extender_1_out;

  assign bit_extender_1_out = {{7{and_2_out}}, and_2_out};  // Bit_Extender bit_extender_1
  assign VX = VY & bit_extender_1_out;  // AND_Gate and_1, 8 bits wide
  and and_2 (and_2_out, T1, enable);
  not not_1 (not_1_out, enable);
  assign bit_extender_2_out = {{3{enable}}, enable};  // Bit_Extender bit_extender_2
  assign bit_extender_3_out = {{3{enable}}, enable};  // Bit_Extender bit_extender_3
  assign bit_extender_4_out = {{3{enable}}, enable};  // Bit_Extender bit_extender_4
  and and_3 (EC, 1'b1, enable);
  assign NC = 4'b0011 & bit_extender_2_out;  // AND_Gate and_4, 4 bits wide
  assign AY = Y & bit_extender_3_out;  // AND_Gate and_5, 4 bits wide
  assign AX = X & bit_extender_4_out;  // AND_Gate and_6, 4 bits wide
  // SAVD savd_1: pin names not known; wires that end beside it: H, and_2_out, not_1_out, SVX, savd_1_p5

  // Notes on the sheet:
  //   8xy0 - [  Vx=Vy              ] - LD Vx, Vy
  //   Sets VX to the value of VY.
endmodule

module _8XY1 (
  input  [3:0] Y,
  input  [3:0] X,
  input  [7:0] VY,
  input  [7:0] VX,
  input  H,
  input  T1,
  input  enable,
  output [3:0] AY,
  output [3:0] AX,
  output [7:0] VX_2,
  output SVX,
  output EC,
  output [3:0] NC
);

  wire and_1_out, not_1_out, savd_1_p5;
  wire [3:0] bit_extender_1_out, bit_extender_2_out, bit_extender_4_out;
  wire [7:0] bit_extender_3_out, or_1_out;

  assign or_1_out = VY | VX;  // OR_Gate or_1, 8 bits wide
  and and_1 (and_1_out, T1, enable);
  assign bit_extender_1_out = {{3{enable}}, enable};  // Bit_Extender bit_extender_1
  assign bit_extender_2_out = {{3{enable}}, enable};  // Bit_Extender bit_extender_2
  assign bit_extender_3_out = {{7{and_1_out}}, and_1_out};  // Bit_Extender bit_extender_3
  not not_1 (not_1_out, enable);
  assign AY = Y & bit_extender_1_out;  // AND_Gate and_2, 4 bits wide
  assign AX = X & bit_extender_2_out;  // AND_Gate and_3, 4 bits wide
  assign VX_2 = or_1_out & bit_extender_3_out;  // AND_Gate and_4, 8 bits wide
  assign bit_extender_4_out = {{3{enable}}, enable};  // Bit_Extender bit_extender_4
  and and_5 (EC, 1'b1, enable);
  assign NC = 4'b0011 & bit_extender_4_out;  // AND_Gate and_6, 4 bits wide
  // SAVD savd_1: pin names not known; wires that end beside it: H, and_1_out, not_1_out, SVX, savd_1_p5

  // Notes on the sheet:
  //   8xy1 - [  Vx=Vx|Vy           ] - OR Vx, Vy
  //   Sets VX to VX or VY. (Bitwise OR operation)
endmodule

module _8XY2 (
  input  [3:0] Y,
  input  [3:0] X,
  input  [7:0] VY,
  input  [7:0] VX,
  input  H,
  input  T1,
  input  enable,
  output [3:0] AY,
  output [3:0] AX,
  output [7:0] VX_2,
  output SVX,
  output EC,
  output [3:0] NC
);

  wire and_2_out, not_1_out, savd_1_p5;
  wire [3:0] bit_extender_2_out, bit_extender_3_out, bit_extender_4_out;
  wire [7:0] and_1_out, bit_extender_1_out;

  assign and_1_out = VY & VX;  // AND_Gate and_1, 8 bits wide
  and and_2 (and_2_out, T1, enable);
  not not_1 (not_1_out, enable);
  assign bit_extender_1_out = {{7{and_2_out}}, and_2_out};  // Bit_Extender bit_extender_1
  assign bit_extender_2_out = {{3{enable}}, enable};  // Bit_Extender bit_extender_2
  assign bit_extender_3_out = {{3{enable}}, enable};  // Bit_Extender bit_extender_3
  assign VX_2 = and_1_out & bit_extender_1_out;  // AND_Gate and_3, 8 bits wide
  assign bit_extender_4_out = {{3{enable}}, enable};  // Bit_Extender bit_extender_4
  assign AY = Y & bit_extender_2_out;  // AND_Gate and_4, 4 bits wide
  assign AX = X & bit_extender_3_out;  // AND_Gate and_5, 4 bits wide
  and and_6 (EC, 1'b1, enable);
  assign NC = 4'b0011 & bit_extender_4_out;  // AND_Gate and_7, 4 bits wide
  // SAVD savd_1: pin names not known; wires that end beside it: H, and_2_out, not_1_out, SVX, savd_1_p5

  // Notes on the sheet:
  //   8xy2 - [  Vx=Vx&Vy           ] - AND Vx, Vy
  //   Sets VX to VX and VY. (Bitwise AND operation)
endmodule

module _8XY3 (
  input  [3:0] Y,
  input  [3:0] X,
  input  [7:0] VY,
  input  [7:0] VX,
  input  H,
  input  T1,
  input  enable,
  output [3:0] AY,
  output [3:0] AX,
  output [7:0] VX_2,
  output SVX,
  output EC,
  output [3:0] NC
);

  wire and_1_out, not_1_out, savd_1_p5;
  wire [3:0] bit_extender_1_out, bit_extender_2_out, bit_extender_4_out;
  wire [7:0] bit_extender_3_out, xor_1_out;

  assign xor_1_out = VY ^ VX;  // XOR_Gate xor_1, 8 bits wide
  and and_1 (and_1_out, T1, enable);
  not not_1 (not_1_out, enable);
  assign bit_extender_1_out = {{3{enable}}, enable};  // Bit_Extender bit_extender_1
  assign bit_extender_2_out = {{3{enable}}, enable};  // Bit_Extender bit_extender_2
  assign bit_extender_3_out = {{7{and_1_out}}, and_1_out};  // Bit_Extender bit_extender_3
  assign AY = Y & bit_extender_1_out;  // AND_Gate and_2, 4 bits wide
  assign AX = X & bit_extender_2_out;  // AND_Gate and_3, 4 bits wide
  assign VX_2 = xor_1_out & bit_extender_3_out;  // AND_Gate and_4, 8 bits wide
  assign bit_extender_4_out = {{3{enable}}, enable};  // Bit_Extender bit_extender_4
  and and_5 (EC, 1'b1, enable);
  assign NC = 4'b0011 & bit_extender_4_out;  // AND_Gate and_6, 4 bits wide
  // SAVD savd_1: pin names not known; wires that end beside it: H, and_1_out, not_1_out, SVX, savd_1_p5

  // Notes on the sheet:
  //   8xy3 - [  Vx=Vx^Vy           ] - XOR Vx, Vy
  //   Sets VX to VX xor VY.
endmodule

module _8XY4 (
  input  [3:0] Y,
  input  [3:0] X,
  input  [7:0] VY,
  input  [7:0] VX,
  input  H,
  input  T1,
  input  enable,
  output [3:0] AY,
  output [3:0] AX,
  output [7:0] VF,
  output SVF,
  output [7:0] VX_2,
  output SVX,
  output EC,
  output [3:0] NC
);

  wire adder_1_cout, and_1_out, not_1_out, savd_2_p5;
  wire [3:0] bit_extender_3_out, bit_extender_4_out, bit_extender_5_out;
  wire [7:0] adder_1_out, bit_extender_1_out, bit_extender_2_out;

  Adder adder_1 (.a(VY), .b(VX), .out(adder_1_out), .cin(1'b0), .cout(adder_1_cout));
  and and_1 (and_1_out, T1, enable);
  not not_1 (not_1_out, enable);
  assign bit_extender_1_out = {{7{1'b0}}, adder_1_cout};  // Bit_Extender bit_extender_1
  assign VF = bit_extender_1_out & bit_extender_2_out;  // AND_Gate and_2, 8 bits wide
  assign bit_extender_2_out = {{7{and_1_out}}, and_1_out};  // Bit_Extender bit_extender_2
  assign VX_2 = adder_1_out & bit_extender_2_out;  // AND_Gate and_3, 8 bits wide
  assign bit_extender_3_out = {{3{enable}}, enable};  // Bit_Extender bit_extender_3
  assign AY = Y & bit_extender_4_out;  // AND_Gate and_4, 4 bits wide
  assign bit_extender_4_out = {{3{enable}}, enable};  // Bit_Extender bit_extender_4
  assign AX = X & bit_extender_5_out;  // AND_Gate and_5, 4 bits wide
  assign bit_extender_5_out = {{3{enable}}, enable};  // Bit_Extender bit_extender_5
  and and_6 (EC, 1'b1, enable);
  assign NC = 4'b0011 & bit_extender_3_out;  // AND_Gate and_7, 4 bits wide
  // SAVD savd_1: pin names not known; wires that end beside it: H, and_1_out, not_1_out, SVF
  // SAVD savd_2: pin names not known; wires that end beside it: H, and_1_out, not_1_out, SVX, savd_2_p5

  // Notes on the sheet:
  //   8xy4 - [  Vx += Vy           ] - ADD Vx, Vy
  //   Adds VY to VX. VF is set to 1 when there's a carry, and to 0 when there isn't.
endmodule

module _8XY5 (
  input  [3:0] Y,
  input  [3:0] X,
  input  [7:0] VX,
  input  [7:0] VY,
  input  H,
  input  T1,
  input  enable,
  output [3:0] AY,
  output [3:0] AX,
  output [7:0] VF,
  output SVF,
  output [7:0] VX_2,
  output SVX,
  output EC,
  output [3:0] NC
);

  wire and_1_out, not_1_out, not_2_out, savd_2_p5, subtractor_1_bout;
  wire [3:0] bit_extender_3_out, bit_extender_4_out, bit_extender_5_out;
  wire [7:0] bit_extender_1_out, bit_extender_2_out, subtractor_1_out;

  Subtractor subtractor_1 (.a(VX), .b(VY), .out(subtractor_1_out), .bin(1'b0), .bout(subtractor_1_bout));
  and and_1 (and_1_out, T1, enable);
  not not_1 (not_1_out, subtractor_1_bout);
  not not_2 (not_2_out, enable);
  assign bit_extender_1_out = {{7{1'b0}}, not_1_out};  // Bit_Extender bit_extender_1
  assign bit_extender_2_out = {{7{and_1_out}}, and_1_out};  // Bit_Extender bit_extender_2
  assign bit_extender_3_out = {{3{enable}}, enable};  // Bit_Extender bit_extender_3
  assign bit_extender_4_out = {{3{enable}}, enable};  // Bit_Extender bit_extender_4
  assign VF = bit_extender_1_out & bit_extender_2_out;  // AND_Gate and_2, 8 bits wide
  assign VX_2 = subtractor_1_out & bit_extender_2_out;  // AND_Gate and_3, 8 bits wide
  assign bit_extender_5_out = {{3{enable}}, enable};  // Bit_Extender bit_extender_5
  assign AY = Y & bit_extender_3_out;  // AND_Gate and_4, 4 bits wide
  assign AX = X & bit_extender_4_out;  // AND_Gate and_5, 4 bits wide
  and and_6 (EC, 1'b1, enable);
  assign NC = 4'b0011 & bit_extender_5_out;  // AND_Gate and_7, 4 bits wide
  // SAVD savd_1: pin names not known; wires that end beside it: H, and_1_out, not_2_out, SVF
  // SAVD savd_2: pin names not known; wires that end beside it: H, and_1_out, not_2_out, SVX, savd_2_p5

  // Notes on the sheet:
  //   8xy5 - [  Vx -= Vy           ] - SUB Vx, Vy
  //   VY is subtracted from VX. VF is set to 0 when there's a borrow, and 1 when there isn't.
endmodule

module _8XY7 (
  input  [3:0] Y,
  input  [3:0] X,
  input  [7:0] VY,
  input  [7:0] VX,
  input  H,
  input  T1,
  input  enable,
  output [3:0] AY,
  output [3:0] AX,
  output [7:0] VF,
  output SVF,
  output [7:0] VX_2,
  output SVX,
  output EC,
  output [3:0] NC
);

  wire and_1_out, not_1_out, not_2_out, savd_2_p5, subtractor_1_bout;
  wire [3:0] bit_extender_3_out, bit_extender_4_out, bit_extender_5_out;
  wire [7:0] bit_extender_1_out, bit_extender_2_out, subtractor_1_out;

  Subtractor subtractor_1 (.a(VY), .b(VX), .out(subtractor_1_out), .bin(1'b0), .bout(subtractor_1_bout));
  and and_1 (and_1_out, T1, enable);
  not not_1 (not_1_out, subtractor_1_bout);
  assign bit_extender_1_out = {{7{1'b0}}, not_1_out};  // Bit_Extender bit_extender_1
  assign bit_extender_2_out = {{7{and_1_out}}, and_1_out};  // Bit_Extender bit_extender_2
  assign bit_extender_3_out = {{3{enable}}, enable};  // Bit_Extender bit_extender_3
  assign bit_extender_4_out = {{3{enable}}, enable};  // Bit_Extender bit_extender_4
  assign VF = bit_extender_1_out & bit_extender_2_out;  // AND_Gate and_2, 8 bits wide
  assign VX_2 = subtractor_1_out & bit_extender_2_out;  // AND_Gate and_3, 8 bits wide
  not not_2 (not_2_out, enable);
  assign bit_extender_5_out = {{3{enable}}, enable};  // Bit_Extender bit_extender_5
  assign AY = Y & bit_extender_3_out;  // AND_Gate and_4, 4 bits wide
  assign AX = X & bit_extender_4_out;  // AND_Gate and_5, 4 bits wide
  and and_6 (EC, 1'b1, enable);
  assign NC = 4'b0011 & bit_extender_5_out;  // AND_Gate and_7, 4 bits wide
  // SAVD savd_1: pin names not known; wires that end beside it: H, and_1_out, not_2_out, SVF
  // SAVD savd_2: pin names not known; wires that end beside it: H, and_1_out, not_2_out, SVX, savd_2_p5

  // Notes on the sheet:
  //   8xy7 - [  Vx=Vy-Vx           ] - SUBN Vx, Vy
  //   Sets VX to VY minus VX. VF is set to 0 when there's a borrow, and 1 when there isn't.
endmodule
