// Logisim project other_chip8_012.circ as structural Verilog: 11 circuits, main circuit RANDM
module RANDM (
  input  H,
  input  Enable,
  input  [7:0] Max,
  output [7:0] def,
  output [7:0] Output
);

  wire cod8_1_validate, comparator_1_gt, nand_1_out, or_1_out;
  wire [2:0] cod8_1_output;
  wire [7:0] and_1_out, and_2_out, and_3_out, and_4_out, and_5_out, and_6_out, bit_extender_3_out,
       bit_extender_4_out, bit_extender_5_out, decoder_1_out0, not_1_out, not_2_out, not_3_out, or_3_out,
       subtractor_1_out;
  wire [8:0] bit_extender_1_out, bit_extender_2_out;

  // Probe on Max
  // Probe on Max
  // Probe on def
  // Probe on def
  Random random_1 (.clk(H), .next(Enable), .out(def), .clr(1'b0));
  COD8 cod8_1 (
    .Enable(1'b1), .Validate(cod8_1_validate), .Output(cod8_1_output), .Input_0(Max[0]), .Input_1(Max[1]),
    .Input_2(Max[2]), .Input_3(Max[3]), .Input_4(Max[4]), .Input_5(Max[5]), .Input_6(Max[6]), .Input_7(Max[7]));
  assign bit_extender_1_out = {{1{1'b0}}, def};  // Bit_Extender bit_extender_1
  assign bit_extender_2_out = {{1{1'b0}}, Max};  // Bit_Extender bit_extender_2
  Decoder #(.select(3), .disabled(0)) decoder_1 (
    .out0(decoder_1_out0[0]), .out1(decoder_1_out0[1]), .out2(decoder_1_out0[2]), .out3(decoder_1_out0[3]),
    .out4(decoder_1_out0[4]), .out5(decoder_1_out0[5]), .out6(decoder_1_out0[6]), .out7(decoder_1_out0[7]),
    .sel(cod8_1_output), .en(cod8_1_validate));
  Comparator #(.width(9)) comparator_1 (
    .a(bit_extender_1_out), .b(bit_extender_2_out), .gt(comparator_1_gt));  // open: eq, lt
  Subtractor subtractor_1 (.a(decoder_1_out0), .b(8'h1), .out(subtractor_1_out), .bin(1'b0));  // open: bout
  assign not_1_out = ~bit_extender_3_out;  // NOT_Gate not_1, 8 bits wide
  assign bit_extender_3_out = {{7{comparator_1_gt}}, comparator_1_gt};  // Bit_Extender bit_extender_3
  assign and_1_out = def & not_1_out;  // AND_Gate and_1, 8 bits wide
  assign and_2_out = bit_extender_3_out & and_6_out;  // AND_Gate and_2, 8 bits wide
  nand nand_1 (nand_1_out, subtractor_1_out[0], subtractor_1_out[1], subtractor_1_out[2], subtractor_1_out[3], subtractor_1_out[4], subtractor_1_out[5], subtractor_1_out[6], subtractor_1_out[7]);
  or or_1 (or_1_out, subtractor_1_out[0], subtractor_1_out[1], subtractor_1_out[2], subtractor_1_out[3], subtractor_1_out[4], subtractor_1_out[5], subtractor_1_out[6], subtractor_1_out[7]);
  assign Output = and_1_out | and_2_out;  // OR_Gate or_2, 8 bits wide
  assign not_2_out = ~bit_extender_4_out;  // NOT_Gate not_2, 8 bits wide
  assign bit_extender_4_out = {{7{nand_1_out}}, nand_1_out};  // Bit_Extender bit_extender_4
  assign not_3_out = ~bit_extender_5_out;  // NOT_Gate not_3, 8 bits wide
  assign bit_extender_5_out = {{7{or_1_out}}, or_1_out};  // Bit_Extender bit_extender_5
  assign and_3_out = {8{1'b1}} & not_2_out;  // AND_Gate and_3, 8 bits wide
  assign and_4_out = bit_extender_4_out & bit_extender_5_out & subtractor_1_out;  // AND_Gate and_4, 8 bits wide
  assign and_5_out = not_3_out & 8'h1;  // AND_Gate and_5, 8 bits wide
  assign and_6_out = def & or_3_out;  // AND_Gate and_6, 8 bits wide
  assign or_3_out = and_3_out | and_5_out | and_4_out;  // OR_Gate or_3, 8 bits wide
endmodule

module CODH (
  input  Input_0,
  input  Input_1,
  input  Input_2,
  input  Input_3,
  input  Input_4,
  input  Input_5,
  input  Input_6,
  input  Input_7,
  input  Input_8,
  input  Input_9,
  input  Input_10,
  input  Input_11,
  input  Input_12,
  input  Input_13,
  input  Input_14,
  input  Input_15,
  input  Enable,
  output Validate,
  output [3:0] Output
);

  wire and_1_out, cod8_1_validate, not_1_out;
  wire [2:0] cod8_1_output, cod8_2_output;

  COD8 cod8_1 (
    .Enable(and_1_out), .Validate(cod8_1_validate), .Output(cod8_1_output), .Input_0(Input_0),
    .Input_1(Input_1), .Input_2(Input_2), .Input_3(Input_3), .Input_4(Input_4), .Input_5(Input_5),
    .Input_6(Input_6), .Input_7(Input_7));
  COD8 cod8_2 (
    .Enable(Enable), .Validate(Output[3]), .Output(cod8_2_output), .Input_0(Input_8), .Input_1(Input_9),
    .Input_2(Input_10), .Input_3(Input_11), .Input_4(Input_12), .Input_5(Input_13), .Input_6(Input_14),
    .Input_7(Input_15));
  assign Output[2:0] = cod8_1_output | cod8_2_output;  // OR_Gate or_1, 3 bits wide
  not not_1 (not_1_out, Output[3]);
  or or_2 (Validate, cod8_1_validate, Output[3]);
  and and_1 (and_1_out, not_1_out, Enable);
endmodule

module UPD (
  input  Verr,
  input  Shift,
  input  [6:0] Input,
  input  Enable,
  output LedUppercase,
  output [6:0] Output
);

  wire d_ff_1_q, d_ff_1_qn, not_1_out;
  wire [5:5] xor_1_out;
  wire [6:0] bit_extender_1_out;

  not not_1 (not_1_out, Shift);
  D_Flip_Flop d_ff_1 (.clk(Verr), .D(d_ff_1_qn), .Q(d_ff_1_q), .Qn(d_ff_1_qn), .preset(1'b0), .en(1'b1), .reset(1'b0));
  xor xor_1 (xor_1_out[5], not_1_out, d_ff_1_q);
  // Probe on Input
  assign bit_extender_1_out = {{6{Enable}}, Enable};  // Bit_Extender bit_extender_1
  not not_2 (LedUppercase, xor_1_out[5]);
  // Probe on {Input[6], xor_1_out[5], Input[4:0]}
  LED led_1 (.in(d_ff_1_q));
  assign Output = {Input[6], xor_1_out[5], Input[4:0]} & bit_extender_1_out;  // AND_Gate and_1, 7 bits wide
  // Probe on Output
endmodule

module LC64 (
  input  E,
  input  [5:0] X,
  input  [4:0] Y,
  input  H,
  input  I,
  input  C,
  output [31:0] out_7,
  output [31:0] out_8,
  output [31:0] out_9,
  output [31:0] out_10,
  output [31:0] out_11,
  output [31:0] out_12,
  output [31:0] out_13,
  output [31:0] out_14,
  output [31:0] out_15,
  output [31:0] out_16,
  output [31:0] out_17,
  output [31:0] out_18,
  output [31:0] out_19,
  output [31:0] out_20,
  output [31:0] out_21,
  output [31:0] out_22,
  output [31:0] out_23,
  output [31:0] out_24,
  output [31:0] out_25,
  output [31:0] out_26,
  output [31:0] out_27,
  output [31:0] out_28,
  output [31:0] out_29,
  output [31:0] out_30,
  output [31:0] out_31,
  output [31:0] out_32,
  output [31:0] out_33,
  output [31:0] out_34,
  output [31:0] out_35,
  output [31:0] out_36,
  output [31:0] out_37,
  output [31:0] out_38,
  output [31:0] out_39,
  output [31:0] out_40,
  output [31:0] out_41,
  output [31:0] out_42,
  output [31:0] out_43,
  output [31:0] out_44,
  output [31:0] out_45,
  output [31:0] out_46,
  output [31:0] out_47,
  output [31:0] out_48,
  output [31:0] out_49,
  output [31:0] out_50,
  output [31:0] out_51,
  output [31:0] out_52,
  output [31:0] out_53,
  output [31:0] out_54,
  output [31:0] out_55,
  output [31:0] out_56,
  output [31:0] out_57,
  output [31:0] out_58,
  output [31:0] out_59,
  output [31:0] out_60,
  output [31:0] out_61,
  output [31:0] out_62,
  output [31:0] out_63,
  output [31:0] out_64,
  output [31:0] out_65,
  output [31:0] out_66,
  output [31:0] out_67,
  output [31:0] out_68,
  output [31:0] out_69,
  output [31:0] out_70
);

  wire decoder_1_out0, decoder_1_out1;

  Decoder #(.disabled(0)) decoder_1 (.out0(decoder_1_out0), .out1(decoder_1_out1), .sel(X[5]), .en(E));
  LC32 lc32_1 (
    .enable(decoder_1_out0), .X(X[4:0]), .Y(Y), .H(H), .I(I), .C(C), .O0(out_7), .out_8(out_8),
    .out_9(out_9), .out_10(out_10), .out_11(out_11), .out_12(out_12), .out_13(out_13), .out_14(out_14),
    .out_15(out_15), .out_16(out_16), .out_17(out_17), .out_18(out_18), .out_19(out_19), .out_20(out_20),
    .out_21(out_21), .out_22(out_22), .out_23(out_23), .out_24(out_24), .out_25(out_25), .out_26(out_26),
    .out_27(out_27), .out_28(out_28), .out_29(out_29), .out_30(out_30), .out_31(out_31), .out_32(out_32),
    .out_33(out_33), .out_34(out_34), .out_35(out_35), .out_36(out_36), .out_37(out_37), .out_38(out_38));
  LC32 lc32_2 (
    .enable(decoder_1_out1), .X(X[4:0]), .Y(Y), .H(H), .I(I), .C(C), .O0(out_39), .out_8(out_40),
    .out_9(out_41), .out_10(out_42), .out_11(out_43), .out_12(out_44), .out_13(out_45), .out_14(out_46),
    .out_15(out_47), .out_16(out_48), .out_17(out_49), .out_18(out_50), .out_19(out_51), .out_20(out_52),
    .out_21(out_53), .out_22(out_54), .out_23(out_55), .out_24(out_56), .out_25(out_57), .out_26(out_58),
    .out_27(out_59), .out_28(out_60), .out_29(out_61), .out_30(out_62), .out_31(out_63), .out_32(out_64),
    .out_33(out_65), .out_34(out_66), .out_35(out_67), .out_36(out_68), .out_37(out_69), .out_38(out_70));
endmodule

module COLC64 (
  input  Enable,
  input  [5:0] X,
  input  [4:0] Y,
  input  I,
  input  H,
  input  CL,
  output OS
);

  wire colc8_1_os, colc8_2_os, colc8_3_os, colc8_4_os, colc8_5_os, colc8_6_os, colc8_7_os, colc8_8_os,
       decoder_1_out0, decoder_1_out1, decoder_1_out2, decoder_1_out3, decoder_1_out4, decoder_1_out5,
       decoder_1_out6, decoder_1_out7;

  Decoder #(.select(3), .disabled(0)) decoder_1 (
    .out0(decoder_1_out0), .out1(decoder_1_out1), .out2(decoder_1_out2), .out3(decoder_1_out3),
    .out4(decoder_1_out4), .out5(decoder_1_out5), .out6(decoder_1_out6), .out7(decoder_1_out7), .sel(X[5:3]),
    .en(Enable));
  COLC8 colc8_1 (.Enable(decoder_1_out0), .X(X[2:0]), .Y(Y), .I(I), .H(H), .CL(CL), .OS(colc8_1_os));
  COLC8 colc8_2 (.Enable(decoder_1_out1), .X(X[2:0]), .Y(Y), .I(I), .H(H), .CL(CL), .OS(colc8_2_os));
  COLC8 colc8_3 (.Enable(decoder_1_out2), .X(X[2:0]), .Y(Y), .I(I), .H(H), .CL(CL), .OS(colc8_3_os));
  COLC8 colc8_4 (.Enable(decoder_1_out3), .X(X[2:0]), .Y(Y), .I(I), .H(H), .CL(CL), .OS(colc8_4_os));
  COLC8 colc8_5 (.Enable(decoder_1_out4), .X(X[2:0]), .Y(Y), .I(I), .H(H), .CL(CL), .OS(colc8_5_os));
  COLC8 colc8_6 (.Enable(decoder_1_out5), .X(X[2:0]), .Y(Y), .I(I), .H(H), .CL(CL), .OS(colc8_6_os));
  COLC8 colc8_7 (.Enable(decoder_1_out6), .X(X[2:0]), .Y(Y), .I(I), .H(H), .CL(CL), .OS(colc8_7_os));
  COLC8 colc8_8 (.Enable(decoder_1_out7), .X(X[2:0]), .Y(Y), .I(I), .H(H), .CL(CL), .OS(colc8_8_os));
  Multiplexer #(.select(3), .enable("false")) multiplexer_1 (
    .in0(colc8_1_os), .in1(colc8_2_os), .in2(colc8_3_os), .in3(colc8_4_os), .in4(colc8_5_os),
    .in5(colc8_6_os), .in6(colc8_7_os), .in7(colc8_8_os), .out(OS), .sel(X[5:3]));
endmodule

module IGRB (
  input  [23:0] I,
  input  CL,
  input  H,
  output [5:0] OX,
  output [4:0] OY,
  output IGD,
  output [11:0] OR,
  output OB
);

  wire and_1_out, comparator_1_lt, comparator_2_lt, comparator_3_lt;
  wire [8:0] bit_extender_1_out, bit_extender_2_out, bit_extender_3_out;
  wire [23:0] igrc_1_oc;

  IGRC igrc_1 (.I(I), .CL(CL), .H(H), .OX(OX), .OY(OY), .IGD(IGD), .OC(igrc_1_oc), .AR(OR));
  assign bit_extender_1_out = {{1{1'b0}}, igrc_1_oc[7:0]};  // Bit_Extender bit_extender_1
  assign bit_extender_2_out = {{1{1'b0}}, igrc_1_oc[15:8]};  // Bit_Extender bit_extender_2
  assign bit_extender_3_out = {{1{1'b0}}, igrc_1_oc[23:16]};  // Bit_Extender bit_extender_3
  Comparator #(.width(9)) comparator_1 (.a(bit_extender_1_out), .b(9'h80), .lt(comparator_1_lt));  // open: gt, eq
  Comparator #(.width(9)) comparator_2 (.a(bit_extender_2_out), .b(9'h80), .lt(comparator_2_lt));  // open: gt, eq
  Comparator #(.width(9)) comparator_3 (.a(bit_extender_3_out), .b(9'h80), .lt(comparator_3_lt));  // open: gt, eq
  and and_1 (and_1_out, comparator_1_lt, comparator_2_lt, comparator_3_lt);
  not not_1 (OB, and_1_out);
endmodule

module IGSC (
  input  DOS,
  input  [5:0] AL,
  input  [4:0] AC,
  input  E,
  input  M,
  input  R,
  input  D,
  input  H,
  input  Store,
  input  [5:0] AC_I,
  input  [4:0] AL_I,
  input  D_I,
  input  ENDI_I,
  output DO,
  output [5:0] AL_2,
  output [4:0] AC_2,
  output clear,
  output Enable,
  output DIS,
  output H_2,
  output ENDI,
  output CL_I,
  output CK_I
);

  wire and_1_out, and_2_out, and_4_out, and_5_out, and_6_out, and_7_out, and_8_out, d_ff_1_q, d_ff_1_qn,
       d_ff_2_q, d_ff_2_qn, not_1_out, not_4_out, or_3_out;
  wire [4:0] and_11_out, and_12_out, bit_extender_2_out, not_3_out;
  wire [5:0] and_9_out, and_10_out, bit_extender_1_out, not_2_out;

  and and_1 (and_1_out, E, M);
  not not_1 (not_1_out, M);
  and and_2 (and_2_out, not_1_out, E);
  and and_3 (CK_I, E, H);
  and and_4 (and_4_out, and_1_out, D);
  and and_5 (and_5_out, and_2_out, D_I);
  and and_6 (and_6_out, and_2_out, ENDI_I);
  and and_7 (and_7_out, and_1_out, Store);
  or or_1 (DIS, and_4_out, and_5_out);
  or or_2 (Enable, and_6_out, and_7_out);
  and and_8 (and_8_out, H, M);
  or or_3 (or_3_out, d_ff_2_q, R);
  assign bit_extender_1_out = {{5{and_1_out}}, and_1_out};  // Bit_Extender bit_extender_1
  assign not_2_out = ~bit_extender_1_out;  // NOT_Gate not_2, 6 bits wide
  assign bit_extender_2_out = {{4{and_1_out}}, and_1_out};  // Bit_Extender bit_extender_2
  assign not_3_out = ~bit_extender_2_out;  // NOT_Gate not_3, 5 bits wide
  or or_4 (clear, R, d_ff_1_q);
  D_Flip_Flop #(.trigger("falling")) d_ff_1 (
    .clk(and_8_out), .D(d_ff_1_qn), .Q(d_ff_1_q), .Qn(d_ff_1_qn), .preset(1'b0), .en(d_ff_2_qn),
    .reset(or_3_out));
  assign and_9_out = AL & bit_extender_1_out;  // AND_Gate and_9, 6 bits wide
  assign and_10_out = not_2_out & AC_I;  // AND_Gate and_10, 6 bits wide
  assign and_11_out = AC & bit_extender_2_out;  // AND_Gate and_11, 5 bits wide
  assign and_12_out = not_3_out & AL_I;  // AND_Gate and_12, 5 bits wide
  D_Flip_Flop #(.trigger("falling")) d_ff_2 (
    .clk(d_ff_1_q), .D(d_ff_2_qn), .Q(d_ff_2_q), .Qn(d_ff_2_qn), .preset(1'b0), .en(1'b1), .reset(R));
  not not_4 (not_4_out, ENDI_I);
  assign AL_2 = and_9_out | and_10_out;  // OR_Gate or_5, 6 bits wide
  assign AC_2 = and_11_out | and_12_out;  // OR_Gate or_6, 5 bits wide
  or or_7 (ENDI, M, not_4_out);

  assign CL_I = R;
  assign DO = DOS;
  assign H_2 = CK_I;
endmodule

module TRFC (
  input  [7:0] DR,
  input  H,
  input  enable,
  input  clear,
  input  [7:0] DRAI,
  input  [11:0] ARAI,
  input  strRAI,
  input  selRAI,
  input  [11:0] MAX,
  input  [7:0] DRG,
  output [8:0] AR,
  output ER,
  output [11:0] ARAO,
  output [7:0] DRAO,
  output strRAO,
  output SelRAO,
  output HRA,
  output clearRA,
  output [11:0] ARG,
  output ERG,
  output EM
);

  wire [11:0] transf_1_ara;

  transf transf_1 (
    .H(H), .enable(enable), .clear(clear), .ARA(transf_1_ara), .AR(AR), .ARG(ARG), .ERG(ERG), .ER(ER),
    .EM(EM), .MAX(MAX));
  transf2 transf2_1 (
    .ARAI(ARAI), .ARA(transf_1_ara), .DR(DR), .DRG(DRG), .DRAI(DRAI), .ERG(ERG), .ER(ER), .EM(EM),
    .strRAI(strRAI), .SelRAI(selRAI), .ARAO(ARAO), .DRAO(DRAO), .strRAO(strRAO), .SelRAO(SelRAO));

  assign clearRA = clear;
  assign HRA = H;
endmodule

module AFFH (
  input  [3:0] V,
  output [6:0] AH
);

  wire decoder_1_out0, decoder_1_out1, decoder_1_out2, decoder_1_out3, decoder_1_out4, decoder_1_out5,
       decoder_1_out6, decoder_1_out7, decoder_1_out8, decoder_1_out9, decoder_1_out10, decoder_1_out11,
       decoder_1_out12, decoder_1_out13, decoder_1_out14, decoder_1_out15;

  Decoder #(.select(4), .disabled(0), .enable("false")) decoder_1 (
    .out0(decoder_1_out0), .out1(decoder_1_out1), .out2(decoder_1_out2), .out3(decoder_1_out3),
    .out4(decoder_1_out4), .out5(decoder_1_out5), .out6(decoder_1_out6), .out7(decoder_1_out7),
    .out8(decoder_1_out8), .out9(decoder_1_out9), .out10(decoder_1_out10), .out11(decoder_1_out11),
    .out12(decoder_1_out12), .out13(decoder_1_out13), .out14(decoder_1_out14), .out15(decoder_1_out15),
    .sel(V));
  or or_1 (AH[3], decoder_1_out2, decoder_1_out3, decoder_1_out4, decoder_1_out5, decoder_1_out6, decoder_1_out8, decoder_1_out9, decoder_1_out10, decoder_1_out11, decoder_1_out13, decoder_1_out14, decoder_1_out15);
  or or_2 (AH[2], decoder_1_out0, decoder_1_out4, decoder_1_out5, decoder_1_out6, decoder_1_out8, decoder_1_out9, decoder_1_out10, decoder_1_out11, decoder_1_out12, decoder_1_out14, decoder_1_out15);
  or or_3 (AH[1], decoder_1_out0, decoder_1_out2, decoder_1_out3, decoder_1_out5, decoder_1_out6, decoder_1_out7, decoder_1_out8, decoder_1_out9, decoder_1_out10, decoder_1_out12, decoder_1_out14, decoder_1_out15);
  or or_4 (AH[0], decoder_1_out0, decoder_1_out1, decoder_1_out2, decoder_1_out3, decoder_1_out4, decoder_1_out7, decoder_1_out8, decoder_1_out9, decoder_1_out10, decoder_1_out13);
  or or_5 (AH[6], decoder_1_out0, decoder_1_out2, decoder_1_out6, decoder_1_out8, decoder_1_out10, decoder_1_out11, decoder_1_out12, decoder_1_out13, decoder_1_out14, decoder_1_out15);
  or or_6 (AH[5], decoder_1_out0, decoder_1_out2, decoder_1_out3, decoder_1_out5, decoder_1_out6, decoder_1_out8, decoder_1_out11, decoder_1_out12, decoder_1_out13, decoder_1_out14);
  or or_7 (AH[4], decoder_1_out0, decoder_1_out1, decoder_1_out3, decoder_1_out4, decoder_1_out5, decoder_1_out6, decoder_1_out7, decoder_1_out8, decoder_1_out9, decoder_1_out10, decoder_1_out11, decoder_1_out13);
endmodule

module COLC64_2 (
  input  Enable,
  input  [5:0] X,
  input  [4:0] Y,
  input  I,
  input  H,
  input  CL,
  output OS
);

  wire [31:0] and_1_out, decoder_1_out0, decoder_2_out0, not_1_out, or_1_out, ram_1_data;

  Decoder #(.select(5), .disabled(0)) decoder_1 (
    .out0(decoder_1_out0[0]), .out1(decoder_1_out0[1]), .out2(decoder_1_out0[2]), .out3(decoder_1_out0[3]),
    .out4(decoder_1_out0[4]), .out5(decoder_1_out0[5]), .out6(decoder_1_out0[6]), .out7(decoder_1_out0[7]),
    .out8(decoder_1_out0[8]), .out9(decoder_1_out0[9]), .out10(decoder_1_out0[10]),
    .out11(decoder_1_out0[11]), .out12(decoder_1_out0[12]), .out13(decoder_1_out0[13]),
    .out14(decoder_1_out0[14]), .out15(decoder_1_out0[15]), .out16(decoder_1_out0[16]),
    .out17(decoder_1_out0[17]), .out18(decoder_1_out0[18]), .out19(decoder_1_out0[19]),
    .out20(decoder_1_out0[20]), .out21(decoder_1_out0[21]), .out22(decoder_1_out0[22]),
    .out23(decoder_1_out0[23]), .out24(decoder_1_out0[24]), .out25(decoder_1_out0[25]),
    .out26(decoder_1_out0[26]), .out27(decoder_1_out0[27]), .out28(decoder_1_out0[28]),
    .out29(decoder_1_out0[29]), .out30(decoder_1_out0[30]), .out31(decoder_1_out0[31]), .sel(Y), .en(I));
  Decoder #(.select(5), .disabled(0)) decoder_2 (
    .out0(decoder_2_out0[0]), .out1(decoder_2_out0[1]), .out2(decoder_2_out0[2]), .out3(decoder_2_out0[3]),
    .out4(decoder_2_out0[4]), .out5(decoder_2_out0[5]), .out6(decoder_2_out0[6]), .out7(decoder_2_out0[7]),
    .out8(decoder_2_out0[8]), .out9(decoder_2_out0[9]), .out10(decoder_2_out0[10]),
    .out11(decoder_2_out0[11]), .out12(decoder_2_out0[12]), .out13(decoder_2_out0[13]),
    .out14(decoder_2_out0[14]), .out15(decoder_2_out0[15]), .out16(decoder_2_out0[16]),
    .out17(decoder_2_out0[17]), .out18(decoder_2_out0[18]), .out19(decoder_2_out0[19]),
    .out20(decoder_2_out0[20]), .out21(decoder_2_out0[21]), .out22(decoder_2_out0[22]),
    .out23(decoder_2_out0[23]), .out24(decoder_2_out0[24]), .out25(decoder_2_out0[25]),
    .out26(decoder_2_out0[26]), .out27(decoder_2_out0[27]), .out28(decoder_2_out0[28]),
    .out29(decoder_2_out0[29]), .out30(decoder_2_out0[30]), .out31(decoder_2_out0[31]), .sel(Y), .en(Enable));
  RAM #(.addrWidth(6), .dataWidth(32), .bus("separate")) ram_1 (
    .addr(X), .din(or_1_out), .data(ram_1_data), .str(Enable), .sel(1'b1), .clk(H), .ld(1'b1), .clr(CL));
  assign not_1_out = ~decoder_2_out0;  // NOT_Gate not_1, 32 bits wide
  assign and_1_out = ram_1_data & not_1_out;  // AND_Gate and_1, 32 bits wide
  assign or_1_out = and_1_out | decoder_1_out0;  // OR_Gate or_1, 32 bits wide
  Multiplexer #(.select(5), .disabled(0), .enable("false")) multiplexer_1 (
    .in0(ram_1_data[0]), .in1(ram_1_data[1]), .in2(ram_1_data[2]), .in3(ram_1_data[3]), .in4(ram_1_data[4]),
    .in5(ram_1_data[5]), .in6(ram_1_data[6]), .in7(ram_1_data[7]), .in8(ram_1_data[8]), .in9(ram_1_data[9]),
    .in10(ram_1_data[10]), .in11(ram_1_data[11]), .in12(ram_1_data[12]), .in13(ram_1_data[13]),
    .in14(ram_1_data[14]), .in15(ram_1_data[15]), .in16(ram_1_data[16]), .in17(ram_1_data[17]),
    .in18(ram_1_data[18]), .in19(ram_1_data[19]), .in20(ram_1_data[20]), .in21(ram_1_data[21]),
    .in22(ram_1_data[22]), .in23(ram_1_data[23]), .in24(ram_1_data[24]), .in25(ram_1_data[25]),
    .in26(ram_1_data[26]), .in27(ram_1_data[27]), .in28(ram_1_data[28]), .in29(ram_1_data[29]),
    .in30(ram_1_data[30]), .in31(ram_1_data[31]), .out(OS), .sel(Y));
endmodule

module RANDMAX (
  input  H,
  input  Enable,
  input  [7:0] Max,
  output [7:0] Def,
  output [7:0] Output
);

  wire cod8_1_validate, nand_1_out, or_1_out;
  wire [2:0] cod8_1_output;
  wire [7:0] and_1_out, and_2_out, and_3_out, bit_extender_1_out, bit_extender_2_out, decoder_1_out0,
       not_1_out, not_2_out, or_2_out, subtractor_1_out;

  // Probe on Max
  // Probe on Max
  Random random_1 (.clk(H), .next(Enable), .out(Def), .clr(1'b0));
  COD8 cod8_1 (
    .Enable(1'b1), .Validate(cod8_1_validate), .Output(cod8_1_output), .Input_0(Max[0]), .Input_1(Max[1]),
    .Input_2(Max[2]), .Input_3(Max[3]), .Input_4(Max[4]), .Input_5(Max[5]), .Input_6(Max[6]), .Input_7(Max[7]));
  Decoder #(.select(3), .disabled(0)) decoder_1 (
    .out0(decoder_1_out0[0]), .out1(decoder_1_out0[1]), .out2(decoder_1_out0[2]), .out3(decoder_1_out0[3]),
    .out4(decoder_1_out0[4]), .out5(decoder_1_out0[5]), .out6(decoder_1_out0[6]), .out7(decoder_1_out0[7]),
    .sel(cod8_1_output), .en(cod8_1_validate));
  Subtractor subtractor_1 (.a(decoder_1_out0), .b(8'h1), .out(subtractor_1_out), .bin(1'b0));  // open: bout
  nand nand_1 (nand_1_out, subtractor_1_out[0], subtractor_1_out[1], subtractor_1_out[2], subtractor_1_out[3], subtractor_1_out[4], subtractor_1_out[5], subtractor_1_out[6], subtractor_1_out[7]);
  or or_1 (or_1_out, subtractor_1_out[0], subtractor_1_out[1], subtractor_1_out[2], subtractor_1_out[3], subtractor_1_out[4], subtractor_1_out[5], subtractor_1_out[6], subtractor_1_out[7]);
  assign not_1_out = ~bit_extender_1_out;  // NOT_Gate not_1, 8 bits wide
  assign bit_extender_1_out = {{7{nand_1_out}}, nand_1_out};  // Bit_Extender bit_extender_1
  assign bit_extender_2_out = {{7{or_1_out}}, or_1_out};  // Bit_Extender bit_extender_2
  assign and_1_out = {8{1'b1}} & not_1_out;  // AND_Gate and_1, 8 bits wide
  assign and_2_out = bit_extender_1_out & subtractor_1_out & bit_extender_2_out;  // AND_Gate and_2, 8 bits wide
  assign not_2_out = ~bit_extender_2_out;  // NOT_Gate not_2, 8 bits wide
  assign and_3_out = not_2_out & 8'h1;  // AND_Gate and_3, 8 bits wide
  assign Output = Def & or_2_out;  // AND_Gate and_4, 8 bits wide
  assign or_2_out = and_1_out | and_2_out | and_3_out;  // OR_Gate or_2, 8 bits wide
endmodule
