// Logisim project other.circ as structural Verilog: 5 circuits, main circuit main
module main (
  input  Buffer,
  input  in_2,
  input  in_3,
  input  in_4,
  input  in_5,
  input  [2:0] in_6,
  input  [2:0] in_7,
  input  [3:0] in_8,
  input  [3:0] in_9,
  output out_10,
  output out_11,
  output out_12,
  output out_13,
  output out_14,
  output out_15,
  output out_16,
  output out_17,
  output out_18,
  output out_19,
  output out_20,
  output out_21,
  output out_22,
  output out_23,
  output out_24,
  output out_25
);

  wire not_1_out, xor_1_out, xor_3_out, xor_4_out, xor_5_out, xor_6_out, xor_9_out, xor_10_out, xor_11_out,
       xor_12_out, xor_13_out, xor_14_out, xor_15_out, xor_16_out;

  buf buffer_1 (out_10, Buffer);
  xor odd_parity_1 (out_17, in_7[0], in_7[1], in_7[2]);
  xor xor_1 (xor_1_out, in_7[0], in_7[1]);
  xor xor_2 (out_18, xor_1_out, in_7[2]);
  xor xor_3 (xor_3_out, in_8[0], in_8[1]);
  xor xor_4 (xor_4_out, in_8[0], in_8[1]);
  xor xor_5 (xor_5_out, in_8[2], in_8[3]);
  assign out_11 = in_4 ? in_2 : 1'bz;  // Controlled_Buffer controlled_buffer_1
  Pull_Resistor pull_resistor_1 (.node(out_11));
  and and_1 (out_14, in_2, in_4);
  xor odd_parity_2 (out_20, in_8[0], in_8[1], in_8[2], in_8[3]);
  xor xor_6 (xor_6_out, xor_3_out, in_8[2]);
  xor xor_7 (out_22, xor_6_out, in_8[3]);
  xor xor_8 (out_24, xor_4_out, xor_5_out);
  not not_1 (not_1_out, in_3);
  Pull_Resistor pull_resistor_2 (.node(out_12));
  assign out_12 = in_5 ? ~in_3 : 1'bz;  // Controlled_Inverter controlled_inverter_1
  and and_2 (out_15, not_1_out, in_5);
  xor xor_9 (xor_9_out, in_6[0], in_6[1]);
  xor xor_10 (xor_10_out, in_9[0], in_9[1]);
  xor xor_11 (xor_11_out, in_9[0], in_9[1]);
  xor xor_12 (xor_12_out, in_9[2], in_9[3]);
  xnor even_parity_1 (out_16, in_6[0], in_6[1], in_6[2]);
  not not_2 (out_19, xor_13_out);
  xor xor_13 (xor_13_out, xor_9_out, in_6[2]);
  xnor even_parity_2 (out_21, in_9[0], in_9[1], in_9[2], in_9[3]);
  xor xor_14 (xor_14_out, xor_10_out, in_9[2]);
  xor xor_15 (xor_15_out, xor_14_out, in_9[3]);
  xor xor_16 (xor_16_out, xor_11_out, xor_12_out);
  not not_3 (out_25, xor_16_out);
  not not_4 (out_23, xor_15_out);

  assign out_13 = Buffer;

  // Notes on the sheet:
  //   Odd Parity
  //   Odd Parity
  //   Controlled Buffer
  //   Controlled Inverter
  //   Even Parity
  //   Even Parity
endmodule

module main2 (
  input  [3:0] Data,
  input  Load,
  input  Shift,
  input  Input,
  input  Clock,
  input  Clear,
  output out_7,
  output [3:0] out_8,
  output out_9,
  output [3:0] out_10
);

  Shift_Register #(.length(4)) shift_register_1 (
    .shift(Shift), .in(Input), .clk(Clock), .out(out_7), .load(Load), .clr(Clear), .d0(Data[3]),
    .q0(out_8[3]), .d1(Data[2]), .q1(out_8[2]), .d2(Data[1]), .q2(out_8[1]), .d3(Data[0]), .q3(out_8[0]));
  SHIFTRG shiftrg_1 (
    .Data(Data), .Input(Input), .Clock(Clock), .Load(Load), .Shift(Shift), .Clear(Clear), .Output(out_9),
    .Data_output(out_10));
endmodule

module main3 (
  input  [2:0] in_1,
  input  [2:0] in_2,
  input  [3:0] in_3,
  input  [3:0] in_4,
  input  [2:0] in_5,
  input  [2:0] in_6,
  input  [2:0] in_7,
  input  [2:0] in_8,
  input  [2:0] in_9,
  input  [2:0] in_10,
  output [1:0] out_11,
  output [1:0] out_12,
  output [2:0] out_13,
  output [2:0] out_14,
  output [3:0] out_15,
  output [3:0] out_16
);

  wire [1:0] adder_2_out, adder_3_out, adder_4_out, adder_5_out, adder_7_out;
  wire [2:2] adder_7_cout;

  BitAdder #(.width(3)) bitadder_1 (.in0(in_1), .out(out_12));
  BitAdder #(.width(4)) bitadder_2 (.in0(in_3), .out(out_13));
  BitAdder #(.width(3)) bitadder_3 (.in0(in_5), .in1(in_6), .in2(in_8), .out(out_15));
  Adder #(.width(1)) adder_1 (.a(in_2[1]), .b(in_2[2]), .out(out_11[0]), .cin(in_2[0]), .cout(out_11[1]));
  Adder #(.width(1)) adder_2 (.a(in_4[1]), .b(in_4[2]), .out(adder_2_out[0]), .cin(in_4[0]), .cout(adder_2_out[1]));
  Adder #(.width(1)) adder_3 (.a(in_7[1]), .b(in_7[2]), .out(adder_3_out[0]), .cin(in_7[0]), .cout(adder_3_out[1]));
  Adder #(.width(1)) adder_4 (.a(in_9[1]), .b(in_9[2]), .out(adder_4_out[0]), .cin(in_9[0]), .cout(adder_4_out[1]));
  Adder #(.width(1)) adder_5 (.a(in_10[1]), .b(in_10[2]), .out(adder_5_out[0]), .cin(in_10[0]), .cout(adder_5_out[1]));
  Adder #(.width(2)) adder_6 (.a(adder_2_out), .b({1'b0, in_4[3]}), .out(out_14[1:0]), .cin(1'b0), .cout(out_14[2]));
  Adder #(.width(2)) adder_7 (.a(adder_3_out), .b(adder_4_out), .out(adder_7_out), .cin(1'b0), .cout(adder_7_cout[2]));
  Adder #(.width(3)) adder_8 (
    .a({adder_7_cout[2], adder_7_out}), .b({1'b0, adder_5_out}), .out(out_16[2:0]), .cin(1'b0),
    .cout(out_16[3]));
endmodule

module SHIFTRG (
  input  [3:0] Data,
  input  Input,
  input  Clock,
  input  Load,
  input  Shift,
  input  Clear,
  output Output,
  output [3:0] Data_output
);

  SHD1B shd1b_1 (
    .Data(Data[3]), .Input(Input), .Load(Load), .Clock(Clock), .Shift(Shift), .Clear(Clear),
    .out_7(Data_output[3]));
  SHD1B shd1b_2 (
    .Data(Data[2]), .Input(Data_output[3]), .Load(Load), .Clock(Clock), .Shift(Shift), .Clear(Clear),
    .out_7(Data_output[2]));
  SHD1B shd1b_3 (
    .Data(Data[1]), .Input(Data_output[2]), .Load(Load), .Clock(Clock), .Shift(Shift), .Clear(Clear),
    .out_7(Data_output[1]));
  SHD1B shd1b_4 (
    .Data(Data[0]), .Input(Data_output[1]), .Load(Load), .Clock(Clock), .Shift(Shift), .Clear(Clear),
    .out_7(Data_output[0]));

  assign Output = Data_output[0];
endmodule

module SHD1B (
  input  Data,
  input  Input,
  input  Load,
  input  Clock,
  input  Shift,
  input  Clear,
  output out_7
);

  wire and_1_out, and_2_out, not_1_out, or_1_out, or_2_out;

  and and_1 (and_1_out, Data, Load);
  and and_2 (and_2_out, Input, not_1_out);
  not not_1 (not_1_out, Load);
  or or_1 (or_1_out, Load, Shift);
  or or_2 (or_2_out, and_1_out, and_2_out);
  D_Flip_Flop d_ff_1 (.clk(Clock), .D(or_2_out), .Q(out_7), .preset(1'b0), .en(or_1_out), .reset(Clear));  // open: Qn
endmodule
